// Logisim project 20151003.circ as structural Verilog
module CPU (
);

  wire [3:0] cpu_ir_1_ssel_dsel, cpu_ir_1_tsel;
  wire [15:0] cpu_alu_1_out_6, cpu_registers_1_out_8, cpu_registers_1_out_9, cpu_registers_1_out_10,
       cpu_registers_1_out_11, cpu_registers_1_out_12, cpu_registers_1_out_13, cpu_registers_1_out_14,
       cpu_registers_1_out_15, cpu_registers_1_out_16, cpu_registers_1_out_17, cpu_registers_1_out_18,
       cpu_registers_1_out_19, cpu_registers_1_out_20, cpu_registers_1_out_21, cpu_registers_1_out_22,
       cpu_registers_1_out_23, cpu_registers_1_sreg, cpu_registers_1_treg, multiplexer_1_out,
       multiplexer_2_out, multiplexer_3_out, undriven, undriven_2;

  CPU_IR cpu_ir_1 (.ssel_dsel(cpu_ir_1_ssel_dsel), .tsel(cpu_ir_1_tsel));  // open: in_1, OPCode, OP2
  CPU_Registers cpu_registers_1 (
    .DataIn(multiplexer_3_out), .dsel(cpu_ir_1_ssel_dsel), .tsel(cpu_ir_1_tsel),
    .out_8(cpu_registers_1_out_8), .out_9(cpu_registers_1_out_9), .out_10(cpu_registers_1_out_10),
    .out_11(cpu_registers_1_out_11), .out_12(cpu_registers_1_out_12), .out_13(cpu_registers_1_out_13),
    .out_14(cpu_registers_1_out_14), .out_15(cpu_registers_1_out_15), .out_16(cpu_registers_1_out_16),
    .out_17(cpu_registers_1_out_17), .out_18(cpu_registers_1_out_18), .out_19(cpu_registers_1_out_19),
    .out_20(cpu_registers_1_out_20), .out_21(cpu_registers_1_out_21), .out_22(cpu_registers_1_out_22),
    .out_23(cpu_registers_1_out_23), .sreg(cpu_registers_1_sreg), .treg(cpu_registers_1_treg));  // open: clock, ssel, we, reset
  Multiplexer #(.select(2), .width(16), .disabled(0), .enable("false")) multiplexer_1 (
    .in0(cpu_registers_1_sreg), .in1(cpu_alu_1_out_6), .out(multiplexer_1_out));  // open: in2, in3, sel
  // Probe on cpu_registers_1_out_8
  // Probe on cpu_registers_1_out_9
  // Probe on cpu_registers_1_out_10
  // Probe on cpu_registers_1_out_11
  // Probe on cpu_registers_1_out_12
  // Probe on cpu_registers_1_out_13
  // Probe on cpu_registers_1_out_14
  // Probe on cpu_registers_1_out_15
  // Probe on cpu_registers_1_out_16
  // Probe on cpu_registers_1_out_17
  // Probe on cpu_registers_1_out_18
  // Probe on cpu_registers_1_out_19
  // Probe on cpu_registers_1_out_20
  // Probe on cpu_registers_1_out_21
  // Probe on cpu_registers_1_out_22
  // Probe on cpu_registers_1_out_23
  Multiplexer #(.select(2), .width(16), .disabled(0), .enable("false")) multiplexer_2 (
    .in0(cpu_registers_1_treg), .in1(cpu_alu_1_out_6), .out(multiplexer_2_out));  // open: in2, in3, sel
  Multiplexer #(.width(16), .disabled(0), .enable("false")) multiplexer_3 (
    .in0(undriven), .in1(undriven_2), .out(multiplexer_3_out));  // open: sel
  CPU_ALU cpu_alu_1 (.out_6(cpu_alu_1_out_6));  // open: A, B, CarryIn, ALUOP, Carry, Overflow, Zero, Sign
endmodule

module CPU_Registers (
  input  clock,
  input  reset,
  input  [15:0] DataIn,
  input  [3:0] dsel,
  input  [3:0] ssel,
  input  [3:0] tsel,
  input  we,
  output [15:0] out_8,
  output [15:0] out_9,
  output [15:0] out_10,
  output [15:0] out_11,
  output [15:0] out_12,
  output [15:0] out_13,
  output [15:0] out_14,
  output [15:0] out_15,
  output [15:0] out_16,
  output [15:0] out_17,
  output [15:0] out_18,
  output [15:0] out_19,
  output [15:0] out_20,
  output [15:0] out_21,
  output [15:0] out_22,
  output [15:0] out_23,
  output [15:0] sreg,
  output [15:0] treg
);

  wire demultiplexer_1_out0, demultiplexer_1_out1, demultiplexer_1_out2, demultiplexer_1_out3,
       demultiplexer_1_out4, demultiplexer_1_out5, demultiplexer_1_out6, demultiplexer_1_out7,
       demultiplexer_1_out8, demultiplexer_1_out9, demultiplexer_1_out10, demultiplexer_1_out11,
       demultiplexer_1_out12, demultiplexer_1_out13, demultiplexer_1_out14, demultiplexer_1_out15;

  Demultiplexer #(.select(4), .enable("false")) demultiplexer_1 (
    .out0(demultiplexer_1_out0), .out1(demultiplexer_1_out1), .out2(demultiplexer_1_out2),
    .out3(demultiplexer_1_out3), .out4(demultiplexer_1_out4), .out5(demultiplexer_1_out5),
    .out6(demultiplexer_1_out6), .out7(demultiplexer_1_out7), .out8(demultiplexer_1_out8),
    .out9(demultiplexer_1_out9), .out10(demultiplexer_1_out10), .out11(demultiplexer_1_out11),
    .out12(demultiplexer_1_out12), .out13(demultiplexer_1_out13), .out14(demultiplexer_1_out14),
    .out15(demultiplexer_1_out15), .in(we), .sel(dsel));
  Register #(.width(16)) register_1 (.D(DataIn), .en(demultiplexer_1_out0), .Q(out_8), .clk(clock), .clr(reset));
  Register #(.width(16)) register_2 (.D(DataIn), .en(demultiplexer_1_out1), .Q(out_9), .clk(clock), .clr(reset));
  Register #(.width(16)) register_3 (.D(DataIn), .en(demultiplexer_1_out2), .Q(out_10), .clk(clock), .clr(reset));
  Register #(.width(16)) register_4 (.D(DataIn), .en(demultiplexer_1_out3), .Q(out_11), .clk(clock), .clr(reset));
  Register #(.width(16)) register_5 (.D(DataIn), .en(demultiplexer_1_out4), .Q(out_12), .clk(clock), .clr(reset));
  Register #(.width(16)) register_6 (.D(DataIn), .en(demultiplexer_1_out5), .Q(out_13), .clk(clock), .clr(reset));
  Register #(.width(16)) register_7 (.D(DataIn), .en(demultiplexer_1_out6), .Q(out_14), .clk(clock), .clr(reset));
  Register #(.width(16)) register_8 (.D(DataIn), .en(demultiplexer_1_out7), .Q(out_15), .clk(clock), .clr(reset));
  Register #(.width(16)) register_9 (.D(DataIn), .en(demultiplexer_1_out8), .Q(out_16), .clk(clock), .clr(reset));
  Register #(.width(16)) register_10 (.D(DataIn), .en(demultiplexer_1_out9), .Q(out_17), .clk(clock), .clr(reset));
  Register #(.width(16)) register_11 (.D(DataIn), .en(demultiplexer_1_out10), .Q(out_18), .clk(clock), .clr(reset));
  Register #(.width(16)) register_12 (.D(DataIn), .en(demultiplexer_1_out11), .Q(out_19), .clk(clock), .clr(reset));
  Register #(.width(16)) register_13 (.D(DataIn), .en(demultiplexer_1_out12), .Q(out_20), .clk(clock), .clr(reset));
  Register #(.width(16)) register_14 (.D(DataIn), .en(demultiplexer_1_out13), .Q(out_21), .clk(clock), .clr(reset));
  Register #(.width(16)) register_15 (.D(DataIn), .en(demultiplexer_1_out14), .Q(out_22), .clk(clock), .clr(reset));
  Register #(.width(16)) register_16 (.D(DataIn), .en(demultiplexer_1_out15), .Q(out_23), .clk(clock), .clr(reset));
  Multiplexer #(.select(4), .width(16), .enable("false")) multiplexer_1 (
    .in0(out_8), .in1(out_9), .in2(out_10), .in3(out_11), .in4(out_12), .in5(out_13), .in6(out_14),
    .in7(out_15), .in8(out_16), .in9(out_17), .in10(out_18), .in11(out_19), .in12(out_20), .in13(out_21),
    .in14(out_22), .in15(out_23), .out(sreg), .sel(ssel));
  Multiplexer #(.select(4), .width(16), .enable("false")) multiplexer_2 (
    .in0(out_8), .in1(out_9), .in2(out_10), .in3(out_11), .in4(out_12), .in5(out_13), .in6(out_14),
    .in7(out_15), .in8(out_16), .in9(out_17), .in10(out_18), .in11(out_19), .in12(out_20), .in13(out_21),
    .in14(out_22), .in15(out_23), .out(treg), .sel(tsel));
endmodule

module CPU_ALU (
  input  CarryIn,
  input  [15:0] A,
  input  [15:0] B,
  input  [4:0] ALUOP,
  output Sign,
  output [15:0] out_6,
  output Carry,
  output Overflow,
  output Zero
);

  wire adder_1_cout, adder_2_cout, adder_3_cout, multiplexer_2_out, multiplexer_4_out, multiplexer_5_out,
       multiplexer_7_out, not_1_out, xor_6_out;
  wire [15:0] adder_1_out, adder_3_out, and_1_out, bit_extender_1_out, multiplexer_1_out, multiplexer_3_out,
       multiplexer_6_out, negator_1_out, not_2_out, or_1_out, shifter_1_out, shifter_2_out, shifter_3_out,
       shifter_4_out, shifter_5_out, xor_1_out, xor_2_out, xor_3_out, xor_4_out, xor_5_out;

  not not_1 (not_1_out, CarryIn);
  assign or_1_out = A | B;  // OR_Gate or_1, 16 bits wide
  assign xor_1_out = A ^ B;  // XOR_Gate xor_1, 16 bits wide
  assign xor_2_out = or_1_out ^ bit_extender_1_out;  // XOR_Gate xor_2, 16 bits wide
  assign xor_3_out = xor_1_out ^ bit_extender_1_out;  // XOR_Gate xor_3, 16 bits wide
  Multiplexer #(.select(2), .width(16), .enable("false")) multiplexer_1 (
    .in0(xor_5_out), .in1(xor_4_out), .in2(xor_2_out), .in3(xor_3_out), .out(multiplexer_1_out),
    .sel(ALUOP[1:0]));
  Multiplexer #(.select(3), .enable("false")) multiplexer_2 (
    .in0(1'b0), .in1(1'b0), .in2(CarryIn), .in3(not_1_out), .in4(1'b0), .in5(1'b0), .in6(1'b0), .in7(1'b0),
    .out(multiplexer_2_out), .sel(ALUOP[2:0]));
  Negator #(.width(16)) negator_1 (.in(B), .out(negator_1_out));
  assign not_2_out = ~B;  // NOT_Gate not_2, 16 bits wide
  assign and_1_out = A & B;  // AND_Gate and_1, 16 bits wide
  assign xor_4_out = and_1_out ^ bit_extender_1_out;  // XOR_Gate xor_4, 16 bits wide
  assign xor_5_out = not_2_out ^ bit_extender_1_out;  // XOR_Gate xor_5, 16 bits wide
  Multiplexer #(.select(3), .width(16), .enable("false")) multiplexer_3 (
    .in0(B), .in1(negator_1_out), .in2(B), .in3(negator_1_out), .in4(16'h1), .in5({16{1'b1}}),
    .in6({16{1'b0}}), .in7({16{1'b0}}), .out(multiplexer_3_out), .sel(ALUOP[2:0]));
  assign bit_extender_1_out = {{15{ALUOP[2]}}, ALUOP[2]};  // Bit_Extender bit_extender_1
  Multiplexer #(.select(4), .enable("false")) multiplexer_4 (
    .in0(1'b0), .in1(A[15]), .in2(A[14]), .in3(A[13]), .in4(A[12]), .in5(A[11]), .in6(A[10]), .in7(A[9]),
    .in8(A[8]), .in9(A[7]), .in10(A[6]), .in11(A[5]), .in12(A[4]), .in13(A[3]), .in14(A[2]), .in15(A[1]),
    .out(multiplexer_4_out), .sel(B[3:0]));
  Shifter #(.width(16)) shifter_1 (.in(A), .\dist (B[3:0]), .out(shifter_1_out));
  Multiplexer #(.select(4), .enable("false")) multiplexer_5 (
    .in0(1'b0), .in1(A[0]), .in2(A[1]), .in3(A[2]), .in4(A[3]), .in5(A[4]), .in6(A[5]), .in7(A[6]),
    .in8(A[7]), .in9(A[8]), .in10(A[9]), .in11(A[10]), .in12(A[11]), .in13(A[12]), .in14(A[13]),
    .in15(A[14]), .out(multiplexer_5_out), .sel(B[3:0]));
  Shifter #(.width(16), .shift("lr")) shifter_2 (.in(A), .\dist (B[3:0]), .out(shifter_2_out));
  Shifter #(.width(16), .shift("ar")) shifter_3 (.in(A), .\dist (B[3:0]), .out(shifter_3_out));
  Shifter #(.width(16), .shift("rl")) shifter_4 (.in(A), .\dist (B[3:0]), .out(shifter_4_out));
  Shifter #(.width(16), .shift("rr")) shifter_5 (.in(A), .\dist (B[3:0]), .out(shifter_5_out));
  Adder #(.width(15)) adder_1 (
    .a(A[14:0]), .b(multiplexer_3_out[14:0]), .out(adder_1_out[14:0]), .cin(multiplexer_2_out),
    .cout(adder_1_cout));
  Adder #(.width(1)) adder_2 (
    .a(A[15]), .b(multiplexer_3_out[15]), .out(adder_1_out[15]), .cin(adder_1_cout), .cout(adder_2_cout));
  Adder #(.width(16)) adder_3 (
    .a(A), .b(multiplexer_3_out), .out(adder_3_out), .cin(multiplexer_2_out), .cout(adder_3_cout));
  Multiplexer #(.select(3), .width(16), .enable("false")) multiplexer_6 (
    .in0(shifter_1_out), .in1(shifter_2_out), .in2(shifter_3_out), .in3(shifter_4_out), .in4(shifter_5_out),
    .in5({16{1'b0}}), .in6({16{1'b0}}), .in7({16{1'b0}}), .out(multiplexer_6_out), .sel(ALUOP[2:0]));
  xor xor_6 (xor_6_out, adder_1_cout, adder_2_cout);
  Multiplexer #(.select(3), .enable("false")) multiplexer_7 (
    .in0(multiplexer_4_out), .in1(multiplexer_5_out), .in2(multiplexer_5_out), .in3(multiplexer_4_out),
    .in4(multiplexer_5_out), .in5(1'b0), .in6(1'b0), .in7(1'b0), .out(multiplexer_7_out), .sel(ALUOP[2:0]));
  Multiplexer #(.select(2), .width(16), .enable("false")) multiplexer_8 (
    .in0(adder_1_out), .in1(adder_3_out), .in2(multiplexer_1_out), .in3(multiplexer_6_out), .out(out_6),
    .sel(ALUOP[4:3]));
  Multiplexer #(.select(2), .enable("false")) multiplexer_9 (
    .in0(adder_2_cout), .in1(adder_3_cout), .in2(1'b0), .in3(multiplexer_7_out), .out(Carry), .sel(ALUOP[4:3]));
  Multiplexer #(.select(2), .enable("false")) multiplexer_10 (
    .in0(xor_6_out), .in1(1'b0), .in2(1'b0), .in3(1'b0), .out(Overflow), .sel(ALUOP[4:3]));
  nor nor_1 (Zero, out_6[0], out_6[1], out_6[2], out_6[3], out_6[4], out_6[5], out_6[6], out_6[7], out_6[8], out_6[9], out_6[10], out_6[11], out_6[12], out_6[13], out_6[14], out_6[15]);
  not not_3 (Sign, out_6[15]);

  // Other names for the same wires on the sheet: LOOP[2:0] = ALUOP[2:0]; HIOP[1:0] = ALUOP[4:3]
endmodule

module CPU_IR (
  input  [15:0] in_1,
  output [5:0] OPCode,
  output [3:0] ssel_dsel,
  output [3:0] tsel,
  output [1:0] OP2
);


  assign OP2 = in_1[1:0];
  assign OPCode = in_1[15:10];
  assign ssel_dsel = in_1[9:6];
  assign tsel = in_1[5:2];
endmodule

module CPU_ID_EX (
  input  [15:0] A,
  input  [15:0] B,
  input  [3:0] dsel,
  input  [4:0] ALUOP
);

  wire undriven, undriven_2;
  wire [3:0] register_3_q;
  wire [4:0] register_4_q;
  wire [15:0] register_1_q, register_2_q;

  Register #(.width(16)) register_1 (.D(A), .Q(register_1_q), .clk(undriven));  // open: en, clr
  Register #(.width(16)) register_2 (.D(B), .Q(register_2_q), .clk(undriven));  // open: en, clr
  Register #(.width(4)) register_3 (.D(dsel), .Q(register_3_q), .clk(undriven));  // open: en, clr
  Register #(.width(5)) register_4 (.D(ALUOP), .Q(register_4_q), .clk(undriven));  // open: en, clr
  Multiplexer #(.width(16), .disabled(0), .enable("false")) multiplexer_1 (
    .in0(register_1_q), .in1({16{1'b0}}), .sel(undriven_2));  // open: out
  Multiplexer #(.width(16), .disabled(0), .enable("false")) multiplexer_2 (
    .in0(register_2_q), .in1({16{1'b0}}), .sel(undriven_2));  // open: out
  Multiplexer #(.width(4), .disabled(0), .enable("false")) multiplexer_3 (
    .in0(register_3_q), .in1(4'b0000), .sel(undriven_2));  // open: out
  Multiplexer #(.width(5), .disabled(0), .enable("false")) multiplexer_4 (
    .in0(register_4_q), .in1({5{1'b0}}), .sel(undriven_2));  // open: out
endmodule
