// Logisim project 20151005.circ as structural Verilog: 13 circuits, main circuit CPU
module main (
);

  wire button_1_out, clock_1_out;
  wire [6:0] keyboard_1_data;

  Keyboard #(.buflen(64)) keyboard_1 (.clk(clock_1_out), .data(keyboard_1_data));  // open: re, clr, avail
  Clock clock_1 (.out(clock_1_out));
  Button button_1 (.out(button_1_out));
  TTY #(.rows(32), .cols(64)) tty_1 (.data(keyboard_1_data), .clk(clock_1_out), .clr(button_1_out));  // open: we
endmodule

module PBBP (
);

  CPU cpu_1 ();  // open: in_1
  RAM ram_1 ();  // open: 地址输入, 数据输入, 对存储器进行访问, 时钟信号, 清零, 数据输出, 写使能
  ROM rom_1 ();  // open: 地址, 写入数据, 保存, 时钟, 加载, 输出地址
endmodule

module RAM (
  input  [15:0] \地址输入 ,
  input  [15:0] \数据输入 ,
  input  \对存储器进行访问 ,
  input  \时钟信号 ,
  input  \写使能 ,
  input  \清零 ,
  output [15:0] \数据输出 
);

  RAM_part #(.addrWidth(16), .dataWidth(16), .bus("separate")) ram_1 (
    .addr(\地址输入 ), .din(\数据输入 ), .data(\数据输出 ), .str(\写使能 ), .sel(\对存储器进行访问 ), .clk(\时钟信号 ), .clr(\清零 ));  // open: ld
endmodule

module ROM (
  input  [23:0] \地址 ,
  input  [15:0] \写入数据 ,
  input  \保存 ,
  input  \时钟 ,
  input  \加载 ,
  output [15:0] \输出地址 
);

  RAM_part #(.addrWidth(24), .dataWidth(16), .bus("separate")) ram_1 (
    .addr(\地址 ), .din(\写入数据 ), .data(\输出地址 ), .str(\保存 ), .clk(\时钟 ), .ld(\加载 ));  // open: sel, clr
endmodule

module CPU (
  input  in_1
);

  wire \cpu_ir_1_存储器写使能 , \cpu_ir_1_对存储器进行访问 , \cpu_ir_1_扩展方式 , \cpu_ir_1_是否从存储器中写回 , undriven;
  wire [1:0] cpu_ir_1_ssel, cpu_ir_1_tsel_2;
  wire [3:0] cpu_id_ex_1_dsel_2, cpu_ir_1_ssel_dsel, cpu_ir_1_tsel;
  wire [4:0] cpu_id_ex_1_aluop_2, cpu_ir_1_aluop;
  wire [15:0] cpu_id_ex_1_a_2, cpu_id_ex_1_b_2, \cpu_if_id_1_指令输出 , cpu_immed_1_out_3, cpu_registers_1_out_8,
       cpu_registers_1_out_9, cpu_registers_1_out_10, cpu_registers_1_out_11, cpu_registers_1_out_12,
       cpu_registers_1_out_13, cpu_registers_1_out_14, cpu_registers_1_out_15, cpu_registers_1_out_16,
       cpu_registers_1_out_17, cpu_registers_1_out_18, cpu_registers_1_out_19, cpu_registers_1_out_20,
       cpu_registers_1_out_21, cpu_registers_1_out_22, cpu_registers_1_out_23, cpu_registers_1_sreg,
       cpu_registers_1_treg, multiplexer_1_out, multiplexer_2_out;

  CPU_IF_ID cpu_if_id_1 (
    .\流水线中断 (in_1), .\时钟 (in_1), .\重启 (undriven), .\产生气泡 (in_1), .\指令输出 (\cpu_if_id_1_指令输出 ));  // open: 指令输入
  CPU_IR cpu_ir_1 (
    .In(\cpu_if_id_1_指令输出 ), .ALUOP(cpu_ir_1_aluop), .\存储器写使能 (\cpu_ir_1_存储器写使能 ),
    .\对存储器进行访问 (\cpu_ir_1_对存储器进行访问 ), .\是否从存储器中写回 (\cpu_ir_1_是否从存储器中写回 ), .ssel_dsel(cpu_ir_1_ssel_dsel),
    .tsel(cpu_ir_1_tsel), .EX_dsel(cpu_id_ex_1_dsel_2), .ssel(cpu_ir_1_ssel), .tsel_2(cpu_ir_1_tsel_2),
    .\扩展方式 (\cpu_ir_1_扩展方式 ));  // open: MEM_dsel
  CPU_Immed cpu_immed_1 (.in_1(\cpu_if_id_1_指令输出 ), .in_2(\cpu_ir_1_扩展方式 ), .out_3(cpu_immed_1_out_3));
  CPU_Registers cpu_registers_1 (
    .ssel(cpu_ir_1_ssel_dsel), .tsel(cpu_ir_1_tsel), .out_8(cpu_registers_1_out_8),
    .out_9(cpu_registers_1_out_9), .out_10(cpu_registers_1_out_10), .out_11(cpu_registers_1_out_11),
    .out_12(cpu_registers_1_out_12), .out_13(cpu_registers_1_out_13), .out_14(cpu_registers_1_out_14),
    .out_15(cpu_registers_1_out_15), .out_16(cpu_registers_1_out_16), .out_17(cpu_registers_1_out_17),
    .out_18(cpu_registers_1_out_18), .out_19(cpu_registers_1_out_19), .out_20(cpu_registers_1_out_20),
    .out_21(cpu_registers_1_out_21), .out_22(cpu_registers_1_out_22), .out_23(cpu_registers_1_out_23),
    .sreg(cpu_registers_1_sreg), .treg(cpu_registers_1_treg), .\重启 (undriven));  // open: 时钟, DataIn, dsel, 写使能
  // Probe on cpu_registers_1_out_8
  // Probe on cpu_registers_1_out_9
  // Probe on cpu_registers_1_out_10
  // Probe on cpu_registers_1_out_11
  // Probe on cpu_registers_1_out_12
  // Probe on cpu_registers_1_out_13
  // Probe on cpu_registers_1_out_14
  // Probe on cpu_registers_1_out_15
  // Probe on cpu_registers_1_out_16
  // Probe on cpu_registers_1_out_17
  // Probe on cpu_registers_1_out_18
  // Probe on cpu_registers_1_out_19
  // Probe on cpu_registers_1_out_20
  // Probe on cpu_registers_1_out_21
  // Probe on cpu_registers_1_out_22
  // Probe on cpu_registers_1_out_23
  Multiplexer #(.select(2), .width(16), .disabled(0), .enable("false")) multiplexer_1 (
    .in0(cpu_registers_1_sreg), .in3(cpu_immed_1_out_3), .out(multiplexer_1_out), .sel(cpu_ir_1_ssel));  // open: in1, in2
  Multiplexer #(.select(2), .width(16), .disabled(0), .enable("false")) multiplexer_2 (
    .in0(cpu_registers_1_treg), .in3(cpu_immed_1_out_3), .out(multiplexer_2_out), .sel(cpu_ir_1_tsel_2));  // open: in1, in2
  CPU_ID_EX cpu_id_ex_1 (
    .A(multiplexer_1_out), .B(multiplexer_2_out), .dsel(cpu_ir_1_ssel_dsel), .ALUOP(cpu_ir_1_aluop),
    .\重启 (undriven), .\存储器写使能 (\cpu_ir_1_存储器写使能 ), .\对存储器进行访问 (\cpu_ir_1_对存储器进行访问 ),
    .\是否从存储器中写回 (\cpu_ir_1_是否从存储器中写回 ), .dsel_2(cpu_id_ex_1_dsel_2), .ALUOP_2(cpu_id_ex_1_aluop_2),
    .A_2(cpu_id_ex_1_a_2), .B_2(cpu_id_ex_1_b_2), .\保存的数据 (cpu_registers_1_sreg));  // open: 时钟, 流水线中断, 产生气泡, 是否从存储器中写回_2, 对存储器进行访问_2, 存储器写使能_2, 保存的数据_2
  CPU_ALU cpu_alu_1 (
    .A(cpu_id_ex_1_a_2), .B(cpu_id_ex_1_b_2), .ALUOP(cpu_id_ex_1_aluop_2));  // open: out_5, CarryIn, Carry, Overflow, Zero
endmodule

module CPU_IF (
  input  [15:0] in_1,
  output [15:0] out_2
);

  wire [15:0] adder_1_out;

  Adder #(.width(16)) adder_1 (.a(out_2), .b(16'h1), .out(adder_1_out));  // open: cin, cout
  Register #(.width(16)) register_1 (.D(adder_1_out), .Q(out_2));  // open: en, clk, clr
endmodule

module CPU_IF_ID (
  input  [15:0] \指令输入 ,
  input  \流水线中断 ,
  input  \时钟 ,
  input  \重启 ,
  input  \产生气泡 ,
  output [15:0] \指令输出 
);

  wire not_1_out;
  wire [15:0] register_1_q;

  not not_1 (not_1_out, \流水线中断 );
  Register #(.width(16)) register_1 (.D(\指令输入 ), .en(not_1_out), .Q(register_1_q), .clk(\时钟 ), .clr(\重启 ));
  Multiplexer #(.width(16), .disabled(0), .enable("false")) multiplexer_1 (
    .in0(register_1_q), .in1({16{1'b0}}), .out(\指令输出 ), .sel(\产生气泡 ));
endmodule

module CPU_IR (
  input  [15:0] In,
  input  [3:0] EX_dsel,
  input  [3:0] MEM_dsel,
  output [4:0] ALUOP,
  output \存储器写使能 ,
  output \对存储器进行访问 ,
  output \是否从存储器中写回 ,
  output \扩展方式 ,
  output [3:0] ssel_dsel,
  output [3:0] tsel,
  output [1:0] ssel,
  output [1:0] tsel_2
);

  wire comparator_2_eq, comparator_3_eq, comparator_4_eq, Immed, multiplexer_2_out;
  wire [1:0] bit_extender_1_out, multiplexer_3_out;
  wire [5:0] rom_1_data;

  Comparator #(.width(4), .mode("unsigned")) comparator_1 (.a(In[9:6]), .b(EX_dsel), .eq(ssel[0]));  // open: gt, lt
  Comparator #(.width(4), .mode("unsigned")) comparator_2 (
    .a(In[5:2]), .b(EX_dsel), .eq(comparator_2_eq));  // open: gt, lt
  Comparator #(.width(4), .mode("unsigned")) comparator_3 (
    .a(MEM_dsel), .b(In[9:6]), .eq(comparator_3_eq));  // open: gt, lt
  Comparator #(.width(4), .mode("unsigned")) comparator_4 (
    .a(MEM_dsel), .b(In[5:2]), .eq(comparator_4_eq));  // open: gt, lt
  Multiplexer #(.disabled(0), .enable("false")) multiplexer_1 (
    .in0(comparator_3_eq), .in1(1'b0), .out(ssel[1]), .sel(comparator_2_eq));
  Multiplexer #(.disabled(0), .enable("false")) multiplexer_2 (
    .in0(comparator_4_eq), .in1(1'b0), .out(multiplexer_2_out), .sel(ssel[0]));
  ROM_part #(.addrWidth(6), .dataWidth(16)) rom_1 (
    .addr(In[15:10]), .data({ALUOP, \存储器写使能 , \对存储器进行访问 , \是否从存储器中写回 , Immed, \扩展方式 , rom_1_data}));  // open: sel
  Multiplexer #(.disabled(0), .enable("false")) multiplexer_3 (
    .in0(comparator_2_eq), .in1(1'b0), .out(multiplexer_3_out[0]), .sel(Immed));
  Multiplexer #(.disabled(0), .enable("false")) multiplexer_4 (
    .in0(multiplexer_2_out), .in1(1'b0), .out(multiplexer_3_out[1]), .sel(Immed));
  assign bit_extender_1_out = {{1{1'b0}}, Immed};  // Bit_Extender bit_extender_1
  assign tsel_2 = multiplexer_3_out ^ bit_extender_1_out;  // XOR_Gate xor_1, 2 bits wide

  assign ssel_dsel = In[9:6];
  assign tsel = In[5:2];
endmodule

module CPU_Registers (
  input  \时钟 ,
  input  \重启 ,
  input  [15:0] DataIn,
  input  [3:0] dsel,
  input  [3:0] ssel,
  input  [3:0] tsel,
  input  \写使能 ,
  output [15:0] out_8,
  output [15:0] out_9,
  output [15:0] out_10,
  output [15:0] out_11,
  output [15:0] out_12,
  output [15:0] out_13,
  output [15:0] out_14,
  output [15:0] out_15,
  output [15:0] out_16,
  output [15:0] out_17,
  output [15:0] out_18,
  output [15:0] out_19,
  output [15:0] out_20,
  output [15:0] out_21,
  output [15:0] out_22,
  output [15:0] out_23,
  output [15:0] sreg,
  output [15:0] treg
);

  wire demultiplexer_1_out0, demultiplexer_1_out1, demultiplexer_1_out2, demultiplexer_1_out3,
       demultiplexer_1_out4, demultiplexer_1_out5, demultiplexer_1_out6, demultiplexer_1_out7,
       demultiplexer_1_out8, demultiplexer_1_out9, demultiplexer_1_out10, demultiplexer_1_out11,
       demultiplexer_1_out12, demultiplexer_1_out13, demultiplexer_1_out14, demultiplexer_1_out15;

  Demultiplexer #(.select(4), .enable("false")) demultiplexer_1 (
    .out0(demultiplexer_1_out0), .out1(demultiplexer_1_out1), .out2(demultiplexer_1_out2),
    .out3(demultiplexer_1_out3), .out4(demultiplexer_1_out4), .out5(demultiplexer_1_out5),
    .out6(demultiplexer_1_out6), .out7(demultiplexer_1_out7), .out8(demultiplexer_1_out8),
    .out9(demultiplexer_1_out9), .out10(demultiplexer_1_out10), .out11(demultiplexer_1_out11),
    .out12(demultiplexer_1_out12), .out13(demultiplexer_1_out13), .out14(demultiplexer_1_out14),
    .out15(demultiplexer_1_out15), .in(\写使能 ), .sel(dsel));
  Register #(.width(16)) register_1 (.D(DataIn), .en(demultiplexer_1_out0), .Q(out_8), .clk(\时钟 ), .clr(\重启 ));
  Register #(.width(16)) register_2 (.D(DataIn), .en(demultiplexer_1_out1), .Q(out_9), .clk(\时钟 ), .clr(\重启 ));
  Register #(.width(16)) register_3 (.D(DataIn), .en(demultiplexer_1_out2), .Q(out_10), .clk(\时钟 ), .clr(\重启 ));
  Register #(.width(16)) register_4 (.D(DataIn), .en(demultiplexer_1_out3), .Q(out_11), .clk(\时钟 ), .clr(\重启 ));
  Register #(.width(16)) register_5 (.D(DataIn), .en(demultiplexer_1_out4), .Q(out_12), .clk(\时钟 ), .clr(\重启 ));
  Register #(.width(16)) register_6 (.D(DataIn), .en(demultiplexer_1_out5), .Q(out_13), .clk(\时钟 ), .clr(\重启 ));
  Register #(.width(16)) register_7 (.D(DataIn), .en(demultiplexer_1_out6), .Q(out_14), .clk(\时钟 ), .clr(\重启 ));
  Register #(.width(16)) register_8 (.D(DataIn), .en(demultiplexer_1_out7), .Q(out_15), .clk(\时钟 ), .clr(\重启 ));
  Register #(.width(16)) register_9 (.D(DataIn), .en(demultiplexer_1_out8), .Q(out_16), .clk(\时钟 ), .clr(\重启 ));
  Register #(.width(16)) register_10 (.D(DataIn), .en(demultiplexer_1_out9), .Q(out_17), .clk(\时钟 ), .clr(\重启 ));
  Register #(.width(16)) register_11 (.D(DataIn), .en(demultiplexer_1_out10), .Q(out_18), .clk(\时钟 ), .clr(\重启 ));
  Register #(.width(16)) register_12 (.D(DataIn), .en(demultiplexer_1_out11), .Q(out_19), .clk(\时钟 ), .clr(\重启 ));
  Register #(.width(16)) register_13 (.D(DataIn), .en(demultiplexer_1_out12), .Q(out_20), .clk(\时钟 ), .clr(\重启 ));
  Register #(.width(16)) register_14 (.D(DataIn), .en(demultiplexer_1_out13), .Q(out_21), .clk(\时钟 ), .clr(\重启 ));
  Register #(.width(16)) register_15 (.D(DataIn), .en(demultiplexer_1_out14), .Q(out_22), .clk(\时钟 ), .clr(\重启 ));
  Register #(.width(16)) register_16 (.D(DataIn), .en(demultiplexer_1_out15), .Q(out_23), .clk(\时钟 ), .clr(\重启 ));
  Multiplexer #(.select(4), .width(16), .enable("false")) multiplexer_1 (
    .in0(out_8), .in1(out_9), .in2(out_10), .in3(out_11), .in4(out_12), .in5(out_13), .in6(out_14),
    .in7(out_15), .in8(out_16), .in9(out_17), .in10(out_18), .in11(out_19), .in12(out_20), .in13(out_21),
    .in14(out_22), .in15(out_23), .out(sreg), .sel(ssel));
  Multiplexer #(.select(4), .width(16), .enable("false")) multiplexer_2 (
    .in0(out_8), .in1(out_9), .in2(out_10), .in3(out_11), .in4(out_12), .in5(out_13), .in6(out_14),
    .in7(out_15), .in8(out_16), .in9(out_17), .in10(out_18), .in11(out_19), .in12(out_20), .in13(out_21),
    .in14(out_22), .in15(out_23), .out(treg), .sel(tsel));
endmodule

module CPU_Immed (
  input  [15:0] in_1,
  input  in_2,
  output [15:0] out_3
);

  wire [15:0] bit_extender_1_out, bit_extender_2_out;

  assign bit_extender_1_out = {{10{in_1[5]}}, in_1[5:0]};  // Bit_Extender bit_extender_1
  assign bit_extender_2_out = {{10{1'b0}}, in_1[5:0]};  // Bit_Extender bit_extender_2
  Multiplexer #(.width(16), .disabled(0), .enable("false")) multiplexer_1 (
    .in0(bit_extender_1_out), .in1(bit_extender_2_out), .out(out_3), .sel(in_2));
endmodule

module CPU_ID_EX (
  input  \是否从存储器中写回 ,
  input  \对存储器进行访问 ,
  input  \存储器写使能 ,
  input  [15:0] \保存的数据 ,
  input  [15:0] A,
  input  [15:0] B,
  input  [3:0] dsel,
  input  [4:0] ALUOP,
  input  \流水线中断 ,
  input  \时钟 ,
  input  \重启 ,
  input  \产生气泡 ,
  output \是否从存储器中写回_2 ,
  output \对存储器进行访问_2 ,
  output \存储器写使能_2 ,
  output [15:0] \保存的数据_2 ,
  output [15:0] A_2,
  output [15:0] B_2,
  output [3:0] dsel_2,
  output [4:0] ALUOP_2
);

  wire not_1_out, register_1_q, register_2_q, register_3_q;
  wire [3:0] register_7_q;
  wire [4:0] register_8_q;
  wire [15:0] register_5_q, register_6_q;

  not not_1 (not_1_out, \流水线中断 );
  Register #(.width(1)) register_1 (.D(\是否从存储器中写回 ), .en(not_1_out), .Q(register_1_q), .clk(\时钟 ), .clr(\重启 ));
  Register #(.width(1)) register_2 (.D(\对存储器进行访问 ), .en(not_1_out), .Q(register_2_q), .clk(\时钟 ), .clr(\重启 ));
  Register #(.width(1)) register_3 (.D(\存储器写使能 ), .en(not_1_out), .Q(register_3_q), .clk(\时钟 ), .clr(\重启 ));
  Register #(.width(16)) register_4 (.D(\保存的数据 ), .en(not_1_out), .Q(\保存的数据_2 ), .clk(\时钟 ), .clr(\重启 ));
  Register #(.width(16)) register_5 (.D(A), .en(not_1_out), .Q(register_5_q), .clk(\时钟 ), .clr(\重启 ));
  Register #(.width(16)) register_6 (.D(B), .en(not_1_out), .Q(register_6_q), .clk(\时钟 ), .clr(\重启 ));
  Register #(.width(4)) register_7 (.D(dsel), .en(not_1_out), .Q(register_7_q), .clk(\时钟 ), .clr(\重启 ));
  Register #(.width(5)) register_8 (.D(ALUOP), .en(not_1_out), .Q(register_8_q), .clk(\时钟 ), .clr(\重启 ));
  Multiplexer #(.disabled(0), .enable("false")) multiplexer_1 (
    .in0(register_1_q), .in1(1'b0), .out(\是否从存储器中写回_2 ), .sel(\产生气泡 ));
  Multiplexer #(.disabled(0), .enable("false")) multiplexer_2 (
    .in0(register_2_q), .in1(1'b0), .out(\对存储器进行访问_2 ), .sel(\产生气泡 ));
  Multiplexer #(.disabled(0), .enable("false")) multiplexer_3 (
    .in0(register_3_q), .in1(1'b0), .out(\存储器写使能_2 ), .sel(\产生气泡 ));
  Multiplexer #(.width(16), .disabled(0), .enable("false")) multiplexer_4 (
    .in0(register_5_q), .in1({16{1'b0}}), .out(A_2), .sel(\产生气泡 ));
  Multiplexer #(.width(16), .disabled(0), .enable("false")) multiplexer_5 (
    .in0(register_6_q), .in1({16{1'b0}}), .out(B_2), .sel(\产生气泡 ));
  Multiplexer #(.width(4), .disabled(0), .enable("false")) multiplexer_6 (
    .in0(register_7_q), .in1(4'b0000), .out(dsel_2), .sel(\产生气泡 ));
  Multiplexer #(.width(5), .disabled(0), .enable("false")) multiplexer_7 (
    .in0(register_8_q), .in1({5{1'b0}}), .out(ALUOP_2), .sel(\产生气泡 ));
endmodule

module CPU_ALU (
  input  CarryIn,
  input  [15:0] A,
  input  [15:0] B,
  input  [4:0] ALUOP,
  output [15:0] out_5,
  output Carry,
  output Overflow,
  output Zero
);

  wire adder_1_cout, adder_2_cout, adder_3_cout, multiplexer_2_out, multiplexer_4_out, multiplexer_5_out,
       multiplexer_7_out, not_1_out, xor_6_out;
  wire [15:0] adder_1_out, adder_3_out, and_1_out, bit_extender_1_out, multiplexer_1_out, multiplexer_3_out,
       multiplexer_6_out, negator_1_out, not_2_out, or_1_out, shifter_1_out, shifter_2_out, shifter_3_out,
       shifter_4_out, shifter_5_out, xor_1_out, xor_2_out, xor_3_out, xor_4_out, xor_5_out;

  not not_1 (not_1_out, CarryIn);
  assign xor_1_out = A ^ B;  // XOR_Gate xor_1, 16 bits wide
  assign or_1_out = A | B;  // OR_Gate or_1, 16 bits wide
  assign xor_2_out = xor_1_out ^ bit_extender_1_out;  // XOR_Gate xor_2, 16 bits wide
  assign xor_3_out = or_1_out ^ bit_extender_1_out;  // XOR_Gate xor_3, 16 bits wide
  Multiplexer #(.select(2), .width(16), .enable("false")) multiplexer_1 (
    .in0(xor_5_out), .in1(xor_4_out), .in2(xor_3_out), .in3(xor_2_out), .out(multiplexer_1_out),
    .sel(ALUOP[1:0]));
  Multiplexer #(.select(3), .enable("false")) multiplexer_2 (
    .in0(1'b0), .in1(1'b0), .in2(CarryIn), .in3(not_1_out), .in4(1'b0), .in5(1'b0), .in6(1'b0), .in7(1'b0),
    .out(multiplexer_2_out), .sel(ALUOP[2:0]));
  Negator #(.width(16)) negator_1 (.in(B), .out(negator_1_out));
  assign not_2_out = ~B;  // NOT_Gate not_2, 16 bits wide
  assign and_1_out = A & B;  // AND_Gate and_1, 16 bits wide
  assign xor_4_out = and_1_out ^ bit_extender_1_out;  // XOR_Gate xor_4, 16 bits wide
  assign xor_5_out = not_2_out ^ bit_extender_1_out;  // XOR_Gate xor_5, 16 bits wide
  Multiplexer #(.select(3), .width(16), .enable("false")) multiplexer_3 (
    .in0(B), .in1(negator_1_out), .in2(B), .in3(negator_1_out), .in4(16'h1), .in5({16{1'b1}}),
    .in6({16{1'b0}}), .in7({16{1'b0}}), .out(multiplexer_3_out), .sel(ALUOP[2:0]));
  assign bit_extender_1_out = {{15{ALUOP[2]}}, ALUOP[2]};  // Bit_Extender bit_extender_1
  Multiplexer #(.select(4), .enable("false")) multiplexer_4 (
    .in0(1'b0), .in1(A[15]), .in2(A[14]), .in3(A[13]), .in4(A[12]), .in5(A[11]), .in6(A[10]), .in7(A[9]),
    .in8(A[8]), .in9(A[7]), .in10(A[6]), .in11(A[5]), .in12(A[4]), .in13(A[3]), .in14(A[2]), .in15(A[1]),
    .out(multiplexer_4_out), .sel(B[3:0]));
  Shifter #(.width(16)) shifter_1 (.in(A), .\dist (B[3:0]), .out(shifter_1_out));
  Multiplexer #(.select(4), .enable("false")) multiplexer_5 (
    .in0(1'b0), .in1(A[0]), .in2(A[1]), .in3(A[2]), .in4(A[3]), .in5(A[4]), .in6(A[5]), .in7(A[6]),
    .in8(A[7]), .in9(A[8]), .in10(A[9]), .in11(A[10]), .in12(A[11]), .in13(A[12]), .in14(A[13]),
    .in15(A[14]), .out(multiplexer_5_out), .sel(B[3:0]));
  Shifter #(.width(16), .shift("lr")) shifter_2 (.in(A), .\dist (B[3:0]), .out(shifter_2_out));
  Shifter #(.width(16), .shift("ar")) shifter_3 (.in(A), .\dist (B[3:0]), .out(shifter_3_out));
  Shifter #(.width(16), .shift("rl")) shifter_4 (.in(A), .\dist (B[3:0]), .out(shifter_4_out));
  Shifter #(.width(16), .shift("rr")) shifter_5 (.in(A), .\dist (B[3:0]), .out(shifter_5_out));
  Adder #(.width(15)) adder_1 (
    .a(A[14:0]), .b(multiplexer_3_out[14:0]), .out(adder_1_out[14:0]), .cin(multiplexer_2_out),
    .cout(adder_1_cout));
  Adder #(.width(1)) adder_2 (
    .a(A[15]), .b(multiplexer_3_out[15]), .out(adder_1_out[15]), .cin(adder_1_cout), .cout(adder_2_cout));
  Adder #(.width(16)) adder_3 (
    .a(A), .b(multiplexer_3_out), .out(adder_3_out), .cin(multiplexer_2_out), .cout(adder_3_cout));
  Multiplexer #(.select(3), .width(16), .enable("false")) multiplexer_6 (
    .in0(shifter_1_out), .in1(shifter_2_out), .in2(shifter_3_out), .in3(shifter_4_out), .in4(shifter_5_out),
    .in5({16{1'b0}}), .in6({16{1'b0}}), .in7({16{1'b0}}), .out(multiplexer_6_out), .sel(ALUOP[2:0]));
  xor xor_6 (xor_6_out, adder_1_cout, adder_2_cout);
  Multiplexer #(.select(3), .enable("false")) multiplexer_7 (
    .in0(multiplexer_4_out), .in1(multiplexer_5_out), .in2(multiplexer_5_out), .in3(multiplexer_4_out),
    .in4(multiplexer_5_out), .in5(1'b0), .in6(1'b0), .in7(1'b0), .out(multiplexer_7_out), .sel(ALUOP[2:0]));
  Multiplexer #(.select(2), .width(16), .enable("false")) multiplexer_8 (
    .in0(adder_1_out), .in1(adder_3_out), .in2(multiplexer_1_out), .in3(multiplexer_6_out), .out(out_5),
    .sel(ALUOP[4:3]));
  Multiplexer #(.select(2), .enable("false")) multiplexer_9 (
    .in0(adder_2_cout), .in1(adder_3_cout), .in2(1'b0), .in3(multiplexer_7_out), .out(Carry), .sel(ALUOP[4:3]));
  Multiplexer #(.select(2), .enable("false")) multiplexer_10 (
    .in0(xor_6_out), .in1(1'b0), .in2(1'b0), .in3(1'b0), .out(Overflow), .sel(ALUOP[4:3]));
  nor nor_1 (Zero, out_5[0], out_5[1], out_5[2], out_5[3], out_5[4], out_5[5], out_5[6], out_5[7], out_5[8], out_5[9], out_5[10], out_5[11], out_5[12], out_5[13], out_5[14], out_5[15]);

  // Other names for the same wires on the sheet: LOOP[2:0] = ALUOP[2:0]; HIOP[1:0] = ALUOP[4:3]
endmodule

module CPU_EX_MEM (
  input  [15:0] \地址 ,
  input  [15:0] \数据 ,
  input  [3:0] dsel,
  input  \存储器写使能 ,
  input  \对存储器进行访问 ,
  input  \是否写回 ,
  output out_7
);

  wire undriven, undriven_2, undriven_3;

  Register #(.width(16)) register_1 (.D(\地址 ), .en(undriven_2), .clk(undriven), .clr(undriven_3));  // open: Q
  Register #(.width(16)) register_2 (.D(\数据 ), .en(undriven_2), .clk(undriven), .clr(undriven_3));  // open: Q
  Register #(.width(4)) register_3 (.D(dsel), .en(undriven_2), .clk(undriven), .clr(undriven_3));  // open: Q
  Register #(.width(1)) register_4 (.D(\存储器写使能 ), .en(undriven_2), .clk(undriven), .clr(undriven_3));  // open: Q
  Register #(.width(1)) register_5 (.D(\对存储器进行访问 ), .en(undriven_2), .clk(undriven), .clr(undriven_3));  // open: Q
  Register #(.width(1)) register_6 (.D(\是否写回 ), .en(undriven_2), .Q(out_7), .clk(undriven), .clr(undriven_3));
endmodule
