// Logisim project 2333 - 副本.circ as structural Verilog
module Registers (
  input  [15:0] DataIn,
  input  [3:0] dsel,
  input  dwe,
  input  clock,
  input  reset,
  input  sre,
  input  [3:0] ssel,
  input  [3:0] tsel,
  input  tre
);

  wire demultiplexer_1_out0, demultiplexer_1_out1, demultiplexer_1_out2, demultiplexer_1_out3,
       demultiplexer_1_out4, demultiplexer_1_out5, demultiplexer_1_out6, demultiplexer_1_out7,
       demultiplexer_1_out8, demultiplexer_1_out9, demultiplexer_1_out10, demultiplexer_1_out11,
       demultiplexer_1_out12, demultiplexer_1_out13, demultiplexer_1_out14, demultiplexer_1_out15;
  wire [15:0] register_1_q, register_2_q, register_3_q, register_4_q, register_5_q, register_6_q,
       register_7_q, register_8_q, register_9_q, register_10_q, register_11_q, register_12_q, register_13_q,
       register_14_q, register_15_q, register_16_q;

  Demultiplexer #(.select(4), .disabled(0), .enable("false")) demultiplexer_1 (
    .out0(demultiplexer_1_out0), .out1(demultiplexer_1_out1), .out2(demultiplexer_1_out2),
    .out3(demultiplexer_1_out3), .out4(demultiplexer_1_out4), .out5(demultiplexer_1_out5),
    .out6(demultiplexer_1_out6), .out7(demultiplexer_1_out7), .out8(demultiplexer_1_out8),
    .out9(demultiplexer_1_out9), .out10(demultiplexer_1_out10), .out11(demultiplexer_1_out11),
    .out12(demultiplexer_1_out12), .out13(demultiplexer_1_out13), .out14(demultiplexer_1_out14),
    .out15(demultiplexer_1_out15), .in(dwe), .sel(dsel));
  Register #(.width(16)) register_1 (.D(DataIn), .en(demultiplexer_1_out0), .Q(register_1_q), .clk(clock), .clr(reset));
  Register #(.width(16)) register_2 (.D(DataIn), .en(demultiplexer_1_out1), .Q(register_2_q), .clk(clock), .clr(reset));
  Register #(.width(16)) register_3 (.D(DataIn), .en(demultiplexer_1_out2), .Q(register_3_q), .clk(clock), .clr(reset));
  Register #(.width(16)) register_4 (.D(DataIn), .en(demultiplexer_1_out3), .Q(register_4_q), .clk(clock), .clr(reset));
  Register #(.width(16)) register_5 (.D(DataIn), .en(demultiplexer_1_out4), .Q(register_5_q), .clk(clock), .clr(reset));
  Register #(.width(16)) register_6 (.D(DataIn), .en(demultiplexer_1_out5), .Q(register_6_q), .clk(clock), .clr(reset));
  Register #(.width(16)) register_7 (.D(DataIn), .en(demultiplexer_1_out6), .Q(register_7_q), .clk(clock), .clr(reset));
  Register #(.width(16)) register_8 (.D(DataIn), .en(demultiplexer_1_out7), .Q(register_8_q), .clk(clock), .clr(reset));
  Register #(.width(16)) register_9 (.D(DataIn), .en(demultiplexer_1_out8), .Q(register_9_q), .clk(clock), .clr(reset));
  Register #(.width(16)) register_10 (
    .D(DataIn), .en(demultiplexer_1_out9), .Q(register_10_q), .clk(clock), .clr(reset));
  Register #(.width(16)) register_11 (
    .D(DataIn), .en(demultiplexer_1_out10), .Q(register_11_q), .clk(clock), .clr(reset));
  Register #(.width(16)) register_12 (
    .D(DataIn), .en(demultiplexer_1_out11), .Q(register_12_q), .clk(clock), .clr(reset));
  Register #(.width(16)) register_13 (
    .D(DataIn), .en(demultiplexer_1_out12), .Q(register_13_q), .clk(clock), .clr(reset));
  Register #(.width(16)) register_14 (
    .D(DataIn), .en(demultiplexer_1_out13), .Q(register_14_q), .clk(clock), .clr(reset));
  Register #(.width(16)) register_15 (
    .D(DataIn), .en(demultiplexer_1_out14), .Q(register_15_q), .clk(clock), .clr(reset));
  Register #(.width(16)) register_16 (
    .D(DataIn), .en(demultiplexer_1_out15), .Q(register_16_q), .clk(clock), .clr(reset));
  Multiplexer #(.select(4), .width(16), .disabled(0)) multiplexer_1 (
    .in0(register_1_q), .in1(register_2_q), .in2(register_3_q), .in3(register_4_q), .in4(register_5_q),
    .in5(register_6_q), .in6(register_7_q), .in7(register_8_q), .in8(register_9_q), .in9(register_10_q),
    .in10(register_11_q), .in11(register_12_q), .in12(register_13_q), .in13(register_14_q),
    .in14(register_15_q), .in15(register_16_q), .sel(ssel), .en(sre));  // open: out
  Multiplexer #(.select(4), .width(16), .disabled(0)) multiplexer_2 (
    .in0(register_1_q), .in1(register_2_q), .in2(register_3_q), .in3(register_4_q), .in4(register_5_q),
    .in5(register_6_q), .in6(register_7_q), .in7(register_8_q), .in8(register_9_q), .in9(register_10_q),
    .in10(register_11_q), .in11(register_12_q), .in12(register_13_q), .in13(register_14_q),
    .in14(register_15_q), .in15(register_16_q), .sel(tsel), .en(tre));  // open: out
endmodule

module ALU (
  input  [7:0] A,
  input  [7:0] B
);
endmodule
