// Logisim project FPU.circ as structural Verilog: 3 circuits, main circuit main
module main (
);

  \存储器  \u_存储器_1  ();  // open: 时钟, 复位, 地址_CPU, CPUWsel, CPUWriteData, 地址_FPU, FPUWSel, FPUWriteData, CPUWSel_2, FPUWSel_2, out_11, out_12
  \数据寄存器  \u_数据寄存器_1  ();  // open: WriteData, WriteEnable, WSel, SSel, DSel, out_8, out_9, clk, rst
endmodule

module \存储器  (
  input  \时钟 ,
  input  \复位 ,
  input  [6:0] \地址_CPU ,
  input  CPUWsel,
  input  [15:0] CPUWriteData,
  input  [6:0] \地址_FPU ,
  input  FPUWSel,
  input  [15:0] FPUWriteData,
  input  CPUWSel_2,
  input  FPUWSel_2,
  output [15:0] out_11,
  output [15:0] out_12
);

  wire [3:0] demultiplexer_1_out1, demultiplexer_1_out2, demultiplexer_1_out3, demultiplexer_1_out4,
       demultiplexer_1_out5, demultiplexer_1_out6, demultiplexer_1_out7, undriven;
  wire [15:0] demultiplexer_3_out0, demultiplexer_3_out1, demultiplexer_3_out2, demultiplexer_3_out3,
       demultiplexer_3_out4, demultiplexer_3_out5, demultiplexer_3_out6, demultiplexer_3_out7, ram_1_data,
       ram_2_data, ram_3_data, ram_4_data, ram_5_data, ram_6_data, ram_7_data, ram_8_data;

  Demultiplexer #(.select(3), .width(4)) demultiplexer_1 (
    .out1(demultiplexer_1_out1), .out2(demultiplexer_1_out2), .out3(demultiplexer_1_out3),
    .out4(demultiplexer_1_out4), .out5(demultiplexer_1_out5), .out6(demultiplexer_1_out6),
    .out7(demultiplexer_1_out7), .in(\地址_CPU [3:0]), .sel(\地址_CPU [6:4]), .en(CPUWsel));  // open: out0
  Demultiplexer #(.select(3), .width(4)) demultiplexer_2 (
    .out1(demultiplexer_1_out1), .out2(demultiplexer_1_out2), .out3(demultiplexer_1_out3),
    .out4(demultiplexer_1_out4), .out5(demultiplexer_1_out5), .out6(demultiplexer_1_out6),
    .out7(demultiplexer_1_out7), .in(\地址_FPU [3:0]), .sel(\地址_FPU [6:4]), .en(FPUWSel));  // open: out0
  Demultiplexer #(.select(3), .width(16)) demultiplexer_3 (
    .out0(demultiplexer_3_out0), .out1(demultiplexer_3_out1), .out2(demultiplexer_3_out2),
    .out3(demultiplexer_3_out3), .out4(demultiplexer_3_out4), .out5(demultiplexer_3_out5),
    .out6(demultiplexer_3_out6), .out7(demultiplexer_3_out7), .in(CPUWriteData), .sel(\地址_CPU [6:4]),
    .en(CPUWsel));
  Demultiplexer #(.select(3), .width(16)) demultiplexer_4 (
    .out0(demultiplexer_3_out0), .out1(demultiplexer_3_out1), .out2(demultiplexer_3_out2),
    .out3(demultiplexer_3_out3), .out4(demultiplexer_3_out4), .out5(demultiplexer_3_out5),
    .out6(demultiplexer_3_out6), .out7(demultiplexer_3_out7), .in(FPUWriteData), .sel(\地址_FPU [6:4]),
    .en(FPUWSel));
  RAM #(.addrWidth(4), .dataWidth(16), .bus("separate")) ram_1 (
    .addr(demultiplexer_1_out1), .din(demultiplexer_3_out0), .data(ram_1_data), .clk(\时钟 ), .clr(\复位 ));  // open: str, sel, ld
  RAM #(.addrWidth(4), .dataWidth(16), .bus("separate")) ram_2 (
    .addr(demultiplexer_1_out2), .din(demultiplexer_3_out1), .data(ram_2_data), .clk(\时钟 ), .clr(\复位 ));  // open: str, sel, ld
  RAM #(.addrWidth(4), .dataWidth(16), .bus("separate")) ram_3 (
    .addr(demultiplexer_1_out3), .din(demultiplexer_3_out2), .data(ram_3_data), .clk(\时钟 ), .clr(\复位 ));  // open: str, sel, ld
  RAM #(.addrWidth(4), .dataWidth(16), .bus("separate")) ram_4 (
    .addr(demultiplexer_1_out4), .din(demultiplexer_3_out3), .data(ram_4_data), .clk(\时钟 ), .clr(\复位 ));  // open: str, sel, ld
  RAM #(.addrWidth(4), .dataWidth(16), .bus("separate")) ram_5 (
    .addr(demultiplexer_1_out5), .din(demultiplexer_3_out4), .data(ram_5_data), .clk(\时钟 ), .clr(\复位 ));  // open: str, sel, ld
  RAM #(.addrWidth(4), .dataWidth(16), .bus("separate")) ram_6 (
    .addr(demultiplexer_1_out6), .din(demultiplexer_3_out5), .data(ram_6_data), .clk(\时钟 ), .clr(\复位 ));  // open: str, sel, ld
  RAM #(.addrWidth(4), .dataWidth(16), .bus("separate")) ram_7 (
    .addr(demultiplexer_1_out7), .din(demultiplexer_3_out6), .data(ram_7_data), .clk(\时钟 ), .clr(\复位 ));  // open: str, sel, ld
  RAM #(.addrWidth(4), .dataWidth(16), .bus("separate")) ram_8 (
    .addr(undriven), .din(demultiplexer_3_out7), .data(ram_8_data), .clk(\时钟 ), .clr(\复位 ));  // open: str, sel, ld
  Multiplexer #(.select(3), .width(16)) multiplexer_1 (
    .in0(ram_1_data), .in1(ram_2_data), .in2(ram_3_data), .in3(ram_4_data), .in4(ram_5_data),
    .in5(ram_6_data), .in6(ram_7_data), .in7(ram_8_data), .out(out_11), .sel(\地址_FPU [6:4]), .en(FPUWSel_2));
  Multiplexer #(.select(3), .width(16)) multiplexer_2 (
    .in0(ram_1_data), .in1(ram_2_data), .in2(ram_3_data), .in3(ram_4_data), .in4(ram_5_data),
    .in5(ram_6_data), .in6(ram_7_data), .in7(ram_8_data), .out(out_12), .sel(\地址_CPU [6:4]), .en(CPUWSel_2));
endmodule

module \数据寄存器  (
  input  [31:0] WriteData,
  input  WriteEnable,
  input  [2:0] WSel,
  input  [2:0] SSel,
  input  [2:0] DSel,
  input  clk,
  input  rst,
  output [31:0] out_8,
  output [31:0] out_9
);

  wire [15:0] register_1_q, register_2_q, register_3_q, register_4_q, register_5_q, register_6_q,
       register_7_q, register_8_q, register_9_q, register_10_q, register_11_q, register_12_q, register_13_q,
       register_14_q, register_15_q, register_16_q;
  wire [31:0] demultiplexer_1_out0, demultiplexer_1_out1, demultiplexer_1_out2, demultiplexer_1_out3,
       demultiplexer_1_out4, demultiplexer_1_out5, demultiplexer_1_out6, demultiplexer_1_out7;

  Demultiplexer #(.select(3), .width(32)) demultiplexer_1 (
    .out0(demultiplexer_1_out0), .out1(demultiplexer_1_out1), .out2(demultiplexer_1_out2),
    .out3(demultiplexer_1_out3), .out4(demultiplexer_1_out4), .out5(demultiplexer_1_out5),
    .out6(demultiplexer_1_out6), .out7(demultiplexer_1_out7), .in(WriteData), .sel(WSel), .en(WriteEnable));
  Register #(.width(16)) register_1 (
    .D(demultiplexer_1_out0[15:0]), .Q(register_1_q), .clk(clk), .clr(rst));  // open: en
  Register #(.width(16)) register_2 (
    .D(demultiplexer_1_out0[31:16]), .Q(register_2_q), .clk(clk), .clr(rst));  // open: en
  Register #(.width(16)) register_3 (
    .D(demultiplexer_1_out1[15:0]), .Q(register_3_q), .clk(clk), .clr(rst));  // open: en
  Register #(.width(16)) register_4 (
    .D(demultiplexer_1_out1[31:16]), .Q(register_4_q), .clk(clk), .clr(rst));  // open: en
  Register #(.width(16)) register_5 (
    .D(demultiplexer_1_out2[15:0]), .Q(register_5_q), .clk(clk), .clr(rst));  // open: en
  Register #(.width(16)) register_6 (
    .D(demultiplexer_1_out2[31:16]), .Q(register_6_q), .clk(clk), .clr(rst));  // open: en
  Register #(.width(16)) register_7 (
    .D(demultiplexer_1_out3[15:0]), .Q(register_7_q), .clk(clk), .clr(rst));  // open: en
  Register #(.width(16)) register_8 (
    .D(demultiplexer_1_out3[31:16]), .Q(register_8_q), .clk(clk), .clr(rst));  // open: en
  Register #(.width(16)) register_9 (
    .D(demultiplexer_1_out4[15:0]), .Q(register_9_q), .clk(clk), .clr(rst));  // open: en
  Register #(.width(16)) register_10 (
    .D(demultiplexer_1_out4[31:16]), .Q(register_10_q), .clk(clk), .clr(rst));  // open: en
  Register #(.width(16)) register_11 (
    .D(demultiplexer_1_out5[15:0]), .Q(register_11_q), .clk(clk), .clr(rst));  // open: en
  Register #(.width(16)) register_12 (
    .D(demultiplexer_1_out5[31:16]), .Q(register_12_q), .clk(clk), .clr(rst));  // open: en
  Register #(.width(16)) register_13 (
    .D(demultiplexer_1_out6[15:0]), .Q(register_13_q), .clk(clk), .clr(rst));  // open: en
  Register #(.width(16)) register_14 (
    .D(demultiplexer_1_out6[31:16]), .Q(register_14_q), .clk(clk), .clr(rst));  // open: en
  Register #(.width(16)) register_15 (
    .D(demultiplexer_1_out7[15:0]), .Q(register_15_q), .clk(clk), .clr(rst));  // open: en
  Register #(.width(16)) register_16 (
    .D(demultiplexer_1_out7[31:16]), .Q(register_16_q), .clk(clk), .clr(rst));  // open: en
  Multiplexer #(.select(3), .width(32), .enable("false")) multiplexer_1 (
    .in0({register_2_q, register_1_q}), .in1({register_4_q, register_3_q}),
    .in2({register_6_q, register_5_q}), .in3({register_8_q, register_7_q}),
    .in4({register_10_q, register_9_q}), .in5({register_12_q, register_11_q}),
    .in6({register_14_q, register_13_q}), .in7({register_16_q, register_15_q}), .out(out_8), .sel(SSel));
  Multiplexer #(.select(3), .width(32), .enable("false")) multiplexer_2 (
    .in0({register_2_q, register_1_q}), .in1({register_4_q, register_3_q}),
    .in2({register_6_q, register_5_q}), .in3({register_8_q, register_7_q}),
    .in4({register_10_q, register_9_q}), .in5({register_12_q, register_11_q}),
    .in6({register_14_q, register_13_q}), .in7({register_16_q, register_15_q}), .out(out_9), .sel(DSel));
endmodule
