// Logisim project 0.circ as structural Verilog
module CPU (
  input  in_1
);

  wire clock_1_out, undriven_3, undriven_4;
  wire [1:0] rc;
  wire [15:0] multiplexer_1_out, multiplexer_2_out, multiplexer_3_out, regs_1_ac, regs_1_ar, regs_1_dr,
       regs_1_mr, regs_1_sreg, regs_1_treg, undriven, undriven_2;

  RC rc_1 (.in_1(clock_1_out), .in_2(in_1), .out_3(rc));
  Clock clock_1 (.out(clock_1_out));
  PC pc_1 (.clk(rc), .rst(in_1));  // open: Immed, AR, sel, Out
  Multiplexer #(.width(16), .enable("false")) multiplexer_1 (
    .in0(undriven), .out(multiplexer_1_out));  // open: in1, sel
  Multiplexer #(.width(16), .enable("false")) multiplexer_2 (
    .in0(regs_1_treg), .in1(undriven_2), .out(multiplexer_2_out));  // open: sel
  Regs regs_1 (
    .regval(multiplexer_1_out), .xchgval(multiplexer_2_out), .we(undriven_3), .xchg_en(undriven_4), .clk(rc),
    .rst(in_1), .sreg(regs_1_sreg), .AC(regs_1_ac), .DR(regs_1_dr), .MR(regs_1_mr), .AR(regs_1_ar),
    .treg(regs_1_treg));  // open: ssel, tsel, dsel
  Multiplexer #(.select(2), .width(16), .enable("false")) multiplexer_3 (
    .in0(regs_1_treg), .out(multiplexer_3_out));  // open: in1, in2, in3, sel
  ALU alu_1 (.in_1(regs_1_sreg), .in_2(multiplexer_3_out));

  // Other names for the same wires on the sheet: rst = in_1
endmodule

module PC (
  input  [15:0] Immed,
  input  [15:0] AR,
  input  [2:0] sel,
  input  [1:0] clk,
  input  rst,
  output [15:0] Out
);

  wire comparator_1_eq;
  wire [15:0] adder_1_out, adder_2_out, adder_3_out, multiplexer_1_out;

  Comparator #(.width(2), .mode("unsigned")) comparator_1 (.a(clk), .b(2'b00), .eq(comparator_1_eq));  // open: gt, lt
  Adder #(.width(16)) adder_1 (.a(Out), .b(16'h2), .out(adder_1_out));  // open: cin, cout
  Adder #(.width(16)) adder_2 (.a(Out), .b(Immed), .out(adder_2_out));  // open: cin, cout
  Adder #(.width(16)) adder_3 (.a(Out), .b(AR), .out(adder_3_out));  // open: cin, cout
  Multiplexer #(.select(3), .width(16), .enable("false")) multiplexer_1 (
    .in0(adder_1_out), .in1(Out), .in2({Out[15:8], Immed[7:0]}), .in3({Out[15:8], AR[7:0]}),
    .in4(adder_2_out), .in5(adder_3_out), .in6(AR), .out(multiplexer_1_out), .sel(sel));  // open: in7
  Register #(.width(16)) register_1 (.D(multiplexer_1_out), .Q(Out), .clk(comparator_1_eq), .clr(rst));  // open: en
endmodule

module Regs (
  input  [15:0] regval,
  input  [15:0] xchgval,
  input  we,
  input  xchg_en,
  input  [1:0] clk,
  input  rst,
  input  [1:0] ssel,
  input  [1:0] tsel,
  input  [1:0] dsel,
  output [15:0] sreg,
  output [15:0] AC,
  output [15:0] DR,
  output [15:0] MR,
  output [15:0] AR,
  output [15:0] treg
);

  wire comparator_1_eq, demultiplexer_1_out0, demultiplexer_1_out1, demultiplexer_1_out2,
       demultiplexer_1_out3, demultiplexer_2_out0, demultiplexer_2_out1, demultiplexer_2_out2,
       demultiplexer_2_out3, or_1_out, or_2_out, or_3_out, or_4_out;
  wire [15:0] multiplexer_1_out, multiplexer_2_out, multiplexer_3_out, multiplexer_4_out;

  Multiplexer #(.width(16), .enable("false")) multiplexer_1 (
    .in0(regval), .in1(xchgval), .out(multiplexer_1_out), .sel(demultiplexer_2_out0));
  Multiplexer #(.width(16), .enable("false")) multiplexer_2 (
    .in0(regval), .in1(xchgval), .out(multiplexer_2_out), .sel(demultiplexer_2_out1));
  Multiplexer #(.width(16), .enable("false")) multiplexer_3 (
    .in0(regval), .in1(xchgval), .out(multiplexer_3_out), .sel(demultiplexer_2_out2));
  Multiplexer #(.width(16), .enable("false")) multiplexer_4 (
    .in0(regval), .in1(xchgval), .out(multiplexer_4_out), .sel(demultiplexer_2_out3));
  or or_1 (or_1_out, demultiplexer_1_out0, demultiplexer_2_out0);
  Demultiplexer #(.select(2), .enable("false")) demultiplexer_1 (
    .out0(demultiplexer_1_out0), .out1(demultiplexer_1_out1), .out2(demultiplexer_1_out2),
    .out3(demultiplexer_1_out3), .in(we), .sel(dsel));
  or or_2 (or_2_out, demultiplexer_1_out2, demultiplexer_2_out2);
  or or_3 (or_3_out, demultiplexer_1_out1, demultiplexer_2_out1);
  Comparator #(.width(2), .mode("unsigned")) comparator_1 (.a(clk), .b(2'b11), .eq(comparator_1_eq));  // open: gt, lt
  or or_4 (or_4_out, demultiplexer_1_out3, demultiplexer_2_out3);
  Demultiplexer #(.select(2), .enable("false")) demultiplexer_2 (
    .out0(demultiplexer_2_out0), .out1(demultiplexer_2_out1), .out2(demultiplexer_2_out2),
    .out3(demultiplexer_2_out3), .in(xchg_en), .sel(ssel));
  Register #(.width(16)) register_1 (.D(multiplexer_1_out), .en(or_1_out), .Q(AC), .clk(comparator_1_eq), .clr(rst));
  Register #(.width(16)) register_2 (.D(multiplexer_2_out), .en(or_3_out), .Q(DR), .clk(comparator_1_eq), .clr(rst));
  Register #(.width(16)) register_3 (.D(multiplexer_3_out), .en(or_2_out), .Q(MR), .clk(comparator_1_eq), .clr(rst));
  Register #(.width(16)) register_4 (.D(multiplexer_4_out), .en(or_4_out), .Q(AR), .clk(comparator_1_eq), .clr(rst));
  Multiplexer #(.select(2), .width(16), .enable("false")) multiplexer_5 (
    .in0(AC), .in1(DR), .in2(MR), .in3(AR), .out(sreg), .sel(ssel));
  Multiplexer #(.select(2), .width(16), .enable("false")) multiplexer_6 (
    .in0(AC), .in1(DR), .in2(MR), .in3(AR), .out(treg), .sel(tsel));
endmodule

module ALU (
  input  [15:0] in_1,
  input  [15:0] in_2
);

  wire adder_1_cout, subtractor_1_bout;
  wire [15:0] adder_1_out, divider_1_out, divider_1_rem, multiplier_1_cout, multiplier_1_out,
       subtractor_1_out;

  Adder #(.width(16)) adder_1 (.a(in_1), .b(in_2), .out(adder_1_out), .cout(adder_1_cout));  // open: cin
  Subtractor #(.width(16)) subtractor_1 (
    .a(in_1), .b(in_2), .out(subtractor_1_out), .bout(subtractor_1_bout));  // open: bin
  Multiplier #(.width(16)) multiplier_1 (
    .a(in_1), .b(in_2), .out(multiplier_1_out), .cout(multiplier_1_cout));  // open: cin
  Divider #(.width(16)) divider_1 (.a(in_1), .b(in_2), .out(divider_1_out), .rem(divider_1_rem));  // open: upper
endmodule

module RC (
  input  in_1,
  input  in_2,
  output [1:0] out_3
);

  wire and_1_out, and_2_out, and_3_out, and_4_out, counter_1_q, counter_2_q, not_1_out;

  not not_1 (not_1_out, in_1);
  Counter #(.width(1), .max('h1)) counter_1 (.Q(counter_1_q), .clk(in_1), .clr(in_2));  // open: load, D, count, carry
  Counter #(.width(1), .max('h1)) counter_2 (
    .Q(counter_2_q), .clk(not_1_out), .clr(in_2));  // open: load, D, count, carry
  and and_1 (and_1_out, ~counter_1_q, counter_2_q);  // AND_Gate
  and and_2 (and_2_out, counter_1_q, counter_2_q);
  and and_3 (and_3_out, ~counter_1_q, counter_2_q);  // AND_Gate
  and and_4 (and_4_out, counter_1_q, ~counter_2_q);  // AND_Gate
  or or_1 (out_3[1], and_1_out, and_2_out);
  or or_2 (out_3[0], and_3_out, and_4_out);
endmodule
