// Logisim project 20170121.circ as structural Verilog
module \算数逻辑单元  (
  input  [15:0] D0,
  input  [15:0] D1,
  input  [15:0] D2,
  input  [15:0] D3,
  input  [15:0] \立即数 ,
  input  [2:0] in_6,
  input  [2:0] in_7,
  input  \运算类指令 ,
  input  \逻辑类指令 ,
  input  \移位类指令 ,
  input  \逻辑类指令2 ,
  input  [5:0] \功能码 
);
endmodule

module \通用寄存器组  (
  input  \写入使能1 ,
  input  [2:0] \写入地址1 ,
  input  [15:0] \写入数据1 ,
  input  \写入使能2 ,
  input  [15:0] \写入数据2 ,
  input  [2:0] \写入地址2 ,
  input  \时钟_2 ,
  input  \时钟_3 ,
  input  \复位 ,
  output [15:0] out_10,
  output [15:0] out_11,
  output [15:0] out_12,
  output [15:0] out_13,
  output [15:0] out_14,
  output [15:0] out_15,
  output [15:0] out_16,
  output [15:0] out_17
);

  wire multiplexer_1_out;
  wire [15:0] demultiplexer_1_out0, demultiplexer_1_out1, demultiplexer_1_out2, demultiplexer_1_out3,
       demultiplexer_1_out4, demultiplexer_1_out5, demultiplexer_1_out6, demultiplexer_1_out7;

  Demultiplexer #(.select(3), .width(16)) demultiplexer_1 (
    .out0(demultiplexer_1_out0), .out1(demultiplexer_1_out1), .out2(demultiplexer_1_out2),
    .out3(demultiplexer_1_out3), .out4(demultiplexer_1_out4), .out5(demultiplexer_1_out5),
    .out6(demultiplexer_1_out6), .out7(demultiplexer_1_out7), .in(\写入数据1 ), .sel(\写入地址1 ), .en(\写入使能1 ));
  Demultiplexer #(.select(3), .width(16)) demultiplexer_2 (
    .out0(demultiplexer_1_out0), .out1(demultiplexer_1_out1), .out2(demultiplexer_1_out2),
    .out3(demultiplexer_1_out3), .out4(demultiplexer_1_out4), .out5(demultiplexer_1_out5),
    .out6(demultiplexer_1_out6), .out7(demultiplexer_1_out7), .in(\写入数据2 ), .sel(\写入地址2 ), .en(\写入使能2 ));
  Multiplexer #(.enable("false")) multiplexer_1 (.in0(\时钟_2 ), .in1(\时钟_3 ), .out(multiplexer_1_out));  // open: sel
  Register #(.width(16)) D0 (.D(demultiplexer_1_out0), .Q(out_10), .clk(multiplexer_1_out), .clr(\复位 ));  // open: en
  Register #(.width(16)) D1 (.D(demultiplexer_1_out1), .Q(out_11), .clk(multiplexer_1_out), .clr(\复位 ));  // open: en
  Register #(.width(16)) D2 (.D(demultiplexer_1_out2), .Q(out_12), .clk(multiplexer_1_out), .clr(\复位 ));  // open: en
  Register #(.width(16)) D3 (.D(demultiplexer_1_out3), .Q(out_13), .clk(multiplexer_1_out), .clr(\复位 ));  // open: en
  Register #(.width(16)) A0 (.D(demultiplexer_1_out4), .Q(out_14), .clk(multiplexer_1_out), .clr(\复位 ));  // open: en
  Register #(.width(16)) A1 (.D(demultiplexer_1_out5), .Q(out_15), .clk(multiplexer_1_out), .clr(\复位 ));  // open: en
  Register #(.width(16)) CBR (.D(demultiplexer_1_out7), .Q(out_17), .clk(multiplexer_1_out), .clr(\复位 ));  // open: en
  Register #(.width(16)) SP ();  // open: D, en, Q, clk, clr
endmodule

module \解码器  (
  input  [15:0] \指令 ,
  output Inst_NOP,
  output Inst_MOVI,
  output Inst_MOVUI,
  output Inst_MOV,
  output Inst_XCHG,
  output \运算类指令 ,
  output \逻辑类指令 ,
  output \移位类指令 ,
  output \逻辑类指令2 ,
  output \装载存储类指令 ,
  output \V类指令 ,
  output \控制寄存器传输指令 ,
  output \跳转类指令 ,
  output Inst_HLT,
  output [15:0] \立即数 
);

  wire I, II, III_I, III_II, IV_I, multiplexer_1_out, or_1_out, or_2_out, VI_I, VI_IV;
  wire [15:0] bit_extender_1_out, bit_extender_2_out, bit_extender_3_out;

  Decoder #(.select(5), .enable("false")) decoder_1 (
    .out0(Inst_NOP), .out4(Inst_MOVI), .out5(Inst_MOVUI), .out6(Inst_MOV), .out7(Inst_XCHG), .out8(\运算类指令 ),
    .out9(\逻辑类指令 ), .out10(\移位类指令 ), .out11(\逻辑类指令2 ), .out12(\装载存储类指令 ), .out13(\V类指令 ),
    .out14(\控制寄存器传输指令 ), .out15(II), .out16(III_II), .out17(VI_IV), .out18(VI_I), .out31(Inst_HLT),
    .sel(\指令 [15:11]));  // open: out1, out2, out3, out19, out20, out21, out22, out23, out24, out25, out26, out27, out28, out29, out30
  assign bit_extender_1_out = {{10{multiplexer_1_out}}, \指令 [5:0]};  // Bit_Extender bit_extender_1
  assign bit_extender_2_out = {{8{\指令 [7]}}, \指令 [7:0]};  // Bit_Extender bit_extender_2
  assign bit_extender_3_out = {{5{\指令 [10]}}, \指令 [10:0]};  // Bit_Extender bit_extender_3
  Multiplexer #(.enable("false")) multiplexer_1 (.in0(1'b0), .in1(\指令 [5]), .out(multiplexer_1_out), .sel(\逻辑类指令2 ));
  assign \立即数  = or_1_out ? bit_extender_1_out : 16'bz;  // Controlled_Buffer controlled_buffer_1
  assign \立即数  = or_2_out ? bit_extender_2_out : 16'bz;  // Controlled_Buffer controlled_buffer_2
  assign \立即数  = II ? bit_extender_3_out : 16'bz;  // Controlled_Buffer controlled_buffer_3
  Pull_Resistor pull_resistor_1 (.node(\立即数 ));
  or or_1 (or_1_out, VI_IV, \装载存储类指令 , \逻辑类指令2 , VI_I, \V类指令 );
  or or_2 (or_2_out, III_II, III_I);
  or or_3 (IV_I, Inst_XCHG, Inst_MOV);
  or or_4 (III_I, Inst_MOVUI, Inst_MOVI);
  or or_5 (I, Inst_HLT, Inst_NOP);
  or or_6 (\跳转类指令 , II, III_II, VI_IV, VI_I);

  // Other names for the same wires on the sheet: IV_A = \运算类指令 ; IV_III = \装载存储类指令 ; IV_L = \逻辑类指令 ; IV_S = \移位类指令 ;
  //   V = \V类指令 ; VI_II = \逻辑类指令2 
endmodule
