// Logisim project 20170612.circ as structural Verilog: 10 circuits, main circuit main
module main (
);

  CPU cpu_1 ();  // open: 时钟, 复位, 来自存贮器
  \内存  \u_内存_1  ();  // open: in_1
endmodule

module CPU (
  input  \时钟 ,
  input  \复位 ,
  input  [15:0] \来自存贮器 
);

  wire \数据传送指令控制中心_1_写使能1 , \数据传送指令控制中心_1_写使能2 , \节拍器_1__0 , \节拍器_1__1 , \节拍器_1__2 , \节拍器_1__3 ,
       \解码器_1_inst_mov , \解码器_1_inst_movi , \解码器_1_inst_movui , \解码器_1_inst_xchg , \解码器_1_v类指令 ,
       \解码器_1_控制寄存器传输指令 , \解码器_1_移位类指令 , \解码器_1_装载存储类指令 , \解码器_1_运算类指令 , \解码器_1_逻辑类指令 , \解码器_1_逻辑类指令2 ;
  wire [2:0] \数据传送指令控制中心_1_写地址2 , \解码器_1_写地址1 , \解码器_1_读地址1__访存时数据 , \解码器_1_读地址2_访存时地址_跳转时地址 ;
  wire [3:0] \算数逻辑单元_1_out_16 ;
  wire [5:0] \解码器_1_功能码 ;
  wire [15:0] \指令寄存器_q , \数据传送指令控制中心_1_写入数据1 , \数据传送指令控制中心_1_写入数据2 , \算数逻辑单元_1_结果 , \解码器_1_立即数 ,
       \通用寄存器组_1_out_10 , \通用寄存器组_1_out_11 , \通用寄存器组_1_out_12 , \通用寄存器组_1_out_13 , \通用寄存器组_1_out_14 ,
       \通用寄存器组_1_out_15 , \通用寄存器组_1_out_16 , \通用寄存器组_1_out_17 ;

  \节拍器  \u_节拍器_1  (.\时钟 (\时钟 ), ._0(\节拍器_1__0 ), ._1(\节拍器_1__1 ), ._2(\节拍器_1__2 ), ._3(\节拍器_1__3 ), .\复位 (\复位 ));
  Register #(.width(16)) \u_指令寄存器  (.D(\来自存贮器 ), .Q(\指令寄存器_q ), .clk(\节拍器_1__1 ), .clr(\复位 ));  // open: en
  \解码器  \u_解码器_1  (
    .\指令 (\指令寄存器_q ), .Inst_MOVI(\解码器_1_inst_movi ), .Inst_MOVUI(\解码器_1_inst_movui ),
    .Inst_MOV(\解码器_1_inst_mov ), .Inst_XCHG(\解码器_1_inst_xchg ), .\运算类指令 (\解码器_1_运算类指令 ),
    .\逻辑类指令 (\解码器_1_逻辑类指令 ), .\移位类指令 (\解码器_1_移位类指令 ), .\逻辑类指令2 (\解码器_1_逻辑类指令2 ), .\装载存储类指令 (\解码器_1_装载存储类指令 ),
    .\V类指令 (\解码器_1_v类指令 ), .\控制寄存器传输指令 (\解码器_1_控制寄存器传输指令 ), .\立即数 (\解码器_1_立即数 ), .\功能码 (\解码器_1_功能码 ),
    .\写地址1 (\解码器_1_写地址1 ), .\读地址1__访存时数据 (\解码器_1_读地址1__访存时数据 ), .\读地址2_访存时地址_跳转时地址 (\解码器_1_读地址2_访存时地址_跳转时地址 ));  // open: Inst_NOP, 跳转类指令, Inst_HLT
  \数据传送指令控制中心  \u_数据传送指令控制中心_1  (
    .\写入数据1 (\数据传送指令控制中心_1_写入数据1 ), .\写使能1 (\数据传送指令控制中心_1_写使能1 ), .\写使能2 (\数据传送指令控制中心_1_写使能2 ),
    .\写地址2 (\数据传送指令控制中心_1_写地址2 ), .\写入数据2 (\数据传送指令控制中心_1_写入数据2 ), .Inst_MOVI(\解码器_1_inst_movi ),
    .Inst_MOVUI(\解码器_1_inst_movui ), .Inst_MOV(\解码器_1_inst_mov ), .Inst_XCHG(\解码器_1_inst_xchg ),
    .\运算类指令 (\解码器_1_运算类指令 ), .\逻辑类指令 (\解码器_1_逻辑类指令 ), .\移位类指令 (\解码器_1_移位类指令 ), .\逻辑类指令2 (\解码器_1_逻辑类指令2 ),
    .\装载存储类指令 (\解码器_1_装载存储类指令 ), .\控制寄存器传输指令 (\解码器_1_控制寄存器传输指令 ), .\ALU运算结果 (\算数逻辑单元_1_结果 ),
    .D0(\通用寄存器组_1_out_10 ), .D1(\通用寄存器组_1_out_11 ), .D2(\通用寄存器组_1_out_12 ), .D3(\通用寄存器组_1_out_13 ),
    .A0(\通用寄存器组_1_out_14 ), .A1(\通用寄存器组_1_out_15 ), .SP(\通用寄存器组_1_out_16 ), .CBR(\通用寄存器组_1_out_17 ),
    .\来自存储器 (\来自存贮器 ), .\立即数 (\解码器_1_立即数 ), .\寄存器读地址1 (\解码器_1_读地址1__访存时数据 ),
    .\寄存器读地址2 (\解码器_1_读地址2_访存时地址_跳转时地址 ), .\功能码 (\解码器_1_功能码 ));  // open: 来自控制寄存器, 异常被触发
  \通用寄存器组  \u_通用寄存器组_1  (
    .\写入使能1 (\数据传送指令控制中心_1_写使能1 ), .\写入地址1 (\解码器_1_写地址1 ), .\写入数据1 (\数据传送指令控制中心_1_写入数据1 ),
    .\写入使能2 (\数据传送指令控制中心_1_写使能2 ), .\写入数据2 (\数据传送指令控制中心_1_写入数据2 ), .\写入地址2 (\数据传送指令控制中心_1_写地址2 ),
    .\时钟_2 (\节拍器_1__1 ), .\复位 (\复位 ), .out_10(\通用寄存器组_1_out_10 ), .out_11(\通用寄存器组_1_out_11 ),
    .out_12(\通用寄存器组_1_out_12 ), .out_13(\通用寄存器组_1_out_13 ), .out_14(\通用寄存器组_1_out_14 ),
    .out_15(\通用寄存器组_1_out_15 ), .out_16(\通用寄存器组_1_out_16 ), .out_17(\通用寄存器组_1_out_17 ), .\时钟_3 (\节拍器_1__3 ));
  // Probe on \通用寄存器组_1_out_10 
  // Probe on \通用寄存器组_1_out_11 
  // Probe on \通用寄存器组_1_out_12 
  // Probe on \通用寄存器组_1_out_13 
  // Probe on \通用寄存器组_1_out_14 
  // Probe on \通用寄存器组_1_out_15 
  // Probe on \通用寄存器组_1_out_16 
  // Probe on \通用寄存器组_1_out_17 
  \算数逻辑单元  \u_算数逻辑单元_1  (
    .D0(\通用寄存器组_1_out_10 ), .D1(\通用寄存器组_1_out_11 ), .D2(\通用寄存器组_1_out_12 ), .D3(\通用寄存器组_1_out_13 ),
    .\立即数 (\解码器_1_立即数 ), .\寄存器读地址1 (\解码器_1_读地址1__访存时数据 ), .\寄存器读地址2 (\解码器_1_读地址2_访存时地址_跳转时地址 ),
    .\运算类指令 (\解码器_1_运算类指令 ), .\逻辑类指令 (\解码器_1_逻辑类指令 ), .\移位类指令 (\解码器_1_移位类指令 ), .\逻辑类指令2 (\解码器_1_逻辑类指令2 ),
    .\功能码 (\解码器_1_功能码 ), .\结果 (\算数逻辑单元_1_结果 ), .out_16(\算数逻辑单元_1_out_16 ));  // open: 进位, 移位位数
endmodule

module \节拍器  (
  input  \时钟 ,
  input  \复位 ,
  output _0,
  output _1,
  output _2,
  output _3
);

  wire counter_1_q, counter_2_q, not_1_out;

  not not_1 (not_1_out, \时钟 );
  Counter #(.width(1), .max('h1)) counter_1 (.Q(counter_1_q), .clk(\时钟 ), .clr(\复位 ));  // open: load, D, count, carry
  Counter #(.width(1), .max('h1)) counter_2 (
    .Q(counter_2_q), .clk(not_1_out), .clr(\复位 ));  // open: load, D, count, carry
  and and_1 (_0, ~counter_1_q, ~counter_2_q);  // AND_Gate
  and and_2 (_1, counter_1_q, ~counter_2_q);  // AND_Gate
  and and_3 (_2, counter_1_q, counter_2_q);
  and and_4 (_3, ~counter_1_q, counter_2_q);  // AND_Gate
endmodule

module \算数逻辑单元  (
  input  \进位 ,
  input  [15:0] D0,
  input  [15:0] D1,
  input  [15:0] D2,
  input  [15:0] D3,
  input  [15:0] \立即数 ,
  input  [2:0] \寄存器读地址1 ,
  input  [2:0] \寄存器读地址2 ,
  input  \运算类指令 ,
  input  \逻辑类指令 ,
  input  \移位类指令 ,
  input  \逻辑类指令2 ,
  input  [5:0] \功能码 ,
  input  [3:0] \移位位数 ,
  output [15:0] \结果 ,
  output [3:0] out_16
);

  wire adder_1_cout, adder_2_cout, and_3_out, pull_resistor_5_node, subtractor_1_bout, subtractor_2_bout,
       xor_2_out, xor_3_out;
  wire [14:0] adder_1_out, subtractor_1_out;
  wire [15:0] and_1_out, and_2_out, divider_1_out, divider_1_rem, multiplexer_1_out, multiplexer_2_out,
       multiplexer_3_out, multiplexer_4_out, multiplexer_5_out, multiplexer_7_out, multiplier_1_cout,
       multiplier_1_out, nand_1_out, nor_1_out, not_1_out, not_2_out, or_1_out, or_2_out,
       pull_resistor_1_node, pull_resistor_2_node, pull_resistor_3_node, pull_resistor_4_node,
       pull_resistor_6_node, shifter_1_out, shifter_2_out, shifter_3_out, shifter_4_out, shifter_5_out,
       shifter_6_out, shifter_7_out, xor_1_out;
  wire [15:15] adder_2_out, subtractor_2_out;

  Multiplexer #(.select(2), .width(16), .enable("false")) multiplexer_1 (
    .in0(D0), .in1(D1), .in2(D2), .in3(D3), .out(multiplexer_1_out), .sel(\寄存器读地址1 [1:0]));
  Multiplexer #(.select(2), .width(16), .enable("false")) multiplexer_2 (
    .in0(D0), .in1(D1), .in2(D2), .in3(D3), .out(multiplexer_2_out), .sel(\寄存器读地址2 [1:0]));
  Adder #(.width(15)) adder_1 (
    .a(multiplexer_1_out[14:0]), .b(multiplexer_2_out[14:0]), .out(adder_1_out), .cin(\进位 ),
    .cout(adder_1_cout));
  Adder #(.width(1)) adder_2 (
    .a(multiplexer_1_out[15]), .b(multiplexer_2_out[15]), .out(adder_2_out[15]), .cin(adder_1_cout),
    .cout(adder_2_cout));
  Subtractor #(.width(15)) subtractor_1 (
    .a(multiplexer_1_out[14:0]), .b(multiplexer_2_out[14:0]), .out(subtractor_1_out), .bin(\进位 ),
    .bout(subtractor_1_bout));
  Subtractor #(.width(1)) subtractor_2 (
    .a(multiplexer_1_out[15]), .b(multiplexer_2_out[15]), .out(subtractor_2_out[15]),
    .bin(subtractor_1_bout), .bout(subtractor_2_bout));
  Pull_Resistor pull_resistor_1 (.node(pull_resistor_1_node));
  Multiplier #(.width(16)) multiplier_1 (
    .a(multiplexer_1_out), .b(multiplexer_2_out), .out(multiplier_1_out), .cin(pull_resistor_1_node),
    .cout(multiplier_1_cout));
  Pull_Resistor pull_resistor_2 (.node(pull_resistor_2_node));
  Divider #(.width(16)) divider_1 (
    .a(multiplexer_1_out), .b(multiplexer_2_out), .out(divider_1_out), .upper(pull_resistor_2_node),
    .rem(divider_1_rem));
  assign and_1_out = multiplexer_1_out & multiplexer_2_out;  // AND_Gate and_1, 16 bits wide
  assign or_1_out = multiplexer_1_out | multiplexer_2_out;  // OR_Gate or_1, 16 bits wide
  assign not_1_out = ~multiplexer_1_out;  // NOT_Gate not_1, 16 bits wide
  assign nor_1_out = ~(multiplexer_1_out | multiplexer_2_out);  // NOR_Gate nor_1, 16 bits wide
  assign nand_1_out = ~(multiplexer_1_out & multiplexer_2_out);  // NAND_Gate nand_1, 16 bits wide
  assign xor_1_out = multiplexer_1_out ^ multiplexer_2_out;  // XOR_Gate xor_1, 16 bits wide
  Shifter #(.width(16)) shifter_1 (.in(multiplexer_1_out), .\dist (\移位位数 ), .out(shifter_1_out));
  Shifter #(.width(16), .shift("lr")) shifter_2 (.in(multiplexer_1_out), .\dist (\移位位数 ), .out(shifter_2_out));
  Shifter #(.width(16), .shift("ar")) shifter_3 (.in(multiplexer_1_out), .\dist (\移位位数 ), .out(shifter_3_out));
  Shifter #(.width(16), .shift("rl")) shifter_4 (.in(multiplexer_1_out), .\dist (\移位位数 ), .out(shifter_4_out));
  Shifter #(.width(16), .shift("rr")) shifter_5 (.in(multiplexer_1_out), .\dist (\移位位数 ), .out(shifter_5_out));
  Shifter #(.width(16)) shifter_6 (.in(multiplexer_1_out), .\dist (\移位位数 ), .out(shifter_6_out));
  Shifter #(.width(16), .shift("lr")) shifter_7 (.in(multiplexer_1_out), .\dist (\移位位数 ), .out(shifter_7_out));
  assign and_2_out = multiplexer_1_out & \立即数 ;  // AND_Gate and_2, 16 bits wide
  assign or_2_out = multiplexer_1_out | \立即数 ;  // OR_Gate or_2, 16 bits wide
  assign not_2_out = ~\立即数 ;  // NOT_Gate not_2, 16 bits wide
  xor xor_2 (xor_2_out, adder_1_cout, adder_2_cout);
  xor xor_3 (xor_3_out, subtractor_1_bout, subtractor_2_bout);
  Pull_Resistor pull_resistor_3 (.node(pull_resistor_3_node));
  Pull_Resistor pull_resistor_4 (.node(pull_resistor_4_node));
  Pull_Resistor pull_resistor_5 (.node(pull_resistor_5_node));
  Pull_Resistor pull_resistor_6 (.node(pull_resistor_6_node));
  Multiplexer #(.select(3), .width(16), .enable("false")) multiplexer_3 (
    .in0({adder_2_out[15], adder_1_out}), .in1({subtractor_2_out[15], subtractor_1_out}),
    .in2({adder_2_out[15], adder_1_out}), .in3({subtractor_2_out[15], subtractor_1_out}),
    .in4(multiplier_1_out), .in5(multiplier_1_cout), .in6(divider_1_out), .in7(divider_1_rem),
    .out(multiplexer_3_out), .sel(\功能码 [2:0]));
  Multiplexer #(.select(3), .width(16), .enable("false")) multiplexer_4 (
    .in0(and_1_out), .in1(or_1_out), .in2(not_1_out), .in3(nor_1_out), .in4(nand_1_out), .in5(xor_1_out),
    .in6(pull_resistor_3_node), .in7(pull_resistor_3_node), .out(multiplexer_4_out), .sel(\功能码 [2:0]));
  Multiplexer #(.select(3), .width(16), .enable("false")) multiplexer_5 (
    .in0(shifter_1_out), .in1(shifter_2_out), .in2(shifter_3_out), .in3(shifter_4_out), .in4(shifter_5_out),
    .in5({shifter_6_out[15:1], \进位 }), .in6({\进位 , shifter_7_out[14:0]}), .in7(pull_resistor_4_node),
    .out(multiplexer_5_out), .sel(\功能码 [2:0]));
  Multiplexer #(.select(3), .enable("false")) multiplexer_6 (
    .in0(multiplexer_1_out[15]), .in1(multiplexer_1_out[0]), .in2(multiplexer_1_out[0]),
    .in3(multiplexer_1_out[0]), .in4(multiplexer_1_out[15]), .in5(multiplexer_1_out[0]),
    .in6(multiplexer_1_out[15]), .in7(pull_resistor_5_node), .sel(\功能码 [2:0]));  // open: out
  Multiplexer #(.select(3), .width(16), .enable("false")) multiplexer_7 (
    .in0(and_2_out), .in1(or_2_out), .in2(not_2_out), .in3(pull_resistor_6_node), .in4(pull_resistor_6_node),
    .in5(pull_resistor_6_node), .in6(pull_resistor_6_node), .in7(pull_resistor_6_node),
    .out(multiplexer_7_out), .sel(\功能码 [2:0]));
  Pull_Resistor pull_resistor_7 (.node({out_16[1], \结果 [14:0]}));
  assign {out_16[1], \结果 [14:0]} = \运算类指令  ? multiplexer_3_out : 16'bz;  // Controlled_Buffer controlled_buffer_1
  assign {out_16[1], \结果 [14:0]} = \逻辑类指令  ? multiplexer_4_out : 16'bz;  // Controlled_Buffer controlled_buffer_2
  assign {out_16[1], \结果 [14:0]} = \移位类指令  ? multiplexer_5_out : 16'bz;  // Controlled_Buffer controlled_buffer_3
  assign {out_16[1], \结果 [14:0]} = \逻辑类指令2  ? multiplexer_7_out : 16'bz;  // Controlled_Buffer controlled_buffer_4
  Multiplexer #(.disabled(0)) multiplexer_8 (
    .in0(adder_2_cout), .in1(subtractor_2_bout), .out(out_16[0]), .sel(\功能码 [0]), .en(and_3_out));
  Multiplexer #(.disabled(0)) multiplexer_9 (
    .in0(xor_2_out), .in1(xor_3_out), .out(out_16[2]), .sel(\功能码 [0]), .en(and_3_out));
  and and_3 (and_3_out, ~\功能码 [2], ~\功能码 [1], \运算类指令 );  // AND_Gate
  nor nor_2 (out_16[3], \结果 [0], \结果 [1], \结果 [2], \结果 [3], \结果 [4], \结果 [5], \结果 [6], \结果 [7], \结果 [9], \结果 [10], \结果 [11], \结果 [12], \结果 [13], \结果 [14], out_16[1], \结果 [8]);

  assign \结果 [15] = out_16[1];
endmodule

module \ALU符号  (
  input  [3:0] \符号_ZVSC ,
  input  \运算类指令 ,
  input  \逻辑类指令 ,
  input  \移位类指令 ,
  input  \逻辑类指令2 ,
  input  \n时钟 ,
  input  \复位 ,
  output [3:0] \状态输出 ,
  output \进位输出 
);

  wire or_1_out;

  or or_1 (or_1_out, \运算类指令 , \逻辑类指令 , \移位类指令 , \逻辑类指令2 );
  Register #(.width(1)) \u_零状态  (.D(\符号_ZVSC [0]), .en(or_1_out), .Q(\状态输出 [0]), .clk(\n时钟 ), .clr(\复位 ));
  Register #(.width(1)) \u_溢出状态  (.D(\符号_ZVSC [1]), .en(or_1_out), .Q(\状态输出 [1]), .clk(\n时钟 ), .clr(\复位 ));
  Register #(.width(1)) \u_符号状态  (.D(\符号_ZVSC [2]), .en(or_1_out), .Q(\状态输出 [2]), .clk(\n时钟 ), .clr(\复位 ));
  Register #(.width(1)) \u_进位状态  (.D(\符号_ZVSC [3]), .en(or_1_out), .Q(\状态输出 [3]), .clk(\n时钟 ), .clr(\复位 ));

  assign \进位输出  = \状态输出 [3];
endmodule

module \通用寄存器组  (
  input  \写入使能1 ,
  input  [2:0] \写入地址1 ,
  input  [15:0] \写入数据1 ,
  input  \写入使能2 ,
  input  [15:0] \写入数据2 ,
  input  [2:0] \写入地址2 ,
  input  \时钟_2 ,
  input  \时钟_3 ,
  input  \复位 ,
  output [15:0] out_10,
  output [15:0] out_11,
  output [15:0] out_12,
  output [15:0] out_13,
  output [15:0] out_14,
  output [15:0] out_15,
  output [15:0] out_16,
  output [15:0] out_17
);

  wire multiplexer_1_out;
  wire [15:0] demultiplexer_1_out0, demultiplexer_1_out1, demultiplexer_1_out2, demultiplexer_1_out3,
       demultiplexer_1_out4, demultiplexer_1_out5, demultiplexer_1_out6, demultiplexer_1_out7;

  Demultiplexer #(.select(3), .width(16)) demultiplexer_1 (
    .out0(demultiplexer_1_out0), .out1(demultiplexer_1_out1), .out2(demultiplexer_1_out2),
    .out3(demultiplexer_1_out3), .out4(demultiplexer_1_out4), .out5(demultiplexer_1_out5),
    .out6(demultiplexer_1_out6), .out7(demultiplexer_1_out7), .in(\写入数据1 ), .sel(\写入地址1 ), .en(\写入使能1 ));
  Demultiplexer #(.select(3), .width(16)) demultiplexer_2 (
    .out0(demultiplexer_1_out0), .out1(demultiplexer_1_out1), .out2(demultiplexer_1_out2),
    .out3(demultiplexer_1_out3), .out4(demultiplexer_1_out4), .out5(demultiplexer_1_out5),
    .out6(demultiplexer_1_out6), .out7(demultiplexer_1_out7), .in(\写入数据2 ), .sel(\写入地址2 ), .en(\写入使能2 ));
  Multiplexer #(.enable("false")) multiplexer_1 (.in0(\时钟_2 ), .in1(\时钟_3 ), .out(multiplexer_1_out));  // open: sel
  Register #(.width(16)) D0 (.D(demultiplexer_1_out0), .Q(out_10), .clk(multiplexer_1_out), .clr(\复位 ));  // open: en
  Register #(.width(16)) D1 (.D(demultiplexer_1_out1), .Q(out_11), .clk(multiplexer_1_out), .clr(\复位 ));  // open: en
  Register #(.width(16)) D2 (.D(demultiplexer_1_out2), .Q(out_12), .clk(multiplexer_1_out), .clr(\复位 ));  // open: en
  Register #(.width(16)) D3 (.D(demultiplexer_1_out3), .Q(out_13), .clk(multiplexer_1_out), .clr(\复位 ));  // open: en
  Register #(.width(16)) A0 (.D(demultiplexer_1_out4), .Q(out_14), .clk(multiplexer_1_out), .clr(\复位 ));  // open: en
  Register #(.width(16)) A1 (.D(demultiplexer_1_out5), .Q(out_15), .clk(multiplexer_1_out), .clr(\复位 ));  // open: en
  Register #(.width(16)) CBR (.D(demultiplexer_1_out7), .Q(out_17), .clk(multiplexer_1_out), .clr(\复位 ));  // open: en
  Register #(.width(16)) SP ();  // open: D, en, Q, clk, clr
endmodule

module \解码器  (
  input  [15:0] \指令 ,
  output Inst_NOP,
  output Inst_MOVI,
  output Inst_MOVUI,
  output Inst_MOV,
  output Inst_XCHG,
  output \运算类指令 ,
  output \逻辑类指令 ,
  output \移位类指令 ,
  output \逻辑类指令2 ,
  output \装载存储类指令 ,
  output \V类指令 ,
  output \控制寄存器传输指令 ,
  output \跳转类指令 ,
  output Inst_HLT,
  output [15:0] \立即数 ,
  output [5:0] \功能码 ,
  output [2:0] \读地址1__访存时数据 ,
  output [2:0] \读地址2_访存时地址_跳转时地址 ,
  output [2:0] \写地址1 
);

  wire I, II, III_I, III_II, IV_I, multiplexer_1_out, or_1_out, or_2_out, or_3_out, or_4_out, or_5_out,
       or_6_out, or_9_out, VI_I, VI_IV;
  wire [2:0] bit_extender_8_out, bit_extender_9_out, bit_extender_10_out, controlled_buffer_8_out;
  wire [5:0] bit_extender_4_out, bit_extender_5_out, bit_extender_6_out, bit_extender_7_out;
  wire [15:0] bit_extender_1_out, bit_extender_2_out, bit_extender_3_out;

  Decoder #(.select(5), .enable("false")) decoder_1 (
    .out0(Inst_NOP), .out4(Inst_MOVI), .out5(Inst_MOVUI), .out6(Inst_MOV), .out7(Inst_XCHG), .out8(\运算类指令 ),
    .out9(\逻辑类指令 ), .out10(\移位类指令 ), .out11(\逻辑类指令2 ), .out12(\装载存储类指令 ), .out13(\V类指令 ),
    .out14(\控制寄存器传输指令 ), .out15(II), .out16(III_II), .out17(VI_IV), .out18(VI_I), .out31(Inst_HLT),
    .sel(\指令 [15:11]));  // open: out1, out2, out3, out19, out20, out21, out22, out23, out24, out25, out26, out27, out28, out29, out30
  assign bit_extender_1_out = {{10{multiplexer_1_out}}, \指令 [5:0]};  // Bit_Extender bit_extender_1
  assign bit_extender_2_out = {{8{\指令 [7]}}, \指令 [7:0]};  // Bit_Extender bit_extender_2
  assign bit_extender_3_out = {{5{\指令 [10]}}, \指令 [10:0]};  // Bit_Extender bit_extender_3
  Multiplexer #(.enable("false")) multiplexer_1 (.in0(1'b0), .in1(\指令 [5]), .out(multiplexer_1_out), .sel(\逻辑类指令2 ));
  assign \立即数  = or_1_out ? bit_extender_1_out : 16'bz;  // Controlled_Buffer controlled_buffer_1
  assign \立即数  = or_2_out ? bit_extender_2_out : 16'bz;  // Controlled_Buffer controlled_buffer_2
  Pull_Resistor pull_resistor_1 (.node(\立即数 ));
  assign \立即数  = II ? bit_extender_3_out : 16'bz;  // Controlled_Buffer controlled_buffer_3
  or or_1 (or_1_out, VI_IV, \装载存储类指令 , VI_I, \逻辑类指令2 );
  or or_2 (or_2_out, III_II, III_I);
  assign bit_extender_4_out = {{5{1'b0}}, \指令 [7]};  // Bit_Extender bit_extender_4
  assign bit_extender_5_out = {{4{1'b0}}, {\指令 [9], \指令 [10]}};  // Bit_Extender bit_extender_5
  assign bit_extender_6_out = {{3{1'b0}}, {\指令 [0], \指令 [1], \指令 [2]}};  // Bit_Extender bit_extender_6
  assign bit_extender_7_out = {{1{1'b0}}, {\指令 [0], \指令 [1], \指令 [2], \指令 [3], \指令 [4]}};  // Bit_Extender bit_extender_7
  assign \功能码  = \装载存储类指令  ? bit_extender_4_out : 6'bz;  // Controlled_Buffer controlled_buffer_4
  Pull_Resistor pull_resistor_2 (.node(\功能码 ));
  assign \功能码  = or_3_out ? bit_extender_5_out : 6'bz;  // Controlled_Buffer controlled_buffer_5
  assign \功能码  = or_5_out ? bit_extender_6_out : 6'bz;  // Controlled_Buffer controlled_buffer_6
  assign \功能码  = or_9_out ? bit_extender_7_out : 6'bz;  // Controlled_Buffer controlled_buffer_7
  or or_3 (or_3_out, \逻辑类指令2 , IV_I);
  assign bit_extender_8_out = {{1{1'b0}}, {\指令 [9], \指令 [10]}};  // Bit_Extender bit_extender_8
  or or_4 (or_4_out, \装载存储类指令 , \移位类指令 , \运算类指令 );
  assign bit_extender_9_out = {{2{1'b0}}, \指令 [10]};  // Bit_Extender bit_extender_9
  assign controlled_buffer_8_out = \装载存储类指令  ? {2'b01, \指令 [8]} : 3'bz;  // Controlled_Buffer controlled_buffer_8
  assign bit_extender_10_out = {{2{1'b0}}, \指令 [9]};  // Bit_Extender bit_extender_10
  assign controlled_buffer_8_out = VI_I ? bit_extender_10_out : 3'bz;  // Controlled_Buffer controlled_buffer_9
  or or_5 (or_5_out, \移位类指令 , \运算类指令 , III_II);
  Pull_Resistor pull_resistor_3 (.node(\读地址1__访存时数据 ));
  assign \读地址1__访存时数据  = or_6_out ? {\指令 [8], \指令 [9], \指令 [10]} : 3'bz;  // Controlled_Buffer controlled_buffer_10
  or or_6 (or_6_out, \逻辑类指令 , IV_I);
  assign \读地址1__访存时数据  = or_4_out ? bit_extender_8_out : 3'bz;  // Controlled_Buffer controlled_buffer_11
  assign \读地址1__访存时数据  = VI_I ? bit_extender_9_out : 3'bz;  // Controlled_Buffer controlled_buffer_12
  or or_7 (IV_I, \逻辑类指令 , Inst_XCHG, Inst_MOV, \控制寄存器传输指令 );
  or or_8 (III_I, Inst_MOVUI, Inst_MOVI);
  or or_9 (or_9_out, \逻辑类指令 , IV_I, \V类指令 , VI_I);
  or or_10 (I, Inst_HLT, Inst_NOP);
  or or_11 (\跳转类指令 , II, III_II, VI_IV, VI_I);

  // Other names for the same wires on the sheet: IV_A = \运算类指令 ; IV_L = \逻辑类指令 ; IV_S = \移位类指令 ; V = \V类指令 ;
  //   VI_II = \逻辑类指令2 ; VI_III = \装载存储类指令 
endmodule

module \数据传送指令控制中心  (
  input  [15:0] D0,
  input  [15:0] D1,
  input  [15:0] D2,
  input  [15:0] D3,
  input  [15:0] A0,
  input  [15:0] A1,
  input  [15:0] SP,
  input  [15:0] CBR,
  input  [2:0] \寄存器读地址1 ,
  input  [2:0] \寄存器读地址2 ,
  input  [15:0] \ALU运算结果 ,
  input  [15:0] \来自存储器 ,
  input  [15:0] \立即数 ,
  input  [15:0] \来自控制寄存器 ,
  input  Inst_MOVI,
  input  Inst_MOVUI,
  input  Inst_MOV,
  input  Inst_XCHG,
  input  \运算类指令 ,
  input  \逻辑类指令 ,
  input  \移位类指令 ,
  input  \逻辑类指令2 ,
  input  \装载存储类指令 ,
  input  \控制寄存器传输指令 ,
  input  \异常被触发 ,
  input  [5:0] \功能码 ,
  output [15:0] \写入数据1 ,
  output \写使能1 ,
  output [15:0] \写入数据2 ,
  output [2:0] \写地址2 ,
  output \写使能2 
);

  wire and_1_out, or_1_out, or_2_out;
  wire [15:0] multiplexer_1_out;

  or or_1 (or_1_out, \运算类指令 , \逻辑类指令 , \移位类指令 , \逻辑类指令2 );
  Multiplexer #(.select(3), .width(16), .enable("false")) multiplexer_1 (
    .in0(D0), .in1(D1), .in2(D2), .in3(D3), .in4(A0), .in5(A1), .in6(SP), .in7(CBR), .out(multiplexer_1_out),
    .sel(\寄存器读地址1 ));
  Multiplexer #(.select(3), .width(16), .enable("false")) multiplexer_2 (
    .in0(D0), .in1(D1), .in2(D2), .in3(D3), .in4(A0), .in5(A1), .in6(SP), .in7(CBR), .out(\写入数据2 ),
    .sel(\寄存器读地址2 ));
  assign \写入数据1  = or_2_out ? multiplexer_1_out : 16'bz;  // Controlled_Buffer controlled_buffer_1
  assign \写入数据1  = or_1_out ? \ALU运算结果  : 16'bz;  // Controlled_Buffer controlled_buffer_2
  assign \写入数据1  = and_1_out ? \来自存储器  : 16'bz;  // Controlled_Buffer controlled_buffer_3
  assign \写入数据1  = Inst_MOVUI ? {\立即数 [7:0], multiplexer_1_out[7:0]} : 16'bz;  // Controlled_Buffer controlled_buffer_4
  assign \写入数据1  = Inst_MOVI ? {multiplexer_1_out[15:8], \立即数 [7:0]} : 16'bz;  // Controlled_Buffer controlled_buffer_5
  and and_1 (and_1_out, \功能码 [0], \装载存储类指令 );
  Pull_Resistor pull_resistor_1 (.node(\写入数据1 ));
  or or_2 (or_2_out, Inst_MOVI, Inst_MOVUI, Inst_MOV, Inst_XCHG, or_1_out, and_1_out, \控制寄存器传输指令 );
  and and_2 (\写使能1 , or_2_out, ~\异常被触发 );  // AND_Gate
  and and_3 (\写使能2 , Inst_XCHG, ~\异常被触发 );  // AND_Gate

  assign \写地址2  = \寄存器读地址1 ;
endmodule

module \堆栈  (
  input  [15:0] \堆栈指针 ,
  input  \V型指令 ,
  input  [5:0] \功能码 
);

  wire and_1_out, comparator_1_eq;

  Comparator #(.width(3)) comparator_1 (.a(\功能码 [5:3]), .b(3'b000), .eq(comparator_1_eq));  // open: gt, lt
  and and_1 (and_1_out, comparator_1_eq, \V型指令 );
  Decoder #(.select(3), .disabled(0)) decoder_1 (
    .sel(\功能码 [2:0]), .en(and_1_out));  // open: out0, out1, out2, out3, out4, out5, out6, out7
  RAM #(.addrWidth(12), .dataWidth(16), .bus("separate")) ram_1 (.addr(\堆栈指针 [11:0]));  // open: din, data, str, sel, clk, ld, clr
endmodule

module \内存  (
  input  [15:0] in_1
);

  RAM #(.addrWidth(16)) ram_1 ();  // open: addr, data, sel, clk, ld, clr
  RAM #(.addrWidth(16)) ram_2 ();  // open: addr, data, sel, clk, ld, clr
endmodule
