// Logisim project 20170917.circ as structural Verilog: 15 circuits, main circuit main
module main (
);

  wire \cpu_1_写使能 , rst, \全局时钟_1_out_1 ;
  wire [6:0] keyboard_1_data;
  wire [15:0] \cpu_1_写数据 , \cpu_1_地址 , \内存_1_输出 ;

  Button button_1 (.out(rst));
  \全局时钟  \u_全局时钟_1  (.out_1(\全局时钟_1_out_1 ));
  CPU cpu_1 (
    .\时钟 (\全局时钟_1_out_1 ), .\复位 (rst), .\来自存贮器 (\内存_1_输出 ), .\地址 (\cpu_1_地址 ), .\写数据 (\cpu_1_写数据 ),
    .\写使能 (\cpu_1_写使能 ));  // open: 异常, 异常_2, 异常_3, 异常_4
  \内存  \u_内存_1  (
    .\地址 (\cpu_1_地址 ), .\复位_写使能 (rst), .\写 (\cpu_1_写使能 ), .\大小端选择_0为小端 (1'b0), .\写入数据 (\cpu_1_写数据 ),
    .\输出 (\内存_1_输出 ));
  Button Ctrl ();  // open: out
  Button UP ();  // open: out
  Button RIGHT ();  // open: out
  Button LEFT ();  // open: out
  Button DOWN ();  // open: out
  TTY #(.rows(16), .cols(64)) tty_1 ();  // open: data, clk, we, clr
  Keyboard keyboard_1 (.data(keyboard_1_data));  // open: clk, re, clr, avail
endmodule

module CPU (
  input  \时钟 ,
  input  \复位 ,
  input  [15:0] \来自存贮器 ,
  input  \异常 ,
  input  \异常_2 ,
  input  \异常_3 ,
  input  \异常_4 ,
  output [15:0] \地址 ,
  output [15:0] \写数据 ,
  output \写使能 
);

  wire \alu符号_1_进位输出 , \堆栈_1_时钟选择 , \数据传送指令控制中心_1_写使能1 , \数据传送指令控制中心_1_写使能2 , \节拍器_1__0 , \节拍器_1__1 ,
       \节拍器_1__2 , \节拍器_1__3 , \解码器_1_inst_hlt , \解码器_1_inst_mov , \解码器_1_inst_movi , \解码器_1_inst_movui ,
       \解码器_1_inst_nop , \解码器_1_inst_xchg , \解码器_1_v类指令 , \解码器_1_与ar相关的跳转 , \解码器_1_其他跳转 , \解码器_1_控制寄存器传输指令 ,
       \解码器_1_直接跳转 , \解码器_1_移位类指令 , \解码器_1_符号比较 , \解码器_1_装载存储类指令 , \解码器_1_运算类指令 , \解码器_1_逻辑类指令 ,
       \解码器_1_逻辑类指令2 ;
  wire [2:0] \数据传送指令控制中心_1_写地址2 , \解码器_1_写地址1 , \解码器_1_读地址1__访存时数据 , \解码器_1_读地址2_访存时地址_跳转时地址 ;
  wire [3:0] \alu符号_1_状态输出 , \算数逻辑单元_1_out_16 , \解码器_1_移位位数 ;
  wire [5:0] \解码器_1_功能码 ;
  wire [15:0] undriven, undriven_2, \堆栈_1_out_15 , \堆栈_1_sp , \指令寄存器_q , \数据传送指令控制中心_1_写入数据1 ,
       \数据传送指令控制中心_1_写入数据2 , \程序计数器_1_out_15 , \算数逻辑单元_1_结果 , \解码器_1_立即数 , \访存控制中心_1_读数据_cpu_2 ,
       \通用寄存器组_1_out_11 , \通用寄存器组_1_out_12 , \通用寄存器组_1_out_13 , \通用寄存器组_1_out_14 , \通用寄存器组_1_out_15 ,
       \通用寄存器组_1_out_16 , \通用寄存器组_1_out_17 ;

  \节拍器  \u_节拍器_1  (.\时钟 (\时钟 ), ._0(\节拍器_1__0 ), ._1(\节拍器_1__1 ), ._2(\节拍器_1__2 ), ._3(\节拍器_1__3 ), .\复位 (\复位 ));
  Register #(.width(16)) \u_指令寄存器  (.D(\访存控制中心_1_读数据_cpu_2 ), .Q(\指令寄存器_q ), .clk(\节拍器_1__1 ), .clr(\复位 ));  // open: en
  \解码器  \u_解码器_1  (
    .\指令 (\指令寄存器_q ), .Inst_NOP(\解码器_1_inst_nop ), .Inst_MOVI(\解码器_1_inst_movi ),
    .Inst_MOVUI(\解码器_1_inst_movui ), .Inst_MOV(\解码器_1_inst_mov ), .Inst_XCHG(\解码器_1_inst_xchg ),
    .\运算类指令 (\解码器_1_运算类指令 ), .\逻辑类指令 (\解码器_1_逻辑类指令 ), .\移位类指令 (\解码器_1_移位类指令 ), .\逻辑类指令2 (\解码器_1_逻辑类指令2 ),
    .\装载存储类指令 (\解码器_1_装载存储类指令 ), .\V类指令 (\解码器_1_v类指令 ), .\控制寄存器传输指令 (\解码器_1_控制寄存器传输指令 ),
    .\直接跳转 (\解码器_1_直接跳转 ), .Inst_HLT(\解码器_1_inst_hlt ), .\立即数 (\解码器_1_立即数 ), .\功能码 (\解码器_1_功能码 ),
    .\写地址1 (\解码器_1_写地址1 ), .\读地址1__访存时数据 (\解码器_1_读地址1__访存时数据 ),
    .\读地址2_访存时地址_跳转时地址 (\解码器_1_读地址2_访存时地址_跳转时地址 ), .\移位位数 (\解码器_1_移位位数 ), .\其他跳转 (\解码器_1_其他跳转 ),
    .\符号比较 (\解码器_1_符号比较 ), .\与AR相关的跳转 (\解码器_1_与ar相关的跳转 ));
  \数据传送指令控制中心  \u_数据传送指令控制中心_1  (
    .\写入数据1 (\数据传送指令控制中心_1_写入数据1 ), .\写使能1 (\数据传送指令控制中心_1_写使能1 ), .\写使能2 (\数据传送指令控制中心_1_写使能2 ),
    .\写地址2 (\数据传送指令控制中心_1_写地址2 ), .\写入数据2 (\数据传送指令控制中心_1_写入数据2 ), .Inst_MOVI(\解码器_1_inst_movi ),
    .Inst_MOVUI(\解码器_1_inst_movui ), .Inst_MOV(\解码器_1_inst_mov ), .Inst_XCHG(\解码器_1_inst_xchg ),
    .\运算类指令 (\解码器_1_运算类指令 ), .\逻辑类指令 (\解码器_1_逻辑类指令 ), .\移位类指令 (\解码器_1_移位类指令 ), .\逻辑类指令2 (\解码器_1_逻辑类指令2 ),
    .\装载存储类指令 (\解码器_1_装载存储类指令 ), .\控制寄存器传输指令 (\解码器_1_控制寄存器传输指令 ), .\ALU运算结果 (\算数逻辑单元_1_结果 ),
    .D0(\通用寄存器组_1_out_11 ), .D1(\通用寄存器组_1_out_12 ), .D2(\通用寄存器组_1_out_13 ), .D3(\通用寄存器组_1_out_14 ),
    .A0(\通用寄存器组_1_out_15 ), .A1(\通用寄存器组_1_out_16 ), .SP(\堆栈_1_sp ), .CBR(\通用寄存器组_1_out_17 ),
    .\来自存储器 (\访存控制中心_1_读数据_cpu_2 ), .\立即数 (\解码器_1_立即数 ), .\来自控制寄存器 (undriven),
    .\寄存器读地址1 (\解码器_1_读地址1__访存时数据 ), .\寄存器读地址2 (\解码器_1_读地址2_访存时地址_跳转时地址 ), .\异常被触发 (1'b0),
    .\功能码 (\解码器_1_功能码 ), .\来自堆栈 (\堆栈_1_out_15 ), .PC(\程序计数器_1_out_15 ));  // open: 与AR有关的跳转指令
  \通用寄存器组  \u_通用寄存器组_1  (
    .\写入使能1 (\数据传送指令控制中心_1_写使能1 ), .\写入地址1 (\解码器_1_写地址1 ), .\写入数据1 (\数据传送指令控制中心_1_写入数据1 ),
    .\写入使能2 (\数据传送指令控制中心_1_写使能2 ), .\写入数据2 (\数据传送指令控制中心_1_写入数据2 ), .\写入地址2 (\数据传送指令控制中心_1_写地址2 ),
    .\时钟_2 (\节拍器_1__2 ), .\复位 (\复位 ), .out_11(\通用寄存器组_1_out_11 ), .out_12(\通用寄存器组_1_out_12 ),
    .out_13(\通用寄存器组_1_out_13 ), .out_14(\通用寄存器组_1_out_14 ), .out_15(\通用寄存器组_1_out_15 ),
    .out_16(\通用寄存器组_1_out_16 ), .out_17(\通用寄存器组_1_out_17 ), .\时钟_3 (\节拍器_1__3 ), .\时钟选择_默认3 (\堆栈_1_时钟选择 ));
  \程序计数器  \u_程序计数器_1  (
    .Inst_HLT(\解码器_1_inst_hlt ), .\功能码 (\解码器_1_功能码 ), .\时钟_0 (\节拍器_1__0 ), .AR0(\通用寄存器组_1_out_15 ),
    .AR1(\通用寄存器组_1_out_16 ), .\立即数 (\解码器_1_立即数 ), .\复位 (\复位 ), .out_15(\程序计数器_1_out_15 ),
    .\ALU符号 (\alu符号_1_状态输出 ), .\异常入口地址 (undriven_2), .\直接跳转 (\解码器_1_直接跳转 ), .\其他跳转 (\解码器_1_其他跳转 ),
    .\符号比较 (\解码器_1_符号比较 ), .\与AR相关的跳转 (\解码器_1_与ar相关的跳转 ), .\读地址1 (\解码器_1_读地址1__访存时数据 ));
  // Probe on \通用寄存器组_1_out_11 
  // Probe on \通用寄存器组_1_out_12 
  // Probe on \通用寄存器组_1_out_13 
  // Probe on \通用寄存器组_1_out_14 
  // Probe on \通用寄存器组_1_out_15 
  // Probe on \通用寄存器组_1_out_16 
  // Probe on \通用寄存器组_1_out_17 
  \访存控制中心  \u_访存控制中心_1  (
    .\地址_MEM (\地址 ), .\写数据_MEM (\写数据 ), .\读数据_CPU_2 (\访存控制中心_1_读数据_cpu_2 ), .\读数据_CPU (\来自存贮器 ),
    .D0(\通用寄存器组_1_out_11 ), .D1(\通用寄存器组_1_out_12 ), .D2(\通用寄存器组_1_out_13 ), .D3(\通用寄存器组_1_out_14 ),
    .A0(\通用寄存器组_1_out_15 ), .A1(\通用寄存器组_1_out_16 ), .\操作数1 (\解码器_1_读地址1__访存时数据 ),
    .\操作数2 (\解码器_1_读地址2_访存时地址_跳转时地址 ), .PC(\程序计数器_1_out_15 ), .\写使能 (\写使能 ), .\时钟_0 (\节拍器_1__0 ),
    .\时钟_1 (\节拍器_1__2 ), .\时钟_2 (\节拍器_1__3 ), .\时钟_3 (\复位 ), .\装载存储指令 (\解码器_1_装载存储类指令 ), .\功能码 (\解码器_1_功能码 ));
  \算数逻辑单元  \u_算数逻辑单元_1  (
    .\进位 (\alu符号_1_进位输出 ), .D0(\通用寄存器组_1_out_11 ), .D1(\通用寄存器组_1_out_12 ), .D2(\通用寄存器组_1_out_13 ),
    .D3(\通用寄存器组_1_out_14 ), .\立即数 (\解码器_1_立即数 ), .\寄存器读地址1 (\解码器_1_读地址1__访存时数据 ),
    .\寄存器读地址2 (\解码器_1_读地址2_访存时地址_跳转时地址 ), .\运算类指令 (\解码器_1_运算类指令 ), .\逻辑类指令 (\解码器_1_逻辑类指令 ),
    .\移位类指令 (\解码器_1_移位类指令 ), .\逻辑类指令2 (\解码器_1_移位类指令 ), .\功能码 (\解码器_1_功能码 ), .\移位位数 (\解码器_1_移位位数 ),
    .\结果 (\算数逻辑单元_1_结果 ), .out_16(\算数逻辑单元_1_out_16 ));
  \堆栈  \u_堆栈_1  (
    .\V型指令 (\解码器_1_v类指令 ), .\功能码 (\解码器_1_功能码 ), .out_15(\堆栈_1_out_15 ), .D0(\通用寄存器组_1_out_11 ),
    .D1(\通用寄存器组_1_out_12 ), .D2(\通用寄存器组_1_out_13 ), .D3(\通用寄存器组_1_out_14 ), .A0(\通用寄存器组_1_out_15 ),
    .A1(\通用寄存器组_1_out_16 ), .CBR(\通用寄存器组_1_out_17 ), .\寄存器地址 (\解码器_1_读地址1__访存时数据 ), .SP(\堆栈_1_sp ),
    .\时钟选择 (\堆栈_1_时钟选择 ), .\复位 (\复位 ), .\生长方向_1为下 (1'b0), .\时间_2 (\节拍器_1__3 ), .\时间_3 (\节拍器_1__2 ));  // open: 栈溢出
  // Probe on \堆栈_1_sp 
  \ALU符号  \alu符号_1  (
    .\符号_ZVSC (\算数逻辑单元_1_out_16 ), .\运算类指令 (\解码器_1_运算类指令 ), .\逻辑类指令 (\解码器_1_逻辑类指令 ), .\移位类指令 (\解码器_1_移位类指令 ),
    .\逻辑类指令2 (\解码器_1_移位类指令 ), .\时钟_2 (\节拍器_1__2 ), .\复位 (\复位 ), .\状态输出 (\alu符号_1_状态输出 ),
    .\进位输出 (\alu符号_1_进位输出 ));
endmodule

module \节拍器  (
  input  \时钟 ,
  input  \复位 ,
  output _0,
  output _1,
  output _2,
  output _3
);

  wire counter_1_q, counter_2_q, not_1_out;

  not not_1 (not_1_out, \时钟 );
  Counter #(.width(1), .max('h1)) counter_1 (.Q(counter_1_q), .clk(\时钟 ), .clr(\复位 ));  // open: load, D, count, carry
  Counter #(.width(1), .max('h1)) counter_2 (
    .Q(counter_2_q), .clk(not_1_out), .clr(\复位 ));  // open: load, D, count, carry
  and and_1 (_0, ~counter_1_q, ~counter_2_q);  // AND_Gate
  and and_2 (_1, counter_1_q, ~counter_2_q);  // AND_Gate
  and and_3 (_2, counter_1_q, counter_2_q);
  and and_4 (_3, ~counter_1_q, counter_2_q);  // AND_Gate
endmodule

module \算数逻辑单元  (
  input  \进位 ,
  input  [15:0] D0,
  input  [15:0] D1,
  input  [15:0] D2,
  input  [15:0] D3,
  input  [15:0] \立即数 ,
  input  [2:0] \寄存器读地址1 ,
  input  [2:0] \寄存器读地址2 ,
  input  \运算类指令 ,
  input  \逻辑类指令 ,
  input  \移位类指令 ,
  input  \逻辑类指令2 ,
  input  [5:0] \功能码 ,
  input  [3:0] \移位位数 ,
  output [15:0] \结果 ,
  output [3:0] out_16
);

  wire adder_1_cout, adder_2_cout, and_3_out, comparator_1_eq, comparator_1_gt, comparator_2_eq,
       comparator_2_gt, multiplexer_9_out, multiplexer_10_out, nor_2_out, subtractor_1_bout,
       subtractor_2_bout, xor_2_out, xor_3_out;
  wire [14:0] adder_1_out, subtractor_1_out;
  wire [15:0] and_1_out, and_2_out, divider_1_out, divider_1_rem, multiplexer_1_out, multiplexer_2_out,
       multiplexer_3_out, multiplexer_4_out, multiplexer_5_out, multiplexer_6_out, multiplier_1_cout,
       multiplier_1_out, nand_1_out, nor_1_out, not_1_out, not_2_out, or_1_out, or_2_out,
       pull_resistor_1_node, pull_resistor_2_node, pull_resistor_3_node, pull_resistor_4_node,
       pull_resistor_5_node, shifter_1_out, shifter_2_out, shifter_3_out, shifter_4_out, shifter_5_out,
       shifter_6_out, shifter_7_out, xor_1_out;
  wire [15:15] adder_2_out, subtractor_2_out;

  Multiplexer #(.select(2), .width(16), .enable("false")) multiplexer_1 (
    .in0(D0), .in1(D1), .in2(D2), .in3(D3), .out(multiplexer_1_out), .sel(\寄存器读地址1 [1:0]));
  Multiplexer #(.select(2), .width(16), .enable("false")) multiplexer_2 (
    .in0(D0), .in1(D1), .in2(D2), .in3(D3), .out(multiplexer_2_out), .sel(\寄存器读地址2 [1:0]));
  Comparator #(.width(16)) comparator_1 (
    .a(multiplexer_1_out), .b(multiplexer_2_out), .gt(comparator_1_gt), .eq(comparator_1_eq));  // open: lt
  Comparator #(.width(16), .mode("unsigned")) comparator_2 (
    .a(multiplexer_1_out), .b(multiplexer_2_out), .gt(comparator_2_gt), .eq(comparator_2_eq));  // open: lt
  Adder #(.width(15)) adder_1 (
    .a(multiplexer_1_out[14:0]), .b(multiplexer_2_out[14:0]), .out(adder_1_out), .cin(\进位 ),
    .cout(adder_1_cout));
  Adder #(.width(1)) adder_2 (
    .a(multiplexer_1_out[15]), .b(multiplexer_2_out[15]), .out(adder_2_out[15]), .cin(adder_1_cout),
    .cout(adder_2_cout));
  Subtractor #(.width(15)) subtractor_1 (
    .a(multiplexer_1_out[14:0]), .b(multiplexer_2_out[14:0]), .out(subtractor_1_out), .bin(\进位 ),
    .bout(subtractor_1_bout));
  Subtractor #(.width(1)) subtractor_2 (
    .a(multiplexer_1_out[15]), .b(multiplexer_2_out[15]), .out(subtractor_2_out[15]),
    .bin(subtractor_1_bout), .bout(subtractor_2_bout));
  Pull_Resistor pull_resistor_1 (.node(pull_resistor_1_node));
  Multiplier #(.width(16)) multiplier_1 (
    .a(multiplexer_1_out), .b(multiplexer_2_out), .out(multiplier_1_out), .cin(pull_resistor_1_node),
    .cout(multiplier_1_cout));
  Pull_Resistor pull_resistor_2 (.node(pull_resistor_2_node));
  Divider #(.width(16)) divider_1 (
    .a(multiplexer_1_out), .b(multiplexer_2_out), .out(divider_1_out), .upper(pull_resistor_2_node),
    .rem(divider_1_rem));
  assign and_1_out = multiplexer_1_out & multiplexer_2_out;  // AND_Gate and_1, 16 bits wide
  assign or_1_out = multiplexer_1_out | multiplexer_2_out;  // OR_Gate or_1, 16 bits wide
  assign not_1_out = ~multiplexer_1_out;  // NOT_Gate not_1, 16 bits wide
  assign nor_1_out = ~(multiplexer_1_out | multiplexer_2_out);  // NOR_Gate nor_1, 16 bits wide
  assign nand_1_out = ~(multiplexer_1_out & multiplexer_2_out);  // NAND_Gate nand_1, 16 bits wide
  assign xor_1_out = multiplexer_1_out ^ multiplexer_2_out;  // XOR_Gate xor_1, 16 bits wide
  Shifter #(.width(16)) shifter_1 (.in(multiplexer_1_out), .\dist (\移位位数 ), .out(shifter_1_out));
  Shifter #(.width(16), .shift("lr")) shifter_2 (.in(multiplexer_1_out), .\dist (\移位位数 ), .out(shifter_2_out));
  Shifter #(.width(16), .shift("ar")) shifter_3 (.in(multiplexer_1_out), .\dist (\移位位数 ), .out(shifter_3_out));
  Shifter #(.width(16), .shift("rl")) shifter_4 (.in(multiplexer_1_out), .\dist (\移位位数 ), .out(shifter_4_out));
  Shifter #(.width(16), .shift("rr")) shifter_5 (.in(multiplexer_1_out), .\dist (\移位位数 ), .out(shifter_5_out));
  Shifter #(.width(16)) shifter_6 (.in(multiplexer_1_out), .\dist (\移位位数 ), .out(shifter_6_out));
  Shifter #(.width(16), .shift("lr")) shifter_7 (.in(multiplexer_1_out), .\dist (\移位位数 ), .out(shifter_7_out));
  assign and_2_out = multiplexer_1_out & \立即数 ;  // AND_Gate and_2, 16 bits wide
  assign or_2_out = multiplexer_1_out | \立即数 ;  // OR_Gate or_2, 16 bits wide
  assign not_2_out = ~\立即数 ;  // NOT_Gate not_2, 16 bits wide
  xor xor_2 (xor_2_out, adder_1_cout, adder_2_cout);
  xor xor_3 (xor_3_out, subtractor_1_bout, subtractor_2_bout);
  Pull_Resistor pull_resistor_3 (.node(pull_resistor_3_node));
  Pull_Resistor pull_resistor_4 (.node(pull_resistor_4_node));
  Pull_Resistor pull_resistor_5 (.node(pull_resistor_5_node));
  Multiplexer #(.select(3), .width(16), .enable("false")) multiplexer_3 (
    .in0({adder_2_out[15], adder_1_out}), .in1({subtractor_2_out[15], subtractor_1_out}),
    .in2({adder_2_out[15], adder_1_out}), .in3({subtractor_2_out[15], subtractor_1_out}),
    .in4(multiplier_1_out), .in5(multiplier_1_cout), .in6(divider_1_out), .in7(divider_1_rem),
    .out(multiplexer_3_out), .sel(\功能码 [2:0]));
  Multiplexer #(.select(3), .width(16), .enable("false")) multiplexer_4 (
    .in0(and_1_out), .in1(or_1_out), .in2(not_1_out), .in3(nor_1_out), .in4(nand_1_out), .in5(xor_1_out),
    .in6(pull_resistor_3_node), .in7(pull_resistor_3_node), .out(multiplexer_4_out), .sel(\功能码 [2:0]));
  Multiplexer #(.select(3), .width(16), .enable("false")) multiplexer_5 (
    .in0(shifter_1_out), .in1(shifter_2_out), .in2(shifter_3_out), .in3(shifter_4_out), .in4(shifter_5_out),
    .in5({shifter_6_out[15:1], \进位 }), .in6({\进位 , shifter_7_out[14:0]}), .in7(pull_resistor_4_node),
    .out(multiplexer_5_out), .sel(\功能码 [2:0]));
  Multiplexer #(.select(3), .width(16), .enable("false")) multiplexer_6 (
    .in0(and_2_out), .in1(or_2_out), .in2(not_2_out), .in3(pull_resistor_5_node), .in4(pull_resistor_5_node),
    .in5(pull_resistor_5_node), .in6(pull_resistor_5_node), .in7(pull_resistor_5_node),
    .out(multiplexer_6_out), .sel(\功能码 [2:0]));
  Pull_Resistor pull_resistor_6 (.node(\结果 ));
  assign \结果  = \运算类指令  ? multiplexer_3_out : 16'bz;  // Controlled_Buffer controlled_buffer_1
  assign \结果  = \逻辑类指令  ? multiplexer_4_out : 16'bz;  // Controlled_Buffer controlled_buffer_2
  assign \结果  = \移位类指令  ? multiplexer_5_out : 16'bz;  // Controlled_Buffer controlled_buffer_3
  assign \结果  = \逻辑类指令2  ? multiplexer_6_out : 16'bz;  // Controlled_Buffer controlled_buffer_4
  Multiplexer #(.disabled(0)) multiplexer_7 (
    .in0(adder_2_cout), .in1(subtractor_2_bout), .out(out_16[0]), .sel(\功能码 [0]), .en(and_3_out));
  Multiplexer #(.disabled(0)) multiplexer_8 (
    .in0(xor_2_out), .in1(xor_3_out), .out(out_16[2]), .sel(\功能码 [0]), .en(and_3_out));
  and and_3 (and_3_out, ~\功能码 [2], ~\功能码 [1], \运算类指令 );  // AND_Gate
  Multiplexer #(.select(3), .enable("false")) multiplexer_9 (
    .in0(nor_2_out), .in1(nor_2_out), .in2(nor_2_out), .in3(nor_2_out), .in4(nor_2_out), .in5(nor_2_out),
    .in6(comparator_1_eq), .in7(comparator_2_eq), .out(multiplexer_9_out), .sel(\功能码 [2:0]));
  Multiplexer #(.select(3), .enable("false")) multiplexer_10 (
    .in0(\结果 [15]), .in1(\结果 [15]), .in2(\结果 [15]), .in3(\结果 [15]), .in4(\结果 [15]), .in5(\结果 [15]),
    .in6(comparator_1_gt), .in7(comparator_2_gt), .out(multiplexer_10_out), .sel(\功能码 [2:0]));
  nor nor_2 (nor_2_out, \结果 [0], \结果 [1], \结果 [2], \结果 [3], \结果 [4], \结果 [5], \结果 [6], \结果 [7], \结果 [9], \结果 [10], \结果 [11], \结果 [12], \结果 [13], \结果 [14], \结果 [15], \结果 [8]);
  Multiplexer #(.enable("false")) multiplexer_11 (
    .in0(nor_2_out), .in1(multiplexer_9_out), .out(out_16[3]), .sel(\逻辑类指令 ));
  Multiplexer #(.enable("false")) multiplexer_12 (
    .in0(\结果 [15]), .in1(multiplexer_10_out), .out(out_16[1]), .sel(\逻辑类指令 ));
endmodule

module \ALU符号  (
  input  [3:0] \符号_ZVSC ,
  input  \运算类指令 ,
  input  \逻辑类指令 ,
  input  \移位类指令 ,
  input  \逻辑类指令2 ,
  input  \时钟_2 ,
  input  \复位 ,
  output [3:0] \状态输出 ,
  output \进位输出 
);

  wire or_1_out;

  or or_1 (or_1_out, \运算类指令 , \逻辑类指令 , \移位类指令 , \逻辑类指令2 );
  Register #(.width(1)) \u_零状态  (.D(\符号_ZVSC [0]), .en(or_1_out), .Q(\状态输出 [0]), .clk(\时钟_2 ), .clr(\复位 ));
  Register #(.width(1)) \u_溢出状态  (.D(\符号_ZVSC [1]), .en(or_1_out), .Q(\状态输出 [1]), .clk(\时钟_2 ), .clr(\复位 ));
  Register #(.width(1)) \u_符号状态  (.D(\符号_ZVSC [2]), .en(or_1_out), .Q(\状态输出 [2]), .clk(\时钟_2 ), .clr(\复位 ));
  Register #(.width(1)) \u_进位状态  (.D(\符号_ZVSC [3]), .en(or_1_out), .Q(\状态输出 [3]), .clk(\时钟_2 ), .clr(\复位 ));

  assign \进位输出  = \状态输出 [3];
endmodule

module \通用寄存器组  (
  input  \写入使能1 ,
  input  [2:0] \写入地址1 ,
  input  [15:0] \写入数据1 ,
  input  \写入使能2 ,
  input  [15:0] \写入数据2 ,
  input  [2:0] \写入地址2 ,
  input  \时钟_3 ,
  input  \时钟_2 ,
  input  \复位 ,
  input  \时钟选择_默认3 ,
  output [15:0] out_11,
  output [15:0] out_12,
  output [15:0] out_13,
  output [15:0] out_14,
  output [15:0] out_15,
  output [15:0] out_16,
  output [15:0] out_17
);

  wire multiplexer_1_out;
  wire [15:0] demultiplexer_1_out0, demultiplexer_1_out1, demultiplexer_1_out2, demultiplexer_1_out3,
       demultiplexer_1_out4, demultiplexer_1_out5, demultiplexer_1_out6, demultiplexer_1_out7;

  Demultiplexer #(.select(3), .width(16), .tristate("true")) demultiplexer_1 (
    .out0(demultiplexer_1_out0), .out1(demultiplexer_1_out1), .out2(demultiplexer_1_out2),
    .out3(demultiplexer_1_out3), .out4(demultiplexer_1_out4), .out5(demultiplexer_1_out5),
    .out6(demultiplexer_1_out6), .out7(demultiplexer_1_out7), .in(\写入数据1 ), .sel(\写入地址1 ), .en(\写入使能1 ));
  Demultiplexer #(.select(3), .width(16), .tristate("true")) demultiplexer_2 (
    .out0(demultiplexer_1_out0), .out1(demultiplexer_1_out1), .out2(demultiplexer_1_out2),
    .out3(demultiplexer_1_out3), .out4(demultiplexer_1_out4), .out5(demultiplexer_1_out5),
    .out6(demultiplexer_1_out6), .out7(demultiplexer_1_out7), .in(\写入数据2 ), .sel(\写入地址2 ), .en(\写入使能2 ));
  Multiplexer #(.enable("false")) multiplexer_1 (.in0(\时钟_3 ), .in1(\时钟_2 ), .out(multiplexer_1_out), .sel(\时钟选择_默认3 ));
  Register #(.width(16)) D0 (.D(demultiplexer_1_out0), .Q(out_11), .clk(multiplexer_1_out), .clr(\复位 ));  // open: en
  Register #(.width(16)) D1 (.D(demultiplexer_1_out1), .Q(out_12), .clk(multiplexer_1_out), .clr(\复位 ));  // open: en
  Register #(.width(16)) D2 (.D(demultiplexer_1_out2), .Q(out_13), .clk(multiplexer_1_out), .clr(\复位 ));  // open: en
  Register #(.width(16)) D3 (.D(demultiplexer_1_out3), .Q(out_14), .clk(multiplexer_1_out), .clr(\复位 ));  // open: en
  Register #(.width(16)) A0 (.D(demultiplexer_1_out4), .Q(out_15), .clk(multiplexer_1_out), .clr(\复位 ));  // open: en
  Register #(.width(16)) A1 (.D(demultiplexer_1_out5), .Q(out_16), .clk(multiplexer_1_out), .clr(\复位 ));  // open: en
  Register #(.width(16)) CBR (.D(demultiplexer_1_out7), .Q(out_17), .clk(multiplexer_1_out), .clr(\复位 ));  // open: en
endmodule

module \解码器  (
  input  [15:0] \指令 ,
  output Inst_NOP,
  output Inst_MOVI,
  output Inst_MOVUI,
  output Inst_MOV,
  output Inst_XCHG,
  output \运算类指令 ,
  output \逻辑类指令 ,
  output \移位类指令 ,
  output \逻辑类指令2 ,
  output \装载存储类指令 ,
  output \V类指令 ,
  output \控制寄存器传输指令 ,
  output \直接跳转 ,
  output \其他跳转 ,
  output \符号比较 ,
  output \与AR相关的跳转 ,
  output Inst_HLT,
  output [15:0] \立即数 ,
  output [5:0] \功能码 ,
  output [2:0] \读地址1__访存时数据 ,
  output [2:0] \读地址2_访存时地址_跳转时地址 ,
  output [2:0] \写地址1 ,
  output [3:0] \移位位数 
);

  wire I, III_I, IV_I, or_1_out, or_2_out, or_3_out, or_4_out, or_5_out, or_6_out, or_9_out;
  wire [0:0] undriven;
  wire [2:0] bit_extender_11_out, bit_extender_12_out, bit_extender_13_out, bit_extender_14_out,
       bit_extender_15_out, bit_extender_16_out;
  wire [5:0] bit_extender_5_out, bit_extender_6_out, bit_extender_7_out, bit_extender_8_out,
       bit_extender_9_out, bit_extender_10_out;
  wire [15:0] bit_extender_1_out, bit_extender_2_out, bit_extender_3_out, bit_extender_4_out;

  Decoder #(.select(5), .enable("false")) decoder_1 (
    .out0(Inst_NOP), .out4(Inst_MOVI), .out5(Inst_MOVUI), .out6(Inst_MOV), .out7(Inst_XCHG), .out8(\运算类指令 ),
    .out9(\逻辑类指令 ), .out10(\移位类指令 ), .out11(\逻辑类指令2 ), .out12(\装载存储类指令 ), .out13(\V类指令 ),
    .out14(\控制寄存器传输指令 ), .out15(\直接跳转 ), .out16(\其他跳转 ), .out17(\符号比较 ), .out18(\与AR相关的跳转 ),
    .out31(Inst_HLT), .sel(\指令 [15:11]));  // open: out1, out2, out3, out19, out20, out21, out22, out23, out24, out25, out26, out27, out28, out29, out30
  assign bit_extender_1_out = {{10{\指令 [5]}}, \指令 [5:0]};  // Bit_Extender bit_extender_1
  assign bit_extender_2_out = {{8{1'b0}}, \指令 [7:0]};  // Bit_Extender bit_extender_2
  assign bit_extender_3_out = {{8{\指令 [7]}}, \指令 [7:0]};  // Bit_Extender bit_extender_3
  assign bit_extender_4_out = {{5{\指令 [10]}}, \指令 [10:0]};  // Bit_Extender bit_extender_4
  assign \立即数  = or_1_out ? bit_extender_1_out : 16'bz;  // Controlled_Buffer controlled_buffer_1
  assign \立即数  = III_I ? bit_extender_2_out : 16'bz;  // Controlled_Buffer controlled_buffer_2
  Controlled_Buffer #(.width(16)) controlled_buffer_3 (.in(bit_extender_3_out), .en(\其他跳转 ));  // open: out
  assign \立即数  = \直接跳转  ? bit_extender_4_out : 16'bz;  // Controlled_Buffer controlled_buffer_4
  Pull_Resistor pull_resistor_1 (.node(\立即数 ));
  or or_1 (or_1_out, \符号比较 , \装载存储类指令 , \逻辑类指令2 , \与AR相关的跳转 );
  assign bit_extender_5_out = {{5{1'b0}}, \指令 [7]};  // Bit_Extender bit_extender_5
  assign bit_extender_6_out = {{4{1'b0}}, {\指令 [9], \指令 [10]}};  // Bit_Extender bit_extender_6
  assign bit_extender_7_out = {{3{1'b0}}, {\指令 [0], \指令 [1], \指令 [2]}};  // Bit_Extender bit_extender_7
  assign bit_extender_8_out = {{1{1'b0}}, {\指令 [0], \指令 [1], \指令 [2], \指令 [3], \指令 [4]}};  // Bit_Extender bit_extender_8
  assign bit_extender_9_out = {{3{1'b0}}, \指令 [8:6]};  // Bit_Extender bit_extender_9
  assign bit_extender_10_out = {{3{1'b0}}, {\指令 [10:9], undriven[0]}};  // Bit_Extender bit_extender_10
  assign \功能码  = \装载存储类指令  ? bit_extender_5_out : 6'bz;  // Controlled_Buffer controlled_buffer_5
  Pull_Resistor pull_resistor_2 (.node(\功能码 ));
  assign \功能码  = or_2_out ? bit_extender_6_out : 6'bz;  // Controlled_Buffer controlled_buffer_6
  assign \功能码  = or_5_out ? bit_extender_7_out : 6'bz;  // Controlled_Buffer controlled_buffer_7
  assign \功能码  = or_9_out ? bit_extender_8_out : 6'bz;  // Controlled_Buffer controlled_buffer_8
  assign \功能码  = \符号比较  ? bit_extender_9_out : 6'bz;  // Controlled_Buffer controlled_buffer_9
  assign \功能码  = \其他跳转  ? bit_extender_10_out : 6'bz;  // Controlled_Buffer controlled_buffer_10
  assign \读地址2_访存时地址_跳转时地址  = \装载存储类指令  ? {2'b01, \指令 [8]} : 3'bz;  // Controlled_Buffer controlled_buffer_11
  or or_2 (or_2_out, \逻辑类指令2 , IV_I);
  assign bit_extender_11_out = {{1{1'b0}}, \指令 [10:9]};  // Bit_Extender bit_extender_11
  or or_3 (or_3_out, \逻辑类指令 , \装载存储类指令 , \移位类指令 , \运算类指令 );
  assign bit_extender_12_out = {{2{1'b0}}, \指令 [10]};  // Bit_Extender bit_extender_12
  assign bit_extender_13_out = {{1{1'b0}}, \指令 [8:7]};  // Bit_Extender bit_extender_13
  assign bit_extender_14_out = {{2{1'b0}}, \指令 [9]};  // Bit_Extender bit_extender_14
  or or_4 (or_4_out, \逻辑类指令 , \运算类指令 );
  or or_5 (or_5_out, \移位类指令 , \运算类指令 , \V类指令 );
  assign \读地址1__访存时数据  = IV_I ? \指令 [10:8] : 3'bz;  // Controlled_Buffer controlled_buffer_12
  Pull_Resistor pull_resistor_3 (.node(\读地址1__访存时数据 ));
  assign \读地址1__访存时数据  = or_3_out ? bit_extender_11_out : 3'bz;  // Controlled_Buffer controlled_buffer_13
  assign \读地址1__访存时数据  = \与AR相关的跳转  ? bit_extender_12_out : 3'bz;  // Controlled_Buffer controlled_buffer_14
  assign \读地址1__访存时数据  = \V类指令  ? \指令 [7:5] : 3'bz;  // Controlled_Buffer controlled_buffer_15
  Pull_Resistor pull_resistor_4 (.node(\读地址2_访存时地址_跳转时地址 ));
  assign \读地址2_访存时地址_跳转时地址  = IV_I ? \指令 [7:5] : 3'bz;  // Controlled_Buffer controlled_buffer_16
  assign \读地址2_访存时地址_跳转时地址  = or_6_out ? bit_extender_13_out : 3'bz;  // Controlled_Buffer controlled_buffer_17
  or or_6 (or_6_out, \运算类指令 , \逻辑类指令 , \移位类指令 );
  assign \读地址2_访存时地址_跳转时地址  = \与AR相关的跳转  ? bit_extender_14_out : 3'bz;  // Controlled_Buffer controlled_buffer_18
  assign \写地址1  = IV_I ? \指令 [7:5] : 3'bz;  // Controlled_Buffer controlled_buffer_19
  assign \写地址1  = III_I ? \指令 [10:8] : 3'bz;  // Controlled_Buffer controlled_buffer_20
  assign bit_extender_15_out = {{1{1'b0}}, \指令 [6:5]};  // Bit_Extender bit_extender_15
  assign \写地址1  = or_4_out ? bit_extender_15_out : 3'bz;  // Controlled_Buffer controlled_buffer_21
  assign \写地址1  = \装载存储类指令  ? {1'b1, \指令 [9], \指令 [10]} : 3'bz;  // Controlled_Buffer controlled_buffer_22
  assign \写地址1  = \移位类指令  ? bit_extender_16_out : 3'bz;  // Controlled_Buffer controlled_buffer_23
  assign bit_extender_16_out = {{1{1'b0}}, \指令 [8:7]};  // Bit_Extender bit_extender_16
  or or_7 (III_I, Inst_MOVUI, Inst_MOVI);
  or or_8 (IV_I, Inst_XCHG, \控制寄存器传输指令 , Inst_MOV);
  or or_9 (or_9_out, \逻辑类指令 , IV_I, \与AR相关的跳转 );
  Pull_Resistor pull_resistor_5 (.node(\写地址1 ));
  assign \移位位数  = \移位类指令  ? \指令 [6:3] : 4'bz;  // Controlled_Buffer controlled_buffer_24
  Pull_Resistor pull_resistor_6 (.node(\移位位数 ));
  or or_10 (I, Inst_HLT, Inst_NOP);

  // Other names for the same wires on the sheet: II = \直接跳转 ; III_II = \其他跳转 ; IV_A = \运算类指令 ; IV_L = \逻辑类指令 ;
  //   IV_S = \移位类指令 ; V = \V类指令 ; VI_I = \与AR相关的跳转 ; VI_II = \逻辑类指令2 ; VI_III = \装载存储类指令 ; VI_IV = \符号比较 
endmodule

module \数据传送指令控制中心  (
  input  [15:0] D0,
  input  [15:0] D1,
  input  [15:0] D2,
  input  [15:0] D3,
  input  [15:0] A0,
  input  [15:0] A1,
  input  [15:0] SP,
  input  [15:0] CBR,
  input  [2:0] \寄存器读地址1 ,
  input  [2:0] \寄存器读地址2 ,
  input  [15:0] \ALU运算结果 ,
  input  [15:0] \来自存储器 ,
  input  [15:0] \立即数 ,
  input  [15:0] \来自控制寄存器 ,
  input  [15:0] \来自堆栈 ,
  input  [15:0] PC,
  input  Inst_MOVI,
  input  Inst_MOVUI,
  input  Inst_MOV,
  input  Inst_XCHG,
  input  \运算类指令 ,
  input  \逻辑类指令 ,
  input  \移位类指令 ,
  input  \逻辑类指令2 ,
  input  \与AR有关的跳转指令 ,
  input  \装载存储类指令 ,
  input  \控制寄存器传输指令 ,
  input  \异常被触发 ,
  input  [5:0] \功能码 ,
  output [15:0] \写入数据1 ,
  output \写使能1 ,
  output [15:0] \写入数据2 ,
  output [2:0] \写地址2 ,
  output \写使能2 
);

  wire and_1_out, and_2_out, comparator_1_eq, or_1_out, or_2_out, or_3_out;
  wire [15:0] multiplexer_1_out;

  Comparator #(.width(2), .mode("unsigned")) comparator_1 (
    .a(\功能码 [2:1]), .b(2'b11), .eq(comparator_1_eq));  // open: gt, lt
  Multiplexer #(.select(3), .width(16), .enable("false")) multiplexer_1 (
    .in0(D0), .in1(D1), .in2(D2), .in3(D3), .in4(A0), .in5(A1), .in6(SP), .in7(CBR), .out(multiplexer_1_out),
    .sel(\寄存器读地址1 ));
  Multiplexer #(.select(3), .width(16), .enable("false")) multiplexer_2 (
    .in0(D0), .in1(D1), .in2(D2), .in3(D3), .in4(A0), .in5(A1), .in6(SP), .in7(CBR), .out(\写入数据2 ),
    .sel(\寄存器读地址2 ));
  and and_1 (and_1_out, \移位类指令 , ~comparator_1_eq);  // AND_Gate
  assign \写入数据1  = or_3_out ? multiplexer_1_out : 16'bz;  // Controlled_Buffer controlled_buffer_1
  assign \写入数据1  = or_2_out ? \ALU运算结果  : 16'bz;  // Controlled_Buffer controlled_buffer_2
  assign \写入数据1  = and_2_out ? \来自存储器  : 16'bz;  // Controlled_Buffer controlled_buffer_3
  assign \写入数据1  = Inst_MOVUI ? {\立即数 [7:0], multiplexer_1_out[7:0]} : 16'bz;  // Controlled_Buffer controlled_buffer_4
  assign \写入数据1  = Inst_MOVI ? {multiplexer_1_out[15:8], \立即数 [7:0]} : 16'bz;  // Controlled_Buffer controlled_buffer_5
  and and_2 (and_2_out, \功能码 [0], \装载存储类指令 );
  Pull_Resistor pull_resistor_1 (.node(\写入数据1 ));
  or or_1 (or_1_out, Inst_MOVI, Inst_MOVUI, Inst_MOV, Inst_XCHG, or_2_out, and_2_out, \控制寄存器传输指令 );
  or or_2 (or_2_out, \运算类指令 , \逻辑类指令 , and_1_out, \逻辑类指令2 );
  or or_3 (or_3_out, Inst_MOV, Inst_XCHG, \控制寄存器传输指令 );
  and and_3 (\写使能1 , or_1_out, ~\异常被触发 );  // AND_Gate
  and and_4 (\写使能2 , Inst_XCHG, ~\异常被触发 );  // AND_Gate

  assign \写地址2  = \寄存器读地址1 ;
endmodule

module \堆栈  (
  input  \复位 ,
  input  [15:0] D0,
  input  [15:0] D1,
  input  [15:0] D2,
  input  [15:0] D3,
  input  [15:0] A0,
  input  [15:0] A1,
  input  [15:0] CBR,
  input  [2:0] \寄存器地址 ,
  input  \生长方向_1为下 ,
  input  [5:0] \功能码 ,
  input  \V型指令 ,
  input  \时间_2 ,
  input  \时间_3 ,
  output [15:0] out_15,
  output [15:0] SP,
  output \栈溢出 ,
  output \时钟选择 
);

  wire adder_1_cout, and_1_out, and_2_out, and_3_out, comparator_1_eq, multiplexer_2_out, multiplexer_3_out,
       multiplexer_4_out, or_1_out, or_3_out, PUSH, SPDEC, SPINC, subtractor_1_bout;
  wire [11:0] adder_1_out, controlled_buffer_2_out, subtractor_1_out;
  wire [15:0] multiplexer_1_out;

  Comparator #(.width(3)) comparator_1 (.a(\功能码 [5:3]), .b(3'b000), .eq(comparator_1_eq));  // open: gt, lt
  Multiplexer #(.select(3), .width(16), .enable("false")) multiplexer_1 (
    .in0(D0), .in1(D1), .in2(D2), .in3(D3), .in4(A0), .in5(A1), .in6({4'b0000, SP[11:0]}), .in7(CBR),
    .out(multiplexer_1_out), .sel(\寄存器地址 ));
  and and_1 (and_1_out, comparator_1_eq, \V型指令 );
  Decoder #(.select(3), .disabled(0)) decoder_1 (
    .out0(PUSH), .out1(\时钟选择 ), .out2(SPINC), .out3(SPDEC), .sel(\功能码 [2:0]), .en(and_1_out));  // open: out4, out5, out6, out7
  Adder #(.width(12)) adder_1 (.a(SP[11:0]), .b(12'h1), .out(adder_1_out), .cout(adder_1_cout));  // open: cin
  Subtractor #(.width(12)) subtractor_1 (
    .a(SP[11:0]), .b(12'h1), .out(subtractor_1_out), .bout(subtractor_1_bout));  // open: bin
  and and_2 (and_2_out, subtractor_1_bout, \生长方向_1为下 );
  and and_3 (and_3_out, adder_1_cout, ~\生长方向_1为下 );  // AND_Gate
  assign out_15 = PUSH ? multiplexer_1_out : 16'bz;  // Controlled_Buffer controlled_buffer_1
  RAM #(.addrWidth(12), .dataWidth(16), .bus("asynch")) ram_1 (
    .addr(SP[11:0]), .data(out_15), .clr(\复位 ));  // open: sel, ld
  assign controlled_buffer_2_out = or_3_out ? adder_1_out : 12'bz;  // Controlled_Buffer controlled_buffer_2
  assign controlled_buffer_2_out = or_1_out ? subtractor_1_out : 12'bz;  // Controlled_Buffer controlled_buffer_3
  or or_1 (or_1_out, multiplexer_3_out, SPDEC);
  or or_2 (\栈溢出 , and_2_out, and_3_out);
  Multiplexer #(.enable("false")) multiplexer_2 (.in0(\时间_3 ), .in1(\时间_2 ), .out(multiplexer_2_out), .sel(\时钟选择 ));
  or or_3 (or_3_out, SPINC, multiplexer_4_out);
  Multiplexer #(.enable("false")) multiplexer_3 (.in0(\时钟选择 ), .in1(PUSH), .out(multiplexer_3_out), .sel(\生长方向_1为下 ));
  Register #(.width(12)) register_1 (
    .D(controlled_buffer_2_out), .Q(SP[11:0]), .clk(multiplexer_2_out), .clr(\复位 ));  // open: en
  Multiplexer #(.enable("false")) multiplexer_4 (.in0(PUSH), .in1(\时钟选择 ), .out(multiplexer_4_out), .sel(\生长方向_1为下 ));

  assign SP[15:12] = 4'b0000;

  // Other names for the same wires on the sheet: POP = \时钟选择 
endmodule

module \访存控制中心  (
  input  [15:0] \读数据_CPU ,
  input  [15:0] D0,
  input  [15:0] D1,
  input  [15:0] D2,
  input  [15:0] D3,
  input  [15:0] A0,
  input  [15:0] A1,
  input  [2:0] \操作数1 ,
  input  [2:0] \操作数2 ,
  input  [15:0] PC,
  input  \时钟_0 ,
  input  \时钟_1 ,
  input  \时钟_2 ,
  input  \时钟_3 ,
  input  \装载存储指令 ,
  input  [5:0] \功能码 ,
  output [15:0] \读数据_CPU_2 ,
  output [15:0] \地址_MEM ,
  output [15:0] \写数据_MEM ,
  output \写使能 
);

  wire [15:0] multiplexer_2_out;

  Multiplexer #(.select(2), .width(16), .enable("false")) multiplexer_1 (
    .in0(D0), .in1(D1), .in2(D2), .in3(D3), .out(\写数据_MEM ), .sel(\操作数1 [1:0]));
  Multiplexer #(.width(16), .enable("false")) multiplexer_2 (
    .in0(A0), .in1(A1), .out(multiplexer_2_out), .sel(\操作数2 [0]));

  assign \写使能  = 1'b0;
  assign \地址_MEM  = PC;
  assign \读数据_CPU_2  = \读数据_CPU ;
endmodule

module \程序计数器  (
  input  \时钟_0 ,
  input  \复位 ,
  input  Inst_HLT,
  input  \直接跳转 ,
  input  \其他跳转 ,
  input  \符号比较 ,
  input  \与AR相关的跳转 ,
  input  [5:0] \功能码 ,
  input  [15:0] AR0,
  input  [15:0] AR1,
  input  [15:0] \立即数 ,
  input  [3:0] \ALU符号 ,
  input  [15:0] \异常入口地址 ,
  input  [2:0] \读地址1 ,
  output [15:0] out_15
);

  wire decoder_1_out0, decoder_1_out1, decoder_1_out2, decoder_1_out3;
  wire [1:0] pc_op;
  wire [15:0] adder_1_out, multiplexer_1_out, multiplexer_2_out, undriven;

  assign pc_op = Inst_HLT ? 2'b11 : 2'bz;  // Controlled_Buffer controlled_buffer_1
  assign pc_op = \直接跳转  ? 2'b01 : 2'bz;  // Controlled_Buffer controlled_buffer_2
  Decoder #(.select(3), .enable("false")) decoder_1 (
    .out0(decoder_1_out0), .out1(decoder_1_out1), .out2(decoder_1_out2), .out3(decoder_1_out3),
    .sel(\功能码 [2:0]));  // open: out4, out5, out6, out7
  Multiplexer #(.width(16), .enable("false")) multiplexer_1 (
    .in0(AR0), .in1(AR1), .out(multiplexer_1_out), .sel(\读地址1 [0]));
  Adder #(.width(16)) adder_1 (.a(out_15), .b(16'h1), .out(adder_1_out));  // open: cin, cout
  Register #(.width(16)) register_1 (.D(multiplexer_2_out), .Q(out_15), .clk(\时钟_0 ), .clr(\复位 ));  // open: en
  Multiplexer #(.select(2), .width(16), .enable("false")) multiplexer_2 (
    .in0(adder_1_out), .in1(\异常入口地址 ), .in2(undriven), .in3(out_15), .out(multiplexer_2_out), .sel(pc_op));
  Pull_Resistor pull_resistor_1 (.node(pc_op));
endmodule

module \控制寄存器  (
  input  [15:0] \数据 
);
endmodule

module \内存  (
  input  [15:0] \地址 ,
  input  [15:0] \写入数据 ,
  input  \复位_写使能 ,
  input  \写 ,
  input  \大小端选择_0为小端 ,
  output [15:0] \输出 
);

  wire not_1_out, not_2_out;
  wire [7:0] controlled_buffer_1_out, controlled_buffer_2_out, multiplexer_2_out, multiplexer_3_out,
       multiplexer_4_out, multiplexer_5_out, multiplexer_6_out, multiplexer_7_out;
  wire [14:0] adder_1_out, multiplexer_1_out;

  Pull_Resistor pull_resistor_1 (.node(\大小端选择_0为小端 ));
  Adder #(.width(15)) adder_1 (.a(\地址 [15:1]), .b(15'h1), .out(adder_1_out));  // open: cin, cout
  Multiplexer #(.width(15), .enable("false")) multiplexer_1 (
    .in0(\地址 [15:1]), .in1(adder_1_out), .out(multiplexer_1_out), .sel(\地址 [0]));
  Multiplexer #(.width(8), .enable("false")) multiplexer_2 (
    .in0(\写入数据 [7:0]), .in1(\写入数据 [15:8]), .out(multiplexer_2_out), .sel(\大小端选择_0为小端 ));
  Multiplexer #(.width(8), .enable("false")) multiplexer_3 (
    .in0(\写入数据 [15:8]), .in1(\写入数据 [7:0]), .out(multiplexer_3_out), .sel(\大小端选择_0为小端 ));
  Multiplexer #(.width(8), .enable("false")) multiplexer_4 (
    .in0(multiplexer_2_out), .in1(multiplexer_3_out), .out(multiplexer_4_out), .sel(\地址 [0]));
  Multiplexer #(.width(8), .enable("false")) multiplexer_5 (
    .in0(multiplexer_3_out), .in1(multiplexer_2_out), .out(multiplexer_5_out), .sel(\地址 [0]));
  not not_1 (not_1_out, \复位_写使能 );
  not not_2 (not_2_out, \写 );
  assign controlled_buffer_1_out = \写  ? multiplexer_4_out : 8'bz;  // Controlled_Buffer controlled_buffer_1
  RAM #(.addrWidth(15), .bus("asynch")) ram_1 (
    .addr(multiplexer_1_out), .data(controlled_buffer_1_out), .sel(not_1_out), .ld(not_2_out), .clr(\复位_写使能 ));
  assign controlled_buffer_2_out = \写  ? multiplexer_5_out : 8'bz;  // Controlled_Buffer controlled_buffer_2
  RAM #(.addrWidth(15), .bus("asynch")) ram_2 (
    .addr(\地址 [15:1]), .data(controlled_buffer_2_out), .sel(not_1_out), .ld(not_2_out), .clr(\复位_写使能 ));
  Multiplexer #(.width(8), .enable("false")) multiplexer_6 (
    .in0(controlled_buffer_1_out), .in1(controlled_buffer_2_out), .out(multiplexer_6_out), .sel(\地址 [0]));
  Multiplexer #(.width(8), .enable("false")) multiplexer_7 (
    .in0(controlled_buffer_2_out), .in1(controlled_buffer_1_out), .out(multiplexer_7_out), .sel(\地址 [0]));
  Multiplexer #(.width(8), .enable("false")) multiplexer_8 (
    .in0(multiplexer_6_out), .in1(multiplexer_7_out), .out(\输出 [7:0]), .sel(\大小端选择_0为小端 ));
  Multiplexer #(.width(8), .enable("false")) multiplexer_9 (
    .in0(multiplexer_7_out), .in1(multiplexer_6_out), .out(\输出 [15:8]), .sel(\大小端选择_0为小端 ));

  // Notes on the sheet:
  //   MEMORY0
  //   MEMORY1
  //   LOW
  //   HIGH
endmodule

module \全局时钟  (
  output out_1
);

  Clock clock_1 (.out(out_1));
endmodule

module \哑终端处理  (
  input  [6:0] in_1,
  input  \时钟 ,
  input  \复位 ,
  input  \加载 ,
  input  \时钟使能 ,
  input  \保存 ,
  output \终端时钟 ,
  output [6:0] \输出 ,
  output \键盘时钟 ,
  output \满中断 
);

  wire and_1_out, and_2_out, and_3_out, comparator_1_eq, comparator_2_eq, comparator_3_eq, decoder_1_out0,
       decoder_1_out1, not_1_out, or_1_out, or_2_out, or_3_out, \列计数_carry ;
  wire [1:0] counter_1_q;
  wire [3:0] counter_2_q;
  wire [4:0] \列计数_q ;

  Counter #(.width(2), .max('h3)) counter_1 (
    .Q(counter_1_q), .clk(and_1_out), .clr(or_1_out));  // open: load, D, count, carry
  and and_1 (and_1_out, \时钟使能 , \时钟 );
  or or_1 (or_1_out, \复位 , ~\时钟使能 );  // OR_Gate
  Decoder #(.select(2), .disabled(0)) decoder_1 (
    .out0(decoder_1_out0), .out1(decoder_1_out1), .out2(\终端时钟 ), .out3(\键盘时钟 ), .sel(counter_1_q));  // open: en
  Comparator #(.width(7)) comparator_1 (.a(in_1), .b(7'b0001000), .eq(comparator_1_eq));  // open: gt, lt
  Comparator #(.width(7)) comparator_2 (.a(in_1), .b(7'b0001010), .eq(comparator_2_eq));  // open: gt, lt
  not not_1 (not_1_out, comparator_2_eq);
  or or_2 (or_2_out, \列计数_carry , comparator_2_eq);
  and and_2 (and_2_out, comparator_2_eq, decoder_1_out0);
  Comparator #(.width(5)) comparator_3 (.a({5{1'b0}}), .b(\列计数_q ), .eq(comparator_3_eq));  // open: gt, lt
  Counter #(.width(5), .max('h1f)) \u_列计数  (
    .load(comparator_1_eq), .count(not_1_out), .Q(\列计数_q ), .carry(\列计数_carry ), .clk(decoder_1_out0),
    .clr(or_3_out));  // open: D
  or or_3 (or_3_out, \复位 , and_2_out);
  Counter #(.width(4), .max('hf), .ongoal("stay")) counter_2 (
    .count(or_2_out), .Q(counter_2_q), .carry(\满中断 ), .clk(decoder_1_out0), .clr(\复位 ));  // open: load, D
  RAM #(.addrWidth(9), .dataWidth(7), .bus("separate")) ram_1 (
    .addr({counter_2_q, \列计数_q }), .din(in_1), .data(\输出 ), .str(\保存 ), .clk(decoder_1_out1), .ld(and_3_out),
    .clr(\复位 ));  // open: sel
  and and_3 (and_3_out, ~\复位 , \加载 );  // AND_Gate

  // Notes on the sheet:
  //   行计数
endmodule
