// Logisim project 20170924_RAM.circ as structural Verilog: 1 circuit, main circuit 内存
module \内存  (
  input  [15:0] \地址 ,
  input  [15:0] \写入数据 ,
  input  \复位_写使能 ,
  input  \写 ,
  input  \大小端选择_0为小端 ,
  output [15:0] \输出 
);

  wire not_1_out, not_2_out;
  wire [7:0] controlled_buffer_1_out, controlled_buffer_2_out, multiplexer_2_out, multiplexer_3_out,
       multiplexer_4_out, multiplexer_5_out, multiplexer_6_out, multiplexer_7_out;
  wire [14:0] adder_1_out, multiplexer_1_out;

  Pull_Resistor pull_resistor_1 (.node(\大小端选择_0为小端 ));
  Adder #(.width(15)) adder_1 (.a(\地址 [15:1]), .b(15'h1), .out(adder_1_out));  // open: cin, cout
  Multiplexer #(.width(15), .enable("false")) multiplexer_1 (
    .in0(\地址 [15:1]), .in1(adder_1_out), .out(multiplexer_1_out), .sel(\地址 [0]));
  Multiplexer #(.width(8), .enable("false")) multiplexer_2 (
    .in0(\写入数据 [7:0]), .in1(\写入数据 [15:8]), .out(multiplexer_2_out), .sel(\大小端选择_0为小端 ));
  Multiplexer #(.width(8), .enable("false")) multiplexer_3 (
    .in0(\写入数据 [15:8]), .in1(\写入数据 [7:0]), .out(multiplexer_3_out), .sel(\大小端选择_0为小端 ));
  Multiplexer #(.width(8), .enable("false")) multiplexer_4 (
    .in0(multiplexer_2_out), .in1(multiplexer_3_out), .out(multiplexer_4_out), .sel(\地址 [0]));
  Multiplexer #(.width(8), .enable("false")) multiplexer_5 (
    .in0(multiplexer_3_out), .in1(multiplexer_2_out), .out(multiplexer_5_out), .sel(\地址 [0]));
  not not_1 (not_1_out, \复位_写使能 );
  not not_2 (not_2_out, \写 );
  assign controlled_buffer_1_out = \写  ? multiplexer_4_out : 8'bz;  // Controlled_Buffer controlled_buffer_1
  RAM #(.addrWidth(15), .bus("asynch")) ram_1 (
    .addr(multiplexer_1_out), .data(controlled_buffer_1_out), .sel(not_1_out), .ld(not_2_out), .clr(\复位_写使能 ));
  assign controlled_buffer_2_out = \写  ? multiplexer_5_out : 8'bz;  // Controlled_Buffer controlled_buffer_2
  RAM #(.addrWidth(15), .bus("asynch")) ram_2 (
    .addr(\地址 [15:1]), .data(controlled_buffer_2_out), .sel(not_1_out), .ld(not_2_out), .clr(\复位_写使能 ));
  Multiplexer #(.width(8), .enable("false")) multiplexer_6 (
    .in0(controlled_buffer_1_out), .in1(controlled_buffer_2_out), .out(multiplexer_6_out), .sel(\地址 [0]));
  Multiplexer #(.width(8), .enable("false")) multiplexer_7 (
    .in0(controlled_buffer_2_out), .in1(controlled_buffer_1_out), .out(multiplexer_7_out), .sel(\地址 [0]));
  Multiplexer #(.width(8), .enable("false")) multiplexer_8 (
    .in0(multiplexer_6_out), .in1(multiplexer_7_out), .out(\输出 [7:0]), .sel(\大小端选择_0为小端 ));
  Multiplexer #(.width(8), .enable("false")) multiplexer_9 (
    .in0(multiplexer_7_out), .in1(multiplexer_6_out), .out(\输出 [15:8]), .sel(\大小端选择_0为小端 ));

  // Notes on the sheet:
  //   MEMORY0
  //   MEMORY1
  //   LOW
  //   HIGH
endmodule
