// Logisim project 20171002_CPU.circ as structural Verilog: 11 circuits, main circuit CPU
module CPU (
  input  \时钟 ,
  input  \复位 ,
  input  [15:0] \来自存贮器 ,
  input  \异常 ,
  input  \异常_2 ,
  input  \异常_3 ,
  input  \异常_4 ,
  output [15:0] \地址 ,
  output [15:0] \写数据 ,
  output \写使能 ,
  output \大小端选择 
);

  wire \alu符号_1_进位输出 , clock_1_out, \堆栈_1_时钟选择 , \堆栈_1_栈溢出 , \控制器_1_中断及恢复 , \控制器_1_大小端选择_1为大端 ,
       \控制器_1_栈生长方向 , \数据传送指令控制中心_1_写使能1 , \数据传送指令控制中心_1_写使能2 , \节拍器_1__0 , \节拍器_1__1 , \节拍器_1__2 ,
       \节拍器_1__3 , \解码器_1_inst_eret , \解码器_1_inst_hlt , \解码器_1_inst_mov , \解码器_1_inst_movi ,
       \解码器_1_inst_movui , \解码器_1_inst_nop , \解码器_1_inst_trap , \解码器_1_inst_xchg , \解码器_1_v类指令 ,
       \解码器_1_与ar相关的跳转 , \解码器_1_其他跳转 , \解码器_1_地址未对齐异常使能 , \解码器_1_控制寄存器传输指令 , \解码器_1_直接跳转 , \解码器_1_移位类指令 ,
       \解码器_1_符号比较 , \解码器_1_符号比较_2 , \解码器_1_装载存储类指令 , \解码器_1_运算类指令 , \解码器_1_逻辑类指令 , \解码器_1_逻辑类指令2 ,
       \访存控制中心_1_地址未对齐异常 ;
  wire [1:0] \解码器_1_符号 ;
  wire [2:0] \数据传送指令控制中心_1_写地址2 , \解码器_1_写地址1 , \解码器_1_读地址1__访存时数据 , \解码器_1_读地址2_访存时地址_跳转时地址 ;
  wire [3:0] \alu符号_1_状态输出 , \算数逻辑单元_1_out_16 , \解码器_1_移位位数 ;
  wire [4:0] \解码器_1_控制寄存器选择 ;
  wire [5:0] \解码器_1_功能码 ;
  wire [15:0] \堆栈_1_out_15 , \堆栈_1_sp , \指令寄存器_q , \控制器_1_new_pc , \控制器_1_输出 , \数据传送指令控制中心_1_写入数据1 ,
       \数据传送指令控制中心_1_写入数据2 , \程序计数器_1_out_18 , \算数逻辑单元_1_结果 , \解码器_1_立即数 , \访存控制中心_1_读数据_cpu ,
       \通用寄存器组_1_out_11 , \通用寄存器组_1_out_12 , \通用寄存器组_1_out_13 , \通用寄存器组_1_out_14 , \通用寄存器组_1_out_15 ,
       \通用寄存器组_1_out_16 , \通用寄存器组_1_out_17 ;

  Clock clock_1 (.out(clock_1_out));
  \节拍器  \u_节拍器_1  (.\时钟 (clock_1_out), ._0(\节拍器_1__0 ), ._1(\节拍器_1__1 ), ._2(\节拍器_1__2 ), ._3(\节拍器_1__3 ), .\复位 (\复位 ));
  Register #(.width(16)) \u_指令寄存器  (.D(\访存控制中心_1_读数据_cpu ), .Q(\指令寄存器_q ), .clk(\节拍器_1__1 ), .clr(\复位 ));  // open: en
  \解码器  \u_解码器_1  (
    .\指令 (\指令寄存器_q ), .Inst_NOP(\解码器_1_inst_nop ), .Inst_MOVI(\解码器_1_inst_movi ),
    .Inst_MOVUI(\解码器_1_inst_movui ), .Inst_MOV(\解码器_1_inst_mov ), .Inst_XCHG(\解码器_1_inst_xchg ),
    .\运算类指令 (\解码器_1_运算类指令 ), .\逻辑类指令 (\解码器_1_逻辑类指令 ), .\移位类指令 (\解码器_1_移位类指令 ), .\逻辑类指令2 (\解码器_1_逻辑类指令2 ),
    .\装载存储类指令 (\解码器_1_装载存储类指令 ), .\V类指令 (\解码器_1_v类指令 ), .\控制寄存器传输指令 (\解码器_1_控制寄存器传输指令 ),
    .\直接跳转 (\解码器_1_直接跳转 ), .Inst_HLT(\解码器_1_inst_hlt ), .\立即数 (\解码器_1_立即数 ), .\功能码 (\解码器_1_功能码 ),
    .\写地址1 (\解码器_1_写地址1 ), .\读地址1__访存时数据 (\解码器_1_读地址1__访存时数据 ),
    .\读地址2_访存时地址_跳转时地址 (\解码器_1_读地址2_访存时地址_跳转时地址 ), .\移位位数 (\解码器_1_移位位数 ), .\其他跳转 (\解码器_1_其他跳转 ),
    .\符号比较 (\解码器_1_符号比较 ), .\与AR相关的跳转 (\解码器_1_与ar相关的跳转 ), .\符号 (\解码器_1_符号 ), .\符号比较_2 (\解码器_1_符号比较_2 ),
    .\控制寄存器选择 (\解码器_1_控制寄存器选择 ), .\地址未对齐异常使能 (\解码器_1_地址未对齐异常使能 ), .Inst_ERET(\解码器_1_inst_eret ),
    .Inst_TRAP(\解码器_1_inst_trap ));
  \数据传送指令控制中心  \u_数据传送指令控制中心_1  (
    .\写入数据1 (\数据传送指令控制中心_1_写入数据1 ), .\写使能1 (\数据传送指令控制中心_1_写使能1 ), .\写使能2 (\数据传送指令控制中心_1_写使能2 ),
    .\写地址2 (\数据传送指令控制中心_1_写地址2 ), .\写入数据2 (\数据传送指令控制中心_1_写入数据2 ), .Inst_MOVI(\解码器_1_inst_movi ),
    .Inst_MOVUI(\解码器_1_inst_movui ), .Inst_MOV(\解码器_1_inst_mov ), .Inst_XCHG(\解码器_1_inst_xchg ),
    .\运算类指令 (\解码器_1_运算类指令 ), .\逻辑类指令 (\解码器_1_逻辑类指令 ), .\移位类指令 (\解码器_1_移位类指令 ), .\逻辑类指令2 (\解码器_1_逻辑类指令2 ),
    .\装载存储类指令 (\解码器_1_装载存储类指令 ), .\控制寄存器传输指令 (\解码器_1_控制寄存器传输指令 ), .\ALU运算结果 (\算数逻辑单元_1_结果 ),
    .D0(\通用寄存器组_1_out_11 ), .D1(\通用寄存器组_1_out_12 ), .D2(\通用寄存器组_1_out_13 ), .D3(\通用寄存器组_1_out_14 ),
    .A0(\通用寄存器组_1_out_15 ), .A1(\通用寄存器组_1_out_16 ), .SP(\堆栈_1_sp ), .CBR(\通用寄存器组_1_out_17 ),
    .\来自存储器 (\访存控制中心_1_读数据_cpu ), .\立即数 (\解码器_1_立即数 ), .\来自控制寄存器 (\控制器_1_输出 ),
    .\寄存器读地址1 (\解码器_1_读地址1__访存时数据 ), .\寄存器读地址2 (\解码器_1_读地址2_访存时地址_跳转时地址 ), .\异常被触发 (\控制器_1_中断及恢复 ),
    .\功能码 (\解码器_1_功能码 ), .\来自堆栈 (\堆栈_1_out_15 ), .PC(\程序计数器_1_out_18 ), .\与AR有关的跳转指令 (\解码器_1_与ar相关的跳转 ));
  \通用寄存器组  \u_通用寄存器组_1  (
    .\写入使能1 (\数据传送指令控制中心_1_写使能1 ), .\写入地址1 (\解码器_1_写地址1 ), .\写入数据1 (\数据传送指令控制中心_1_写入数据1 ),
    .\写入使能2 (\数据传送指令控制中心_1_写使能2 ), .\写入数据2 (\数据传送指令控制中心_1_写入数据2 ), .\写入地址2 (\数据传送指令控制中心_1_写地址2 ),
    .clk_2(\节拍器_1__2 ), .\复位 (\复位 ), .out_11(\通用寄存器组_1_out_11 ), .out_12(\通用寄存器组_1_out_12 ),
    .out_13(\通用寄存器组_1_out_13 ), .out_14(\通用寄存器组_1_out_14 ), .out_15(\通用寄存器组_1_out_15 ),
    .out_16(\通用寄存器组_1_out_16 ), .out_17(\通用寄存器组_1_out_17 ), .clk_3(\节拍器_1__3 ), .\时钟选择_默认3 (\堆栈_1_时钟选择 ));
  \程序计数器  \u_程序计数器_1  (
    .Inst_HLT(\解码器_1_inst_hlt ), .\功能码 (\解码器_1_功能码 ), .clk_0(\节拍器_1__0 ), .AR0(\通用寄存器组_1_out_15 ),
    .AR1(\通用寄存器组_1_out_16 ), .\立即数 (\解码器_1_立即数 ), .\复位 (\复位 ), .out_18(\程序计数器_1_out_18 ),
    .\ALU符号 (\alu符号_1_状态输出 ), .\异常入口地址 (\控制器_1_new_pc ), .\直接跳转 (\解码器_1_直接跳转 ), .\其他跳转 (\解码器_1_其他跳转 ),
    .\符号比较 (\解码器_1_符号比较 ), .\与AR相关的跳转 (\解码器_1_与ar相关的跳转 ), .\读地址1 (\解码器_1_读地址1__访存时数据 ), .\符号选择 (\解码器_1_符号 ),
    .\符号比较_2 (\解码器_1_符号比较_2 ), .\中断及恢复 (\控制器_1_中断及恢复 ));
  // Probe on \通用寄存器组_1_out_11 
  // Probe on \通用寄存器组_1_out_12 
  // Probe on \通用寄存器组_1_out_13 
  // Probe on \通用寄存器组_1_out_14 
  // Probe on \通用寄存器组_1_out_15 
  // Probe on \通用寄存器组_1_out_16 
  // Probe on \通用寄存器组_1_out_17 
  \访存控制中心  \u_访存控制中心_1  (
    .\地址_MEM (\地址 ), .\写数据_MEM (\写数据 ), .\读数据_CPU (\访存控制中心_1_读数据_cpu ), .D0(\通用寄存器组_1_out_11 ),
    .D1(\通用寄存器组_1_out_12 ), .D2(\通用寄存器组_1_out_13 ), .D3(\通用寄存器组_1_out_14 ), .A0(\通用寄存器组_1_out_15 ),
    .A1(\通用寄存器组_1_out_16 ), .\操作数1 (\解码器_1_读地址1__访存时数据 ), .\操作数2 (\解码器_1_读地址2_访存时地址_跳转时地址 ),
    .PC(\程序计数器_1_out_18 ), .\写使能 (\写使能 ), .\时钟_2 (\节拍器_1__3 ), .\时钟_3 (\复位 ), .\装载存储指令 (\解码器_1_装载存储类指令 ),
    .\功能码 (\解码器_1_功能码 ), .\读数据_MEM (\来自存贮器 ), .Immed(\解码器_1_立即数 ), .\地址未对齐异常使能 (\解码器_1_地址未对齐异常使能 ),
    .\地址未对齐异常 (\访存控制中心_1_地址未对齐异常 ), .\大小端 (\控制器_1_大小端选择_1为大端 ), .\大小端_2 (\大小端选择 ));
  // Probe on \程序计数器_1_out_18 
  \算数逻辑单元  \u_算数逻辑单元_1  (
    .\进位 (\alu符号_1_进位输出 ), .D0(\通用寄存器组_1_out_11 ), .D1(\通用寄存器组_1_out_12 ), .D2(\通用寄存器组_1_out_13 ),
    .D3(\通用寄存器组_1_out_14 ), .\立即数 (\解码器_1_立即数 ), .\寄存器读地址1 (\解码器_1_读地址1__访存时数据 ),
    .\寄存器读地址2 (\解码器_1_读地址2_访存时地址_跳转时地址 ), .\运算类指令 (\解码器_1_运算类指令 ), .\逻辑类指令 (\解码器_1_逻辑类指令 ),
    .\移位类指令 (\解码器_1_移位类指令 ), .\逻辑类指令2 (\解码器_1_逻辑类指令2 ), .\功能码 (\解码器_1_功能码 ), .\移位位数 (\解码器_1_移位位数 ),
    .\结果 (\算数逻辑单元_1_结果 ), .out_16(\算数逻辑单元_1_out_16 ));
  \堆栈  \u_堆栈_1  (
    .\V型指令 (\解码器_1_v类指令 ), .\功能码 (\解码器_1_功能码 ), .out_15(\堆栈_1_out_15 ), .D0(\通用寄存器组_1_out_11 ),
    .D1(\通用寄存器组_1_out_12 ), .D2(\通用寄存器组_1_out_13 ), .D3(\通用寄存器组_1_out_14 ), .A0(\通用寄存器组_1_out_15 ),
    .A1(\通用寄存器组_1_out_16 ), .CBR(\通用寄存器组_1_out_17 ), .\寄存器地址 (\解码器_1_读地址1__访存时数据 ), .SP(\堆栈_1_sp ),
    .\时钟选择 (\堆栈_1_时钟选择 ), .\复位 (\复位 ), .\栈溢出 (\堆栈_1_栈溢出 ), .\生长方向_1为下 (\控制器_1_栈生长方向 ), .clk_2(\节拍器_1__3 ),
    .clk_3(\节拍器_1__2 ));
  // Probe on \堆栈_1_sp 
  \ALU符号  \alu符号_1  (
    .\符号_ZVSC (\算数逻辑单元_1_out_16 ), .\运算类指令 (\解码器_1_运算类指令 ), .\逻辑类指令 (\解码器_1_逻辑类指令 ), .\移位类指令 (\解码器_1_移位类指令 ),
    .\逻辑类指令2 (\解码器_1_逻辑类指令2 ), .\时钟_2 (\节拍器_1__2 ), .\复位 (\复位 ), .\状态输出 (\alu符号_1_状态输出 ),
    .\进位输出 (\alu符号_1_进位输出 ));
  \控制器  \u_控制器_1  (
    .\数据 (\通用寄存器组_1_out_17 ), .\地址 (\解码器_1_控制寄存器选择 ), .PC(\程序计数器_1_out_18 ), .\中断_0 (\异常 ), .\中断_1 (\异常_2 ),
    .\中断_2 (\异常_3 ), .\中断_3 (\异常_4 ), .\符号 (\alu符号_1_状态输出 ), .\符号选择 (\解码器_1_符号 ), .\运算类指令 (\解码器_1_运算类指令 ),
    .\栈溢出 (\堆栈_1_栈溢出 ), .\地址未对齐 (\访存控制中心_1_地址未对齐异常 ), .Inst_TRAP(\解码器_1_inst_trap ),
    .\控制寄存器传输指令 (\解码器_1_控制寄存器传输指令 ), .Inst_ERET(\解码器_1_inst_eret ), .clk_3(\节拍器_1__3 ), .rst(\复位 ),
    .\中断及恢复 (\控制器_1_中断及恢复 ), .\大小端选择_1为大端 (\控制器_1_大小端选择_1为大端 ), .\栈生长方向 (\控制器_1_栈生长方向 ), .\功能码 (\解码器_1_功能码 ),
    .\输出 (\控制器_1_输出 ), .new_PC(\控制器_1_new_pc ), .clk_2(\节拍器_1__2 ), .clk_0(\节拍器_1__0 ));

  // Other names for the same wires on the sheet: Addr[15:0] = \地址 ; DRead[15:0] = \来自存贮器 ; DWrite[15:0] = \写数据 ;
  //   EndianSelect = \大小端选择 ; int_0 = \异常 ; int_1 = \异常_2 ; int_2 = \异常_3 ; int_3 = \异常_4 ; WriteEnable = \写使能 
endmodule

module \节拍器  (
  input  \时钟 ,
  input  \复位 ,
  output _0,
  output _1,
  output _2,
  output _3
);

  wire counter_1_q, counter_2_q, not_1_out;

  not not_1 (not_1_out, \时钟 );
  Counter #(.width(1), .max('h1)) counter_1 (.Q(counter_1_q), .clk(\时钟 ), .clr(\复位 ));  // open: load, D, count, carry
  Counter #(.width(1), .max('h1)) counter_2 (
    .Q(counter_2_q), .clk(not_1_out), .clr(\复位 ));  // open: load, D, count, carry
  and and_1 (_0, ~counter_1_q, ~counter_2_q);  // AND_Gate
  and and_2 (_1, counter_1_q, ~counter_2_q);  // AND_Gate
  and and_3 (_2, counter_1_q, counter_2_q);
  and and_4 (_3, ~counter_1_q, counter_2_q);  // AND_Gate
endmodule

module \算数逻辑单元  (
  input  \进位 ,
  input  [15:0] D0,
  input  [15:0] D1,
  input  [15:0] D2,
  input  [15:0] D3,
  input  [15:0] \立即数 ,
  input  [2:0] \寄存器读地址1 ,
  input  [2:0] \寄存器读地址2 ,
  input  \运算类指令 ,
  input  \逻辑类指令 ,
  input  \移位类指令 ,
  input  \逻辑类指令2 ,
  input  [5:0] \功能码 ,
  input  [3:0] \移位位数 ,
  output [15:0] \结果 ,
  output [3:0] out_16
);

  wire adder_1_cout, adder_2_cout, and_3_out, comparator_1_eq, comparator_1_gt, comparator_2_eq,
       comparator_2_gt, multiplexer_9_out, multiplexer_10_out, nor_2_out, subtractor_1_bout,
       subtractor_2_bout, xor_2_out, xor_3_out;
  wire [14:0] adder_1_out, subtractor_1_out;
  wire [15:0] and_1_out, and_2_out, divider_1_out, divider_1_rem, multiplexer_1_out, multiplexer_2_out,
       multiplexer_3_out, multiplexer_4_out, multiplexer_5_out, multiplexer_6_out, multiplier_1_cout,
       multiplier_1_out, nand_1_out, nor_1_out, not_1_out, not_2_out, or_1_out, or_2_out,
       pull_resistor_1_node, pull_resistor_2_node, pull_resistor_3_node, pull_resistor_4_node,
       pull_resistor_5_node, shifter_1_out, shifter_2_out, shifter_3_out, shifter_4_out, shifter_5_out,
       shifter_6_out, shifter_7_out, xor_1_out;
  wire [15:15] adder_2_out, subtractor_2_out;

  Multiplexer #(.select(2), .width(16), .enable("false")) multiplexer_1 (
    .in0(D0), .in1(D1), .in2(D2), .in3(D3), .out(multiplexer_1_out), .sel(\寄存器读地址1 [1:0]));
  Multiplexer #(.select(2), .width(16), .enable("false")) multiplexer_2 (
    .in0(D0), .in1(D1), .in2(D2), .in3(D3), .out(multiplexer_2_out), .sel(\寄存器读地址2 [1:0]));
  Comparator #(.width(16)) comparator_1 (
    .a(multiplexer_1_out), .b(multiplexer_2_out), .gt(comparator_1_gt), .eq(comparator_1_eq));  // open: lt
  Comparator #(.width(16), .mode("unsigned")) comparator_2 (
    .a(multiplexer_1_out), .b(multiplexer_2_out), .gt(comparator_2_gt), .eq(comparator_2_eq));  // open: lt
  Adder #(.width(15)) adder_1 (
    .a(multiplexer_1_out[14:0]), .b(multiplexer_2_out[14:0]), .out(adder_1_out), .cin(\进位 ),
    .cout(adder_1_cout));
  Adder #(.width(1)) adder_2 (
    .a(multiplexer_1_out[15]), .b(multiplexer_2_out[15]), .out(adder_2_out[15]), .cin(adder_1_cout),
    .cout(adder_2_cout));
  Subtractor #(.width(15)) subtractor_1 (
    .a(multiplexer_1_out[14:0]), .b(multiplexer_2_out[14:0]), .out(subtractor_1_out), .bin(\进位 ),
    .bout(subtractor_1_bout));
  Subtractor #(.width(1)) subtractor_2 (
    .a(multiplexer_1_out[15]), .b(multiplexer_2_out[15]), .out(subtractor_2_out[15]),
    .bin(subtractor_1_bout), .bout(subtractor_2_bout));
  Pull_Resistor pull_resistor_1 (.node(pull_resistor_1_node));
  Multiplier #(.width(16)) multiplier_1 (
    .a(multiplexer_1_out), .b(multiplexer_2_out), .out(multiplier_1_out), .cin(pull_resistor_1_node),
    .cout(multiplier_1_cout));
  Pull_Resistor pull_resistor_2 (.node(pull_resistor_2_node));
  Divider #(.width(16)) divider_1 (
    .a(multiplexer_1_out), .b(multiplexer_2_out), .out(divider_1_out), .upper(pull_resistor_2_node),
    .rem(divider_1_rem));
  assign and_1_out = multiplexer_1_out & multiplexer_2_out;  // AND_Gate and_1, 16 bits wide
  assign or_1_out = multiplexer_1_out | multiplexer_2_out;  // OR_Gate or_1, 16 bits wide
  assign not_1_out = ~multiplexer_1_out;  // NOT_Gate not_1, 16 bits wide
  assign nor_1_out = ~(multiplexer_1_out | multiplexer_2_out);  // NOR_Gate nor_1, 16 bits wide
  assign nand_1_out = ~(multiplexer_1_out & multiplexer_2_out);  // NAND_Gate nand_1, 16 bits wide
  assign xor_1_out = multiplexer_1_out ^ multiplexer_2_out;  // XOR_Gate xor_1, 16 bits wide
  Shifter #(.width(16)) shifter_1 (.in(multiplexer_1_out), .\dist (\移位位数 ), .out(shifter_1_out));
  Shifter #(.width(16), .shift("lr")) shifter_2 (.in(multiplexer_1_out), .\dist (\移位位数 ), .out(shifter_2_out));
  Shifter #(.width(16), .shift("ar")) shifter_3 (.in(multiplexer_1_out), .\dist (\移位位数 ), .out(shifter_3_out));
  Shifter #(.width(16), .shift("rl")) shifter_4 (.in(multiplexer_1_out), .\dist (\移位位数 ), .out(shifter_4_out));
  Shifter #(.width(16), .shift("rr")) shifter_5 (.in(multiplexer_1_out), .\dist (\移位位数 ), .out(shifter_5_out));
  Shifter #(.width(16)) shifter_6 (.in(multiplexer_1_out), .\dist (\移位位数 ), .out(shifter_6_out));
  Shifter #(.width(16), .shift("lr")) shifter_7 (.in(multiplexer_1_out), .\dist (\移位位数 ), .out(shifter_7_out));
  assign and_2_out = multiplexer_1_out & \立即数 ;  // AND_Gate and_2, 16 bits wide
  assign or_2_out = multiplexer_1_out | \立即数 ;  // OR_Gate or_2, 16 bits wide
  assign not_2_out = ~\立即数 ;  // NOT_Gate not_2, 16 bits wide
  xor xor_2 (xor_2_out, adder_1_cout, adder_2_cout);
  xor xor_3 (xor_3_out, subtractor_1_bout, subtractor_2_bout);
  Pull_Resistor pull_resistor_3 (.node(pull_resistor_3_node));
  Pull_Resistor pull_resistor_4 (.node(pull_resistor_4_node));
  Pull_Resistor pull_resistor_5 (.node(pull_resistor_5_node));
  Multiplexer #(.select(3), .width(16), .enable("false")) multiplexer_3 (
    .in0({adder_2_out[15], adder_1_out}), .in1({subtractor_2_out[15], subtractor_1_out}),
    .in2({adder_2_out[15], adder_1_out}), .in3({subtractor_2_out[15], subtractor_1_out}),
    .in4(multiplier_1_out), .in5(multiplier_1_cout), .in6(divider_1_out), .in7(divider_1_rem),
    .out(multiplexer_3_out), .sel(\功能码 [2:0]));
  Multiplexer #(.select(3), .width(16), .enable("false")) multiplexer_4 (
    .in0(and_1_out), .in1(or_1_out), .in2(not_1_out), .in3(nor_1_out), .in4(nand_1_out), .in5(xor_1_out),
    .in6(pull_resistor_3_node), .in7(pull_resistor_3_node), .out(multiplexer_4_out), .sel(\功能码 [2:0]));
  Multiplexer #(.select(3), .width(16), .enable("false")) multiplexer_5 (
    .in0(shifter_1_out), .in1(shifter_2_out), .in2(shifter_3_out), .in3(shifter_4_out), .in4(shifter_5_out),
    .in5({shifter_6_out[15:1], \进位 }), .in6({\进位 , shifter_7_out[14:0]}), .in7(pull_resistor_4_node),
    .out(multiplexer_5_out), .sel(\功能码 [2:0]));
  Multiplexer #(.select(3), .width(16), .enable("false")) multiplexer_6 (
    .in0(and_2_out), .in1(or_2_out), .in2(not_2_out), .in3(pull_resistor_5_node), .in4(pull_resistor_5_node),
    .in5(pull_resistor_5_node), .in6(pull_resistor_5_node), .in7(pull_resistor_5_node),
    .out(multiplexer_6_out), .sel(\功能码 [2:0]));
  Pull_Resistor pull_resistor_6 (.node(\结果 ));
  assign \结果  = \运算类指令  ? multiplexer_3_out : 16'bz;  // Controlled_Buffer controlled_buffer_1
  assign \结果  = \逻辑类指令  ? multiplexer_4_out : 16'bz;  // Controlled_Buffer controlled_buffer_2
  assign \结果  = \移位类指令  ? multiplexer_5_out : 16'bz;  // Controlled_Buffer controlled_buffer_3
  assign \结果  = \逻辑类指令2  ? multiplexer_6_out : 16'bz;  // Controlled_Buffer controlled_buffer_4
  Multiplexer #(.disabled(0)) multiplexer_7 (
    .in0(adder_2_cout), .in1(subtractor_2_bout), .out(out_16[0]), .sel(\功能码 [0]), .en(and_3_out));
  Multiplexer #(.disabled(0)) multiplexer_8 (
    .in0(xor_2_out), .in1(xor_3_out), .out(out_16[2]), .sel(\功能码 [0]), .en(and_3_out));
  and and_3 (and_3_out, ~\功能码 [2], ~\功能码 [1], \运算类指令 );  // AND_Gate
  Multiplexer #(.select(3), .enable("false")) multiplexer_9 (
    .in0(nor_2_out), .in1(nor_2_out), .in2(nor_2_out), .in3(nor_2_out), .in4(nor_2_out), .in5(nor_2_out),
    .in6(comparator_1_eq), .in7(comparator_2_eq), .out(multiplexer_9_out), .sel(\功能码 [2:0]));
  Multiplexer #(.select(3), .enable("false")) multiplexer_10 (
    .in0(\结果 [15]), .in1(\结果 [15]), .in2(\结果 [15]), .in3(\结果 [15]), .in4(\结果 [15]), .in5(\结果 [15]),
    .in6(comparator_1_gt), .in7(comparator_2_gt), .out(multiplexer_10_out), .sel(\功能码 [2:0]));
  nor nor_2 (nor_2_out, \结果 [0], \结果 [1], \结果 [2], \结果 [3], \结果 [4], \结果 [5], \结果 [6], \结果 [7], \结果 [9], \结果 [10], \结果 [11], \结果 [12], \结果 [13], \结果 [14], \结果 [15], \结果 [8]);
  Multiplexer #(.enable("false")) multiplexer_11 (
    .in0(nor_2_out), .in1(multiplexer_9_out), .out(out_16[3]), .sel(\逻辑类指令 ));
  Multiplexer #(.enable("false")) multiplexer_12 (
    .in0(\结果 [15]), .in1(multiplexer_10_out), .out(out_16[1]), .sel(\逻辑类指令 ));
endmodule

module \ALU符号  (
  input  [3:0] \符号_ZVSC ,
  input  \运算类指令 ,
  input  \逻辑类指令 ,
  input  \移位类指令 ,
  input  \逻辑类指令2 ,
  input  \时钟_2 ,
  input  \复位 ,
  output [3:0] \状态输出 ,
  output \进位输出 
);

  wire or_1_out;

  or or_1 (or_1_out, \运算类指令 , \逻辑类指令 , \移位类指令 , \逻辑类指令2 );
  Register #(.width(1)) \u_进位状态  (.D(\符号_ZVSC [0]), .en(or_1_out), .Q(\状态输出 [0]), .clk(\时钟_2 ), .clr(\复位 ));
  Register #(.width(1)) \u_符号状态  (.D(\符号_ZVSC [1]), .en(or_1_out), .Q(\状态输出 [1]), .clk(\时钟_2 ), .clr(\复位 ));
  Register #(.width(1)) \u_溢出状态  (.D(\符号_ZVSC [2]), .en(or_1_out), .Q(\状态输出 [2]), .clk(\时钟_2 ), .clr(\复位 ));
  Register #(.width(1)) \u_零状态  (.D(\符号_ZVSC [3]), .en(or_1_out), .Q(\状态输出 [3]), .clk(\时钟_2 ), .clr(\复位 ));

  assign \进位输出  = \状态输出 [0];
endmodule

module \通用寄存器组  (
  input  \写入使能1 ,
  input  [2:0] \写入地址1 ,
  input  [15:0] \写入数据1 ,
  input  \写入使能2 ,
  input  [15:0] \写入数据2 ,
  input  [2:0] \写入地址2 ,
  input  clk_3,
  input  clk_2,
  input  \复位 ,
  input  \时钟选择_默认3 ,
  output [15:0] out_11,
  output [15:0] out_12,
  output [15:0] out_13,
  output [15:0] out_14,
  output [15:0] out_15,
  output [15:0] out_16,
  output [15:0] out_17
);

  wire multiplexer_1_out;
  wire [15:0] demultiplexer_1_out0, demultiplexer_1_out1, demultiplexer_1_out2, demultiplexer_1_out3,
       demultiplexer_1_out4, demultiplexer_1_out5, demultiplexer_1_out6, demultiplexer_1_out7;

  Demultiplexer #(.select(3), .width(16), .tristate("true")) demultiplexer_1 (
    .out0(demultiplexer_1_out0), .out1(demultiplexer_1_out1), .out2(demultiplexer_1_out2),
    .out3(demultiplexer_1_out3), .out4(demultiplexer_1_out4), .out5(demultiplexer_1_out5),
    .out6(demultiplexer_1_out6), .out7(demultiplexer_1_out7), .in(\写入数据1 ), .sel(\写入地址1 ), .en(\写入使能1 ));
  Demultiplexer #(.select(3), .width(16), .tristate("true")) demultiplexer_2 (
    .out0(demultiplexer_1_out0), .out1(demultiplexer_1_out1), .out2(demultiplexer_1_out2),
    .out3(demultiplexer_1_out3), .out4(demultiplexer_1_out4), .out5(demultiplexer_1_out5),
    .out6(demultiplexer_1_out6), .out7(demultiplexer_1_out7), .in(\写入数据2 ), .sel(\写入地址2 ), .en(\写入使能2 ));
  Multiplexer #(.enable("false")) multiplexer_1 (.in0(clk_3), .in1(clk_2), .out(multiplexer_1_out), .sel(\时钟选择_默认3 ));
  Register #(.width(16)) D0 (.D(demultiplexer_1_out0), .Q(out_11), .clk(multiplexer_1_out), .clr(\复位 ));  // open: en
  Register #(.width(16)) D1 (.D(demultiplexer_1_out1), .Q(out_12), .clk(multiplexer_1_out), .clr(\复位 ));  // open: en
  Register #(.width(16)) D2 (.D(demultiplexer_1_out2), .Q(out_13), .clk(multiplexer_1_out), .clr(\复位 ));  // open: en
  Register #(.width(16)) D3 (.D(demultiplexer_1_out3), .Q(out_14), .clk(multiplexer_1_out), .clr(\复位 ));  // open: en
  Register #(.width(16)) A0 (.D(demultiplexer_1_out4), .Q(out_15), .clk(multiplexer_1_out), .clr(\复位 ));  // open: en
  Register #(.width(16)) A1 (.D(demultiplexer_1_out5), .Q(out_16), .clk(multiplexer_1_out), .clr(\复位 ));  // open: en
  Register #(.width(16)) CBR (.D(demultiplexer_1_out7), .Q(out_17), .clk(multiplexer_1_out), .clr(\复位 ));  // open: en
endmodule

module \解码器  (
  input  [15:0] \指令 ,
  output Inst_NOP,
  output Inst_MOVI,
  output Inst_MOVUI,
  output Inst_MOV,
  output Inst_XCHG,
  output \运算类指令 ,
  output \逻辑类指令 ,
  output \移位类指令 ,
  output \逻辑类指令2 ,
  output \装载存储类指令 ,
  output \V类指令 ,
  output \控制寄存器传输指令 ,
  output \直接跳转 ,
  output \其他跳转 ,
  output \符号比较 ,
  output \与AR相关的跳转 ,
  output Inst_TRAP,
  output Inst_ERET,
  output Inst_HLT,
  output [15:0] \立即数 ,
  output [5:0] \功能码 ,
  output [2:0] \读地址1__访存时数据 ,
  output [2:0] \读地址2_访存时地址_跳转时地址 ,
  output [2:0] \写地址1 ,
  output [3:0] \移位位数 ,
  output [1:0] \符号 ,
  output \符号比较_2 ,
  output [4:0] \控制寄存器选择 ,
  output \地址未对齐异常使能 
);

  wire I, III_I, IV_I, or_1_out, or_2_out, or_3_out, or_4_out, or_7_out, or_8_out;
  wire [2:0] bit_extender_12_out, bit_extender_13_out, bit_extender_14_out, bit_extender_15_out,
       bit_extender_16_out, bit_extender_17_out;
  wire [5:0] bit_extender_5_out, bit_extender_6_out, bit_extender_7_out, bit_extender_8_out,
       bit_extender_9_out, bit_extender_10_out, bit_extender_11_out;
  wire [15:0] bit_extender_1_out, bit_extender_2_out, bit_extender_3_out, bit_extender_4_out;

  Decoder #(.select(5), .enable("false")) decoder_1 (
    .out0(Inst_NOP), .out4(Inst_MOVI), .out5(Inst_MOVUI), .out6(Inst_MOV), .out7(Inst_XCHG), .out8(\运算类指令 ),
    .out9(\逻辑类指令 ), .out10(\移位类指令 ), .out11(\逻辑类指令2 ), .out12(\装载存储类指令 ), .out13(\V类指令 ),
    .out14(\控制寄存器传输指令 ), .out15(\直接跳转 ), .out16(\其他跳转 ), .out17(\符号比较 ), .out18(\与AR相关的跳转 ),
    .out19(Inst_TRAP), .out20(Inst_ERET), .out31(Inst_HLT), .sel(\指令 [15:11]));  // open: out1, out2, out3, out21, out22, out23, out24, out25, out26, out27, out28, out29, out30
  assign bit_extender_1_out = {{10{\指令 [10]}}, {6{\指令 [10]}}};  // Bit_Extender bit_extender_1
  assign bit_extender_2_out = {{8{1'b0}}, {8{\指令 [10]}}};  // Bit_Extender bit_extender_2
  assign bit_extender_3_out = {{8{\指令 [10]}}, {8{\指令 [10]}}};  // Bit_Extender bit_extender_3
  assign bit_extender_4_out = {{5{\指令 [10]}}, {11{\指令 [10]}}};  // Bit_Extender bit_extender_4
  assign \立即数  = or_1_out ? bit_extender_1_out : 16'bz;  // Controlled_Buffer controlled_buffer_1
  assign \立即数  = III_I ? bit_extender_2_out : 16'bz;  // Controlled_Buffer controlled_buffer_2
  assign \立即数  = \其他跳转  ? bit_extender_3_out : 16'bz;  // Controlled_Buffer controlled_buffer_3
  Pull_Resistor pull_resistor_1 (.node(\立即数 ));
  assign \立即数  = \直接跳转  ? bit_extender_4_out : 16'bz;  // Controlled_Buffer controlled_buffer_4
  or or_1 (or_1_out, \符号比较 , \装载存储类指令 , \逻辑类指令2 , \与AR相关的跳转 );
  assign bit_extender_5_out = {{5{1'b0}}, \指令 [10]};  // Bit_Extender bit_extender_5
  Pull_Resistor pull_resistor_2 (.node(\功能码 ));
  assign \功能码  = \装载存储类指令  ? bit_extender_5_out : 6'bz;  // Controlled_Buffer controlled_buffer_5
  assign bit_extender_6_out = {{4{1'b0}}, {2{\指令 [10]}}};  // Bit_Extender bit_extender_6
  assign \功能码  = \逻辑类指令2  ? bit_extender_6_out : 6'bz;  // Controlled_Buffer controlled_buffer_6
  assign \功能码  = or_7_out ? bit_extender_7_out : 6'bz;  // Controlled_Buffer controlled_buffer_7
  assign bit_extender_7_out = {{3{1'b0}}, {3{\指令 [10]}}};  // Bit_Extender bit_extender_7
  assign bit_extender_8_out = {{1{1'b0}}, {5{\指令 [10]}}};  // Bit_Extender bit_extender_8
  assign \功能码  = or_8_out ? bit_extender_8_out : 6'bz;  // Controlled_Buffer controlled_buffer_8
  assign \功能码  = \符号比较  ? bit_extender_9_out : 6'bz;  // Controlled_Buffer controlled_buffer_9
  assign bit_extender_9_out = {{3{1'b0}}, {3{\指令 [10]}}};  // Bit_Extender bit_extender_9
  assign bit_extender_10_out = {{3{1'b0}}, {3{\指令 [10]}}};  // Bit_Extender bit_extender_10
  assign \功能码  = \其他跳转  ? bit_extender_10_out : 6'bz;  // Controlled_Buffer controlled_buffer_10
  assign \功能码  = \与AR相关的跳转  ? bit_extender_11_out : 6'bz;  // Controlled_Buffer controlled_buffer_11
  assign bit_extender_11_out = {{3{1'b0}}, {3{\指令 [10]}}};  // Bit_Extender bit_extender_11
  assign \读地址2_访存时地址_跳转时地址  = \装载存储类指令  ? {2'b01, \指令 [10]} : 3'bz;  // Controlled_Buffer controlled_buffer_12
  assign bit_extender_12_out = {{1{1'b0}}, {2{\指令 [10]}}};  // Bit_Extender bit_extender_12
  or or_2 (or_2_out, \逻辑类指令 , \装载存储类指令 , \移位类指令 , \运算类指令 );
  assign bit_extender_13_out = {{2{1'b0}}, \指令 [10]};  // Bit_Extender bit_extender_13
  assign bit_extender_14_out = {{1{1'b0}}, {2{\指令 [10]}}};  // Bit_Extender bit_extender_14
  assign bit_extender_15_out = {{2{1'b0}}, \指令 [10]};  // Bit_Extender bit_extender_15
  or or_3 (or_3_out, \逻辑类指令 , \运算类指令 );
  Pull_Resistor pull_resistor_3 (.node(\读地址1__访存时数据 ));
  assign \读地址1__访存时数据  = IV_I ? {3{\指令 [10]}} : 3'bz;  // Controlled_Buffer controlled_buffer_13
  assign \读地址1__访存时数据  = or_2_out ? bit_extender_12_out : 3'bz;  // Controlled_Buffer controlled_buffer_14
  assign \读地址1__访存时数据  = \与AR相关的跳转  ? bit_extender_13_out : 3'bz;  // Controlled_Buffer controlled_buffer_15
  assign \读地址1__访存时数据  = \V类指令  ? {3{\指令 [10]}} : 3'bz;  // Controlled_Buffer controlled_buffer_16
  assign \读地址1__访存时数据  = \控制寄存器传输指令  ? 3'b111 : 3'bz;  // Controlled_Buffer controlled_buffer_17
  Pull_Resistor pull_resistor_4 (.node(\读地址2_访存时地址_跳转时地址 ));
  assign \读地址2_访存时地址_跳转时地址  = IV_I ? {3{\指令 [10]}} : 3'bz;  // Controlled_Buffer controlled_buffer_18
  assign \读地址2_访存时地址_跳转时地址  = or_4_out ? bit_extender_14_out : 3'bz;  // Controlled_Buffer controlled_buffer_19
  or or_4 (or_4_out, \运算类指令 , \逻辑类指令 , \移位类指令 );
  assign \读地址2_访存时地址_跳转时地址  = \与AR相关的跳转  ? bit_extender_15_out : 3'bz;  // Controlled_Buffer controlled_buffer_20
  assign \写地址1  = IV_I ? {3{\指令 [10]}} : 3'bz;  // Controlled_Buffer controlled_buffer_21
  assign \写地址1  = III_I ? {3{\指令 [10]}} : 3'bz;  // Controlled_Buffer controlled_buffer_22
  assign bit_extender_16_out = {{1{1'b0}}, {2{\指令 [10]}}};  // Bit_Extender bit_extender_16
  assign \写地址1  = or_3_out ? bit_extender_16_out : 3'bz;  // Controlled_Buffer controlled_buffer_23
  assign \写地址1  = \装载存储类指令  ? {1'b1, {2{\指令 [10]}}} : 3'bz;  // Controlled_Buffer controlled_buffer_24
  assign \写地址1  = \移位类指令  ? bit_extender_17_out : 3'bz;  // Controlled_Buffer controlled_buffer_25
  assign bit_extender_17_out = {{1{1'b0}}, {2{\指令 [10]}}};  // Bit_Extender bit_extender_17
  assign \写地址1  = \与AR相关的跳转  ? {2'b10, \指令 [10]} : 3'bz;  // Controlled_Buffer controlled_buffer_26
  assign \写地址1  = \控制寄存器传输指令  ? 3'b111 : 3'bz;  // Controlled_Buffer controlled_buffer_27
  assign \控制寄存器选择  = \控制寄存器传输指令  ? {5{\指令 [10]}} : 5'bz;  // Controlled_Buffer controlled_buffer_28
  Pull_Resistor pull_resistor_5 (.node(\控制寄存器选择 ));
  Pull_Resistor pull_resistor_6 (.node(\地址未对齐异常使能 ));
  assign \地址未对齐异常使能  = \装载存储类指令  ? \指令 [10] : 1'bz;  // Controlled_Buffer controlled_buffer_29
  or or_5 (III_I, Inst_MOVUI, Inst_MOVI);
  or or_6 (IV_I, Inst_XCHG, Inst_MOV);
  or or_7 (or_7_out, \移位类指令 , \运算类指令 , \V类指令 );
  or or_8 (or_8_out, \逻辑类指令 , \控制寄存器传输指令 , IV_I);
  Pull_Resistor pull_resistor_7 (.node(\写地址1 ));
  assign \移位位数  = \移位类指令  ? {4{\指令 [10]}} : 4'bz;  // Controlled_Buffer controlled_buffer_30
  Pull_Resistor pull_resistor_8 (.node(\移位位数 ));
  Pull_Resistor pull_resistor_9 (.node(\符号 ));
  assign \符号  = \运算类指令  ? {2{\指令 [10]}} : 2'bz;  // Controlled_Buffer controlled_buffer_31
  assign \符号  = \符号比较  ? {2{\指令 [10]}} : 2'bz;  // Controlled_Buffer controlled_buffer_32
  and and_1 (\符号比较_2 , \指令 [10], \符号比较 );
  or or_9 (I, Inst_HLT, Inst_NOP);

  assign \指令 [9:0] = {10{\指令 [10]}};

  // Other names for the same wires on the sheet: II = \直接跳转 ; III_II = \其他跳转 ; IV_A = \运算类指令 ; IV_II = \控制寄存器传输指令 ;
  //   IV_L = \逻辑类指令 ; IV_S = \移位类指令 ; V = \V类指令 ; VI_I = \与AR相关的跳转 ; VI_II = \逻辑类指令2 ; VI_III = \装载存储类指令 ;
  //   VI_IV = \符号比较 
endmodule

module \数据传送指令控制中心  (
  input  [15:0] D0,
  input  [15:0] D1,
  input  [15:0] D2,
  input  [15:0] D3,
  input  [15:0] A0,
  input  [15:0] A1,
  input  [15:0] SP,
  input  [15:0] CBR,
  input  [2:0] \寄存器读地址1 ,
  input  [2:0] \寄存器读地址2 ,
  input  [15:0] \ALU运算结果 ,
  input  [15:0] \来自存储器 ,
  input  [15:0] \立即数 ,
  input  [15:0] \来自控制寄存器 ,
  input  [15:0] \来自堆栈 ,
  input  [15:0] PC,
  input  Inst_MOVI,
  input  Inst_MOVUI,
  input  Inst_MOV,
  input  Inst_XCHG,
  input  \运算类指令 ,
  input  \逻辑类指令 ,
  input  \移位类指令 ,
  input  \逻辑类指令2 ,
  input  \与AR有关的跳转指令 ,
  input  \装载存储类指令 ,
  input  \控制寄存器传输指令 ,
  input  \异常被触发 ,
  input  [5:0] \功能码 ,
  output [15:0] \写入数据1 ,
  output \写使能1 ,
  output [15:0] \写入数据2 ,
  output [2:0] \写地址2 ,
  output \写使能2 
);

  wire and_1_out, and_2_out, and_3_out, and_4_out, and_5_out, comparator_1_eq, comparator_2_eq,
       comparator_3_eq, or_1_out, or_2_out, or_3_out, or_4_out;
  wire [15:0] multiplexer_1_out;

  Comparator #(.width(2), .mode("unsigned")) comparator_1 (
    .a(\功能码 [2:1]), .b(2'b11), .eq(comparator_1_eq));  // open: gt, lt
  Comparator #(.width(3)) comparator_2 (.a(\功能码 [2:0]), .b(3'b101), .eq(comparator_2_eq));  // open: gt, lt
  Comparator #(.width(3)) comparator_3 (.a(\功能码 [2:0]), .b(3'b111), .eq(comparator_3_eq));  // open: gt, lt
  Multiplexer #(.select(3), .width(16), .enable("false")) multiplexer_1 (
    .in0(D0), .in1(D1), .in2(D2), .in3(D3), .in4(A0), .in5(A1), .in6(SP), .in7(CBR), .out(multiplexer_1_out),
    .sel(\寄存器读地址1 ));
  Multiplexer #(.select(3), .width(16), .enable("false")) multiplexer_2 (
    .in0(D0), .in1(D1), .in2(D2), .in3(D3), .in4(A0), .in5(A1), .in6(SP), .in7(CBR), .out(\写入数据2 ),
    .sel(\寄存器读地址2 ));
  and and_1 (and_1_out, \移位类指令 , ~comparator_1_eq);  // AND_Gate
  or or_1 (or_1_out, comparator_2_eq, comparator_3_eq);
  assign \写入数据1  = or_4_out ? multiplexer_1_out : 16'bz;  // Controlled_Buffer controlled_buffer_1
  assign \写入数据1  = or_3_out ? \ALU运算结果  : 16'bz;  // Controlled_Buffer controlled_buffer_2
  assign \写入数据1  = and_3_out ? \来自存储器  : 16'bz;  // Controlled_Buffer controlled_buffer_3
  assign \写入数据1  = Inst_MOVUI ? {\立即数 [7:0], multiplexer_1_out[7:0]} : 16'bz;  // Controlled_Buffer controlled_buffer_4
  assign \写入数据1  = Inst_MOVI ? {multiplexer_1_out[15:8], \立即数 [7:0]} : 16'bz;  // Controlled_Buffer controlled_buffer_5
  assign \写入数据1  = and_4_out ? PC : 16'bz;  // Controlled_Buffer controlled_buffer_6
  and and_2 (and_2_out, \逻辑类指令 , ~or_1_out);  // AND_Gate
  and and_3 (and_3_out, \功能码 [0], \装载存储类指令 );
  and and_4 (and_4_out, \与AR有关的跳转指令 , or_1_out);
  or or_2 (or_2_out, and_4_out, Inst_MOVI, Inst_MOVUI, Inst_MOV, Inst_XCHG, or_3_out, and_3_out, and_5_out);
  Pull_Resistor pull_resistor_1 (.node(\写入数据1 ));
  or or_3 (or_3_out, \运算类指令 , and_2_out, and_1_out, \逻辑类指令2 );
  or or_4 (or_4_out, Inst_MOV, Inst_XCHG, and_5_out);
  and and_5 (and_5_out, \控制寄存器传输指令 , \功能码 [0]);
  and and_6 (\写使能1 , or_2_out, ~\异常被触发 );  // AND_Gate
  and and_7 (\写使能2 , Inst_XCHG, ~\异常被触发 );  // AND_Gate

  assign \写地址2  = \寄存器读地址1 ;
endmodule

module \堆栈  (
  input  \复位 ,
  input  [15:0] D0,
  input  [15:0] D1,
  input  [15:0] D2,
  input  [15:0] D3,
  input  [15:0] A0,
  input  [15:0] A1,
  input  [15:0] CBR,
  input  [2:0] \寄存器地址 ,
  input  \生长方向_1为下 ,
  input  [5:0] \功能码 ,
  input  \V型指令 ,
  input  clk_2,
  input  clk_3,
  output [15:0] out_15,
  output [15:0] SP,
  output \栈溢出 ,
  output \时钟选择 
);

  wire adder_1_cout, and_1_out, and_2_out, and_3_out, comparator_1_eq, multiplexer_2_out, multiplexer_3_out,
       multiplexer_4_out, not_1_out, or_1_out, or_2_out, or_3_out, PUSH, SPDEC, SPINC, subtractor_1_bout;
  wire [11:0] adder_1_out, controlled_buffer_2_out, subtractor_1_out;
  wire [15:0] multiplexer_1_out;

  Comparator #(.width(3)) comparator_1 (.a(\功能码 [5:3]), .b(3'b000), .eq(comparator_1_eq));  // open: gt, lt
  Multiplexer #(.select(3), .width(16), .enable("false")) multiplexer_1 (
    .in0(D0), .in1(D1), .in2(D2), .in3(D3), .in4(A0), .in5(A1), .in6({4'b0000, SP[11:0]}), .in7(CBR),
    .out(multiplexer_1_out), .sel(\寄存器地址 ));
  and and_1 (and_1_out, comparator_1_eq, \V型指令 );
  Decoder #(.select(3), .disabled(0)) decoder_1 (
    .out0(PUSH), .out1(\时钟选择 ), .out2(SPINC), .out3(SPDEC), .sel(\功能码 [2:0]), .en(and_1_out));  // open: out4, out5, out6, out7
  Adder #(.width(12)) adder_1 (.a(SP[11:0]), .b(12'h1), .out(adder_1_out), .cout(adder_1_cout));  // open: cin
  Subtractor #(.width(12)) subtractor_1 (
    .a(SP[11:0]), .b(12'h1), .out(subtractor_1_out), .bout(subtractor_1_bout));  // open: bin
  and and_2 (and_2_out, subtractor_1_bout, \生长方向_1为下 );
  and and_3 (and_3_out, adder_1_cout, ~\生长方向_1为下 );  // AND_Gate
  assign out_15 = PUSH ? multiplexer_1_out : 16'bz;  // Controlled_Buffer controlled_buffer_1
  RAM #(.addrWidth(12), .dataWidth(16), .bus("asynch")) ram_1 (
    .addr(SP[11:0]), .data(out_15), .clr(\复位 ));  // open: sel, ld
  assign controlled_buffer_2_out = or_3_out ? adder_1_out : 12'bz;  // Controlled_Buffer controlled_buffer_2
  assign controlled_buffer_2_out = or_1_out ? subtractor_1_out : 12'bz;  // Controlled_Buffer controlled_buffer_3
  or or_1 (or_1_out, multiplexer_3_out, SPDEC);
  or or_2 (or_2_out, and_2_out, and_3_out);
  and and_4 (\栈溢出 , or_2_out, \V型指令 );
  Multiplexer #(.enable("false")) multiplexer_2 (.in0(clk_3), .in1(clk_2), .out(multiplexer_2_out), .sel(\时钟选择 ));
  not not_1 (not_1_out, \栈溢出 );
  or or_3 (or_3_out, SPINC, multiplexer_4_out);
  Multiplexer #(.enable("false")) multiplexer_3 (.in0(\时钟选择 ), .in1(PUSH), .out(multiplexer_3_out), .sel(\生长方向_1为下 ));
  Register #(.width(12)) register_1 (
    .D(controlled_buffer_2_out), .en(not_1_out), .Q(SP[11:0]), .clk(multiplexer_2_out), .clr(\复位 ));
  Multiplexer #(.enable("false")) multiplexer_4 (.in0(PUSH), .in1(\时钟选择 ), .out(multiplexer_4_out), .sel(\生长方向_1为下 ));

  assign SP[15:12] = 4'b0000;

  // Other names for the same wires on the sheet: POP = \时钟选择 
endmodule

module \访存控制中心  (
  input  [15:0] \读数据_MEM ,
  input  [15:0] D0,
  input  [15:0] D1,
  input  [15:0] D2,
  input  [15:0] D3,
  input  [15:0] A0,
  input  [15:0] A1,
  input  [2:0] \操作数1 ,
  input  [2:0] \操作数2 ,
  input  [15:0] PC,
  input  [15:0] Immed,
  input  \时钟_2 ,
  input  \时钟_3 ,
  input  \装载存储指令 ,
  input  [5:0] \功能码 ,
  input  \地址未对齐异常使能 ,
  input  \大小端 ,
  output [15:0] \读数据_CPU ,
  output [15:0] \地址_MEM ,
  output [15:0] \写数据_MEM ,
  output \写使能 ,
  output \地址未对齐异常 ,
  output \大小端_2 
);

  wire and_1_out, and_2_out, comparator_1_eq, or_1_out;
  wire [0:0] adder_1_out;
  wire [5:0] pull_resistor_1_node;
  wire [14:0] adder_1_out_2;
  wire [15:0] multiplexer_2_out;

  Comparator #(.width(6)) comparator_1 (.a(\功能码 ), .b(pull_resistor_1_node), .eq(comparator_1_eq));  // open: gt, lt
  Pull_Resistor pull_resistor_1 (.node(pull_resistor_1_node));
  Multiplexer #(.select(2), .width(16), .enable("false")) multiplexer_1 (
    .in0(D0), .in1(D1), .in2(D2), .in3(D3), .out(\写数据_MEM ), .sel(\操作数1 [1:0]));
  Multiplexer #(.width(16), .enable("false")) multiplexer_2 (
    .in0(A0), .in1(A1), .out(multiplexer_2_out), .sel(\操作数2 [0]));
  Multiplexer #(.width(16), .enable("false")) multiplexer_3 (
    .in0(PC), .in1({adder_1_out_2, adder_1_out[0]}), .out(\地址_MEM ), .sel(and_1_out));
  Adder #(.width(16)) adder_1 (
    .a(multiplexer_2_out), .b(Immed), .out({adder_1_out_2, adder_1_out[0]}));  // open: cin, cout
  and and_1 (and_1_out, or_1_out, \装载存储指令 );
  or or_1 (or_1_out, \时钟_2 , \时钟_3 );
  and and_2 (and_2_out, \装载存储指令 , comparator_1_eq);
  and and_3 (\地址未对齐异常 , adder_1_out[0], \地址未对齐异常使能 );
  and and_4 (\写使能 , and_2_out, ~\地址未对齐异常 );  // AND_Gate

  assign \大小端_2  = \大小端 ;
  assign \读数据_CPU  = \读数据_MEM ;
endmodule

module \程序计数器  (
  input  clk_0,
  input  \复位 ,
  input  \中断及恢复 ,
  input  Inst_HLT,
  input  \直接跳转 ,
  input  \其他跳转 ,
  input  \符号比较 ,
  input  \与AR相关的跳转 ,
  input  [5:0] \功能码 ,
  input  [15:0] \异常入口地址 ,
  input  [15:0] AR0,
  input  [15:0] AR1,
  input  [15:0] \立即数 ,
  input  [2:0] \读地址1 ,
  input  [3:0] \ALU符号 ,
  input  [1:0] \符号选择 ,
  input  \符号比较_2 ,
  output [15:0] out_18
);

  wire and_1_out, and_2_out, and_3_out, and_4_out, and_5_out, and_6_out, and_7_out, and_8_out, and_9_out,
       and_10_out, and_11_out, and_12_out, and_13_out, and_14_out, decoder_1_out0, decoder_1_out1,
       decoder_1_out2, decoder_1_out3, decoder_1_out4, decoder_1_out5, decoder_1_out7, multiplexer_2_out,
       or_1_out, or_2_out, or_3_out, or_4_out, or_5_out, \跳转 ;
  wire [1:0] pc_op;
  wire [15:0] adder_1_out, adder_2_out, adder_3_out, adder_4_out, AR, multiplexer_3_out, pull_resistor_2_node;

  assign pc_op = \中断及恢复  ? 2'b01 : 2'bz;  // Controlled_Buffer controlled_buffer_1
  assign pc_op = Inst_HLT ? 2'b11 : 2'bz;  // Controlled_Buffer controlled_buffer_2
  and and_1 (and_1_out, \跳转 , \符号比较 );
  Decoder #(.select(3), .enable("false")) decoder_1 (
    .out0(decoder_1_out0), .out1(decoder_1_out1), .out2(decoder_1_out2), .out3(decoder_1_out3),
    .out4(decoder_1_out4), .out5(decoder_1_out5), .out7(decoder_1_out7), .sel(\功能码 [2:0]));  // open: out6
  Multiplexer #(.width(16), .enable("false")) multiplexer_1 (.in0(AR0), .in1(AR1), .out(AR), .sel(\读地址1 [0]));
  Multiplexer #(.select(2), .enable("false")) multiplexer_2 (
    .in0(\ALU符号 [0]), .in1(\ALU符号 [1]), .in2(\ALU符号 [2]), .in3(\ALU符号 [3]), .out(multiplexer_2_out),
    .sel(\符号选择 ));
  Adder #(.width(16)) adder_1 (.a(out_18), .b(16'h2), .out(adder_1_out));  // open: cin, cout
  assign pc_op = or_1_out ? 2'b10 : 2'bz;  // Controlled_Buffer controlled_buffer_3
  or or_1 (or_1_out, \直接跳转 , \其他跳转 , and_1_out, \与AR相关的跳转 );
  xnor xnor_1 (\跳转 , multiplexer_2_out, \符号比较_2 );
  Multiplexer #(.select(2), .width(16), .enable("false")) multiplexer_3 (
    .in0(adder_1_out), .in1(\异常入口地址 ), .in2(pull_resistor_2_node), .in3(out_18), .out(multiplexer_3_out),
    .sel(pc_op));
  Register #(.width(16)) register_1 (.D(multiplexer_3_out), .Q(out_18), .clk(clk_0), .clr(\复位 ));  // open: en
  Pull_Resistor pull_resistor_1 (.node(pc_op));
  Adder #(.width(16)) adder_2 (.a(16'h2), .b(AR), .out(adder_2_out));  // open: cin, cout
  Adder #(.width(16)) adder_3 (.a(out_18), .b(AR), .out(adder_3_out));  // open: cin, cout
  Adder #(.width(16)) adder_4 (.a(out_18), .b(\立即数 ), .out(adder_4_out));  // open: cin, cout
  Pull_Resistor pull_resistor_2 (.node(pull_resistor_2_node));
  and and_2 (and_2_out, decoder_1_out7, \与AR相关的跳转 );
  assign pull_resistor_2_node = and_2_out ? adder_2_out : 16'bz;  // Controlled_Buffer controlled_buffer_4
  assign pull_resistor_2_node = or_3_out ? adder_3_out : 16'bz;  // Controlled_Buffer controlled_buffer_5
  assign pull_resistor_2_node = or_2_out ? adder_4_out : 16'bz;  // Controlled_Buffer controlled_buffer_6
  assign pull_resistor_2_node = \直接跳转  ? \立即数  : 16'bz;  // Controlled_Buffer controlled_buffer_7
  assign pull_resistor_2_node = and_8_out ? {out_18[15:8], \立即数 [7:0]} : 16'bz;  // Controlled_Buffer controlled_buffer_8
  assign pull_resistor_2_node = or_4_out ? {out_18[15:6], AR[5:0]} : 16'bz;  // Controlled_Buffer controlled_buffer_9
  assign pull_resistor_2_node = or_5_out ? {out_18[15:6], \立即数 [5:0]} : 16'bz;  // Controlled_Buffer controlled_buffer_10
  and and_3 (and_3_out, decoder_1_out5, \与AR相关的跳转 );
  and and_4 (and_4_out, decoder_1_out1, \其他跳转 );
  and and_5 (and_5_out, decoder_1_out1, \符号比较 );
  and and_6 (and_6_out, decoder_1_out1, \与AR相关的跳转 );
  and and_7 (and_7_out, decoder_1_out3, \符号比较 );
  or or_2 (or_2_out, and_7_out, and_9_out, and_4_out);
  or or_3 (or_3_out, and_6_out, and_3_out, and_5_out);
  and and_8 (and_8_out, \其他跳转 , decoder_1_out0);
  and and_9 (and_9_out, decoder_1_out3, \与AR相关的跳转 );
  and and_10 (and_10_out, \与AR相关的跳转 , decoder_1_out0);
  and and_11 (and_11_out, \与AR相关的跳转 , decoder_1_out4);
  and and_12 (and_12_out, \符号比较 , decoder_1_out0);
  or or_4 (or_4_out, and_12_out, and_10_out, and_11_out);
  and and_13 (and_13_out, decoder_1_out2, \符号比较 );
  and and_14 (and_14_out, decoder_1_out2, \与AR相关的跳转 );
  or or_5 (or_5_out, and_14_out, and_13_out);

  // Other names for the same wires on the sheet: immed[15:0] = \立即数 ; immed_7_0[7:0] = \立即数 [7:0];
  //   immed_10_0[10:0] = \立即数 [10:0]; AR_5_0[5:0] = AR[5:0]; AR_7_0[7:0] = AR[7:0]; AR_10_0[10:0] = AR[10:0];
  //   immed_5_0[5:0] = \立即数 [5:0]; PC[15:0] = out_18; PC_15_6[9:0] = out_18[15:6]; PC_15_8[7:0] = out_18[15:8];
  //   PC_15_11[4:0] = out_18[15:11]
endmodule

module \控制器  (
  input  [15:0] \数据 ,
  input  [4:0] \地址 ,
  input  [15:0] PC,
  input  \中断_0 ,
  input  \中断_1 ,
  input  \中断_2 ,
  input  \中断_3 ,
  input  [3:0] \符号 ,
  input  [1:0] \符号选择 ,
  input  \运算类指令 ,
  input  \栈溢出 ,
  input  \地址未对齐 ,
  input  Inst_TRAP,
  input  \控制寄存器传输指令 ,
  input  Inst_ERET,
  input  [5:0] \功能码 ,
  input  clk_0,
  input  clk_2,
  input  clk_3,
  input  rst,
  output [15:0] \输出 ,
  output \中断及恢复 ,
  output \大小端选择_1为大端 ,
  output \栈生长方向 ,
  output [15:0] new_PC
);

  wire and_1_out, and_2_out, and_3_out, and_4_out, and_6_out, and_7_out, and_8_out, comparator_2_eq,
       d_ff_1_qn, en, not_1_out, or_1_out, or_2_out, or_3_out, or_4_out, or_5_out, \中断级 , \中断被触发 ;
  wire [2:0] EXCode, EXCode_I;
  wire [3:0] and_5_out;
  wire [5:0] pull_resistor_1_node;
  wire [15:0] multiplexer_1_out, pull_resistor_5_node, R8, R11;
  wire [15:3] R9;

  Comparator #(.width(5)) comparator_1 (.a(\地址 ), .b(5'b01000), .eq(en));  // open: gt, lt
  Comparator #(.width(6)) comparator_2 (.a(\功能码 ), .b(pull_resistor_1_node), .eq(comparator_2_eq));  // open: gt, lt
  Pull_Resistor pull_resistor_1 (.node(pull_resistor_1_node));
  or or_1 (or_1_out, clk_0, clk_2, clk_3);
  and and_1 (and_1_out, \符号 [0], \符号选择 [0]);
  or or_2 (or_2_out, and_1_out, and_2_out);
  and and_2 (and_2_out, \符号 [2], \符号选择 [1]);
  and and_3 (and_3_out, \控制寄存器传输指令 , comparator_2_eq);
  and and_4 (and_4_out, en, ~\中断被触发 );  // AND_Gate
  assign and_5_out = ~R8[7:4] & {\中断_3 , \中断_2 , \中断_1 , \中断_0 };  // AND_Gate and_5, 4 bits wide
  and and_6 (and_6_out, or_2_out, \运算类指令 );
  or or_3 (or_3_out, and_3_out, Inst_ERET);
  not not_1 (not_1_out, R8[1]);
  or or_4 (or_4_out, and_5_out[0], and_5_out[1], and_5_out[2], and_5_out[3]);
  and and_7 (and_7_out, or_3_out, ~R8[0]);  // AND_Gate
  and and_8 (and_8_out, or_3_out, R8[0]);
  Register #(.width(1)) BE_LE (.D(\数据 [14]), .en(and_4_out), .Q(\大小端选择_1为大端 ), .clk(clk_3), .clr(rst));
  Register #(.width(1)) \u_栈生长方向  (.D(\数据 [13]), .en(and_4_out), .Q(\栈生长方向 ), .clk(clk_3), .clr(rst));
  Register #(.width(4)) \u_中断屏蔽寄存器  (.D(\数据 [12:9]), .en(and_4_out), .Q(R8[7:4]), .clk(clk_3), .clr(rst));
  Register #(.width(1)) \u_中断级  (.D(\中断级 ), .Q(R8[1]), .clk(clk_3), .clr(rst));  // open: en
  Register #(.width(1), .trigger("high")) \u_异常有效  (.D(not_1_out), .Q(R8[2]), .clk(clk_3), .clr(rst));  // open: en
  Register #(.width(1), .trigger("high")) \u_模式  (.D(R8[1]), .Q(R8[0]), .clk(clk_3), .clr(rst));  // open: en
  Register #(.width(4)) \u_中断请求  (
    .D({\中断_3 , \中断_2 , \中断_1 , \中断_0 }), .Q(R9[6:3]), .clk(clk_3), .clr(rst));  // open: en
  Register #(.width(3)) register_1 (.D(EXCode_I), .Q(EXCode), .clk(clk_3), .clr(rst));  // open: en
  Register #(.width(16)) EPC (.D(PC), .en(\中断被触发 ), .Q(R11), .clk(clk_3), .clr(rst));
  or or_5 (or_5_out, or_4_out, and_6_out, \栈溢出 , \地址未对齐 , Inst_TRAP, and_7_out);
  Pull_Resistor pull_resistor_2 (.node(EXCode_I));
  assign EXCode_I = or_4_out ? 3'b001 : 3'bz;  // Controlled_Buffer controlled_buffer_1
  assign EXCode_I = and_6_out ? 3'b010 : 3'bz;  // Controlled_Buffer controlled_buffer_2
  assign EXCode_I = \栈溢出  ? 3'b011 : 3'bz;  // Controlled_Buffer controlled_buffer_3
  assign EXCode_I = \地址未对齐  ? 3'b100 : 3'bz;  // Controlled_Buffer controlled_buffer_4
  Pull_Resistor pull_resistor_3 (.node({R9, EXCode}));
  and and_9 (\中断被触发 , R8[2], or_5_out);
  assign EXCode_I = Inst_TRAP ? 3'b101 : 3'bz;  // Controlled_Buffer controlled_buffer_5
  assign EXCode_I = and_7_out ? 3'b110 : 3'bz;  // Controlled_Buffer controlled_buffer_6
  Pull_Resistor pull_resistor_4 (.node({R8[15], \大小端选择_1为大端 , \栈生长方向 , R8[12:0]}));
  Pull_Resistor pull_resistor_5 (.node(pull_resistor_5_node));
  xor xor_1 (\中断及恢复 , \中断被触发 , and_8_out);
  Multiplexer #(.select(3), .width(16), .enable("false")) multiplexer_1 (
    .in0(pull_resistor_5_node), .in1(16'hff00), .in2(16'hff00), .in3(16'hfe80), .in4(16'hff00),
    .in5(16'hff00), .in6(16'hff00), .in7(pull_resistor_5_node), .out(multiplexer_1_out), .sel(EXCode));
  Multiplexer #(.select(5), .width(16), .enable("false")) multiplexer_2 (
    .in0({16{1'b0}}), .in8({R8[15], \大小端选择_1为大端 , \栈生长方向 , R8[12:0]}), .in9({R9, EXCode}), .in11(R11),
    .in15(16'h401), .out(\输出 ), .sel(\地址 ));  // open: in1, in2, in3, in4, in5, in6, in7, in10, in12, in13, in14, in16, in17, in18, in19, in20, in21, in22, in23, in24, in25, in26, in27, in28, in29, in30, in31
  D_Flip_Flop d_ff_1 (.clk(\中断及恢复 ), .D(d_ff_1_qn), .Q(\中断级 ), .Qn(d_ff_1_qn), .en(or_1_out));  // open: preset, reset
  Multiplexer #(.width(16), .enable("false")) multiplexer_3 (
    .in0(multiplexer_1_out), .in1(R11), .out(new_PC), .sel(and_8_out));
  // also tied to GND on the sheet: {R8[3], R8[15]}

  // Other names for the same wires on the sheet: cregsel[4:0] = \地址 ; 模式 = R8[0]; 异常有效 = R8[2]; 中断屏蔽[3:0] = R8[7:4];
  //   R8[14:13] = {\大小端选择_1为大端 , \栈生长方向 }; SG = \栈生长方向 ; BE = \大小端选择_1为大端 ; R8_I[15:0] = \数据 ; R9[2:0] = EXCode;
  //   中断请求[3:0] = R9[6:3]; 中断请求_I[3:0] = {\中断_3 , \中断_2 , \中断_1 , \中断_0 }
endmodule
