// Logisim project TOO_20171001.circ as structural Verilog: 2 circuits, main circuit main
module main (
);

  wire button_1_out, clock_1_out, \cpu_1_写使能 , \节拍器_1__0 , \节拍器_1__1 , \节拍器_1__2 , \节拍器_1__3 ;
  wire [5:0] wave_1_out_12, wave_1_out_13, wave_1_out_14, wave_1_out_15, wave_1_out_16, wave_1_out_17,
       wave_1_out_18, wave_1_out_19, wave_1_out_20, wave_1_out_21, wave_1_out_22, wave_1_out_23,
       wave_1_out_24, wave_1_out_25, wave_1_out_26, wave_1_out_27, wave_1_out_28, wave_1_out_29,
       wave_1_out_30, wave_1_out_31, wave_1_out_32, wave_1_out_33, wave_1_out_34, wave_1_out_35,
       wave_1_out_36, wave_1_out_37, wave_1_out_38, wave_1_out_39, wave_1_out_42, wave_1_out_45,
       wave_1_out_48, wave_1_out_51;
  wire [15:0] cpu_1_ir, cpu_1_out_10, cpu_1_out_11, cpu_1_out_12, cpu_1_pc, \cpu_1_写数据 , \cpu_1_地址 ,
       wave_1_out_40, wave_1_out_41, wave_1_out_43, wave_1_out_44, wave_1_out_46, wave_1_out_47,
       wave_1_out_49, wave_1_out_50, wave_1_out_52, wave_1_out_53, wave_1_out_54, wave_1_out_55,
       wave_1_out_56, wave_1_out_57, wave_1_out_58, wave_1_out_59, wave_1_out_60, wave_1_out_61,
       wave_1_out_62, wave_1_out_63, wave_1_out_64, wave_1_out_65, wave_1_out_66, wave_1_out_67,
       wave_1_out_68, wave_1_out_69, wave_1_out_70, wave_1_out_71, wave_1_out_72, wave_1_out_73,
       wave_1_out_74, wave_1_out_75, wave_1_out_76, wave_1_out_77, wave_1_out_78, wave_1_out_79,
       wave_1_out_80, wave_1_out_81, wave_1_out_82, wave_1_out_83, \内存_1_输出 ;

  Clock #(.highDuration(2), .lowDuration(2)) clock_1 (.out(clock_1_out));
  \节拍器  \u_节拍器_1  (
    .\时钟 (clock_1_out), ._0(\节拍器_1__0 ), ._1(\节拍器_1__1 ), ._2(\节拍器_1__2 ), ._3(\节拍器_1__3 ),
    .\复位 (button_1_out));
  Button button_1 (.out(button_1_out));
  CPU cpu_1 (
    .\时钟 (clock_1_out), .\复位 (button_1_out), .\来自存贮器 (\内存_1_输出 ), .\地址 (\cpu_1_地址 ), .\写数据 (\cpu_1_写数据 ),
    .\写使能 (\cpu_1_写使能 ), .PC(cpu_1_pc), .IR(cpu_1_ir), .out_10(cpu_1_out_10), .out_11(cpu_1_out_11),
    .out_12(cpu_1_out_12));  // open: 异常, 异常_2, 异常_3, 异常_4, out_13, out_14, out_15, out_16, out_17
  \内存  \u_内存_1  (
    .\地址 (\cpu_1_地址 ), .\复位_写使能 (1'b0), .\写 (\cpu_1_写使能 ), .\大小端选择_0为小端 (1'b0), .\写入数据 (\cpu_1_写数据 ),
    .\输出 (\内存_1_输出 ));
  Wave wave_1 (
    .clk(clock_1_out), .clk_0(\节拍器_1__0 ), .clk_1(\节拍器_1__1 ), .clk_2(\节拍器_1__2 ), .clk_3(\节拍器_1__3 ),
    .rst(button_1_out), .PC(cpu_1_pc), .out_12(wave_1_out_12), .out_15(wave_1_out_15),
    .out_18(wave_1_out_18), .out_21(wave_1_out_21), .out_24(wave_1_out_24), .out_27(wave_1_out_27),
    .out_30(wave_1_out_30), .out_33(wave_1_out_33), .out_13(wave_1_out_13), .out_16(wave_1_out_16),
    .out_19(wave_1_out_19), .out_22(wave_1_out_22), .out_25(wave_1_out_25), .out_28(wave_1_out_28),
    .out_31(wave_1_out_31), .out_34(wave_1_out_34), .out_14(wave_1_out_14), .out_17(wave_1_out_17),
    .out_20(wave_1_out_20), .out_23(wave_1_out_23), .out_26(wave_1_out_26), .out_29(wave_1_out_29),
    .out_32(wave_1_out_32), .out_35(wave_1_out_35), .out_36(wave_1_out_36), .out_37(wave_1_out_37),
    .out_38(wave_1_out_38), .out_39(wave_1_out_39), .out_42(wave_1_out_42), .out_45(wave_1_out_45),
    .out_48(wave_1_out_48), .out_51(wave_1_out_51), .out_40(wave_1_out_40), .out_43(wave_1_out_43),
    .out_46(wave_1_out_46), .out_49(wave_1_out_49), .out_41(wave_1_out_41), .out_44(wave_1_out_44),
    .out_47(wave_1_out_47), .out_50(wave_1_out_50), .out_52(wave_1_out_52), .out_53(wave_1_out_53),
    .out_54(wave_1_out_54), .out_55(wave_1_out_55), .out_56(wave_1_out_56), .out_57(wave_1_out_57),
    .out_58(wave_1_out_58), .out_59(wave_1_out_59), .IR(cpu_1_ir), .out_60(wave_1_out_60),
    .out_61(wave_1_out_61), .out_62(wave_1_out_62), .out_63(wave_1_out_63), .out_64(wave_1_out_64),
    .out_65(wave_1_out_65), .out_66(wave_1_out_66), .out_67(wave_1_out_67), .out_68(wave_1_out_68),
    .out_69(wave_1_out_69), .out_70(wave_1_out_70), .out_71(wave_1_out_71), .out_72(wave_1_out_72),
    .out_73(wave_1_out_73), .out_74(wave_1_out_74), .out_75(wave_1_out_75), .R0(cpu_1_out_10),
    .R1(cpu_1_out_11), .out_76(wave_1_out_76), .out_77(wave_1_out_77), .out_78(wave_1_out_78),
    .out_79(wave_1_out_79), .out_80(wave_1_out_80), .out_81(wave_1_out_81), .out_82(wave_1_out_82),
    .out_83(wave_1_out_83), .R2(cpu_1_out_12));
  DotMatrix #(.matrixcols(32), .matrixrows(6)) dotmatrix_1 (
    .col0(wave_1_out_12), .col1(wave_1_out_15), .col2(wave_1_out_18), .col3(wave_1_out_21),
    .col4(wave_1_out_24), .col5(wave_1_out_27), .col6(wave_1_out_30), .col7(wave_1_out_33),
    .col8(wave_1_out_13), .col9(wave_1_out_16), .col10(wave_1_out_19), .col11(wave_1_out_22),
    .col12(wave_1_out_25), .col13(wave_1_out_28), .col14(wave_1_out_31), .col15(wave_1_out_34),
    .col16(wave_1_out_14), .col17(wave_1_out_17), .col18(wave_1_out_20), .col19(wave_1_out_23),
    .col20(wave_1_out_26), .col21(wave_1_out_29), .col22(wave_1_out_32), .col23(wave_1_out_35),
    .col24(wave_1_out_36), .col25(wave_1_out_37), .col26(wave_1_out_38), .col27(wave_1_out_39),
    .col28(wave_1_out_42), .col29(wave_1_out_45), .col30(wave_1_out_48), .col31(wave_1_out_51));
  // Probe on wave_1_out_40
  // Probe on wave_1_out_43
  // Probe on wave_1_out_52
  // Probe on wave_1_out_53
  // Probe on wave_1_out_60
  // Probe on wave_1_out_68
  // Probe on wave_1_out_76
  // Probe on wave_1_out_49
  // Probe on wave_1_out_46
  // Probe on wave_1_out_54
  // Probe on wave_1_out_55
  // Probe on wave_1_out_61
  // Probe on wave_1_out_62
  // Probe on wave_1_out_70
  // Probe on wave_1_out_69
  // Probe on wave_1_out_77
  // Probe on wave_1_out_78
  // Probe on wave_1_out_44
  // Probe on wave_1_out_41
  // Probe on wave_1_out_56
  // Probe on wave_1_out_57
  // Probe on wave_1_out_63
  // Probe on wave_1_out_64
  // Probe on wave_1_out_72
  // Probe on wave_1_out_71
  // Probe on wave_1_out_79
  // Probe on wave_1_out_80
  // Probe on wave_1_out_50
  // Probe on wave_1_out_47
  // Probe on wave_1_out_59
  // Probe on wave_1_out_58
  // Probe on wave_1_out_65
  // Probe on wave_1_out_66
  // Probe on wave_1_out_74
  // Probe on wave_1_out_73
  // Probe on wave_1_out_81
  // Probe on wave_1_out_82
  // Probe on wave_1_out_67
  // Probe on wave_1_out_75
  // Probe on wave_1_out_83
endmodule

module Wave (
  input  clk,
  input  clk_0,
  input  clk_1,
  input  clk_2,
  input  clk_3,
  input  rst,
  input  [15:0] PC,
  input  [15:0] IR,
  input  [15:0] R0,
  input  [15:0] R1,
  input  [15:0] R2,
  output [5:0] out_12,
  output [5:0] out_13,
  output [5:0] out_14,
  output [5:0] out_15,
  output [5:0] out_16,
  output [5:0] out_17,
  output [5:0] out_18,
  output [5:0] out_19,
  output [5:0] out_20,
  output [5:0] out_21,
  output [5:0] out_22,
  output [5:0] out_23,
  output [5:0] out_24,
  output [5:0] out_25,
  output [5:0] out_26,
  output [5:0] out_27,
  output [5:0] out_28,
  output [5:0] out_29,
  output [5:0] out_30,
  output [5:0] out_31,
  output [5:0] out_32,
  output [5:0] out_33,
  output [5:0] out_34,
  output [5:0] out_35,
  output [5:0] out_36,
  output [5:0] out_37,
  output [5:0] out_38,
  output [5:0] out_39,
  output [15:0] out_40,
  output [15:0] out_41,
  output [5:0] out_42,
  output [15:0] out_43,
  output [15:0] out_44,
  output [5:0] out_45,
  output [15:0] out_46,
  output [15:0] out_47,
  output [5:0] out_48,
  output [15:0] out_49,
  output [15:0] out_50,
  output [5:0] out_51,
  output [15:0] out_52,
  output [15:0] out_53,
  output [15:0] out_54,
  output [15:0] out_55,
  output [15:0] out_56,
  output [15:0] out_57,
  output [15:0] out_58,
  output [15:0] out_59,
  output [15:0] out_60,
  output [15:0] out_61,
  output [15:0] out_62,
  output [15:0] out_63,
  output [15:0] out_64,
  output [15:0] out_65,
  output [15:0] out_66,
  output [15:0] out_67,
  output [15:0] out_68,
  output [15:0] out_69,
  output [15:0] out_70,
  output [15:0] out_71,
  output [15:0] out_72,
  output [15:0] out_73,
  output [15:0] out_74,
  output [15:0] out_75,
  output [15:0] out_76,
  output [15:0] out_77,
  output [15:0] out_78,
  output [15:0] out_79,
  output [15:0] out_80,
  output [15:0] out_81,
  output [15:0] out_82,
  output [15:0] out_83
);

  wire clock_1_out;

  Clock clock_1 (.out(clock_1_out));
  Shift_Register #(.width(6), .length(32)) shift_register_1 (
    .in({clk, clk_0, clk_1, clk_2, clk_3, rst}), .clk(clock_1_out), .clr(rst), .q0(out_12), .q1(out_15),
    .q2(out_18), .q3(out_21), .q4(out_24), .q5(out_27), .q6(out_30), .q7(out_33), .q8(out_13), .q9(out_16),
    .q10(out_19), .q11(out_22), .q12(out_25), .q13(out_28), .q14(out_31), .q15(out_34), .q16(out_14),
    .q17(out_17), .q18(out_20), .q19(out_23), .q20(out_26), .q21(out_29), .q22(out_32), .q23(out_35),
    .q24(out_36), .q25(out_37), .q26(out_38), .q27(out_39), .q28(out_42), .q29(out_45), .q30(out_48),
    .q31(out_51));  // open: shift, out, load, d0, d1, d2, d3, d4, d5, d6, d7, d8, d9, d10, d11, d12, d13, d14, d15, d16, d17, d18, d19, d20, d21, d22, d23, d24, d25, d26, d27, d28, d29, d30, d31
  Shift_Register #(.width(16)) shift_register_2 (
    .in(PC), .clk(clk_0), .clr(rst), .q0(out_40), .q1(out_43), .q2(out_46), .q3(out_49), .q4(out_41),
    .q5(out_44), .q6(out_47), .q7(out_50));  // open: shift, out, load, d0, d1, d2, d3, d4, d5, d6, d7
  Shift_Register #(.width(16)) shift_register_3 (
    .in(IR), .clk(clk_1), .clr(rst), .q0(out_52), .q1(out_54), .q2(out_56), .q3(out_58), .q4(out_53),
    .q5(out_55), .q6(out_57), .q7(out_59));  // open: shift, out, load, d0, d1, d2, d3, d4, d5, d6, d7
  Shift_Register #(.width(16)) shift_register_4 (
    .in(R0), .clk(clk_3), .clr(rst), .q0(out_60), .q1(out_62), .q2(out_64), .q3(out_66), .q4(out_61),
    .q5(out_63), .q6(out_65), .q7(out_67));  // open: shift, out, load, d0, d1, d2, d3, d4, d5, d6, d7
  Shift_Register #(.width(16)) shift_register_5 (
    .in(R1), .clk(clk_3), .clr(rst), .q0(out_68), .q1(out_70), .q2(out_72), .q3(out_74), .q4(out_69),
    .q5(out_71), .q6(out_73), .q7(out_75));  // open: shift, out, load, d0, d1, d2, d3, d4, d5, d6, d7
  Shift_Register #(.width(16)) shift_register_6 (
    .in(R2), .clk(clk_3), .clr(rst), .q0(out_76), .q1(out_78), .q2(out_80), .q3(out_82), .q4(out_77),
    .q5(out_79), .q6(out_81), .q7(out_83));  // open: shift, out, load, d0, d1, d2, d3, d4, d5, d6, d7
endmodule
