// Logisim project PBBP V0.02.1.circ as structural Verilog: 10 circuits, main circuit main
module main (
);

  wire bus_1_i__osel, bus_1_i_oclk, bus_1_ramsel, bus_1_ramstr, closk_out, cpu_1_str, reset_out;
  wire [3:0] cpu_1__0, cpu_1__0_2, cpu_1__3, cpu_1__3_2, cpu_1_immed, cpu_1_immed_2, inputs_outputs_1_out1,
       inputs_outputs_1_out1_2, inputs_outputs_1_out2, inputs_outputs_1_out2_2, inputs_outputs_1_out3;
  wire [7:0] bus_1_i1, bus_1_i2, cpu_1__1, cpu_1__2, cpu_1_addr, cpu_1_dataout, cpu_1_ir, cpu_1_pc,
       inputs_outputs_1_o, inputs_outputs_1_out0, ram_1_o1, ram_1_o2, register_1_q, register_2_q,
       register_3_q, register_4_q;
  wire [7:4] inputs_outputs_1_out3_2;

  CPU cpu_1 (
    .Clock(closk_out), .Reset(reset_out), .Data1(bus_1_i1), .Data2(bus_1_i2), .DataOut(cpu_1_dataout),
    ._0({cpu_1__0_2, cpu_1__0}), ._1(cpu_1__1), ._2(cpu_1__2), ._3({cpu_1__3_2, cpu_1__3}), .pc(cpu_1_pc),
    .ir(cpu_1_ir), .immed({cpu_1_immed_2, cpu_1_immed}), .str(cpu_1_str), .Addr(cpu_1_addr));
  Clock closk (.out(closk_out));
  Button reset (.out(reset_out));
  RAM ram_1 (
    .Addr(cpu_1_addr), .Str(bus_1_ramstr), .DataIn(cpu_1_dataout), .O1(ram_1_o1), .O2(ram_1_o2),
    .RAMsel(bus_1_ramsel));
  Hex_Digit_Display hex_digit_display_1 (.value(cpu_1__0_2));  // open: dp
  Hex_Digit_Display hex_digit_display_2 (.value(cpu_1__0));  // open: dp
  Hex_Digit_Display hex_digit_display_3 (.value(cpu_1_pc[3:0]));  // open: dp
  Hex_Digit_Display hex_digit_display_4 (.value(cpu_1_pc[7:4]));  // open: dp
  Register register_1 (.Q(register_1_q));  // open: D, en, clk, clr
  Register register_2 (.Q(register_2_q));  // open: D, en, clk, clr
  Register register_3 (.Q(register_3_q));  // open: D, en, clk, clr
  Register register_4 (.Q(register_4_q));  // open: D, en, clk, clr
  Hex_Digit_Display hex_digit_display_5 (.value(cpu_1__1[7:4]));  // open: dp
  Hex_Digit_Display hex_digit_display_6 (.value(cpu_1__1[3:0]));  // open: dp
  Hex_Digit_Display hex_digit_display_7 (.value(cpu_1_ir[3:0]));  // open: dp
  Hex_Digit_Display hex_digit_display_8 (.value(cpu_1_ir[7:4]));  // open: dp
  Inputs_Outputs inputs_outputs_1 (
    .Addr(cpu_1_addr), .DataIn(cpu_1_dataout), .clk(bus_1_i_oclk), .sel(bus_1_i__osel), ._0(register_1_q),
    ._1(register_2_q), ._2(register_3_q), ._3(register_4_q), .O(inputs_outputs_1_o),
    .Out0(inputs_outputs_1_out0), .Out1({inputs_outputs_1_out1_2, inputs_outputs_1_out1}),
    .Out2({inputs_outputs_1_out2_2, inputs_outputs_1_out2}),
    .Out3({inputs_outputs_1_out3_2, inputs_outputs_1_out3}), .rst(reset_out));
  Hex_Digit_Display hex_digit_display_9 (.value(cpu_1__2[7:4]));  // open: dp
  Hex_Digit_Display hex_digit_display_10 (.value(cpu_1_immed_2));  // open: dp
  Bus bus_1 (
    .Address(cpu_1_addr), .store(cpu_1_str), .RAMsel(bus_1_ramsel), .I__Osel(bus_1_i__osel),
    .RAMstr(bus_1_ramstr), .I_Oclk(bus_1_i_oclk), .D1(ram_1_o1), .D2(ram_1_o2), .I_O(inputs_outputs_1_o),
    .I1(bus_1_i1), .I2(bus_1_i2));
  Hex_Digit_Display hex_digit_display_11 (.value(cpu_1__2[3:0]));  // open: dp
  Hex_Digit_Display hex_digit_display_12 (.value(cpu_1__3_2));  // open: dp
  Hex_Digit_Display hex_digit_display_13 (.value(cpu_1_immed));  // open: dp
  Hex_Digit_Display hex_digit_display_14 (.value(inputs_outputs_1_out0[7:4]));  // open: dp
  Hex_Digit_Display hex_digit_display_15 (.value(cpu_1__3));  // open: dp
  Hex_Digit_Display hex_digit_display_16 (.value(inputs_outputs_1_out0[3:0]));  // open: dp
  Hex_Digit_Display hex_digit_display_17 (.value(inputs_outputs_1_out1_2));  // open: dp
  Hex_Digit_Display hex_digit_display_18 (.value(inputs_outputs_1_out1));  // open: dp
  Hex_Digit_Display hex_digit_display_19 (.value(inputs_outputs_1_out2_2));  // open: dp
  Hex_Digit_Display hex_digit_display_20 (.value(inputs_outputs_1_out2));  // open: dp
  Hex_Digit_Display hex_digit_display_21 (.value(inputs_outputs_1_out3_2));  // open: dp
  Hex_Digit_Display hex_digit_display_22 (.value(inputs_outputs_1_out3));  // open: dp

  // Notes on the sheet:
  //   r0
  //   pc
  //   r1
  //   ir
  //   r3
  //   immed
  //   r4
endmodule

module CPU (
  input  Clock,
  input  Reset,
  input  [7:0] Data1,
  input  [7:0] Data2,
  output [7:0] pc,
  output [7:0] _0,
  output [7:0] _1,
  output [7:0] _2,
  output [7:0] _3,
  output [7:0] ir,
  output [7:0] immed,
  output [7:0] Addr,
  output str,
  output [7:0] DataOut
);

  wire _0_t, _1_t, _2_t, _3_t, _4, mem, reg_we, tunnel;
  wire [1:0] dregsel, dsel, pc_ce, ssel;
  wire [2:0] ALUOP, timer;
  wire [7:0] cpu_alu_1_out, cpu_gpr_1_sreg, multiplexer_2_out, multiplexer_3_out;

  CPU_PC cpu_pc_1 (.JumpAddr(immed), .pc_ce(pc_ce), .clock(_0_t), .reset(Reset), .PC(pc));
  CPU_Timer cpu_timer_1 (.clock(Clock), .reset(Reset), .Timer(timer));
  Decoder #(.select(3), .enable("false")) decoder_1 (
    .out0(_0_t), .out1(_1_t), .out2(_2_t), .out3(_3_t), .out4(_4), .sel(timer));  // open: out5, out6, out7
  Multiplexer #(.width(8), .enable("false")) multiplexer_1 (.in0(pc), .in1(immed), .out(Addr), .sel(mem));
  Multiplexer #(.width(8), .enable("false")) multiplexer_2 (
    .in0(cpu_alu_1_out), .in1(Data1), .out(multiplexer_2_out), .sel(mem));
  Register u_IR (.D(Data1), .Q(ir), .clk(_1_t), .clr(Reset));  // open: en
  CPU_GPR cpu_gpr_1 (
    .regval(multiplexer_2_out), .clock(_4), .reset(Reset), .dsel(dsel), .we(reg_we), .ssel(ssel),
    .sreg(cpu_gpr_1_sreg), .r0(_0), .r1(_1), .r2(_2), .r3(_3), .dreg(DataOut));
  Register Immediate (.D(Data2), .Q(immed), .clk(_1_t), .clr(Reset));  // open: en
  Multiplexer #(.select(2), .width(8), .enable("false")) multiplexer_3 (
    .in0(DataOut), .in1(immed), .in2({8{1'b0}}), .in3({8{1'b0}}), .out(multiplexer_3_out), .sel(dregsel));
  CPU_ALU cpu_alu_1 (._1(cpu_gpr_1_sreg), ._2(multiplexer_3_out), .in_3(ALUOP), .Out(cpu_alu_1_out), .out_5(tunnel));
  CPU_Decoder cpu_decoder_1 (
    .pc_ce(pc_ce), .mem(mem), .inst(ir), .Timer(timer), .reg_we(reg_we), .dsel(dsel), .ssel(ssel),
    .regsel(dregsel), .aluop(ALUOP), .a_b(tunnel), .str(str));

  // Other names for the same wires on the sheet: ar_out[7:0] = immed; dr_i[7:0] = Data1; inst[7:0] = ir; rst = Reset
endmodule

module CPU_Decoder (
  input  a_b,
  input  [2:0] Timer,
  input  [7:0] inst,
  output [1:0] regsel,
  output [2:0] aluop,
  output [1:0] dsel,
  output [1:0] ssel,
  output [1:0] pc_ce,
  output reg_we,
  output str,
  output mem
);

  wire multiplexer_5_out, multiplexer_8_out;
  wire [1:0] multiplexer_1_out, multiplexer_2_out;

  Multiplexer #(.width(2), .enable("false")) multiplexer_1 (
    .in0(2'b01), .in1(2'b10), .out(multiplexer_1_out), .sel(a_b));
  Multiplexer #(.width(2), .enable("false")) multiplexer_2 (
    .in0(2'b10), .in1(2'b01), .out(multiplexer_2_out), .sel(a_b));
  Multiplexer #(.select(4), .width(2), .enable("false")) multiplexer_3 (
    .in0(2'b00), .in1(2'b00), .in2(2'b01), .in3(2'b01), .in4(2'b01), .in5(2'b10), .in6(multiplexer_1_out),
    .in7(multiplexer_2_out), .in8(multiplexer_1_out), .in9(2'b00), .in10(2'b00), .in11(2'b00), .in12(2'b00),
    .in13(2'b00), .in14(2'b01), .in15(2'b11), .out(pc_ce), .sel(inst[7:4]));
  Multiplexer #(.select(4), .width(2), .enable("false")) multiplexer_4 (
    .in0(2'b00), .in1(2'b00), .in2(2'b01), .in3(2'b00), .in4(2'b00), .in5(2'b00), .in6(2'b00), .in7(2'b00),
    .in8(2'b10), .in9(2'b00), .in10(2'b00), .in11(2'b00), .in12(2'b00), .in13(2'b00), .in14(2'b01),
    .in15(2'b00), .out(regsel), .sel(inst[7:4]));
  Multiplexer #(.select(4), .enable("false")) multiplexer_5 (
    .in0(1'b0), .in1(1'b0), .in2(1'b0), .in3(1'b0), .in4(1'b1), .in5(1'b0), .in6(1'b0), .in7(1'b0),
    .in8(1'b0), .in9(1'b0), .in10(1'b0), .in11(1'b0), .in12(1'b0), .in13(1'b0), .in14(1'b0), .in15(1'b0),
    .out(multiplexer_5_out), .sel(inst[7:4]));
  Multiplexer #(.select(3), .enable("false")) multiplexer_6 (
    .in0(1'b0), .in1(1'b0), .in2(1'b0), .in3(multiplexer_5_out), .in4(1'b0), .out(str), .sel(Timer));  // open: in5, in6, in7
  Multiplexer #(.select(4), .width(3), .enable("false")) multiplexer_7 (
    .in0(3'b000), .in1(3'b000), .in2(3'b000), .in3(3'b000), .in4(3'b000), .in5(3'b000), .in6(3'b000),
    .in7(3'b000), .in8(3'b000), .in9(3'b001), .in10(3'b010), .in11(3'b011), .in12(3'b100), .in13(3'b101),
    .in14(3'b110), .in15(3'b000), .out(aluop), .sel(inst[7:4]));
  Multiplexer #(.select(4), .enable("false")) multiplexer_8 (
    .in0(1'b0), .in1(1'b0), .in2(1'b0), .in3(1'b1), .in4(1'b1), .in5(1'b0), .in6(1'b0), .in7(1'b0),
    .in8(1'b0), .in9(1'b0), .in10(1'b0), .in11(1'b0), .in12(1'b0), .in13(1'b0), .in14(1'b0), .in15(1'b0),
    .out(multiplexer_8_out), .sel(inst[7:4]));
  Multiplexer #(.select(3), .enable("false")) multiplexer_9 (
    .in0(1'b0), .in1(1'b0), .in2(multiplexer_8_out), .in3(multiplexer_8_out), .in4(multiplexer_8_out),
    .out(mem), .sel(Timer));  // open: in5, in6, in7
  Multiplexer #(.select(4), .enable("false")) multiplexer_10 (
    .in0(1'b0), .in1(1'b1), .in2(1'b1), .in3(1'b1), .in4(1'b0), .in5(1'b0), .in6(1'b0), .in7(1'b0),
    .in8(1'b0), .in9(1'b1), .in10(1'b1), .in11(1'b1), .in12(1'b1), .in13(1'b1), .in14(1'b1), .in15(1'b0),
    .out(reg_we), .sel(inst[7:4]));

  assign dsel = inst[1:0];
  assign ssel = inst[3:2];

  // Other names for the same wires on the sheet: op1[3:0] = inst[7:4]

  // Notes on the sheet:
  //   pc_ce
  //   regsel
  //   0000 nop 0001 mov 0010 movi 0011 lod 0100 str 0101 jmp/jr 0110 be 0111 bne 1000 bez 1001 add 1010 sub 1011 and 1100 or 1101 not 1110 s 1111 hlt
  //   mem
  //   reg_we
endmodule

module CPU_PC (
  input  [7:0] JumpAddr,
  input  [1:0] pc_ce,
  input  clock,
  input  reset,
  output [7:0] PC
);

  wire [7:0] adder_1_out, adder_2_out, multiplexer_1_out;

  Adder adder_1 (.a(PC), .b(8'h1), .out(adder_1_out));  // open: cin, cout
  Adder adder_2 (.a(PC), .b(8'h2), .out(adder_2_out));  // open: cin, cout
  Register register_1 (.D(multiplexer_1_out), .Q(PC), .clk(clock), .clr(reset));  // open: en
  Multiplexer #(.select(2), .width(8), .enable("false")) multiplexer_1 (
    .in0(adder_1_out), .in1(adder_2_out), .in2(JumpAddr), .in3(PC), .out(multiplexer_1_out), .sel(pc_ce));
endmodule

module CPU_Timer (
  input  clock,
  input  reset,
  output [2:0] Timer
);

  wire comparator_1_eq;
  wire [2:0] adder_1_out, multiplexer_1_out;

  Adder #(.width(3)) adder_1 (.a(Timer), .b(3'b001), .out(adder_1_out));  // open: cin, cout
  Multiplexer #(.width(3), .enable("false")) multiplexer_1 (
    .in0(adder_1_out), .in1(3'b000), .out(multiplexer_1_out), .sel(comparator_1_eq));
  Register #(.width(3)) register_1 (.D(multiplexer_1_out), .Q(Timer), .clk(clock), .clr(reset));  // open: en
  Comparator #(.width(3), .mode("unsigned")) comparator_1 (
    .a(Timer), .b(3'b100), .eq(comparator_1_eq));  // open: gt, lt
endmodule

module CPU_GPR (
  input  [7:0] regval,
  input  clock,
  input  reset,
  input  [1:0] dsel,
  input  we,
  input  [1:0] ssel,
  output [7:0] sreg,
  output [7:0] r0,
  output [7:0] r1,
  output [7:0] r2,
  output [7:0] r3,
  output [7:0] dreg
);

  wire demultiplexer_1_out0, demultiplexer_1_out1, demultiplexer_1_out2, demultiplexer_1_out3;

  Demultiplexer #(.select(2), .enable("false")) demultiplexer_1 (
    .out0(demultiplexer_1_out0), .out1(demultiplexer_1_out1), .out2(demultiplexer_1_out2),
    .out3(demultiplexer_1_out3), .in(we), .sel(dsel));
  Register register_1 (.D(regval), .en(demultiplexer_1_out0), .Q(r0), .clk(clock), .clr(reset));
  Register register_2 (.D(regval), .en(demultiplexer_1_out1), .Q(r1), .clk(clock), .clr(reset));
  Register register_3 (.D(regval), .en(demultiplexer_1_out2), .Q(r2), .clk(clock), .clr(reset));
  Register register_4 (.D(regval), .en(demultiplexer_1_out3), .Q(r3), .clk(clock), .clr(reset));
  Multiplexer #(.select(2), .width(8), .enable("false")) multiplexer_1 (
    .in0(r0), .in1(r1), .in2(r2), .in3(r3), .out(sreg), .sel(ssel));
  Multiplexer #(.select(2), .width(8), .enable("false")) multiplexer_2 (
    .in0(r0), .in1(r1), .in2(r2), .in3(r3), .out(dreg), .sel(dsel));
endmodule

module CPU_ALU (
  input  [7:0] _1,
  input  [7:0] _2,
  input  [2:0] in_3,
  output [7:0] Out,
  output out_5
);

  wire [7:0] adder_1_out, and_1_out, multiplexer_1_out, not_1_out, or_1_out, shifter_1_out, shifter_2_out,
       shifter_3_out, subtractor_1_out;

  assign not_1_out = ~_1;  // NOT_Gate not_1, 8 bits wide
  Adder adder_1 (.a(_1), .b(_2), .out(adder_1_out));  // open: cin, cout
  Subtractor subtractor_1 (.a(_1), .b(_2), .out(subtractor_1_out));  // open: bin, bout
  assign and_1_out = _1 & _2;  // AND_Gate and_1, 8 bits wide
  assign or_1_out = _1 | _2;  // OR_Gate or_1, 8 bits wide
  Shifter shifter_1 (.in(_1), .\dist (_2[2:0]), .out(shifter_1_out));
  Shifter #(.shift("lr")) shifter_2 (.in(_1), .\dist (_2[2:0]), .out(shifter_2_out));
  Shifter #(.shift("ar")) shifter_3 (.in(_1), .\dist (_2[2:0]), .out(shifter_3_out));
  Multiplexer #(.select(2), .width(8), .enable("false")) multiplexer_1 (
    .in0(shifter_1_out), .in1(shifter_2_out), .in2(shifter_1_out), .in3(shifter_3_out),
    .out(multiplexer_1_out), .sel(_2[4:3]));
  Multiplexer #(.select(3), .width(8), .enable("false")) multiplexer_2 (
    .in0(_2), .in1(adder_1_out), .in2(subtractor_1_out), .in3(and_1_out), .in4(or_1_out), .in5(not_1_out),
    .in6(multiplexer_1_out), .in7({8{1'b0}}), .out(Out), .sel(in_3));
  Comparator #(.mode("unsigned")) comparator_1 (.a(_1), .b(_2), .eq(out_5));  // open: gt, lt
endmodule

module RAM (
  input  [7:0] Addr,
  input  [7:0] DataIn,
  input  Str,
  input  RAMsel,
  output [7:0] O1,
  output [7:0] O2
);

  wire ld, nand_1_out, not_2_out, not_3_out, not_4_out, or_1_out;
  wire [6:0] adder_1_out, multiplexer_1_out;
  wire [7:0] controlled_buffer_1_out, controlled_buffer_2_out;

  not not_1 (ld, Str);
  Adder #(.width(7)) adder_1 (.a(7'b0000001), .b(Addr[7:1]), .out(adder_1_out));  // open: cin, cout
  Multiplexer #(.width(7), .enable("false")) multiplexer_1 (
    .in0(Addr[7:1]), .in1(adder_1_out), .out(multiplexer_1_out), .sel(Addr[0]));
  nand nand_1 (nand_1_out, ~ld, Addr[0]);  // NAND_Gate
  or or_1 (or_1_out, Addr[0], ld);
  not not_2 (not_2_out, or_1_out);
  assign controlled_buffer_1_out = not_2_out ? DataIn : 8'bz;  // Controlled_Buffer controlled_buffer_1
  RAM_part #(.addrWidth(7), .bus("asynch")) ram_1 (
    .addr(multiplexer_1_out), .data(controlled_buffer_1_out), .sel(RAMsel), .ld(or_1_out));  // open: clr
  not not_3 (not_3_out, nand_1_out);
  assign controlled_buffer_2_out = not_3_out ? DataIn : 8'bz;  // Controlled_Buffer controlled_buffer_2
  RAM_part #(.addrWidth(7), .bus("asynch")) ram_2 (
    .addr(Addr[7:1]), .data(controlled_buffer_2_out), .sel(RAMsel), .ld(nand_1_out));  // open: clr
  Multiplexer #(.width(8), .enable("false")) multiplexer_2 (
    .in0(controlled_buffer_1_out), .in1(controlled_buffer_2_out), .out(O1), .sel(Addr[0]));
  Multiplexer #(.width(8), .enable("false")) multiplexer_3 (
    .in0(controlled_buffer_1_out), .in1(controlled_buffer_2_out), .out(O2), .sel(not_4_out));
  not not_4 (not_4_out, Addr[0]);
endmodule

module Bus (
  input  [7:0] Address,
  input  store,
  input  [7:0] D1,
  input  [7:0] D2,
  input  [7:0] I_O,
  output RAMsel,
  output I__Osel,
  output RAMstr,
  output I_Oclk,
  output [7:0] I1,
  output [7:0] I2
);

  wire decoder_1_out0, decoder_1_out1, decoder_1_out2, decoder_1_out3, decoder_1_out4, decoder_1_out5,
       decoder_1_out6, decoder_1_out7, decoder_1_out8, decoder_1_out9, decoder_1_out10, decoder_1_out11,
       decoder_1_out12, decoder_1_out13, decoder_1_out14, decoder_1_out15, decoder_1_out16, decoder_1_out17,
       decoder_1_out18, decoder_1_out19, decoder_1_out20, decoder_1_out21, decoder_1_out22, decoder_1_out23,
       decoder_1_out24, decoder_1_out25, decoder_1_out26, decoder_1_out27, decoder_1_out28, decoder_1_out29,
       decoder_1_out30;

  Decoder #(.select(5), .enable("false")) decoder_1 (
    .out0(decoder_1_out0), .out1(decoder_1_out1), .out2(decoder_1_out2), .out3(decoder_1_out3),
    .out4(decoder_1_out4), .out5(decoder_1_out5), .out6(decoder_1_out6), .out7(decoder_1_out7),
    .out8(decoder_1_out8), .out9(decoder_1_out9), .out10(decoder_1_out10), .out11(decoder_1_out11),
    .out12(decoder_1_out12), .out13(decoder_1_out13), .out14(decoder_1_out14), .out15(decoder_1_out15),
    .out16(decoder_1_out16), .out17(decoder_1_out17), .out18(decoder_1_out18), .out19(decoder_1_out19),
    .out20(decoder_1_out20), .out21(decoder_1_out21), .out22(decoder_1_out22), .out23(decoder_1_out23),
    .out24(decoder_1_out24), .out25(decoder_1_out25), .out26(decoder_1_out26), .out27(decoder_1_out27),
    .out28(decoder_1_out28), .out29(decoder_1_out29), .out30(decoder_1_out30), .out31(I__Osel),
    .sel(Address[7:3]));
  or or_1 (RAMsel, decoder_1_out0, decoder_1_out1, decoder_1_out2, decoder_1_out3, decoder_1_out4, decoder_1_out5, decoder_1_out6, decoder_1_out7, decoder_1_out8, decoder_1_out9, decoder_1_out10, decoder_1_out11, decoder_1_out12, decoder_1_out13, decoder_1_out14, decoder_1_out15, decoder_1_out16, decoder_1_out17, decoder_1_out18, decoder_1_out19, decoder_1_out20, decoder_1_out21, decoder_1_out22, decoder_1_out23, decoder_1_out24, decoder_1_out25, decoder_1_out26, decoder_1_out27, decoder_1_out28, decoder_1_out29, decoder_1_out30);
  and and_1 (RAMstr, RAMsel, store);
  and and_2 (I_Oclk, store, I__Osel);
  Multiplexer #(.width(8), .enable("false")) multiplexer_1 (.in0(I_O), .in1(D1), .out(I1), .sel(RAMsel));

  assign I2 = D2;
endmodule

module Inputs_Outputs (
  input  [7:0] Addr,
  input  [7:0] _0,
  input  [7:0] _1,
  input  [7:0] _2,
  input  [7:0] _3,
  input  [7:0] DataIn,
  input  clk,
  input  sel,
  input  rst,
  output [7:0] O,
  output [7:0] Out0,
  output [7:0] Out1,
  output [7:0] Out2,
  output [7:0] Out3
);

  wire demultiplexer_1_out0, demultiplexer_1_out1, demultiplexer_1_out2, demultiplexer_1_out3;

  Demultiplexer #(.select(2), .enable("false")) demultiplexer_1 (
    .out0(demultiplexer_1_out0), .out1(demultiplexer_1_out1), .out2(demultiplexer_1_out2),
    .out3(demultiplexer_1_out3), .in(sel), .sel(Addr[1:0]));
  Register register_1 (.D(DataIn), .en(demultiplexer_1_out0), .Q(Out0), .clk(clk), .clr(rst));
  Register register_2 (.D(DataIn), .en(demultiplexer_1_out1), .Q(Out1), .clk(clk), .clr(rst));
  Register register_3 (.D(DataIn), .en(demultiplexer_1_out2), .Q(Out2), .clk(clk), .clr(rst));
  Register register_4 (.D(DataIn), .en(demultiplexer_1_out3), .Q(Out3), .clk(clk), .clr(rst));
  Multiplexer #(.select(3), .width(8), .enable("false")) multiplexer_1 (
    .in0(_0), .in1(_1), .in2(_2), .in3(_3), .in4(Out0), .in5(Out1), .in6(Out2), .in7(Out3), .out(O),
    .sel(Addr[2:0]));

  // Other names for the same wires on the sheet: sels[1:0] = Addr[1:0]
endmodule
