// Logisim project Stack.circ as structural Verilog: 2 circuits, main circuit main
module main (
  input  [15:0] in_1,
  input  PUSH,
  input  POP,
  input  Reset,
  input  [1:0] Rh,
  output [15:0] out_6
);

  wire decoder_1_out2, decoder_1_out3, not_1_out, not_2_out;
  wire [7:0] sp_1_sp;

  not not_1 (not_1_out, Reset);
  Decoder #(.select(2), .disabled(0)) decoder_1 (
    .out2(decoder_1_out2), .out3(decoder_1_out3), .sel(Rh), .en(not_1_out));  // open: out0, out1
  SP sp_1 (.POP(POP), .PUSH(PUSH), .Reset(Reset), .SP(sp_1_sp), .Rh4(decoder_1_out3));  // open: Error
  not not_2 (not_2_out, POP);
  assign out_6 = POP ? in_1 : 16'bz;  // Controlled_Buffer controlled_buffer_1
  RAM #(.dataWidth(16)) ram_1 (
    .addr(sp_1_sp), .data(out_6), .clk(decoder_1_out2), .ld(not_2_out), .clr(Reset));  // open: sel
endmodule

module SP (
  input  POP,
  input  PUSH,
  input  Rh4,
  input  Reset,
  output Error,
  output [7:0] SP
);

  wire adder_1_cout, and_1_out, and_2_out, and_3_out, or_1_out, subtractor_1_bout;
  wire [7:0] adder_1_out, controlled_buffer_1_out, subtractor_1_out;

  Adder adder_1 (.a(SP), .b(8'h1), .out(adder_1_out), .cout(adder_1_cout));  // open: cin
  Subtractor subtractor_1 (.a(SP), .b(8'h1), .out(subtractor_1_out), .bout(subtractor_1_bout));  // open: bin
  or or_1 (or_1_out, POP, PUSH);
  and and_1 (and_1_out, POP, subtractor_1_bout);
  or or_2 (Error, and_1_out, and_2_out);
  and and_2 (and_2_out, PUSH, adder_1_cout);
  assign controlled_buffer_1_out = PUSH ? adder_1_out : 8'bz;  // Controlled_Buffer controlled_buffer_1
  assign controlled_buffer_1_out = POP ? subtractor_1_out : 8'bz;  // Controlled_Buffer controlled_buffer_2
  and and_3 (and_3_out, or_1_out, Rh4);
  Register register_1 (.D(controlled_buffer_1_out), .Q(SP), .clk(and_3_out), .clr(Reset));  // open: en
endmodule
