// Logisim project 00000.circ as structural Verilog
module CPU (
  input  [15:0] in_1,
  output [15:0] out_2
);

  wire [15:0] ar, cpu_ir_1_instruction, cpu_pc_1_pc_pointer, dr, immed, mr, multiplexer_2_out,
       multiplexer_3_out;

  CPU_PC cpu_pc_1 (.Immed(immed), .AR(ar), .PC_Pointer(cpu_pc_1_pc_pointer));  // open: Select, Clock, Reset, INT
  Multiplexer #(.select(2), .width(16), .enable("false")) multiplexer_1 (
    .in0(cpu_pc_1_pc_pointer), .in1(immed), .in2(ar), .in3({16{1'b0}}), .out(out_2));  // open: sel
  CPU_IR cpu_ir_1 (.In(in_1), .Instruction(cpu_ir_1_instruction));  // open: Clock, Reset
  CPU_AR cpu_ar_1 (.Immed(immed), .DR(dr), .AR(ar), .MR(mr));  // open: Select, Clock, Reset, PC
  CPU_Immed cpu_immed_1 (.Immed(cpu_ir_1_instruction), .Extension_Immediate(immed));  // open: Extend_Mode, Immed_Exist
  CPU_MR cpu_mr_1 (.RAM(in_1), .DR(dr), .AR(ar), .MR(mr), .Immed(immed));  // open: Select, Clock, Reset
  CPU_DR cpu_dr_1 (.Immed(immed), .AR(ar), .MR(mr), .ALU({16{1'b0}}), .DR(dr));  // open: Select, Clock, Reset
  Multiplexer #(.select(2), .width(16), .enable("false")) multiplexer_2 (
    .in0(immed), .in1(ar), .in2(mr), .in3(dr), .out(multiplexer_2_out));  // open: sel
  Multiplexer #(.select(2), .width(16), .enable("false")) multiplexer_3 (
    .in0(immed), .in1(ar), .in2(mr), .in3(dr), .out(multiplexer_3_out));  // open: sel
endmodule

module CPU_PC (
  input  [15:0] Immed,
  input  [15:0] AR,
  input  [15:0] INT,
  input  [1:0] Select,
  input  Clock,
  input  Reset,
  output [15:0] PC_Pointer
);

  wire [15:0] adder_1_out, multiplexer_1_out;

  Adder #(.width(16)) adder_1 (.a(PC_Pointer), .b(16'h2), .out(adder_1_out));  // open: cin, cout
  Multiplexer #(.select(2), .width(16), .enable("false")) multiplexer_1 (
    .in0(adder_1_out), .in1({PC_Pointer[15:8], Immed[7:0]}), .in2(AR), .in3(INT), .out(multiplexer_1_out),
    .sel(Select));
  Register #(.width(16)) register_1 (.D(multiplexer_1_out), .Q(PC_Pointer), .clk(Clock), .clr(Reset));  // open: en
endmodule

module CPU_IR (
  input  [15:0] In,
  input  Clock,
  input  Reset,
  output [15:0] Instruction
);

  // Probe on In
  Register #(.width(16)) register_1 (.D(In), .Q(Instruction), .clk(Clock), .clr(Reset));  // open: en
endmodule

module CPU_AR (
  input  [15:0] Immed,
  input  [15:0] DR,
  input  [15:0] MR,
  input  [15:0] PC,
  input  [1:0] Select,
  input  Clock,
  input  Reset,
  output [15:0] AR
);

  wire [15:0] multiplexer_1_out;

  Multiplexer #(.select(2), .width(16), .enable("false")) multiplexer_1 (
    .in0(Immed), .in1(DR), .in2(MR), .in3(PC), .out(multiplexer_1_out), .sel(Select));
  Register #(.width(16)) register_1 (.D(multiplexer_1_out), .Q(AR), .clk(Clock), .clr(Reset));  // open: en
endmodule

module CPU_Immed (
  input  [15:0] Immed,
  input  Extend_Mode,
  input  Immed_Exist,
  output [15:0] Extension_Immediate
);

  wire [15:0] bit_extender_1_out, bit_extender_2_out, multiplexer_1_out;

  assign bit_extender_1_out = {{8{1'b0}}, Immed[7:0]};  // Bit_Extender bit_extender_1
  Multiplexer #(.width(16), .enable("false")) multiplexer_1 (
    .in0(bit_extender_1_out), .in1(bit_extender_2_out), .out(multiplexer_1_out), .sel(Extend_Mode));
  assign bit_extender_2_out = {{8{Immed[7]}}, Immed[7:0]};  // Bit_Extender bit_extender_2
  Multiplexer #(.width(16), .enable("false")) multiplexer_2 (
    .in0(multiplexer_1_out), .in1({16{1'b0}}), .out(Extension_Immediate), .sel(Immed_Exist));
endmodule

module CPU_MR (
  input  [15:0] RAM,
  input  [15:0] DR,
  input  [15:0] AR,
  input  [15:0] Immed,
  input  [1:0] Select,
  input  Clock,
  input  Reset,
  output [15:0] MR
);

  wire [15:0] multiplexer_1_out;

  Multiplexer #(.select(2), .width(16), .enable("false")) multiplexer_1 (
    .in0(RAM), .in1(DR), .in2(AR), .in3(Immed), .out(multiplexer_1_out), .sel(Select));
  Register #(.width(16)) register_1 (.D(multiplexer_1_out), .Q(MR), .clk(Clock), .clr(Reset));  // open: en
endmodule

module CPU_DR (
  input  [15:0] Immed,
  input  [15:0] AR,
  input  [15:0] MR,
  input  [15:0] ALU,
  input  [1:0] Select,
  input  Clock,
  input  Reset,
  output [15:0] DR
);

  wire [15:0] multiplexer_1_out;

  Multiplexer #(.select(2), .width(16), .enable("false")) multiplexer_1 (
    .in0(Immed), .in1(AR), .in2(MR), .in3(ALU), .out(multiplexer_1_out), .sel(Select));
  Register #(.width(16)) register_1 (.D(multiplexer_1_out), .Q(DR), .clk(Clock), .clr(Reset));  // open: en
endmodule

module CPU_Decoder (
  input  [15:0] Inst
);
endmodule

module RAM (
  input  [15:0] in_1,
  input  [15:0] in_2,
  input  Store,
  input  Select,
  output [15:0] out_5
);

  wire ld;
  wire [7:0] multiplexer_2_out, multiplexer_3_out;
  wire [14:0] adder_1_out, ADDR0;

  not not_1 (ld, Store);
  Multiplexer #(.width(15), .enable("false")) multiplexer_1 (
    .in0(in_1[15:1]), .in1(adder_1_out), .out(ADDR0), .sel(in_1[0]));
  Adder #(.width(15)) adder_1 (.a(in_1[15:1]), .b(15'h1), .out(adder_1_out));  // open: cin, cout
  Multiplexer #(.width(8), .enable("false")) multiplexer_2 (
    .in0(in_2[7:0]), .in1(in_2[15:8]), .out(multiplexer_2_out), .sel(in_1[0]));
  assign out_5[7:0] = Store ? multiplexer_2_out : 8'bz;  // Controlled_Buffer controlled_buffer_1
  RAM_part #(.addrWidth(15), .bus("asynch")) ram_1 (
    .addr(ADDR0), .data(out_5[7:0]), .sel(Select), .ld(ld));  // open: clr
  RAM_part #(.addrWidth(15), .bus("asynch")) ram_2 (
    .addr(in_1[15:1]), .data(out_5[15:8]), .sel(Select), .ld(ld));  // open: clr
  assign out_5[15:8] = Store ? multiplexer_3_out : 8'bz;  // Controlled_Buffer controlled_buffer_2
  Multiplexer #(.width(8), .enable("false")) multiplexer_3 (
    .in0(in_2[15:8]), .in1(in_2[7:0]), .out(multiplexer_3_out), .sel(in_1[0]));

  // Other names for the same wires on the sheet: _0 = in_1[0]; ADDR1[14:0] = in_1[15:1]; D0[7:0] = in_2[7:0];
  //   D1[7:0] = in_2[15:8]; sel = Select; str = Store
endmodule
