// Logisim project SG.circ as structural Verilog: 1 circuit, main circuit main
module main (
  input  [6:0] in_1,
  input  [6:0] in_2,
  input  [6:0] in_3,
  input  [6:0] in_4,
  input  [6:0] in_5
);

  wire clock_1_out, decoder_1_out0, decoder_1_out1;
  wire [6:0] rom_1_data, shift_register_1_q0, shift_register_1_q1, shift_register_1_q2, shift_register_1_q3,
       shift_register_1_q4, shift_register_1_q5, shift_register_1_q6, shift_register_1_q7,
       shift_register_1_q8, shift_register_1_q9, shift_register_1_q10, shift_register_1_q11,
       shift_register_1_q12, shift_register_1_q13, shift_register_1_q14, shift_register_1_q15,
       shift_register_1_q16, shift_register_1_q17, shift_register_1_q18, shift_register_1_q19;
  wire [7:0] counter_1_q;

  // Probe on in_1
  // Probe on in_2
  // Probe on in_3
  // Probe on in_4
  // Probe on in_5
  Counter counter_1 (.load(1'b1), .count(1'b1), .Q(counter_1_q), .clk(decoder_1_out1));  // open: D, carry, clr
  Decoder #(.enable("false")) decoder_1 (.out0(decoder_1_out0), .out1(decoder_1_out1), .sel(clock_1_out));
  Clock clock_1 (.out(clock_1_out));
  ROM #(.dataWidth(7)) rom_1 (.addr(counter_1_q), .data(rom_1_data));  // open: sel
  Shift_Register #(.width(7), .length(20)) shift_register_1 (
    .in(rom_1_data), .clk(decoder_1_out0), .q0(shift_register_1_q0), .q1(shift_register_1_q1),
    .q2(shift_register_1_q2), .q3(shift_register_1_q3), .q4(shift_register_1_q4), .q5(shift_register_1_q5),
    .q6(shift_register_1_q6), .q7(shift_register_1_q7), .q8(shift_register_1_q8), .q9(shift_register_1_q9),
    .q10(shift_register_1_q10), .q11(shift_register_1_q11), .q12(shift_register_1_q12),
    .q13(shift_register_1_q13), .q14(shift_register_1_q14), .q15(shift_register_1_q15),
    .q16(shift_register_1_q16), .q17(shift_register_1_q17), .q18(shift_register_1_q18),
    .q19(shift_register_1_q19));  // open: shift, out, load, clr, d0, d1, d2, d3, d4, d5, d6, d7, d8, d9, d10, d11, d12, d13, d14, d15, d16, d17, d18, d19
  DotMatrix #(.matrixcols(20), .dotshape("circle")) dotmatrix_1 (
    .col0(shift_register_1_q19), .col1(shift_register_1_q18), .col2(shift_register_1_q17),
    .col3(shift_register_1_q16), .col4(shift_register_1_q15), .col5(shift_register_1_q14),
    .col6(shift_register_1_q13), .col7(shift_register_1_q12), .col8(shift_register_1_q11),
    .col9(shift_register_1_q10), .col10(shift_register_1_q9), .col11(shift_register_1_q8),
    .col12(shift_register_1_q7), .col13(shift_register_1_q6), .col14(shift_register_1_q5),
    .col15(shift_register_1_q4), .col16(shift_register_1_q3), .col17(shift_register_1_q2),
    .col18(shift_register_1_q1), .col19(shift_register_1_q0));

  // Notes on the sheet:
  //   contents of rom_1 (hex, n*v repeats v):
  //   0 3e 41 41 41 7f 0 4*1 7f 0 31 4a 4c 48 7f 0 3e 4*41 3e 0 7e 1 7e 1 7e 0 0 3e 41 41 41 3e 0 4*1 7f 0
  //   4*1 7f 0 4*49 7f 0 7f 8 8 8 7f
endmodule
