// Logisim project 000.circ as structural Verilog
module CPU_Registers (
  input  [15:0] in_1
);
endmodule

module CPU_ALU (
  input  Cin,
  input  [15:0] A,
  input  [15:0] B,
  input  in_4,
  input  [4:0] in_5,
  output [15:0] out_6,
  output [4:0] out_7
);

  wire adder_1_cout, adder_2_cout, d_ff_1_q, d_ff_1_qn, decoder_1_out1, decoder_1_out4, decoder_1_out5,
       multiplexer_3_out, multiplexer_4_out, multiplexer_5_out, multiplexer_6_out, multiplexer_7_out,
       multiplexer_12_out, multiplexer_13_out, not_3_out, not_4_out, xor_6_out;
  wire [1:0] or_2_out;
  wire [14:0] adder_1_out;
  wire [15:0] and_1_out, bit_extender_1_out, multiplexer_1_out, multiplexer_2_out, multiplexer_8_out,
       not_1_out, not_2_out, or_1_out, shifter_1_out, shifter_2_out, shifter_3_out, shifter_4_out,
       shifter_5_out, xor_1_out, xor_2_out, xor_3_out, xor_4_out, xor_5_out;
  wire [15:15] adder_2_out;

  D_Flip_Flop d_ff_1 (.clk(in_4), .D(d_ff_1_qn), .Q(d_ff_1_q), .Qn(d_ff_1_qn));  // open: preset, en, reset
  Comparator #(.width(16)) comparator_1 (.a(A), .b(B));  // open: gt, eq, lt
  assign bit_extender_1_out = {{15{in_5[2]}}, in_5[2]};  // Bit_Extender bit_extender_1
  assign not_1_out = ~B;  // NOT_Gate not_1, 16 bits wide
  assign and_1_out = B & A;  // AND_Gate and_1, 16 bits wide
  assign or_1_out = B | A;  // OR_Gate or_1, 16 bits wide
  assign xor_1_out = B ^ A;  // XOR_Gate xor_1, 16 bits wide
  assign xor_2_out = bit_extender_1_out ^ not_1_out;  // XOR_Gate xor_2, 16 bits wide
  assign xor_3_out = bit_extender_1_out ^ and_1_out;  // XOR_Gate xor_3, 16 bits wide
  assign xor_4_out = bit_extender_1_out ^ or_1_out;  // XOR_Gate xor_4, 16 bits wide
  assign xor_5_out = bit_extender_1_out ^ xor_1_out;  // XOR_Gate xor_5, 16 bits wide
  Multiplexer #(.select(2), .width(16), .enable("false")) multiplexer_1 (
    .in0(xor_2_out), .in1(xor_3_out), .in2(xor_4_out), .in3(xor_5_out), .out(multiplexer_1_out),
    .sel(in_5[1:0]));
  Decoder #(.select(3), .enable("false")) decoder_1 (
    .out1(decoder_1_out1), .out4(decoder_1_out4), .out5(decoder_1_out5), .sel(in_5[2:0]));  // open: out0, out2, out3, out6, out7
  assign not_2_out = ~B;  // NOT_Gate not_2, 16 bits wide
  Shifter #(.width(16)) shifter_1 (.in(B), .\dist (A[3:0]), .out(shifter_1_out));
  Shifter #(.width(16), .shift("lr")) shifter_2 (.in(B), .\dist (A[3:0]), .out(shifter_2_out));
  Shifter #(.width(16), .shift("ar")) shifter_3 (.in(B), .\dist (A[3:0]), .out(shifter_3_out));
  Shifter #(.width(16), .shift("rl")) shifter_4 (.in(B), .\dist (A[3:0]), .out(shifter_4_out));
  Shifter #(.width(16), .shift("rr")) shifter_5 (.in(B), .\dist (A[3:0]), .out(shifter_5_out));
  not not_3 (not_3_out, Cin);
  or or_2 (or_2_out[0], decoder_1_out1, decoder_1_out5);
  or or_3 (or_2_out[1], decoder_1_out5, decoder_1_out4, decoder_1_out4);
  Multiplexer #(.select(3), .width(16), .enable("false")) multiplexer_2 (
    .in0(B), .in1(B), .in2(16'h1), .in3({16{1'b0}}), .in4(not_2_out), .in5(not_2_out), .in6({16{1'b1}}),
    .out(multiplexer_2_out), .sel(in_5[2:0]));  // open: in7
  Multiplexer #(.select(2), .enable("false")) multiplexer_3 (
    .in0(1'b0), .in1(1'b1), .in2(Cin), .in3(not_3_out), .out(multiplexer_3_out), .sel(or_2_out));
  Adder #(.width(15)) adder_1 (
    .a(A[14:0]), .b(multiplexer_2_out[14:0]), .out(adder_1_out), .cin(multiplexer_3_out), .cout(adder_1_cout));
  Adder #(.width(1)) adder_2 (
    .a(A[15]), .b(multiplexer_2_out[15]), .out(adder_2_out[15]), .cin(adder_1_cout), .cout(adder_2_cout));
  xor xor_6 (xor_6_out, adder_1_cout, adder_2_cout);
  Multiplexer #(.enable("false")) multiplexer_4 (.in0(xor_6_out), .in1(1'b0), .out(multiplexer_4_out), .sel(d_ff_1_q));
  Multiplexer #(.select(4), .enable("false")) multiplexer_5 (
    .in0(1'b0), .in1(B[15]), .in2(B[14]), .in3(B[13]), .in4(B[12]), .in5(B[11]), .in6(B[10]), .in7(B[9]),
    .in8(B[8]), .in9(B[7]), .in10(B[6]), .in11(B[5]), .in12(B[4]), .in13(B[3]), .in14(B[2]), .in15(B[1]),
    .out(multiplexer_5_out), .sel(A[3:0]));
  Multiplexer #(.select(4), .enable("false")) multiplexer_6 (
    .in0(B[0]), .in1(B[1]), .in2(B[2]), .in3(B[3]), .in4(B[4]), .in5(B[5]), .in6(B[6]), .in7(B[7]),
    .in8(B[8]), .in9(B[9]), .in10(B[10]), .in11(B[11]), .in12(B[12]), .in13(B[13]), .in14(B[14]),
    .in15(1'b0), .out(multiplexer_6_out), .sel(A[3:0]));
  Multiplexer #(.select(3), .enable("false")) multiplexer_7 (
    .in0(multiplexer_5_out), .in1(multiplexer_5_out), .in2(multiplexer_6_out), .in3(multiplexer_6_out),
    .in4(multiplexer_5_out), .in5(multiplexer_6_out), .in6(1'b0), .in7(1'b0), .out(multiplexer_7_out),
    .sel(in_5[2:0]));
  Multiplexer #(.select(3), .width(16), .enable("false")) multiplexer_8 (
    .in0(shifter_1_out), .in1(shifter_1_out), .in2(shifter_2_out), .in3(shifter_3_out), .in4(shifter_4_out),
    .in5(shifter_5_out), .in6({16{1'b0}}), .in7({16{1'b0}}), .out(multiplexer_8_out), .sel(in_5[2:0]));
  Multiplexer #(.select(2), .width(16), .enable("false")) multiplexer_9 (
    .in0({adder_2_out[15], adder_1_out}), .in1(multiplexer_1_out), .in2(multiplexer_8_out), .in3({16{1'b0}}),
    .out(out_6), .sel(in_5[4:3]));
  Multiplexer #(.select(2), .enable("false")) multiplexer_10 (
    .in0(adder_2_cout), .in1(1'b0), .in2(multiplexer_7_out), .in3(1'b0), .out(out_7[1]), .sel(in_5[4:3]));
  Multiplexer #(.select(2), .enable("false")) multiplexer_11 (
    .in0(multiplexer_4_out), .in1(1'b0), .in2(1'b0), .in3(1'b0), .out(out_7[2]), .sel(in_5[4:3]));
  Multiplexer #(.enable("false")) multiplexer_12 (
    .in0(1'b0), .in1(not_4_out), .out(multiplexer_12_out), .sel(d_ff_1_q));
  not not_4 (not_4_out, out_6[0]);
  Multiplexer #(.enable("false")) multiplexer_13 (
    .in0(1'b0), .in1(out_6[15]), .out(multiplexer_13_out), .sel(d_ff_1_q));
  Multiplexer #(.select(2), .enable("false")) multiplexer_14 (
    .in0(multiplexer_12_out), .in1(1'b0), .in2(1'b0), .in3(1'b0), .out(out_7[4]), .sel(in_5[4:3]));
  nor nor_1 (out_7[0], out_6[0], out_6[1], out_6[2], out_6[3], out_6[4], out_6[5], out_6[6], out_6[7], out_6[8], out_6[9], out_6[10], out_6[11], out_6[12], out_6[13], out_6[14], out_6[15]);
  Multiplexer #(.select(2), .enable("false")) multiplexer_15 (
    .in0(multiplexer_13_out), .in1(1'b0), .in2(1'b0), .in3(1'b0), .out(out_7[3]), .sel(in_5[4:3]));

  // Notes on the sheet:
  //   算数单元
  //   逻辑单元
  //   移位单元
  //   SAR
  //   SOL
  //   SOR
  //   SHL
  //   SHR
  //   SAL
endmodule

module \CPU_立即数扩展  (
  input  [4:0] in_1,
  input  in_2,
  output [15:0] out_3
);

  wire [11:0] bit_extender_2_out;
  wire [15:0] bit_extender_1_out;

  assign bit_extender_1_out = {{11{1'b0}}, in_1};  // Bit_Extender bit_extender_1
  assign bit_extender_2_out = {{11{in_1[4]}}, in_1[4]};  // Bit_Extender bit_extender_2
  Multiplexer #(.width(16), .enable("false")) multiplexer_1 (
    .in0(bit_extender_1_out), .in1({bit_extender_2_out, in_1[3:0]}), .out(out_3), .sel(in_2));
endmodule

module CPU_ID (
  input  [15:0] in_1,
  output [5:0] OPCode
);


  assign OPCode = in_1[5:0];
endmodule
