// Logisim project 00001.circ as structural Verilog
module CPU (
  input  Clock,
  input  Reset,
  output [15:0] out_3
);

  wire _0, _1, _2, _3, acwe, arwe, drwe, mrwe, not_1_out;
  wire [1:0] addrsel, cpu_rc_1_out;
  wire [15:0] ac, ar, cpu_ir_1_out, dr, imm, mr, pc;

  CPU_RC cpu_rc_1 (.Clock(Clock), .Reset(Reset), .Out(cpu_rc_1_out));
  Decoder #(.select(2), .disabled(0)) decoder_1 (
    .out0(_0), .out1(_1), .out2(_2), .out3(_3), .sel(cpu_rc_1_out), .en(not_1_out));
  not not_1 (not_1_out, Reset);
  CPU_PC cpu_pc_1 (.Immed(imm), .AR(ar), .Clock(_0), .Reset(Reset), .Out(pc));  // open: PCSel
  CPU_IR cpu_ir_1 (.Clock(_1), .Reset(Reset), .Out(cpu_ir_1_out));  // open: Inst
  // Probe on pc
  CPU_Immed cpu_immed_1 (.Inst(cpu_ir_1_out), .Immed(imm));  // open: ImmedSel
  // Probe on cpu_ir_1_out
  Multiplexer #(.select(2), .width(16), .enable("false")) multiplexer_1 (
    .in0(pc), .in1(ar), .in2(imm), .in3({16{1'b0}}), .out(out_3), .sel(addrsel));
  // Probe on imm
  Register #(.width(16)) register_1 (.en(acwe), .Q(ac), .clk(_3), .clr(Reset));  // open: D
  Register #(.width(16)) register_2 (.en(drwe), .Q(dr), .clk(_3), .clr(Reset));  // open: D
  Register #(.width(16)) register_3 (.en(mrwe), .Q(mr), .clk(_3), .clr(Reset));  // open: D
  Register #(.width(16)) register_4 (.en(arwe), .Q(ar), .clk(_3), .clr(Reset));  // open: D

  // Other names for the same wires on the sheet: clk = Clock; rst = Reset
endmodule

module CPU_RC (
  input  Clock,
  input  Reset,
  output [1:0] Out
);

  wire and_1_out, and_2_out, and_3_out, and_4_out, counter_1_q, counter_2_q;

  Counter #(.width(1), .max('h1)) counter_1 (.Q(counter_1_q), .clk(Clock), .clr(Reset));  // open: load, D, count, carry
  Counter #(.width(1), .max('h1), .trigger("falling")) counter_2 (
    .Q(counter_2_q), .clk(Clock), .clr(Reset));  // open: load, D, count, carry
  and and_1 (and_1_out, ~counter_1_q, counter_2_q);  // AND_Gate
  and and_2 (and_2_out, counter_1_q, counter_2_q);
  and and_3 (and_3_out, ~counter_1_q, counter_2_q);  // AND_Gate
  and and_4 (and_4_out, counter_1_q, ~counter_2_q);  // AND_Gate
  or or_1 (Out[1], and_1_out, and_2_out);
  or or_2 (Out[0], and_3_out, and_4_out);
endmodule

module CPU_PC (
  input  [15:0] Immed,
  input  [15:0] AR,
  input  [1:0] PCSel,
  input  Clock,
  input  Reset,
  output [15:0] Out
);

  wire [15:0] adder_1_out, adder_2_out, multiplexer_1_out;

  Adder #(.width(16)) adder_1 (.a(Out), .b(16'h2), .out(adder_1_out));  // open: cin, cout
  Adder #(.width(16)) adder_2 (.a(AR), .b(Immed), .out(adder_2_out));  // open: cin, cout
  Multiplexer #(.select(2), .width(16), .enable("false")) multiplexer_1 (
    .in0(adder_1_out), .in1(adder_2_out), .in2(AR), .in3(Out), .out(multiplexer_1_out), .sel(PCSel));
  Register #(.width(16)) register_1 (.D(multiplexer_1_out), .Q(Out), .clk(Clock), .clr(Reset));  // open: en
endmodule

module CPU_IR (
  input  [15:0] Inst,
  input  Clock,
  input  Reset,
  output [15:0] Out
);

  Register #(.width(16)) register_1 (.D(Inst), .Q(Out), .clk(Clock), .clr(Reset));  // open: en
endmodule

module CPU_Immed (
  input  [15:0] Inst,
  input  [1:0] ImmedSel,
  output [15:0] Immed
);

  wire [15:0] bit_extender_1_out, bit_extender_2_out;

  assign bit_extender_1_out = {{8{1'b0}}, Inst[7:0]};  // Bit_Extender bit_extender_1
  assign bit_extender_2_out = {{8{1'b0}}, Inst[7:0]};  // Bit_Extender bit_extender_2
  Multiplexer #(.width(16), .disabled(0)) multiplexer_1 (
    .in0(bit_extender_1_out), .in1(bit_extender_2_out), .out(Immed), .sel(ImmedSel[0]), .en(ImmedSel[1]));
endmodule
