// Logisim project 001.circ as structural Verilog
module CPU (
  input  [15:0] in_1,
  output [15:0] out_2
);

  wire undriven, undriven_2;
  wire [15:0] cpu_if_id_reg_1_out_4, regisres_1_out_8, regisres_1_out_9;

  CPU_IF cpu_if_1 (.Clk(undriven_2), .out_6(out_2), .Reset(undriven));  // open: in_1, in_2, in_3
  CPU_IF__ID_reg cpu_if_id_reg_1 (.in_1(in_1), .in_2(undriven_2), .in_3(undriven), .out_4(cpu_if_id_reg_1_out_4));
  Regisres regisres_1 (
    .in_6(undriven_2), .in_7(undriven), .out_8(regisres_1_out_8), .out_9(regisres_1_out_9));  // open: in_1, in_2, in_3, in_4, in_5
  Multiplexer #(.select(2), .width(16), .enable("false")) multiplexer_1 (.in0(regisres_1_out_8));  // open: in1, in2, in3, out, sel
  Multiplexer #(.select(2), .width(16), .enable("false")) multiplexer_2 (.in0(regisres_1_out_9));  // open: in1, in2, in3, out, sel
endmodule

module CPU_IF__ID_reg (
  input  [15:0] in_1,
  input  in_2,
  input  in_3,
  output [15:0] out_4
);

  Register #(.width(16)) register_1 (.D(in_1), .Q(out_4), .clk(in_2), .clr(in_3));  // open: en
endmodule

module CPU_IF (
  input  [15:0] in_1,
  input  [15:0] in_2,
  input  [1:0] in_3,
  input  Clk,
  input  Reset,
  output [15:0] out_6
);

  wire [15:0] adder_1_out, multiplexer_1_out;

  Adder #(.width(16)) adder_1 (.a(16'h1), .b(out_6), .out(adder_1_out));  // open: cin, cout
  Multiplexer #(.select(2), .width(16), .enable("false")) multiplexer_1 (
    .in0(adder_1_out), .in1(in_1), .in2({out_6[15:10], in_1[9:0]}), .in3(in_2), .out(multiplexer_1_out),
    .sel(in_3));
  Register #(.width(16)) register_1 (.D(multiplexer_1_out), .Q(out_6), .clk(Clk), .clr(Reset));  // open: en
endmodule

module ID (
  input  [15:0] in_1,
  output [4:0] ALU_OP,
  output [3:0] RSCode_RDCode,
  output [3:0] RTCode
);

  ROM #(.addrWidth(6), .dataWidth(16)) rom_1 (.addr(in_1[15:10]));  // open: data, sel

  assign RSCode_RDCode = in_1[9:6];
  assign RTCode = in_1[5:2];
endmodule

module Regisres (
  input  [15:0] in_1,
  input  [3:0] in_2,
  input  [3:0] in_3,
  input  [3:0] in_4,
  input  in_5,
  input  in_6,
  input  in_7,
  output [15:0] out_8,
  output [15:0] out_9
);

  wire demultiplexer_1_out0, demultiplexer_1_out1, demultiplexer_1_out2, demultiplexer_1_out3,
       demultiplexer_1_out4, demultiplexer_1_out5, demultiplexer_1_out6, demultiplexer_1_out7,
       demultiplexer_1_out8, demultiplexer_1_out9, demultiplexer_1_out10, demultiplexer_1_out11,
       demultiplexer_1_out12, demultiplexer_1_out13, demultiplexer_1_out14, demultiplexer_1_out15;
  wire [15:0] register_1_q, register_2_q, register_3_q, register_4_q, register_5_q, register_6_q,
       register_7_q, register_8_q, register_9_q, register_10_q, register_11_q, register_12_q, register_13_q,
       register_14_q, register_15_q, register_16_q;

  Demultiplexer #(.select(4), .enable("false")) demultiplexer_1 (
    .out0(demultiplexer_1_out0), .out1(demultiplexer_1_out1), .out2(demultiplexer_1_out2),
    .out3(demultiplexer_1_out3), .out4(demultiplexer_1_out4), .out5(demultiplexer_1_out5),
    .out6(demultiplexer_1_out6), .out7(demultiplexer_1_out7), .out8(demultiplexer_1_out8),
    .out9(demultiplexer_1_out9), .out10(demultiplexer_1_out10), .out11(demultiplexer_1_out11),
    .out12(demultiplexer_1_out12), .out13(demultiplexer_1_out13), .out14(demultiplexer_1_out14),
    .out15(demultiplexer_1_out15), .in(in_5), .sel(in_2));
  Register #(.width(16)) register_1 (.D(in_1), .en(demultiplexer_1_out0), .Q(register_1_q), .clk(in_6), .clr(in_7));
  Register #(.width(16)) register_2 (.D(in_1), .en(demultiplexer_1_out1), .Q(register_2_q), .clk(in_6), .clr(in_7));
  Register #(.width(16)) register_3 (.D(in_1), .en(demultiplexer_1_out2), .Q(register_3_q), .clk(in_6), .clr(in_7));
  Register #(.width(16)) register_4 (.D(in_1), .en(demultiplexer_1_out3), .Q(register_4_q), .clk(in_6), .clr(in_7));
  Register #(.width(16)) register_5 (.D(in_1), .en(demultiplexer_1_out4), .Q(register_5_q), .clk(in_6), .clr(in_7));
  Register #(.width(16)) register_6 (.D(in_1), .en(demultiplexer_1_out5), .Q(register_6_q), .clk(in_6), .clr(in_7));
  Register #(.width(16)) register_7 (.D(in_1), .en(demultiplexer_1_out6), .Q(register_7_q), .clk(in_6), .clr(in_7));
  Register #(.width(16)) register_8 (.D(in_1), .en(demultiplexer_1_out7), .Q(register_8_q), .clk(in_6), .clr(in_7));
  Register #(.width(16)) register_9 (.D(in_1), .en(demultiplexer_1_out8), .Q(register_9_q), .clk(in_6), .clr(in_7));
  Register #(.width(16)) register_10 (.D(in_1), .en(demultiplexer_1_out9), .Q(register_10_q), .clk(in_6), .clr(in_7));
  Register #(.width(16)) register_11 (.D(in_1), .en(demultiplexer_1_out10), .Q(register_11_q), .clk(in_6), .clr(in_7));
  Register #(.width(16)) register_12 (.D(in_1), .en(demultiplexer_1_out11), .Q(register_12_q), .clk(in_6), .clr(in_7));
  Register #(.width(16)) register_13 (.D(in_1), .en(demultiplexer_1_out12), .Q(register_13_q), .clk(in_6), .clr(in_7));
  Register #(.width(16)) register_14 (.D(in_1), .en(demultiplexer_1_out13), .Q(register_14_q), .clk(in_6), .clr(in_7));
  Register #(.width(16)) register_15 (.D(in_1), .en(demultiplexer_1_out14), .Q(register_15_q), .clk(in_6), .clr(in_7));
  Register #(.width(16)) register_16 (.D(in_1), .en(demultiplexer_1_out15), .Q(register_16_q), .clk(in_6), .clr(in_7));
  Multiplexer #(.select(4), .width(16), .enable("false")) multiplexer_1 (
    .in0(register_1_q), .in1(register_2_q), .in2(register_3_q), .in3(register_4_q), .in4(register_5_q),
    .in5(register_6_q), .in6(register_7_q), .in7(register_8_q), .in8(register_9_q), .in9(register_10_q),
    .in10(register_11_q), .in11(register_12_q), .in12(register_13_q), .in13(register_14_q),
    .in14(register_15_q), .in15(register_16_q), .out(out_8), .sel(in_3));
  Multiplexer #(.select(4), .width(16), .enable("false")) multiplexer_2 (
    .in0(register_1_q), .in1(register_2_q), .in2(register_3_q), .in3(register_4_q), .in4(register_5_q),
    .in5(register_6_q), .in6(register_7_q), .in7(register_8_q), .in8(register_9_q), .in9(register_10_q),
    .in10(register_11_q), .in11(register_12_q), .in12(register_13_q), .in13(register_14_q),
    .in14(register_15_q), .in15(register_16_q), .out(out_9), .sel(in_4));
endmodule
