// Logisim project 2333.circ as structural Verilog: 1 circuit, main circuit main
module main (
  input  in_1
);

  wire adder_1_cout, clock_1_out, d_ff_1_q, decoder_1_out0, decoder_1_out1, decoder_1_out2, decoder_1_out3,
       decoder_2_out0, decoder_2_out1, decoder_2_out2, decoder_2_out3, demultiplexer_1_out0,
       demultiplexer_1_out1, demultiplexer_1_out2, demultiplexer_1_out3, multiplexer_3_out;
  wire [1:0] counter_2_q, register_1_q_2, register_1_q_3;
  wire [3:0] adder_1_out, counter_1_q, multiplexer_1_out, multiplexer_2_out, multiplexer_4_out,
       multiplexer_5_out, register_1_q, register_2_q, register_3_q, register_4_q, register_5_q, register_6_q;
  wire [7:0] rom_1_data;

  Clock clock_1 (.out(clock_1_out));
  Counter #(.width(4), .max('hf)) counter_1 (
    .Q(counter_1_q), .clk(decoder_1_out0), .clr(in_1));  // open: load, D, count, carry
  Decoder #(.select(2), .enable("false")) decoder_1 (
    .out0(decoder_1_out0), .out1(decoder_1_out1), .out2(decoder_1_out2), .out3(decoder_1_out3),
    .sel(counter_2_q));
  Counter #(.width(2), .max('h3)) counter_2 (.Q(counter_2_q), .clk(clock_1_out));  // open: load, D, count, carry, clr
  ROM #(.addrWidth(4)) rom_1 (.addr(counter_1_q), .data(rom_1_data));  // open: sel
  Register register_1 (
    .D(rom_1_data), .Q({register_1_q_3, register_1_q_2, register_1_q}), .clk(decoder_1_out1), .clr(in_1));  // open: en
  Decoder #(.select(2), .enable("false")) decoder_2 (
    .out0(decoder_2_out0), .out1(decoder_2_out1), .out2(decoder_2_out2), .out3(decoder_2_out3),
    .sel(register_1_q[1:0]));
  Demultiplexer #(.select(2), .enable("false")) demultiplexer_1 (
    .out0(demultiplexer_1_out0), .out1(demultiplexer_1_out1), .out2(demultiplexer_1_out2),
    .out3(demultiplexer_1_out3), .in(decoder_2_out1), .sel(register_1_q[3:2]));
  Register #(.width(4)) register_2 (
    .D(register_6_q), .en(demultiplexer_1_out1), .Q(register_2_q), .clk(decoder_1_out2), .clr(in_1));
  Register #(.width(4)) register_3 (
    .D(register_6_q), .en(demultiplexer_1_out0), .Q(register_3_q), .clk(decoder_1_out2), .clr(in_1));
  Register #(.width(4)) register_4 (
    .D(register_6_q), .en(demultiplexer_1_out2), .Q(register_4_q), .clk(decoder_1_out2), .clr(in_1));
  Register #(.width(4)) register_5 (
    .D(register_6_q), .en(demultiplexer_1_out3), .Q(register_5_q), .clk(decoder_1_out2), .clr(in_1));
  Multiplexer #(.select(2), .width(4), .enable("false")) multiplexer_1 (
    .in0(register_3_q), .in1(register_2_q), .in2(register_4_q), .in3(register_5_q), .out(multiplexer_1_out),
    .sel(register_1_q_2));
  Multiplexer #(.select(2), .width(4), .enable("false")) multiplexer_2 (
    .in0(register_3_q), .in1(register_2_q), .in2(register_4_q), .in3(register_5_q), .out(multiplexer_2_out),
    .sel(register_1_q_3));
  Multiplexer #(.enable("false")) multiplexer_3 (
    .in0(1'b0), .in1(d_ff_1_q), .out(multiplexer_3_out), .sel(decoder_2_out2));
  Multiplexer #(.width(4), .enable("false")) multiplexer_4 (
    .in0(multiplexer_1_out), .in1({register_1_q_3, register_1_q_2}), .out(multiplexer_4_out),
    .sel(decoder_2_out0));
  Multiplexer #(.width(4), .enable("false")) multiplexer_5 (
    .in0(multiplexer_2_out), .in1({register_1_q_3, register_1_q_2}), .out(multiplexer_5_out),
    .sel(decoder_2_out3));
  Register #(.width(4)) register_6 (.D(adder_1_out), .Q(register_6_q), .clk(decoder_1_out3), .clr(in_1));  // open: en
  Adder #(.width(4)) adder_1 (
    .a(multiplexer_4_out), .b(multiplexer_5_out), .out(adder_1_out), .cin(multiplexer_3_out),
    .cout(adder_1_cout));
  D_Flip_Flop d_ff_1 (.clk(decoder_1_out3), .D(adder_1_cout), .Q(d_ff_1_q), .reset(in_1));  // open: Qn, preset, en

  // Notes on the sheet:
  //   contents of rom_1 (hex, n*v repeats v):
  //   f0 1
endmodule
