// Logisim project 002.circ as structural Verilog: 6 circuits, main circuit main
module main (
);

  wire clock_1_out, cpu_1_ram_ce, rst_out;
  wire [7:0] cpu_1_addr, cpu_1_dataout, ram_1_dataout;

  Button rst (.out(rst_out));
  Clock clock_1 (.out(clock_1_out));
  CPU cpu_1 (
    .in_2(rst_out), .clk(clock_1_out), .DataIn(ram_1_dataout), .Addr(cpu_1_addr), .DataOut(cpu_1_dataout),
    .RAM_ce(cpu_1_ram_ce));
  RAM ram_1 (
    .DataOut(ram_1_dataout), .Addr(cpu_1_addr), .DataIn(cpu_1_dataout), .we(cpu_1_ram_ce), .clk(clock_1_out),
    .rst(rst_out));
  Hex_Digit_Display hex_digit_display_1 (.value(cpu_1_addr[7:4]));  // open: dp
  Hex_Digit_Display hex_digit_display_2 (.value(ram_1_dataout[7:4]));  // open: dp
  Hex_Digit_Display hex_digit_display_3 (.value(cpu_1_addr[3:0]));  // open: dp
  Hex_Digit_Display hex_digit_display_4 (.value(ram_1_dataout[3:0]));  // open: dp

  // Notes on the sheet:
  //   PBBP v0.01
endmodule

module RAM (
  input  [7:0] Addr,
  input  [7:0] DataIn,
  input  we,
  input  clk,
  input  rst,
  output [7:0] DataOut
);

  wire decoder_1_out5;
  wire [2:0] counter_1_q;

  Counter #(.width(3), .max('h7)) counter_1 (.Q(counter_1_q), .clk(clk), .clr(rst));  // open: load, D, count, carry
  Decoder #(.select(3), .enable("false")) decoder_1 (
    .out5(decoder_1_out5), .sel(counter_1_q));  // open: out0, out1, out2, out3, out4, out6, out7
  RAM_part #(.bus("separate")) ram_1 (
    .addr(Addr), .din(DataIn), .data(DataOut), .str(we), .clk(decoder_1_out5));  // open: sel, ld, clr
endmodule

module CPU (
  input  [7:0] DataIn,
  input  in_2,
  input  clk,
  output [7:0] Addr,
  output RAM_ce,
  output [7:0] DataOut
);

  wire A___B, Carry, drce, immed_clk, immed_rst, ir_clk, ir_rst, jmp_ce, ls, not_1_out, PC_clk,
       Registers_clk, we;
  wire [1:0] dsel, OP_s, ssel;
  wire [2:0] ALUOP;
  wire [3:0] OPCode;
  wire [7:0] counter_1_q, cpu_alu_1_out, cpu_registers_1__0, cpu_registers_1__1, cpu_registers_1__2,
       cpu_registers_1__3, cpu_registers_1_sreg, DR, multiplexer_1_out, multiplexer_2_out;

  Register register_1 (.D(DataIn), .Q({OPCode, ssel, dsel}), .clk(ir_clk), .clr(ir_rst));  // open: en
  Register register_2 (.D(DataIn), .Q(DR), .clk(immed_clk), .clr(immed_rst));  // open: en
  // Probe on cpu_registers_1__0
  // Probe on cpu_registers_1__1
  // Probe on cpu_registers_1__2
  Multiplexer #(.width(8), .enable("false")) multiplexer_1 (
    .in0(cpu_alu_1_out), .in1(DR), .out(multiplexer_1_out), .sel(drce));
  // Probe on OPCode
  // Probe on cpu_registers_1__3
  CPU_Registers cpu_registers_1 (
    .DReg_In(multiplexer_1_out), .we(we), .ssel(ssel), .dsel(dsel), .dreg(DataOut),
    .sreg(cpu_registers_1_sreg), .clk(Registers_clk), .rst(in_2), ._0(cpu_registers_1__0),
    ._1(cpu_registers_1__1), ._2(cpu_registers_1__2), ._3(cpu_registers_1__3));
  not not_1 (not_1_out, jmp_ce);
  Multiplexer #(.select(2), .width(8), .enable("false")) multiplexer_2 (
    .in0(cpu_registers_1_sreg), .in1(DR), .in2({8{1'b0}}), .in3({8{1'b0}}), .out(multiplexer_2_out),
    .sel(OP_s));
  Counter counter_1 (
    .load(jmp_ce), .D(DR), .count(not_1_out), .Q(counter_1_q), .clk(PC_clk), .clr(in_2));  // open: carry
  Multiplexer #(.width(8), .enable("false")) multiplexer_3 (.in0(counter_1_q), .in1(DR), .out(Addr), .sel(ls));
  CPU_ALU cpu_alu_1 (
    .s(DataOut), .d(multiplexer_2_out), .A___B(A___B), .Carry(Carry), .in_3(ALUOP), .Out(cpu_alu_1_out));
  CPU_ID cpu_id_1 (
    .Carry(Carry), .A____B(A___B), .OPCode(OPCode), .CLK(clk), .PC_clk(PC_clk), .IR_clk(ir_clk),
    .PC_ce(jmp_ce), .ls(ls), .RAM_ce(RAM_ce), .Registers_we(we), .OP_s(OP_s), .rst(in_2), .ir_rst(ir_rst),
    .immed_rst(immed_rst), .Immed_clk(immed_clk), .Registers_clk(Registers_clk), .ALUOP(ALUOP), .dsel_in(drce));

  // Other names for the same wires on the sheet: rst = in_2
endmodule

module CPU_Registers (
  input  [7:0] DReg_In,
  input  [1:0] ssel,
  input  we,
  input  clk,
  input  rst,
  input  [1:0] dsel,
  output [7:0] _0,
  output [7:0] _1,
  output [7:0] _2,
  output [7:0] _3,
  output [7:0] dreg,
  output [7:0] sreg
);

  wire demultiplexer_1_out0, demultiplexer_1_out1, demultiplexer_1_out2, demultiplexer_1_out3;

  Demultiplexer #(.select(2), .enable("false")) demultiplexer_1 (
    .out0(demultiplexer_1_out0), .out1(demultiplexer_1_out1), .out2(demultiplexer_1_out2),
    .out3(demultiplexer_1_out3), .in(we), .sel(dsel));
  Register register_1 (.D(DReg_In), .en(demultiplexer_1_out0), .Q(_0), .clk(clk), .clr(rst));
  Register register_2 (.D(DReg_In), .en(demultiplexer_1_out1), .Q(_1), .clk(clk), .clr(rst));
  Register register_3 (.D(DReg_In), .en(demultiplexer_1_out2), .Q(_2), .clk(clk), .clr(rst));
  Register register_4 (.D(DReg_In), .en(demultiplexer_1_out3), .Q(_3), .clk(clk), .clr(rst));
  Multiplexer #(.select(2), .width(8), .enable("false")) multiplexer_1 (
    .in0(_0), .in1(_1), .in2(_2), .in3(_3), .out(sreg), .sel(ssel));
  Multiplexer #(.select(2), .width(8), .enable("false")) multiplexer_2 (
    .in0(_0), .in1(_1), .in2(_2), .in3(_3), .out(dreg), .sel(dsel));
endmodule

module CPU_ID (
  input  Carry,
  input  A____B,
  input  [3:0] OPCode,
  input  CLK,
  input  rst,
  output immed_rst,
  output ir_rst,
  output PC_clk,
  output Immed_clk,
  output IR_clk,
  output [1:0] OP_s,
  output Registers_we,
  output PC_ce,
  output ls,
  output [2:0] ALUOP,
  output RAM_ce,
  output Registers_clk,
  output dsel_in
);

  wire _4th, _5th, _6th, ADD, AND, and_1_out, and_2_out, and_3_out, and_4_out, and_5_out, and_6_out,
       and_11_out, and_12_out, and_14_out, BE, BEZ, BNE, HLT, Immed, JMP, LOD, MOV, MOVI, NOP, NOT,
       not_1_out, OR, or_1_out, or_2_out, or_3_out, or_4_out, or_5_out, or_6_out, or_7_out, or_8_out,
       or_11_out, or_13_out, or_14_out, or_15_out, or_16_out, PC_1, PC_2, S, STR, SUB;
  wire [2:0] counter_1_q;

  Decoder #(.select(4), .enable("false")) decoder_1 (
    .out0(NOP), .out1(MOV), .out2(MOVI), .out3(LOD), .out4(STR), .out5(JMP), .out6(ADD), .out7(BE),
    .out8(BNE), .out9(BEZ), .out10(SUB), .out11(S), .out12(AND), .out13(OR), .out14(NOT), .out15(HLT),
    .sel(OPCode));
  Counter #(.width(3), .max('h7)) counter_1 (.Q(counter_1_q), .clk(CLK), .clr(rst));  // open: load, D, count, carry
  Decoder #(.select(3), .enable("false")) decoder_2 (
    .out0(PC_1), .out1(IR_clk), .out2(PC_2), .out3(Immed), .out4(_4th), .out5(_5th), .out6(_6th),
    .out7(Registers_clk), .sel(counter_1_q));
  and and_1 (and_1_out, BE, A____B);
  and and_2 (and_2_out, BNE, ~A____B);  // AND_Gate
  and and_3 (and_3_out, BEZ, A____B);
  or or_1 (or_1_out, MOVI, LOD, STR, JMP, BE, BNE, BEZ, S);
  and and_4 (and_4_out, LOD, _6th);
  or or_2 (or_2_out, BEZ, BNE, BE);
  or or_3 (or_3_out, JMP, and_1_out, and_2_out, and_3_out);
  or or_4 (or_4_out, LOD, STR);
  or or_5 (or_5_out, LOD, MOVI);
  and and_5 (and_5_out, PC_2, or_1_out);
  not not_1 (not_1_out, or_1_out);
  and and_6 (and_6_out, or_1_out, ~or_2_out);  // AND_Gate
  and and_7 (PC_ce, or_6_out, or_3_out);
  or or_6 (or_6_out, _4th, _5th, _6th);
  or or_7 (or_7_out, _4th, _5th, _6th, Registers_clk);
  and and_8 (ls, or_7_out, or_4_out);
  and and_9 (RAM_ce, _5th, STR);
  and and_10 (dsel_in, or_7_out, or_5_out);
  and and_11 (and_11_out, Immed, or_1_out);
  or or_8 (or_8_out, not_1_out, or_2_out);
  and and_12 (and_12_out, or_3_out, _5th);
  or or_9 (immed_rst, rst, PC_1);
  or or_10 (ir_rst, rst, Registers_clk);
  and and_13 (PC_clk, ~HLT, or_11_out);  // AND_Gate
  or or_11 (or_11_out, PC_1, and_5_out, and_12_out);
  or or_12 (Immed_clk, and_4_out, and_11_out);
  assign OP_s = BEZ ? 2'b10 : 2'bz;  // Controlled_Buffer controlled_buffer_1
  assign OP_s = and_6_out ? 2'b01 : 2'bz;  // Controlled_Buffer controlled_buffer_2
  assign OP_s = or_8_out ? 2'b00 : 2'bz;  // Controlled_Buffer controlled_buffer_3
  or or_13 (or_13_out, ADD, SUB);
  or or_14 (or_14_out, OR, NOT, S, MOV, AND, LOD, MOVI);
  and and_14 (and_14_out, or_13_out, Carry);
  and and_15 (Registers_we, or_14_out, ~and_14_out);  // AND_Gate
  assign ALUOP = or_15_out ? 3'b000 : 3'bz;  // Controlled_Buffer controlled_buffer_4
  or or_15 (or_15_out, NOP, MOV, MOVI, LOD, STR, JMP, HLT);
  assign ALUOP = ADD ? 3'b001 : 3'bz;  // Controlled_Buffer controlled_buffer_5
  assign ALUOP = SUB ? 3'b010 : 3'bz;  // Controlled_Buffer controlled_buffer_6
  assign ALUOP = or_16_out ? 3'b011 : 3'bz;  // Controlled_Buffer controlled_buffer_7
  or or_16 (or_16_out, BEZ, BNE, BE);
  assign ALUOP = S ? 3'b100 : 3'bz;  // Controlled_Buffer controlled_buffer_8
  assign ALUOP = AND ? 3'b101 : 3'bz;  // Controlled_Buffer controlled_buffer_9
  assign ALUOP = OR ? 3'b110 : 3'bz;  // Controlled_Buffer controlled_buffer_10
  assign ALUOP = NOT ? 3'b111 : 3'bz;  // Controlled_Buffer controlled_buffer_11

  // Other names for the same wires on the sheet: IR_1 = IR_clk; Registers = Registers_clk
endmodule

module CPU_ALU (
  input  [7:0] s,
  input  [7:0] d,
  input  [2:0] in_3,
  output Carry,
  output A___B,
  output [7:0] Out
);

  wire adder_1_cout, subtractor_1_bout;
  wire [7:0] adder_1_out, and_1_out, multiplexer_1_out, not_1_out, or_1_out, shifter_1_out, shifter_2_out,
       subtractor_1_out;

  assign and_1_out = s & d;  // AND_Gate and_1, 8 bits wide
  assign or_1_out = s | d;  // OR_Gate or_1, 8 bits wide
  assign not_1_out = ~s;  // NOT_Gate not_1, 8 bits wide
  Adder adder_1 (.a(s), .b(d), .out(adder_1_out), .cout(adder_1_cout));  // open: cin
  Subtractor subtractor_1 (.a(s), .b(d), .out(subtractor_1_out), .bout(subtractor_1_bout));  // open: bin
  Comparator comparator_1 (.a(s), .b(d), .eq(A___B));  // open: gt, lt
  Shifter shifter_1 (.in(s), .\dist (d[2:0]), .out(shifter_1_out));
  Multiplexer #(.width(8), .enable("false")) multiplexer_1 (
    .in0(shifter_1_out), .in1(shifter_2_out), .out(multiplexer_1_out), .sel(d[3]));
  Shifter #(.shift("lr")) shifter_2 (.in(s), .\dist (d[2:0]), .out(shifter_2_out));
  Multiplexer #(.select(3), .width(8), .enable("false")) multiplexer_2 (
    .in0(d), .in1(adder_1_out), .in2(subtractor_1_out), .in3({8{1'b0}}), .in4(multiplexer_1_out),
    .in5(and_1_out), .in6(or_1_out), .in7(not_1_out), .out(Out), .sel(in_3));
  Multiplexer #(.select(3), .enable("false")) multiplexer_3 (
    .in0(adder_1_cout), .in1(subtractor_1_bout), .in2(1'b0), .in3(1'b0), .in4(1'b0), .in5(1'b0), .in6(1'b0),
    .in7(1'b0), .out(Carry), .sel(in_3));
endmodule
