// Logisim project RAM.circ as structural Verilog: 1 circuit, main circuit main
module main (
  input  [15:0] StoreData,
  input  [15:0] Address,
  input  Store,
  input  Clear,
  output [15:0] out_5
);

  wire not_1_out, not_2_out;
  wire [14:0] adder_1_out, multiplexer_1_out;

  assign out_5[15:8] = Store ? StoreData[15:8] : 8'bz;  // Controlled_Buffer controlled_buffer_1
  Adder #(.width(15)) adder_1 (.a(Address[15:1]), .b(15'h1), .out(adder_1_out));  // open: cin, cout
  Multiplexer #(.width(15), .enable("false")) multiplexer_1 (
    .in0(Address[15:1]), .in1(adder_1_out), .out(multiplexer_1_out), .sel(Address[0]));
  assign out_5[7:0] = Store ? StoreData[7:0] : 8'bz;  // Controlled_Buffer controlled_buffer_2
  not not_1 (not_1_out, Store);
  not not_2 (not_2_out, Store);
  RAM #(.addrWidth(15), .bus("asynch")) ram_1 (
    .addr(Address[15:1]), .data(out_5[7:0]), .ld(not_1_out), .clr(Clear));  // open: sel
  RAM #(.addrWidth(15), .bus("asynch")) ram_2 (
    .addr(multiplexer_1_out), .data(out_5[15:8]), .ld(not_2_out), .clr(Clear));  // open: sel
endmodule
