// Logisim project TEST.circ as structural Verilog
module main (
  input  [3:0] in_1,
  input  [3:0] in_2,
  input  [3:0] in_3,
  input  [3:0] in_4
);

  wire and_1_out, button_1_out, clock_1_out, counter_1_carry, counter_2_carry, counter_3_carry,
       counter_4_carry, decoder_1_out0, decoder_1_out1, decoder_1_out2, decoder_1_out3, decoder_1_out4,
       decoder_1_out5, decoder_1_out6, decoder_1_out7, decoder_1_out8, decoder_1_out9, decoder_1_out10,
       decoder_1_out11, decoder_1_out12, decoder_1_out13, decoder_1_out14, decoder_1_out15, fowading_3_rs_rd,
       fowading_3_rt_rd, nor_1_out;
  wire [3:0] counter_1_q, counter_2_q, counter_3_q, counter_4_q, fowading_1_rs_rd;

  Clock clock_1 (.out(clock_1_out));
  and and_1 (and_1_out, clock_1_out, ~counter_4_carry);  // AND_Gate
  Counter #(.width(4), .max('hf)) counter_1 (
    .Q(counter_1_q), .carry(counter_1_carry), .clk(and_1_out));  // open: load, D, count, clr
  Counter #(.width(4), .max('hf)) counter_2 (
    .Q(counter_2_q), .carry(counter_2_carry), .clk(counter_1_carry));  // open: load, D, count, clr
  Counter #(.width(4), .max('hf)) counter_3 (
    .Q(counter_3_q), .carry(counter_3_carry), .clk(counter_2_carry));  // open: load, D, count, clr
  Counter #(.width(4), .max('hf)) counter_4 (
    .Q(counter_4_q), .carry(counter_4_carry), .clk(counter_3_carry));  // open: load, D, count, clr
  Fowading fowading_1 (
    .rs(counter_1_q), .rt(counter_2_q), .rd(counter_3_q), .in_4(button_1_out), .rs_rd(fowading_1_rs_rd[0]),
    .rt_rd(fowading_1_rs_rd[1]));
  Fowading fowading_2 (
    .rs(counter_1_q), .rt(counter_2_q), .rd(counter_4_q), .in_4(button_1_out), .rs_rd(fowading_1_rs_rd[2]),
    .rt_rd(fowading_1_rs_rd[3]));
  Button button_1 (.out(button_1_out));
  Fowading fowading_3 (
    .rs(in_1), .rt(in_2), .rd(in_3), .in_4(1'b1), .rs_rd(fowading_3_rs_rd), .rt_rd(fowading_3_rt_rd));
  Fowading fowading_4 (.rs(in_1), .rt(in_2), .rd(in_4), .in_4(nor_1_out));  // open: rs_rd, rt_rd
  nor nor_1 (nor_1_out, fowading_3_rs_rd, fowading_3_rt_rd);
  Decoder #(.select(4), .enable("false")) decoder_1 (
    .out0(decoder_1_out0), .out1(decoder_1_out1), .out2(decoder_1_out2), .out3(decoder_1_out3),
    .out4(decoder_1_out4), .out5(decoder_1_out5), .out6(decoder_1_out6), .out7(decoder_1_out7),
    .out8(decoder_1_out8), .out9(decoder_1_out9), .out10(decoder_1_out10), .out11(decoder_1_out11),
    .out12(decoder_1_out12), .out13(decoder_1_out13), .out14(decoder_1_out14), .out15(decoder_1_out15),
    .sel(fowading_1_rs_rd));
  Counter #(.width(16), .max('hffff)) counter_5 (.clk(decoder_1_out0));  // open: load, D, count, Q, carry, clr
  Counter #(.width(16), .max('hffff)) counter_6 (.clk(decoder_1_out15));  // open: load, D, count, Q, carry, clr
  Counter #(.width(16), .max('hffff)) counter_7 (.clk(decoder_1_out1));  // open: load, D, count, Q, carry, clr
  Counter #(.width(16), .max('hffff)) counter_8 (.clk(decoder_1_out14));  // open: load, D, count, Q, carry, clr
  Counter #(.width(16), .max('hffff)) counter_9 (.clk(decoder_1_out2));  // open: load, D, count, Q, carry, clr
  Counter #(.width(16), .max('hffff)) counter_10 (.clk(decoder_1_out3));  // open: load, D, count, Q, carry, clr
  Counter #(.width(16), .max('hffff)) counter_11 (.clk(decoder_1_out12));  // open: load, D, count, Q, carry, clr
  Counter #(.width(16), .max('hffff)) counter_12 (.clk(decoder_1_out13));  // open: load, D, count, Q, carry, clr
  Counter #(.width(16), .max('hffff)) counter_13 (.clk(decoder_1_out5));  // open: load, D, count, Q, carry, clr
  Counter #(.width(16), .max('hffff)) counter_14 (.clk(decoder_1_out4));  // open: load, D, count, Q, carry, clr
  Counter #(.width(16), .max('hffff)) counter_15 (.clk(decoder_1_out11));  // open: load, D, count, Q, carry, clr
  Counter #(.width(16), .max('hffff)) counter_16 (.clk(decoder_1_out10));  // open: load, D, count, Q, carry, clr
  Counter #(.width(16), .max('hffff)) counter_17 (.clk(decoder_1_out6));  // open: load, D, count, Q, carry, clr
  Counter #(.width(16), .max('hffff)) counter_18 (.clk(decoder_1_out9));  // open: load, D, count, Q, carry, clr
  Counter #(.width(16), .max('hffff)) counter_19 (.clk(decoder_1_out7));  // open: load, D, count, Q, carry, clr
  Counter #(.width(16), .max('hffff)) counter_20 (.clk(decoder_1_out8));  // open: load, D, count, Q, carry, clr

  // Notes on the sheet:
  //   196f 0c5b 0275 00fd 0c40 00e0 00e0 0000 0010 0000 0000 00e0 0000 001d 00ee 0275
endmodule

module Fowading (
  input  [3:0] rs,
  input  [3:0] rt,
  input  [3:0] rd,
  input  in_4,
  output rs_rd,
  output rt_rd
);

  wire comparator_1_eq, comparator_2_eq;

  Comparator #(.width(4), .mode("unsigned")) comparator_1 (.a(rs), .b(rd), .eq(comparator_1_eq));  // open: gt, lt
  Comparator #(.width(4), .mode("unsigned")) comparator_2 (.a(rt), .b(rd), .eq(comparator_2_eq));  // open: gt, lt
  assign rt_rd = in_4 ? comparator_2_eq : 1'bz;  // Controlled_Buffer controlled_buffer_1
  assign rs_rd = in_4 ? comparator_1_eq : 1'bz;  // Controlled_Buffer controlled_buffer_2
endmodule
