// Logisim project 00.circ as structural Verilog
module main (
);

  CPU cpu_1 ();  // open: rst
  Processor processor_1 ();
  RAM ram_1 ();  // open: Address, Data_i, sel, str, out_5
  Disk disk_1 ();  // open: in_1, in_2, out_3
endmodule

module RAM (
  input  [15:0] Address,
  input  [15:0] Data_i,
  input  sel,
  input  str,
  output [15:0] out_5
);

  wire and_1_out, not_1_out;

  assign out_5 = and_1_out ? Data_i : 16'bz;  // Controlled_Buffer controlled_buffer_1
  and and_1 (and_1_out, not_1_out, sel);
  not not_1 (not_1_out, str);
  RAM_part #(.addrWidth(16), .dataWidth(16), .bus("asynch")) ram_1 (
    .addr(Address), .data(out_5), .sel(sel), .ld(not_1_out));  // open: clr
endmodule

module Disk (
  input  [23:0] in_1,
  input  in_2,
  output [7:0] out_3
);

  ROM #(.addrWidth(24)) rom_1 (.addr(in_1), .data(out_3), .sel(in_2));
endmodule

module CPU (
  input  rst
);

  wire _0, clock_1_out, regfile_1_stackoverflow, undriven, undriven_2;
  wire [1:0] ry_1_out_3;
  wire [15:0] regfile_1_ac, regfile_1_ja, regfile_1_m1, regfile_1_m2, regfile_1_ma, regfile_1_md,
       regfile_1_sp;

  Ry ry_1 (.clk(clock_1_out), .rst(rst), .out_3(ry_1_out_3));
  Clock clock_1 (.out(clock_1_out));
  Decoder #(.select(2), .enable("false")) decoder_1 (.out0(_0), .sel(ry_1_out_3));  // open: out1, out2, out3
  PC pc_1 (.clk(_0));  // open: JumpAddr, Int_RetAddr, opcode, rst, out_6
  Regfile regfile_1 (
    .rst(undriven_2), .AC(regfile_1_ac), .M1(regfile_1_m1), .M2(regfile_1_m2), .MD(regfile_1_md),
    .MA(regfile_1_ma), .JA(regfile_1_ja), .SP(regfile_1_sp), .clk_3(undriven), .POP(1'b0), .PUSH(1'b0),
    .STACKADD(1'b0), .STACKSUB(1'b0), .StackOverflow(regfile_1_stackoverflow));  // open: regval1, w1we, w1sel, regval2, w2we, w2sel, clk_4, out_21
  Stack stack_1 (
    .Stack_Pionter(regfile_1_sp), .in_2(regfile_1_ac), .in_3(regfile_1_m1), .in_4(regfile_1_m2),
    .in_5(regfile_1_md), .in_6(regfile_1_ma), .in_7(regfile_1_ja), .PUSH(1'b0), .clk_3(undriven),
    .rst(undriven_2), .StackOberflow(regfile_1_stackoverflow));  // open: in_9, out_13
endmodule

module PC (
  input  [15:0] JumpAddr,
  input  [15:0] Int_RetAddr,
  input  clk,
  input  rst,
  input  [4:0] opcode,
  output [15:0] out_6
);

  wire [1:0] multiplexer_1_out, multiplexer_2_out;
  wire [15:0] adder_1_out, multiplexer_3_out;

  Adder #(.width(16)) adder_1 (.a(out_6), .b(16'h1), .out(adder_1_out));  // open: cin, cout
  Multiplexer #(.select(3), .width(2), .enable("false")) multiplexer_1 (
    .in0(2'b00), .in1(2'b00), .in2(2'b00), .in3(2'b00), .in4(2'b01), .in5(2'b00), .in6(2'b00),
    .in7(multiplexer_2_out), .out(multiplexer_1_out), .sel(opcode[4:2]));
  Multiplexer #(.select(2), .width(2), .enable("false")) multiplexer_2 (
    .in0(2'b00), .in1(2'b00), .in2(2'b00), .in3(2'b11), .out(multiplexer_2_out), .sel(opcode[1:0]));
  Multiplexer #(.select(2), .width(16), .enable("false")) multiplexer_3 (
    .in0(adder_1_out), .in1(JumpAddr), .in2(Int_RetAddr), .in3(out_6), .out(multiplexer_3_out),
    .sel(multiplexer_1_out));
  Register #(.width(16)) register_1 (.D(multiplexer_3_out), .Q(out_6), .clk(clk), .clr(rst));  // open: en
endmodule

module Ry (
  input  clk,
  input  rst,
  output [1:0] out_3
);

  wire [1:0] counter_1_q;

  Counter #(.width(1), .max('h1)) counter_1 (.Q(counter_1_q[0]), .clk(clk), .clr(rst));  // open: load, D, count, carry
  Counter #(.width(1), .max('h1), .trigger("falling")) counter_2 (
    .Q(counter_1_q[1]), .clk(clk), .clr(rst));  // open: load, D, count, carry
  ROM #(.addrWidth(2), .dataWidth(2)) rom_1 (.addr(counter_1_q), .data(out_3));  // open: sel
endmodule

module Decoder_1st (
  input  [15:0] in_1,
  output [4:0] opcode,
  output [2:0] ssel
);

  wire [2:0] bit_extender_1_out, multiplexer_1_out, multiplexer_2_out;

  Multiplexer #(.select(2), .width(3), .enable("false")) multiplexer_1 (
    .in0(3'b000), .in1(in_1[10:8]), .in2(in_1[10:8]), .in3(3'b000), .out(multiplexer_1_out), .sel(in_1[12:11]));
  Multiplexer #(.select(2), .width(3), .enable("false")) multiplexer_2 (
    .in0(3'b000), .out(multiplexer_2_out), .sel(in_1[12:11]));  // open: in1, in2, in3
  assign bit_extender_1_out = {{1{1'b0}}, in_1[10:9]};  // Bit_Extender bit_extender_1
  Multiplexer #(.select(3), .width(3), .enable("false")) multiplexer_3 (
    .in0(3'b000), .in1(multiplexer_1_out), .in2(bit_extender_1_out), .in3(bit_extender_1_out),
    .in4(multiplexer_2_out), .in5(3'b000), .in6(3'b011), .in7(3'b000), .out(ssel), .sel(in_1[15:13]));

  assign opcode = in_1[15:11];

  // Other names for the same wires on the sheet: op2[1:0] = in_1[12:11]; op1[2:0] = in_1[15:13]
endmodule

module Regfile (
  input  [15:0] regval1,
  input  w1we,
  input  [2:0] w1sel,
  input  [15:0] regval2,
  input  w2we,
  input  [2:0] w2sel,
  input  clk_3,
  input  clk_4,
  input  rst,
  input  POP,
  input  PUSH,
  input  STACKADD,
  input  STACKSUB,
  output [15:0] AC,
  output [15:0] M1,
  output [15:0] M2,
  output [15:0] MD,
  output [15:0] MA,
  output [15:0] JA,
  output [15:0] SP,
  output [15:0] out_21,
  output StackOverflow
);

  wire and_1_out, and_2_out, comparator_1_eq, comparator_2_eq, multiplexer_1_out, multiplexer_3_out,
       multiplexer_4_out, not_1_out, or_1_out, or_2_out;
  wire [15:0] adder_1_out, demultiplexer_1_out0, demultiplexer_1_out1, demultiplexer_1_out2,
       demultiplexer_1_out3, demultiplexer_1_out4, demultiplexer_1_out5, demultiplexer_1_out6,
       demultiplexer_1_out7, multiplexer_2_out, multiplexer_5_out;

  Demultiplexer #(.select(3), .width(16)) demultiplexer_1 (
    .out0(demultiplexer_1_out0), .out1(demultiplexer_1_out1), .out2(demultiplexer_1_out2),
    .out3(demultiplexer_1_out3), .out4(demultiplexer_1_out4), .out5(demultiplexer_1_out5),
    .out6(demultiplexer_1_out6), .out7(demultiplexer_1_out7), .in(regval1), .sel(w1sel), .en(w1we));
  Demultiplexer #(.select(3), .width(16)) demultiplexer_2 (
    .out0(demultiplexer_1_out0), .out1(demultiplexer_1_out1), .out2(demultiplexer_1_out2),
    .out3(demultiplexer_1_out3), .out4(demultiplexer_1_out4), .out5(demultiplexer_1_out5),
    .out6(demultiplexer_1_out6), .out7(demultiplexer_1_out7), .in(regval2), .sel(w2sel), .en(w2we));
  or or_1 (or_1_out, POP, PUSH, STACKADD, STACKSUB);
  not not_1 (not_1_out, POP);
  Multiplexer #(.enable("false")) multiplexer_1 (.in0(clk_3), .in1(clk_4), .out(multiplexer_1_out), .sel(not_1_out));
  Multiplexer #(.width(16), .enable("false")) multiplexer_2 (
    .in0(demultiplexer_1_out6), .in1(adder_1_out), .out(multiplexer_2_out), .sel(or_1_out));
  Multiplexer #(.enable("false")) multiplexer_3 (.in0(clk_3), .in1(clk_4), .out(multiplexer_3_out), .sel(POP));
  Multiplexer #(.enable("false")) multiplexer_4 (.in0(PUSH), .in1(POP), .out(multiplexer_4_out), .sel(1'b0));
  Register #(.width(16)) u_AC (.D(demultiplexer_1_out0), .Q(AC), .clk(multiplexer_1_out), .clr(rst));  // open: en
  Register #(.width(16)) D1 (.D(demultiplexer_1_out1), .Q(M1), .clk(multiplexer_1_out), .clr(rst));  // open: en
  Register #(.width(16)) D2 (.D(demultiplexer_1_out2), .Q(M2), .clk(multiplexer_1_out), .clr(rst));  // open: en
  Register #(.width(16)) u_MD (.D(demultiplexer_1_out3), .Q(MD), .clk(multiplexer_1_out), .clr(rst));  // open: en
  Register #(.width(16)) u_MA (.D(demultiplexer_1_out4), .Q(MA), .clk(multiplexer_1_out), .clr(rst));  // open: en
  Register #(.width(16)) u_JA (.D(demultiplexer_1_out5), .Q(JA), .clk(multiplexer_1_out), .clr(rst));  // open: en
  Register #(.width(16)) u_SP (.D(multiplexer_2_out), .Q(SP), .clk(multiplexer_3_out), .clr(rst));  // open: en
  Register #(.width(16)) register_1 (
    .D(demultiplexer_1_out7), .Q(out_21), .clk(multiplexer_1_out), .clr(rst));  // open: en
  Comparator #(.width(16), .mode("unsigned")) comparator_1 (
    .a(SP), .b({16{1'b0}}), .eq(comparator_1_eq));  // open: gt, lt
  Comparator #(.width(16), .mode("unsigned")) comparator_2 (
    .a(SP), .b({16{1'b1}}), .eq(comparator_2_eq));  // open: gt, lt
  Multiplexer #(.width(16), .enable("false")) multiplexer_5 (
    .in0(16'h1), .in1({16{1'b1}}), .out(multiplexer_5_out), .sel(or_2_out));
  or or_2 (or_2_out, multiplexer_4_out, STACKSUB);
  Adder #(.width(16)) adder_1 (.a(SP), .b(multiplexer_5_out), .out(adder_1_out));  // open: cin, cout
  and and_1 (and_1_out, comparator_1_eq, POP);
  and and_2 (and_2_out, multiplexer_4_out, comparator_2_eq);
  or or_3 (StackOverflow, and_2_out, and_1_out);

  // Notes on the sheet:
  //   生长方向
  //   0 - 1 +(StackAddress)
endmodule

module Stack (
  input  [15:0] Stack_Pionter,
  input  [15:0] in_2,
  input  [15:0] in_3,
  input  [15:0] in_4,
  input  [15:0] in_5,
  input  [15:0] in_6,
  input  [15:0] in_7,
  input  PUSH,
  input  [2:0] in_9,
  input  clk_3,
  input  StackOberflow,
  input  rst,
  output [15:0] out_13
);

  wire and_1_out, and_2_out;
  wire [15:0] multiplexer_1_out;

  and and_1 (and_1_out, clk_3, PUSH);
  Multiplexer #(.select(3), .width(16), .enable("false")) multiplexer_1 (
    .in0(in_2), .in1(in_3), .in2(in_4), .in3(in_5), .in4(in_6), .in5(in_7), .out(multiplexer_1_out),
    .sel(in_9));  // open: in6, in7
  and and_2 (and_2_out, and_1_out, StackOberflow);
  RAM_part #(.addrWidth(16), .dataWidth(16), .bus("separate")) ram_1 (
    .addr(Stack_Pionter), .din(multiplexer_1_out), .data(out_13), .str(PUSH), .clk(and_2_out), .clr(rst));  // open: sel, ld
endmodule
