// Logisim project 20160430.circ as structural Verilog
module Regfile (
  input  [15:0] in_1,
  input  in_2,
  input  [2:0] in_3,
  input  [15:0] in_4,
  input  in_5,
  input  [2:0] in_6,
  input  clk_3,
  input  clk_4,
  input  rst,
  input  [4:0] opcode,
  input  [5:0] funct,
  output [15:0] AC,
  output [15:0] D1,
  output [15:0] D2,
  output [15:0] MD,
  output [15:0] MA,
  output [15:0] JA,
  output [15:0] SP,
  output StackOverflow
);

  wire adder_1_cout, and_1_out, and_2_out, and_3_out, and_4_out, and_5_out, and_6_out, and_7_out, and_8_out,
       and_9_out, and_10_out, decoder_1_out28, decoder_2_out0, decoder_2_out1, decoder_2_out3, or_1_out,
       or_2_out, or_3_out, subtractor_1_bout;
  wire [15:0] adder_1_out, demultiplexer_1_out0, demultiplexer_1_out1, demultiplexer_1_out2,
       demultiplexer_1_out3, demultiplexer_1_out4, demultiplexer_1_out5, demultiplexer_1_out6,
       multiplexer_1_out, multiplexer_2_out, subtractor_1_out;

  Demultiplexer #(.select(3), .width(16)) demultiplexer_1 (
    .out0(demultiplexer_1_out0), .out1(demultiplexer_1_out1), .out2(demultiplexer_1_out2),
    .out3(demultiplexer_1_out3), .out4(demultiplexer_1_out4), .out5(demultiplexer_1_out5),
    .out6(demultiplexer_1_out6), .in(in_1), .sel(in_3), .en(in_2));  // open: out7
  Demultiplexer #(.select(3), .width(16)) demultiplexer_2 (
    .out0(demultiplexer_1_out0), .out1(demultiplexer_1_out1), .out2(demultiplexer_1_out2),
    .out3(demultiplexer_1_out3), .out4(demultiplexer_1_out4), .out5(demultiplexer_1_out5),
    .out6(demultiplexer_1_out6), .in(in_4), .sel(in_6), .en(in_5));  // open: out7
  Decoder_part #(.select(5), .disabled(0), .enable("false")) decoder_1 (
    .out28(decoder_1_out28), .sel(opcode));  // open: out0, out1, out2, out3, out4, out5, out6, out7, out8, out9, out10, out11, out12, out13, out14, out15, out16, out17, out18, out19, out20, out21, out22, out23, out24, out25, out26, out27, out29, out30, out31
  Decoder_part #(.select(2), .enable("false")) decoder_2 (
    .out0(decoder_2_out0), .out1(decoder_2_out1), .out3(decoder_2_out3), .sel(funct[1:0]));  // open: out2
  and and_1 (and_1_out, and_2_out, clk_4);
  and and_2 (and_2_out, decoder_1_out28, decoder_2_out0);
  and and_3 (and_3_out, decoder_1_out28, decoder_2_out1);
  and and_4 (and_4_out, decoder_1_out28, decoder_2_out3);
  and and_5 (and_5_out, and_3_out, clk_3);
  Multiplexer #(.width(16), .enable("false")) multiplexer_1 (
    .in0(demultiplexer_1_out6), .in1(multiplexer_2_out), .out(multiplexer_1_out), .sel(decoder_1_out28));
  and and_6 (and_6_out, 1'b0, and_2_out);
  Register #(.width(16)) u_AC (.D(demultiplexer_1_out0), .Q(AC), .clk(or_2_out), .clr(rst));  // open: en
  Register #(.width(16)) u_D1 (.D(demultiplexer_1_out1), .Q(D1), .clk(or_2_out), .clr(rst));  // open: en
  Register #(.width(16)) u_D2 (.D(demultiplexer_1_out2), .Q(D2), .clk(or_2_out), .clr(rst));  // open: en
  Register #(.width(16)) u_MD (.D(demultiplexer_1_out3), .Q(MD), .clk(or_2_out), .clr(rst));  // open: en
  Register #(.width(16)) u_MA (.D(demultiplexer_1_out4), .Q(MA), .clk(or_2_out), .clr(rst));  // open: en
  Register #(.width(16)) u_JA (.D(demultiplexer_1_out5), .Q(JA), .clk(or_2_out), .clr(rst));  // open: en
  Register #(.width(16)) u_SP (.D(multiplexer_1_out), .Q(SP), .clk(or_1_out), .clr(rst));  // open: en
  or or_1 (or_1_out, and_7_out, and_8_out);
  and and_7 (and_7_out, clk_3, and_2_out);
  and and_8 (and_8_out, clk_4, and_3_out);
  or or_2 (or_2_out, clk_4, and_5_out, and_1_out);
  Adder #(.width(16)) adder_1 (.a(SP), .b(16'h1), .out(adder_1_out), .cout(adder_1_cout));  // open: cin
  or or_3 (or_3_out, and_6_out, and_4_out);
  Subtractor #(.width(16)) subtractor_1 (
    .a(SP), .b(16'h1), .out(subtractor_1_out), .bout(subtractor_1_bout));  // open: bin
  and and_9 (and_9_out, subtractor_1_bout, or_3_out);
  and and_10 (and_10_out, adder_1_cout, ~or_3_out);  // AND_Gate
  Multiplexer #(.width(16), .enable("false")) multiplexer_2 (
    .in0(adder_1_out), .in1(subtractor_1_out), .out(multiplexer_2_out), .sel(or_3_out));
  or or_4 (StackOverflow, and_9_out, and_10_out);

  // Notes on the sheet:
  //   1 PUSH-SUB  0-PUSH-ADD
  //   ---------------- STACK POINTER ----------------------------------------------------------------------
  //   PUSH 11100 00 xxxxxxxxx
  //   POP 11100 01 xxxxxxxxx
  //   SPADD 11100 10 xxxxxxxxx
  //   SPSUB11100 11 xxxxxxxxx
endmodule

module Decoder (
  input  [15:0] Instruction
);

  wire [15:0] bit_extender_1_out, bit_extender_2_out;

  assign bit_extender_1_out = {{10{Instruction[5]}}, Instruction[5:0]};  // Bit_Extender bit_extender_1
  Multiplexer #(.width(16), .disabled(0)) multiplexer_1 (
    .in0(bit_extender_1_out), .in1(bit_extender_2_out));  // open: out, sel, en
  assign bit_extender_2_out = {{8{Instruction[7]}}, Instruction[7:0]};  // Bit_Extender bit_extender_2
endmodule
