// Logisim project FPU_ro.circ as structural Verilog
module ADDSUB (
  input  Sub_mode,
  input  [31:0] A,
  input  [31:0] B,
  output [31:0] out_4
);

  wire adder_1_cout, bitfinder_1_found, realop_1_sub_2, realop_1_switch, subtractor_3_bout;
  wire [4:0] subreduce1_1_out_2;
  wire [7:0] adder_2_out, and_1_out, and_2_out, multiplexer_3_out, or_1_out, subtractor_1_out,
       subtractor_2_out, subtractor_5_out;
  wire [7:7] adder_2_cout, subtractor_1_bout, subtractor_2_bout;
  wire [22:0] and_3_out, multiplexer_5_out;
  wire [23:0] adder_1_out, multiplexer_4_out, shifter_1_out, shifter_2_out, subreduce1_1_out_3,
       subreduce2_1_out_3, subreduce4_1_out_3, subreduce8_1_out_3, subreduce16_1_out_3, subtractor_3_out,
       subtractor_4_out;
  wire [31:0] multiplexer_1_out, multiplexer_2_out, multiplexer_6_out;
  wire [31:31] xor_1_out;

  REALOP realop_1 (.ASIGN(A[31]), .BSIGN(B[31]), .SUB(Sub_mode), .SUB_2(realop_1_sub_2), .SWITCH(realop_1_switch));
  Multiplexer #(.width(32), .enable("false")) multiplexer_1 (
    .in0(A), .in1(B), .out(multiplexer_1_out), .sel(realop_1_switch));
  Multiplexer #(.width(32), .enable("false")) multiplexer_2 (
    .in0(B), .in1(A), .out(multiplexer_2_out), .sel(realop_1_switch));
  Subtractor subtractor_1 (
    .a(multiplexer_2_out[30:23]), .b(multiplexer_1_out[30:23]), .out(subtractor_1_out),
    .bout(subtractor_1_bout[7]));  // open: bin
  Multiplexer #(.width(8), .enable("false")) multiplexer_3 (
    .in0(multiplexer_1_out[30:23]), .in1(multiplexer_2_out[30:23]), .out(multiplexer_3_out),
    .sel(subtractor_2_bout[7]));
  Subtractor subtractor_2 (
    .a(multiplexer_1_out[30:23]), .b(multiplexer_2_out[30:23]), .out(subtractor_2_out),
    .bout(subtractor_2_bout[7]));  // open: bin
  assign and_1_out = subtractor_1_out & ~{8{subtractor_1_bout[7]}};  // AND_Gate and_1, 8 bits wide
  assign and_2_out = subtractor_2_out & ~{8{subtractor_2_bout[7]}};  // AND_Gate and_2, 8 bits wide
  Shifter #(.width(24), .shift("lr")) shifter_1 (
    .in({1'b1, multiplexer_2_out[22:0]}), .\dist (and_2_out[4:0]), .out(shifter_1_out));
  Shifter #(.width(24), .shift("lr")) shifter_2 (
    .in({1'b1, multiplexer_1_out[22:0]}), .\dist (and_1_out[4:0]), .out(shifter_2_out));
  Adder #(.width(24)) adder_1 (
    .a(shifter_2_out), .b(shifter_1_out), .out(adder_1_out), .cout(adder_1_cout));  // open: cin
  Subtractor #(.width(24)) subtractor_3 (
    .a(shifter_2_out), .b(shifter_1_out), .out(subtractor_3_out), .bout(subtractor_3_bout));  // open: bin
  Subtractor #(.width(24)) subtractor_4 (
    .a(shifter_1_out), .b(shifter_2_out), .out(subtractor_4_out));  // open: bin, bout
  Adder adder_2 (.a({8{1'b0}}), .b(multiplexer_3_out), .out(adder_2_out), .cin(adder_1_cout), .cout(adder_2_cout[7]));
  Multiplexer #(.width(24), .enable("false")) multiplexer_4 (
    .in0(subtractor_3_out), .in1(subtractor_4_out), .out(multiplexer_4_out), .sel(subtractor_3_bout));
  Multiplexer #(.width(23), .enable("false")) multiplexer_5 (
    .in0(adder_1_out[22:0]), .in1(adder_1_out[23:1]), .out(multiplexer_5_out), .sel(adder_1_cout));
  BitFinder #(.width(24)) bitfinder_1 (.in(multiplexer_4_out), .found(bitfinder_1_found));  // open: index
  SUBREDUCE16 subreduce16_1 (.in_1(multiplexer_4_out), .out_3(subreduce16_1_out_3), .out_2(subreduce1_1_out_2[4]));
  SUBREDUCE8 subreduce8_1 (.in_1(subreduce16_1_out_3), .out_3(subreduce8_1_out_3), .out_2(subreduce1_1_out_2[3]));
  SUBREDUCE4 subreduce4_1 (.in_1(subreduce8_1_out_3), .out_3(subreduce4_1_out_3), .out_2(subreduce1_1_out_2[2]));
  SUBREDUCE2 subreduce2_1 (.in_1(subreduce4_1_out_3), .out_3(subreduce2_1_out_3), .out_2(subreduce1_1_out_2[1]));
  SUBREDUCE1 subreduce1_1 (.in_1(subreduce2_1_out_3), .out_3(subreduce1_1_out_3), .out_2(subreduce1_1_out_2[0]));
  assign and_3_out = multiplexer_5_out & ~{23{adder_2_cout[7]}};  // AND_Gate and_3, 23 bits wide
  assign or_1_out = {8{adder_2_cout[7]}} | adder_2_out;  // OR_Gate or_1, 8 bits wide
  Multiplexer #(.width(32), .enable("false")) multiplexer_6 (
    .in0({32{1'b0}}), .in1({xor_1_out[31], subtractor_5_out, subreduce1_1_out_3[22:0]}),
    .out(multiplexer_6_out), .sel(bitfinder_1_found));
  Subtractor subtractor_5 (
    .a(multiplexer_3_out), .b({3'b000, subreduce1_1_out_2}), .out(subtractor_5_out));  // open: bin, bout
  xor xor_1 (xor_1_out[31], subtractor_3_bout, multiplexer_1_out[31]);
  Multiplexer #(.width(32), .enable("false")) multiplexer_7 (
    .in0({multiplexer_1_out[31], or_1_out, and_3_out}), .in1(multiplexer_6_out), .out(out_4),
    .sel(realop_1_sub_2));
endmodule

module REALOP (
  input  SUB,
  input  ASIGN,
  input  BSIGN,
  output SUB_2,
  output SWITCH
);

  wire xor_1_out;

  xor xor_1 (xor_1_out, ASIGN, BSIGN);
  xor xor_2 (SUB_2, SUB, xor_1_out);
  and and_1 (SWITCH, ASIGN, ~BSIGN, ~SUB);  // AND_Gate
endmodule

module SUBREDUCE16 (
  input  [23:0] in_1,
  output out_2,
  output [23:0] out_3
);

  wire bitfinder_1_found;

  Multiplexer #(.width(8), .enable("false")) multiplexer_1 (
    .in0(in_1[7:0]), .in1(in_1[23:16]), .out(out_3[23:16]), .sel(bitfinder_1_found));
  BitFinder #(.width(16)) bitfinder_1 (.in(in_1[23:8]), .found(bitfinder_1_found));  // open: index
  Multiplexer #(.width(8), .enable("false")) multiplexer_2 (
    .in0({8{1'b0}}), .in1(in_1[15:8]), .out(out_3[15:8]), .sel(bitfinder_1_found));
  Multiplexer #(.width(8), .enable("false")) multiplexer_3 (
    .in0({8{1'b0}}), .in1(in_1[7:0]), .out(out_3[7:0]), .sel(bitfinder_1_found));
  not not_1 (out_2, bitfinder_1_found);
endmodule

module SUBREDUCE8 (
  input  [23:0] in_1,
  output out_2,
  output [23:0] out_3
);

  wire bitfinder_1_found;
  wire [4:4] pull_resistor_1_node;

  BitFinder bitfinder_1 (.in(in_1[23:16]), .found(bitfinder_1_found));  // open: index
  Pull_Resistor pull_resistor_1 (.node(pull_resistor_1_node[4]));
  not not_1 (out_2, bitfinder_1_found);
  Shifter #(.width(24)) shifter_1 (
    .in(in_1), .\dist ({pull_resistor_1_node[4], out_2, {3{pull_resistor_1_node[4]}}}), .out(out_3));
endmodule

module SUBREDUCE4 (
  input  [23:0] in_1,
  output out_2,
  output [23:0] out_3
);

  wire bitfinder_1_found;
  wire [4:4] pull_resistor_1_node;

  BitFinder #(.width(4)) bitfinder_1 (.in(in_1[23:20]), .found(bitfinder_1_found));  // open: index
  Pull_Resistor pull_resistor_1 (.node(pull_resistor_1_node[4]));
  not not_1 (out_2, bitfinder_1_found);
  Shifter #(.width(24)) shifter_1 (
    .in(in_1), .\dist ({{2{pull_resistor_1_node[4]}}, out_2, {2{pull_resistor_1_node[4]}}}), .out(out_3));
endmodule

module SUBREDUCE2 (
  input  [23:0] in_1,
  output out_2,
  output [23:0] out_3
);

  wire bitfinder_1_found;
  wire [4:4] pull_resistor_1_node;

  BitFinder #(.width(2)) bitfinder_1 (.in(in_1[23:22]), .found(bitfinder_1_found));  // open: index
  Pull_Resistor pull_resistor_1 (.node(pull_resistor_1_node[4]));
  not not_1 (out_2, bitfinder_1_found);
  Shifter #(.width(24)) shifter_1 (
    .in(in_1), .\dist ({{3{pull_resistor_1_node[4]}}, out_2, pull_resistor_1_node[4]}), .out(out_3));
endmodule

module SUBREDUCE1 (
  input  [23:0] in_1,
  output out_2,
  output [23:0] out_3
);

  wire [4:4] pull_resistor_1_node;

  Pull_Resistor pull_resistor_1 (.node(pull_resistor_1_node[4]));
  not not_1 (out_2, in_1[23]);
  Shifter #(.width(24)) shifter_1 (.in(in_1), .\dist ({{4{pull_resistor_1_node[4]}}, out_2}), .out(out_3));
endmodule
