// Logisim project lambdaCPU v4.circ as structural Verilog: 23 circuits, main circuit test circuit
module test_circuit (
);

  wire clock_1_out, main_1_clk_, main_1_ld, main_1_ram_sel, main_1_str;
  wire [31:0] main_1_program_addr, main_1_ram_addr, main_1_ram_data_in, ram_1_data, rom_1_data;

  Clock clock_1 (.out(clock_1_out));
  main main_1 (
    .clk_out(clock_1_out), .ram_sel(main_1_ram_sel), .str(main_1_str), .clk_(main_1_clk_), .ld(main_1_ld),
    .ram_addr(main_1_ram_addr), .ram_data_in(main_1_ram_data_in), .ram_data_out(ram_1_data),
    .program_addr(main_1_program_addr), .program_data(rom_1_data));
  RAM #(.addrWidth(24), .dataWidth(32), .bus("separate")) ram_1 (
    .addr(main_1_ram_addr[23:0]), .din(main_1_ram_data_in), .data(ram_1_data), .str(main_1_str),
    .sel(main_1_ram_sel), .clk(main_1_clk_), .ld(main_1_ld));  // open: clr
  ROM #(.addrWidth(24), .dataWidth(32)) rom_1 (.addr(main_1_program_addr[23:0]), .data(rom_1_data));  // open: sel

  // Notes on the sheet:
  //   contents of rom_1 (hex, n*v repeats v):
  //   34020126 411822 1c60fffe 20210001 ac010000
endmodule

module main (
  input  [31:0] program_data,
  input  [31:0] ram_data_out,
  output clk_out,
  output [31:0] program_addr,
  output ram_sel,
  output str,
  output clk_,
  output [31:0] ram_addr,
  output [31:0] ram_data_in,
  output ld
);

  wire and_1_out, bit_extender_1_out, branch_predictor_1_branch_taken,
       branch_unit_1_branch_correction_needed, decoder_1_out1, decoder_1_out2, ex_mem_1_prediction_2,
       ex_mem_1_wb_en_2, ex_mem_1_wb_mux_2, falling_edge_1_out_2, id_ex_1_branch_prediction_2,
       id_ex_1_wb_enable_2, id_ex_1_wb_mux_2, instruction_decode_1_wb_enable, instruction_decode_1_wb_mux,
       mem_wb_1_wb_en_2, mem_wb_1_wb_mux_2, not_1_out, or_1_out;
  wire [1:0] ex_mem_1_pcmux_2, id_ex_1_hilo_ctl_2, id_ex_1_hilo_ctl_2_2, id_ex_1_mem_ctl_2,
       id_ex_1_op_b_mux_2, id_ex_1_pc_mux_2, instruction_decode_1_hilo_write,
       instruction_decode_1_hilo_writemux, instruction_decode_1_mem_ctl_1_store__2_load,
       instruction_decode_1_op_b_mux__0__t__1_signedimm__2_unsignedimm__3_0,
       instruction_decode_1_pc_mux__0_pc_1__1_pc_imm__2__s__3_jmpaddr;
  wire [4:0] ex_mem_1_rd_2, id_ex_1_rd_2, id_ex_1_rs_2, id_ex_1_rt_2, id_ex_1_shamt_2,
       instruction_decode_1_rd, instruction_decode_1_rs, instruction_decode_1_rt, instruction_decode_1_shamt,
       mem_wb_1_rd_2, multiplexer_3_out;
  wire [5:0] id_ex_1_alu_opcode_2, instruction_decode_1_aluop;
  wire [15:0] ex_mem_1_imm16_2, id_ex_1_imm16_2, instruction_decode_1_imm16;
  wire [25:0] instruction_decode_1_jumpaddr;
  wire [31:0] adder_1_out, alu_1_hi, alu_1_lo, alu_1_result, branch_predictor_1_pcnext_2,
       branch_unit_1_pcnext__out, ex_mem_1_hilo_2, ex_mem_1_pcnext_2, ex_mem_1_result_2, ex_mem_1_s_2,
       ex_mem_1_s_new_2, forward_1_a, forward_1_b, hilo_register_1_hi_lo, id_ex_1_pc___1_2, id_ex_1_s_2,
       id_ex_1_t_2, IF_ID_IR_q, IF_ID_PCnext_q, mem_wb_1_hilo_2, mem_wb_1_result_2, multiplexer_2_out,
       multiplexer_4_out, multiplexer_5_out, multiplexer_6_out, opb_selector_1_b_out, PC_q, register_1_q,
       register_2_q, register_3_q, register_4_q, register_5_q, register_6_q, register_file_1_s,
       register_file_1_t;

  Clock clock_1 (.out(clk_out));
  not not_1 (not_1_out, branch_unit_1_branch_correction_needed);
  Register #(.width(32)) PC (.D(multiplexer_2_out), .Q(PC_q), .clk(clk_out));  // open: en, clr
  Multiplexer #(.width(32), .disabled(0), .enable("false")) multiplexer_1 (
    .in0(multiplexer_2_out), .in1(PC_q), .out(program_addr), .sel(not_1_out));
  Adder #(.width(32)) adder_1 (.a(32'h1), .b(program_addr), .out(adder_1_out));  // open: cin, cout
  falling_edge falling_edge_1 (.in_1(clk_out), .out_2(falling_edge_1_out_2));
  Register #(.width(32)) IF_ID_PCnext (
    .D(adder_1_out), .Q(IF_ID_PCnext_q), .clk(clk_out), .clr(and_1_out));  // open: en
  Register #(.width(32)) IF_ID_IR (.D(program_data), .Q(IF_ID_IR_q), .clk(clk_out), .clr(and_1_out));  // open: en
  Register #(.width(32)) register_1 (.D(program_data), .en(clk_out), .Q(register_1_q), .clk(clk_out));  // open: clr
  Register #(.width(32)) register_2 (.D(program_addr), .en(clk_out), .Q(register_2_q), .clk(clk_out));  // open: clr
  and and_1 (and_1_out, branch_unit_1_branch_correction_needed, falling_edge_1_out_2);
  Register_File register_file_1 (
    .d(multiplexer_6_out), .rd_enable(mem_wb_1_wb_en_2), .rd(mem_wb_1_rd_2), .s(register_file_1_s),
    .t(register_file_1_t), .Clock(clk_out), .rt(instruction_decode_1_rt), .rs(instruction_decode_1_rs));  // open: Clear
  Instruction_Decode instruction_decode_1 (
    .Instruction(IF_ID_IR_q), .MEM_ctl_1_store__2_load(instruction_decode_1_mem_ctl_1_store__2_load),
    .imm16(instruction_decode_1_imm16), .shamt(instruction_decode_1_shamt), .rd(instruction_decode_1_rd),
    .rt(instruction_decode_1_rt), .rs(instruction_decode_1_rs), .JumpAddr(instruction_decode_1_jumpaddr),
    .ALUop(instruction_decode_1_aluop),
    .Op_B_mux__0__t__1_signedimm__2_unsignedimm__3_0(instruction_decode_1_op_b_mux__0__t__1_signedimm__2_unsignedimm__3_0),
    .PC_Mux__0_pc_1__1_pc_imm__2__s__3_jmpAddr(instruction_decode_1_pc_mux__0_pc_1__1_pc_imm__2__s__3_jmpaddr),
    .WB_enable(instruction_decode_1_wb_enable), .HILO_write(instruction_decode_1_hilo_write[0]),
    .HILO_readmux(instruction_decode_1_hilo_write[1]), .HILO_writemux(instruction_decode_1_hilo_writemux),
    .WB_mux(instruction_decode_1_wb_mux));
  Multiplexer #(.width(32), .disabled(0), .enable("false")) multiplexer_2 (
    .in0(branch_unit_1_pcnext__out), .in1(branch_predictor_1_pcnext_2), .out(multiplexer_2_out),
    .sel(branch_predictor_1_branch_taken));
  branch_predictor branch_predictor_1 (
    .PC___1(IF_ID_PCnext_q), .PCNext_2(branch_predictor_1_pcnext_2),
    .branch_taken(branch_predictor_1_branch_taken), .imm16(instruction_decode_1_imm16),
    .PCmux(instruction_decode_1_pc_mux__0_pc_1__1_pc_imm__2__s__3_jmpaddr), .PCNext(adder_1_out),
    .s(register_file_1_s), .jAddr(instruction_decode_1_jumpaddr));
  ID_EX id_ex_1 (
    .PC___1(IF_ID_PCnext_q), .s(register_file_1_s), .t(register_file_1_t), .rs(instruction_decode_1_rs),
    .rt(instruction_decode_1_rt), .rd(instruction_decode_1_rd), .imm16(instruction_decode_1_imm16),
    .shamt(instruction_decode_1_shamt), .wb_enable(instruction_decode_1_wb_enable),
    .ALU_opcode(instruction_decode_1_aluop),
    .op_B_mux(instruction_decode_1_op_b_mux__0__t__1_signedimm__2_unsignedimm__3_0),
    .PC_mux(instruction_decode_1_pc_mux__0_pc_1__1_pc_imm__2__s__3_jmpaddr),
    .mem_ctl(instruction_decode_1_mem_ctl_1_store__2_load),
    .HILO_ctl({instruction_decode_1_hilo_writemux, instruction_decode_1_hilo_write}),
    .PC___1_2(id_ex_1_pc___1_2), .s_2(id_ex_1_s_2), .t_2(id_ex_1_t_2), .rs_2(id_ex_1_rs_2),
    .rt_2(id_ex_1_rt_2), .rd_2(id_ex_1_rd_2), .imm16_2(id_ex_1_imm16_2), .shamt_2(id_ex_1_shamt_2),
    .wb_enable_2(id_ex_1_wb_enable_2), .ALU_opcode_2(id_ex_1_alu_opcode_2), .op_B_mux_2(id_ex_1_op_b_mux_2),
    .PC_mux_2(id_ex_1_pc_mux_2), .mem_ctl_2(id_ex_1_mem_ctl_2),
    .HILO_ctl_2({id_ex_1_hilo_ctl_2_2, id_ex_1_hilo_ctl_2}), .Clock(clk_out),
    .branch_prediction(branch_predictor_1_branch_taken), .branch_prediction_2(id_ex_1_branch_prediction_2),
    .wb_mux(instruction_decode_1_wb_mux), .wb_mux_2(id_ex_1_wb_mux_2));  // open: Clear
  forward forward_1 (
    .rs(id_ex_1_rs_2), .rt(id_ex_1_rt_2), .rd__ex(multiplexer_3_out), .s(id_ex_1_s_2), .t(id_ex_1_t_2),
    .d__mem(multiplexer_5_out), .rd__mem(ex_mem_1_rd_2), .d__ex(multiplexer_4_out), .A(forward_1_a),
    .B(forward_1_b), .clk(clk_out), .mem_load(ld), .WB_addr__wb(mem_wb_1_rd_2), .wb_en__wb(mem_wb_1_wb_en_2),
    .wb_en__ex(id_ex_1_wb_enable_2));
  Register #(.width(32)) register_3 (.D(register_1_q), .en(clk_out), .Q(register_3_q), .clk(clk_out));  // open: clr
  Register #(.width(32)) register_4 (.D(register_2_q), .en(clk_out), .Q(register_4_q), .clk(clk_out));  // open: clr
  HILO_register hilo_register_1 (
    .write_en(id_ex_1_hilo_ctl_2[0]), .read_mux(id_ex_1_hilo_ctl_2[1]), .write_mux(id_ex_1_hilo_ctl_2_2),
    .HI(alu_1_hi), .LO(alu_1_lo), .HI_LO(hilo_register_1_hi_lo), .res(alu_1_result), .clk(clk_out));
  Multiplexer #(.width(5), .disabled(0), .enable("false")) multiplexer_3 (
    .in0(id_ex_1_rd_2), .in1(id_ex_1_rt_2), .out(multiplexer_3_out), .sel(or_1_out));
  opB_selector opb_selector_1 (
    .imm_in(id_ex_1_imm16_2), .B_out(opb_selector_1_b_out), .opBmux(id_ex_1_op_b_mux_2), .B_in(forward_1_b));
  Decoder #(.select(2), .disabled(0), .enable("false")) decoder_1 (
    .out1(decoder_1_out1), .out2(decoder_1_out2), .sel(id_ex_1_op_b_mux_2));  // open: out0, out3
  Multiplexer #(.width(32), .disabled(0), .enable("false")) multiplexer_4 (
    .in0(alu_1_result), .in1(hilo_register_1_hi_lo), .out(multiplexer_4_out), .sel(id_ex_1_wb_mux_2));
  ALU alu_1 (
    .A(forward_1_a), .B(opb_selector_1_b_out), .\function (id_ex_1_alu_opcode_2), .shamt(id_ex_1_shamt_2),
    .HI(alu_1_hi), .LO(alu_1_lo), .Result(alu_1_result));
  or or_1 (or_1_out, decoder_1_out1, decoder_1_out2);
  EX_MEM ex_mem_1 (
    .t(forward_1_b), .HILO(hilo_register_1_hi_lo), .wb_en(id_ex_1_wb_enable_2), .mem_ctl(id_ex_1_mem_ctl_2),
    .t_2(ram_data_in), .HILO_2(ex_mem_1_hilo_2), .wb_en_2(ex_mem_1_wb_en_2), .mem_ctl_2({ld, str}),
    .Clock(clk_out), .result(alu_1_result), .result_2(ex_mem_1_result_2), .rd(multiplexer_3_out),
    .rd_2(ex_mem_1_rd_2), .wb_mux(id_ex_1_wb_mux_2), .wb_mux_2(ex_mem_1_wb_mux_2), .pcmux(id_ex_1_pc_mux_2),
    .pcmux_2(ex_mem_1_pcmux_2), .s(id_ex_1_s_2), .s_2(ex_mem_1_s_2), .imm16(id_ex_1_imm16_2),
    .imm16_2(ex_mem_1_imm16_2), .PCnext(id_ex_1_pc___1_2), .PCnext_2(ex_mem_1_pcnext_2),
    .prediction(id_ex_1_branch_prediction_2), .prediction_2(ex_mem_1_prediction_2), .s_new(forward_1_a),
    .s_new_2(ex_mem_1_s_new_2));  // open: Clear
  Register #(.width(32)) register_5 (.D(register_3_q), .en(clk_out), .Q(register_5_q), .clk(clk_out));  // open: clr
  Register #(.width(32)) register_6 (.D(register_4_q), .en(clk_out), .Q(register_6_q), .clk(clk_out));  // open: clr
  branch_unit branch_unit_1 (
    .PC___1(ex_mem_1_pcnext_2), .prediction(ex_mem_1_prediction_2), .PCmux(ex_mem_1_pcmux_2),
    .PCNext__out(branch_unit_1_pcnext__out), .imm16(ex_mem_1_imm16_2),
    .branch_correction_needed(branch_unit_1_branch_correction_needed), .test_result(bit_extender_1_out),
    .PCNext__in(adder_1_out), .s(ex_mem_1_s_2), .s_new(ex_mem_1_s_new_2));
  Bit_Extender #(.in_width(32), .out_width(1)) bit_extender_1 (.in(ex_mem_1_result_2), .out(bit_extender_1_out));
  assign ram_addr = ex_mem_1_result_2;  // Buffer buffer_1, 32 bits wide
  or or_2 (ram_sel, str, ld);
  falling_edge falling_edge_2 (.in_1(clk_out), .out_2(clk_));
  Multiplexer #(.width(32), .disabled(0), .enable("false")) multiplexer_5 (
    .in0(ex_mem_1_result_2), .in1(ram_data_out), .out(multiplexer_5_out), .sel(ram_sel));
  MEM_WB mem_wb_1 (
    .rd(ex_mem_1_rd_2), .result(multiplexer_5_out), .HILO(ex_mem_1_hilo_2), .wb_en(ex_mem_1_wb_en_2),
    .rd_2(mem_wb_1_rd_2), .result_2(mem_wb_1_result_2), .HILO_2(mem_wb_1_hilo_2), .wb_en_2(mem_wb_1_wb_en_2),
    .Clock(clk_out), .wb_mux(ex_mem_1_wb_mux_2), .wb_mux_2(mem_wb_1_wb_mux_2));  // open: Clear
  Register #(.width(32)) register_7 (.D(register_5_q), .en(clk_out), .clk(clk_out));  // open: Q, clr
  Register #(.width(32)) register_8 (.D(register_6_q), .en(clk_out), .clk(clk_out));  // open: Q, clr
  Multiplexer #(.width(32), .disabled(0), .enable("false")) multiplexer_6 (
    .in0(mem_wb_1_result_2), .in1(mem_wb_1_hilo_2), .out(multiplexer_6_out), .sel(mem_wb_1_wb_mux_2));

  // Other names for the same wires on the sheet: clk = clk_out

  // Notes on the sheet:
  //   I/O:
  //   CORE:
endmodule

module hex_generator (
  input  [5:0] opcode,
  input  [4:0] rs,
  input  [4:0] rt,
  input  [4:0] rd,
  input  [4:0] shamt,
  input  [5:0] aluFunc,
  input  [15:0] imm,
  input  [25:0] jTarget,
  input  [1:0] opmode__0_rtype__1_itype__2_jtype
);

  wire [31:0] multiplexer_1_out;

  // Probe on multiplexer_1_out
  Multiplexer #(.select(2), .width(32), .disabled(0), .enable("false")) multiplexer_1 (
    .in0({opcode, rs, rt, rd, shamt, aluFunc}), .in1({opcode, rs, rt, imm}), .in2({opcode, jTarget}),
    .out(multiplexer_1_out), .sel(opmode__0_rtype__1_itype__2_jtype));  // open: in3
endmodule

module ID_EX (
  input  wb_mux,
  input  branch_prediction,
  input  [31:0] PC___1,
  input  [31:0] s,
  input  [31:0] t,
  input  [4:0] rs,
  input  [4:0] rt,
  input  [4:0] rd,
  input  [15:0] imm16,
  input  [4:0] shamt,
  input  wb_enable,
  input  [5:0] ALU_opcode,
  input  [1:0] op_B_mux,
  input  [1:0] PC_mux,
  input  [1:0] mem_ctl,
  input  [3:0] HILO_ctl,
  input  Clock,
  input  Clear,
  output wb_mux_2,
  output branch_prediction_2,
  output [31:0] PC___1_2,
  output [31:0] s_2,
  output [31:0] t_2,
  output [4:0] rs_2,
  output [4:0] rt_2,
  output [4:0] rd_2,
  output [15:0] imm16_2,
  output [4:0] shamt_2,
  output wb_enable_2,
  output [5:0] ALU_opcode_2,
  output [1:0] op_B_mux_2,
  output [1:0] PC_mux_2,
  output [1:0] mem_ctl_2,
  output [3:0] HILO_ctl_2
);

  Register #(.width(1)) register_1 (.D(wb_mux), .en(Clock), .Q(wb_mux_2), .clk(Clock), .clr(Clear));
  Register #(.width(1)) register_2 (
    .D(branch_prediction), .en(Clock), .Q(branch_prediction_2), .clk(Clock), .clr(Clear));
  Register #(.width(32)) register_3 (.D(PC___1), .en(Clock), .Q(PC___1_2), .clk(Clock), .clr(Clear));
  Register #(.width(32)) register_4 (.D(s), .en(Clock), .Q(s_2), .clk(Clock), .clr(Clear));
  Register #(.width(32)) register_5 (.D(t), .en(Clock), .Q(t_2), .clk(Clock), .clr(Clear));
  Register #(.width(5)) register_6 (.D(rs), .en(Clock), .Q(rs_2), .clk(Clock), .clr(Clear));
  Register #(.width(5)) register_7 (.D(rt), .en(Clock), .Q(rt_2), .clk(Clock), .clr(Clear));
  Register #(.width(5)) register_8 (.D(rd), .en(Clock), .Q(rd_2), .clk(Clock), .clr(Clear));
  Register #(.width(16)) register_9 (.D(imm16), .en(Clock), .Q(imm16_2), .clk(Clock), .clr(Clear));
  Register #(.width(5)) register_10 (.D(shamt), .en(Clock), .Q(shamt_2), .clk(Clock), .clr(Clear));
  Register #(.width(1)) register_11 (.D(wb_enable), .en(Clock), .Q(wb_enable_2), .clk(Clock), .clr(Clear));
  Register #(.width(6)) register_12 (.D(ALU_opcode), .en(Clock), .Q(ALU_opcode_2), .clk(Clock), .clr(Clear));
  Register #(.width(2)) register_13 (.D(op_B_mux), .en(Clock), .Q(op_B_mux_2), .clk(Clock), .clr(Clear));
  Register #(.width(2)) register_14 (.D(PC_mux), .en(Clock), .Q(PC_mux_2), .clk(Clock), .clr(Clear));
  Register #(.width(2)) register_15 (.D(mem_ctl), .en(Clock), .Q(mem_ctl_2), .clk(Clock), .clr(Clear));
  Register #(.width(4)) register_16 (.D(HILO_ctl), .en(Clock), .Q(HILO_ctl_2), .clk(Clock), .clr(Clear));
endmodule

module EX_MEM (
  input  [31:0] s_new,
  input  [31:0] PCnext,
  input  prediction,
  input  [1:0] pcmux,
  input  [31:0] s,
  input  [15:0] imm16,
  input  wb_mux,
  input  [4:0] rd,
  input  [31:0] result,
  input  [31:0] t,
  input  [31:0] HILO,
  input  wb_en,
  input  [1:0] mem_ctl,
  input  Clock,
  input  Clear,
  output [31:0] s_new_2,
  output [31:0] PCnext_2,
  output prediction_2,
  output [1:0] pcmux_2,
  output [31:0] s_2,
  output [15:0] imm16_2,
  output wb_mux_2,
  output [4:0] rd_2,
  output [31:0] result_2,
  output [31:0] t_2,
  output [31:0] HILO_2,
  output wb_en_2,
  output [1:0] mem_ctl_2
);

  Register #(.width(32)) register_1 (.D(s_new), .en(Clock), .Q(s_new_2), .clk(Clock), .clr(Clear));
  Register #(.width(32)) register_2 (.D(PCnext), .en(Clock), .Q(PCnext_2), .clk(Clock), .clr(Clear));
  Register #(.width(1)) register_3 (.D(prediction), .en(Clock), .Q(prediction_2), .clk(Clock), .clr(Clear));
  Register #(.width(2)) register_4 (.D(pcmux), .en(Clock), .Q(pcmux_2), .clk(Clock), .clr(Clear));
  Register #(.width(32)) register_5 (.D(s), .en(Clock), .Q(s_2), .clk(Clock), .clr(Clear));
  Register #(.width(16)) register_6 (.D(imm16), .en(Clock), .Q(imm16_2), .clk(Clock), .clr(Clear));
  Register #(.width(1)) register_7 (.D(wb_mux), .en(Clock), .Q(wb_mux_2), .clk(Clock), .clr(Clear));
  Register #(.width(5)) register_8 (.D(rd), .en(Clock), .Q(rd_2), .clk(Clock), .clr(Clear));
  Register #(.width(32)) register_9 (.D(result), .en(Clock), .Q(result_2), .clk(Clock), .clr(Clear));
  Register #(.width(32)) register_10 (.D(t), .en(Clock), .Q(t_2), .clk(Clock), .clr(Clear));
  Register #(.width(32)) register_11 (.D(HILO), .en(Clock), .Q(HILO_2), .clk(Clock), .clr(Clear));
  Register #(.width(1)) register_12 (.D(wb_en), .en(Clock), .Q(wb_en_2), .clk(Clock), .clr(Clear));
  Register #(.width(2)) register_13 (.D(mem_ctl), .en(Clock), .Q(mem_ctl_2), .clk(Clock), .clr(Clear));
endmodule

module MEM_WB (
  input  wb_mux,
  input  [4:0] rd,
  input  [31:0] result,
  input  [31:0] HILO,
  input  wb_en,
  input  Clock,
  input  Clear,
  output wb_mux_2,
  output [4:0] rd_2,
  output [31:0] result_2,
  output [31:0] HILO_2,
  output wb_en_2
);

  Register #(.width(1)) register_1 (.D(wb_mux), .en(Clock), .Q(wb_mux_2), .clk(Clock), .clr(Clear));
  Register #(.width(5)) register_2 (.D(rd), .en(Clock), .Q(rd_2), .clk(Clock), .clr(Clear));
  Register #(.width(32)) register_3 (.D(result), .en(Clock), .Q(result_2), .clk(Clock), .clr(Clear));
  Register #(.width(32)) register_4 (.D(HILO), .en(Clock), .Q(HILO_2), .clk(Clock), .clr(Clear));
  Register #(.width(1)) register_5 (.D(wb_en), .en(Clock), .Q(wb_en_2), .clk(Clock), .clr(Clear));
endmodule

module ALU (
  input  [31:0] A,
  input  [31:0] B,
  input  [5:0] \function ,
  input  [4:0] shamt,
  output [31:0] HI,
  output [31:0] LO,
  output [31:0] Result
);

  wire comparator_1_lt, comparator_2_lt, comparator_3_eq, comparator_3_gt, comparator_3_lt, decoder_1_out4,
       decoder_1_out6, decoder_1_out7, decoder_1_out24, decoder_1_out26, not_1_out, not_2_out, not_3_out,
       not_4_out, not_5_out, not_6_out, or_1_out, or_3_out;
  wire [4:0] bit_extender_1_out, multiplexer_1_out, multiplexer_2_out, multiplexer_3_out;
  wire [31:0] adder_1_out, and_1_out, bit_extender_2_out, bit_extender_3_out, bit_extender_4_out,
       bit_extender_5_out, bit_extender_6_out, bit_extender_7_out, bit_extender_8_out, bit_extender_9_out,
       divider_1_out, divider_1_rem, multiplier_1_cout, multiplier_1_out, nor_1_out, or_2_out, shifter_1_out,
       shifter_2_out, shifter_3_out, subtractor_1_out, xor_1_out;

  not not_1 (not_1_out, \function [5]);
  Decoder #(.select(5), .disabled(0)) decoder_1 (
    .out4(decoder_1_out4), .out6(decoder_1_out6), .out7(decoder_1_out7), .out24(decoder_1_out24),
    .out26(decoder_1_out26), .sel(\function [4:0]), .en(not_1_out));  // open: out0, out1, out2, out3, out5, out8, out9, out10, out11, out12, out13, out14, out15, out16, out17, out18, out19, out20, out21, out22, out23, out25, out27, out28, out29, out30, out31
  or or_1 (or_1_out, decoder_1_out4, decoder_1_out6, decoder_1_out7);
  Bit_Extender #(.in_width(32), .out_width(5)) bit_extender_1 (.in(A), .out(bit_extender_1_out));
  Multiplexer #(.width(5), .disabled(0), .enable("false")) multiplexer_1 (
    .in0(shamt), .in1(bit_extender_1_out), .out(multiplexer_1_out), .sel(or_1_out));
  Multiplexer #(.width(5), .disabled(0), .enable("false")) multiplexer_2 (
    .in0(shamt), .in1(bit_extender_1_out), .out(multiplexer_2_out), .sel(or_1_out));
  Multiplexer #(.width(5), .disabled(0), .enable("false")) multiplexer_3 (
    .in0(shamt), .in1(bit_extender_1_out), .out(multiplexer_3_out), .sel(or_1_out));
  Adder #(.width(32)) adder_1 (.a(A), .b(B), .out(adder_1_out));  // open: cin, cout
  Subtractor #(.width(32)) subtractor_1 (.a(A), .b(B), .out(subtractor_1_out));  // open: bin, bout
  Multiplier #(.width(32)) multiplier_1 (.a(A), .b(B), .out(multiplier_1_out), .cout(multiplier_1_cout));  // open: cin
  Divider #(.width(32)) divider_1 (.a(A), .b(B), .out(divider_1_out), .rem(divider_1_rem));  // open: upper
  assign and_1_out = A & B;  // AND_Gate and_1, 32 bits wide
  assign or_2_out = A | B;  // OR_Gate or_2, 32 bits wide
  assign xor_1_out = A ^ B;  // XOR_Gate xor_1, 32 bits wide
  assign nor_1_out = ~(A | B);  // NOR_Gate nor_1, 32 bits wide
  Shifter #(.width(32)) shifter_1 (.in(B), .\dist (multiplexer_1_out), .out(shifter_1_out));
  Shifter #(.width(32), .shift("lr")) shifter_2 (.in(B), .\dist (multiplexer_2_out), .out(shifter_2_out));
  Shifter #(.width(32), .shift("ar")) shifter_3 (.in(B), .\dist (multiplexer_3_out), .out(shifter_3_out));
  Comparator #(.width(32)) comparator_1 (.a(A), .b(B), .lt(comparator_1_lt));  // open: gt, eq
  assign bit_extender_2_out = {{31{1'b0}}, comparator_1_lt};  // Bit_Extender bit_extender_2
  Comparator #(.width(32), .mode("unsigned")) comparator_2 (.a(A), .b(B), .lt(comparator_2_lt));  // open: gt, eq
  assign bit_extender_3_out = {{31{1'b0}}, comparator_2_lt};  // Bit_Extender bit_extender_3
  Comparator #(.width(32)) comparator_3 (
    .a(A), .b(B), .gt(comparator_3_gt), .eq(comparator_3_eq), .lt(comparator_3_lt));
  not not_2 (not_2_out, comparator_3_lt);
  not not_3 (not_3_out, comparator_3_eq);
  not not_4 (not_4_out, comparator_3_gt);
  not not_5 (not_5_out, not_4_out);
  assign bit_extender_4_out = {{31{1'b0}}, comparator_3_lt};  // Bit_Extender bit_extender_4
  assign bit_extender_5_out = {{31{1'b0}}, not_2_out};  // Bit_Extender bit_extender_5
  assign bit_extender_6_out = {{31{1'b0}}, comparator_3_eq};  // Bit_Extender bit_extender_6
  assign bit_extender_7_out = {{31{1'b0}}, not_3_out};  // Bit_Extender bit_extender_7
  assign bit_extender_8_out = {{31{1'b0}}, not_4_out};  // Bit_Extender bit_extender_8
  assign bit_extender_9_out = {{31{1'b0}}, not_5_out};  // Bit_Extender bit_extender_9
  assign HI = decoder_1_out26 ? divider_1_rem : 32'bz;  // Controlled_Buffer controlled_buffer_1
  assign HI = decoder_1_out24 ? multiplier_1_cout : 32'bz;  // Controlled_Buffer controlled_buffer_2
  assign LO = decoder_1_out24 ? multiplier_1_out : 32'bz;  // Controlled_Buffer controlled_buffer_3
  assign LO = decoder_1_out26 ? divider_1_out : 32'bz;  // Controlled_Buffer controlled_buffer_4
  not not_6 (not_6_out, \function [5]);
  Multiplexer #(.select(5), .width(32)) multiplexer_4 (
    .in0(shifter_1_out), .in1({32{1'b0}}), .in2(shifter_2_out), .in3(shifter_3_out), .in4(shifter_1_out),
    .in5({32{1'b0}}), .in6(shifter_2_out), .in7(shifter_3_out), .in8({32{1'b0}}), .in9({32{1'b0}}),
    .in10({32{1'b0}}), .in11({32{1'b0}}), .in12({32{1'b0}}), .in13({32{1'b0}}), .in14({32{1'b0}}),
    .in15({32{1'b0}}), .in16({32{1'b0}}), .in17({32{1'b0}}), .in18({32{1'b0}}), .in19({32{1'b0}}),
    .in20({32{1'b0}}), .in21({32{1'b0}}), .in22({32{1'b0}}), .in23({32{1'b0}}), .in24({32{1'b0}}),
    .in25({32{1'b0}}), .in26({32{1'b0}}), .in27({32{1'b0}}), .in28({32{1'b0}}), .in29({32{1'b0}}),
    .in30({32{1'b0}}), .in31({32{1'b0}}), .out(Result), .sel(\function [4:0]), .en(not_6_out));
  Pull_Resistor pull_resistor_1 (.node(HI));
  Pull_Resistor pull_resistor_2 (.node(LO));
  or or_3 (or_3_out, decoder_1_out26, decoder_1_out24);
  // Probe on or_3_out
  Multiplexer #(.select(5), .width(32)) multiplexer_5 (
    .in0(adder_1_out), .in1(adder_1_out), .in2(subtractor_1_out), .in3(subtractor_1_out), .in4(and_1_out),
    .in5(or_2_out), .in6(xor_1_out), .in7(nor_1_out), .in8({32{1'b0}}), .in9({32{1'b0}}),
    .in10(bit_extender_2_out), .in11(bit_extender_3_out), .in12({32{1'b0}}), .in13({32{1'b0}}),
    .in14({32{1'b0}}), .in15({32{1'b0}}), .in16(bit_extender_4_out), .in17(bit_extender_5_out),
    .in18(bit_extender_6_out), .in19(bit_extender_7_out), .in20(bit_extender_8_out),
    .in21(bit_extender_9_out), .in22({32{1'b0}}), .in23({32{1'b0}}), .in24({32{1'b0}}), .in25({32{1'b0}}),
    .in26({32{1'b0}}), .in27({32{1'b0}}), .in28({32{1'b0}}), .in29({32{1'b0}}), .in30({32{1'b0}}),
    .in31({32{1'b0}}), .out(Result), .sel(\function [4:0]), .en(\function [5]));
endmodule

module Instruction_Decode (
  input  [31:0] Instruction,
  output [1:0] MEM_ctl_1_store__2_load,
  output [15:0] imm16,
  output [4:0] shamt,
  output [4:0] rd,
  output [4:0] rt,
  output [4:0] rs,
  output [25:0] JumpAddr,
  output [5:0] ALUop,
  output [1:0] Op_B_mux__0__t__1_signedimm__2_unsignedimm__3_0,
  output [1:0] PC_Mux__0_pc_1__1_pc_imm__2__s__3_jmpAddr,
  output WB_enable,
  output HILO_write,
  output HILO_readmux,
  output [1:0] HILO_writemux,
  output WB_mux
);

  wire add_2_out, add_out, addiu_out, addu_out, and_2_out, and_out, andi_out, beq_out, bgez_out, bgtz_out,
       bit_extender_1_out, blez_out, bltz_out, bne_out, buffer_1_out, comparator_1_eq, comparator_2_eq,
       comparator_3_eq, comparator_4_eq, comparator_5_eq, comparator_6_eq, comparator_7_eq, comparator_8_eq,
       comparator_9_eq, comparator_10_eq, comparator_11_eq, comparator_12_eq, comparator_13_eq,
       comparator_14_eq, comparator_15_eq, comparator_16_eq, comparator_17_eq, comparator_18_eq,
       comparator_19_eq, comparator_20_eq, comparator_21_eq, comparator_22_eq, comparator_23_eq,
       comparator_24_eq, comparator_25_eq, comparator_26_eq, comparator_27_eq, comparator_28_eq,
       comparator_29_eq, comparator_30_eq, comparator_31_eq, comparator_32_eq, comparator_33_eq,
       comparator_34_eq, comparator_35_eq, comparator_36_eq, comparator_37_eq, comparator_38_eq,
       comparator_39_eq, comparator_40_eq, div_out, j_out, jr_out, lui_out, mfhi_out, mflo_out, mpy_out,
       mthi_out, mtlo_out, nor_2_out, nor_3_out, nor_4_out, nor_out, not_1_out, or_2_out, or_3_out, or_4_out,
       or_5_out, or_6_out, or_7_out, or_9_out, or_10_out, or_11_out, or_out, ori_out, sll_out, sllv_out,
       slt_out, slti_out, sltiu_out, sltu_out, sra_out, srav_out, srl_out, srlv_out, sub_out, subu_out,
       unimp_2_out, unimp_out, xor_out, xori_out;
  wire [31:26] multiplexer_1_out;

  Comparator #(.width(6)) comparator_1 (.a(Instruction[31:26]), .b(6'b101011), .eq(comparator_1_eq));  // open: gt, lt
  Comparator #(.width(6)) comparator_2 (.a(Instruction[31:26]), .b(6'b100011), .eq(comparator_2_eq));  // open: gt, lt
  Comparator #(.width(6)) comparator_3 (.a(Instruction[31:26]), .b(6'b001111), .eq(comparator_3_eq));  // open: gt, lt
  Comparator #(.width(6)) comparator_4 (.a(Instruction[31:26]), .b(6'b001110), .eq(comparator_4_eq));  // open: gt, lt
  Comparator #(.width(6)) comparator_5 (.a(Instruction[31:26]), .b(6'b001101), .eq(comparator_5_eq));  // open: gt, lt
  Comparator #(.width(6)) comparator_6 (.a(Instruction[31:26]), .b(6'b001100), .eq(comparator_6_eq));  // open: gt, lt
  Comparator #(.width(6)) comparator_7 (.a(Instruction[31:26]), .b(6'b001011), .eq(comparator_7_eq));  // open: gt, lt
  Comparator #(.width(6)) comparator_8 (.a(Instruction[31:26]), .b(6'b001010), .eq(comparator_8_eq));  // open: gt, lt
  Comparator #(.width(6)) comparator_9 (.a(Instruction[31:26]), .b(6'b001001), .eq(comparator_9_eq));  // open: gt, lt
  Comparator #(.width(6)) comparator_10 (.a(Instruction[31:26]), .b(6'b001000), .eq(comparator_10_eq));  // open: gt, lt
  Comparator #(.width(6)) comparator_11 (.a(Instruction[31:26]), .b(6'b000111), .eq(comparator_11_eq));  // open: gt, lt
  Comparator #(.width(6)) comparator_12 (.a(Instruction[31:26]), .b(6'b000110), .eq(comparator_12_eq));  // open: gt, lt
  Comparator #(.width(6)) comparator_13 (.a(Instruction[31:26]), .b(6'b000101), .eq(comparator_13_eq));  // open: gt, lt
  Comparator #(.width(6)) comparator_14 (.a(Instruction[31:26]), .b(6'b000100), .eq(comparator_14_eq));  // open: gt, lt
  Comparator #(.width(6)) comparator_15 (.a(Instruction[31:26]), .b(6'b000010), .eq(comparator_15_eq));  // open: gt, lt
  Comparator #(.width(6)) comparator_16 (.a(Instruction[31:26]), .b(6'b000001), .eq(comparator_16_eq));  // open: gt, lt
  Comparator #(.width(6)) comparator_17 (.a(Instruction[31:26]), .b({6{1'b0}}), .eq(comparator_17_eq));  // open: gt, lt
  Bit_Extender #(.in_width(5), .out_width(1)) bit_extender_1 (.in(Instruction[20:16]), .out(bit_extender_1_out));
  Comparator #(.width(6)) comparator_18 (.a(Instruction[5:0]), .b(6'b100000), .eq(comparator_18_eq));  // open: gt, lt
  Comparator #(.width(6)) comparator_19 (.a(Instruction[5:0]), .b(6'b100010), .eq(comparator_19_eq));  // open: gt, lt
  Comparator #(.width(6)) comparator_20 (.a(Instruction[5:0]), .b(6'b011000), .eq(comparator_20_eq));  // open: gt, lt
  Comparator #(.width(6)) comparator_21 (.a(Instruction[5:0]), .b(6'b011010), .eq(comparator_21_eq));  // open: gt, lt
  Comparator #(.width(6)) comparator_22 (.a(Instruction[5:0]), .b(6'b100001), .eq(comparator_22_eq));  // open: gt, lt
  Comparator #(.width(6)) comparator_23 (.a(Instruction[5:0]), .b(6'b100011), .eq(comparator_23_eq));  // open: gt, lt
  Comparator #(.width(6)) comparator_24 (.a(Instruction[5:0]), .b(6'b100100), .eq(comparator_24_eq));  // open: gt, lt
  Comparator #(.width(6)) comparator_25 (.a(Instruction[5:0]), .b(6'b100101), .eq(comparator_25_eq));  // open: gt, lt
  Comparator #(.width(6)) comparator_26 (.a(Instruction[5:0]), .b(6'b100110), .eq(comparator_26_eq));  // open: gt, lt
  Comparator #(.width(6)) comparator_27 (.a(Instruction[5:0]), .b(6'b100111), .eq(comparator_27_eq));  // open: gt, lt
  Comparator #(.width(6)) comparator_28 (.a(Instruction[5:0]), .b(6'b101010), .eq(comparator_28_eq));  // open: gt, lt
  Comparator #(.width(6)) comparator_29 (.a(Instruction[5:0]), .b(6'b101011), .eq(comparator_29_eq));  // open: gt, lt
  Comparator #(.width(6)) comparator_30 (.a(Instruction[5:0]), .b({6{1'b0}}), .eq(comparator_30_eq));  // open: gt, lt
  Comparator #(.width(6)) comparator_31 (.a(Instruction[5:0]), .b(6'b000010), .eq(comparator_31_eq));  // open: gt, lt
  Comparator #(.width(6)) comparator_32 (.a(Instruction[5:0]), .b(6'b000011), .eq(comparator_32_eq));  // open: gt, lt
  Comparator #(.width(6)) comparator_33 (.a(Instruction[5:0]), .b(6'b000100), .eq(comparator_33_eq));  // open: gt, lt
  Comparator #(.width(6)) comparator_34 (.a(Instruction[5:0]), .b(6'b000110), .eq(comparator_34_eq));  // open: gt, lt
  Comparator #(.width(6)) comparator_35 (.a(Instruction[5:0]), .b(6'b000111), .eq(comparator_35_eq));  // open: gt, lt
  Comparator #(.width(6)) comparator_36 (.a(Instruction[5:0]), .b(6'b001000), .eq(comparator_36_eq));  // open: gt, lt
  Comparator #(.width(6)) comparator_37 (.a(Instruction[5:0]), .b(6'b010000), .eq(comparator_37_eq));  // open: gt, lt
  Comparator #(.width(6)) comparator_38 (.a(Instruction[5:0]), .b(6'b010010), .eq(comparator_38_eq));  // open: gt, lt
  Comparator #(.width(6)) comparator_39 (.a(Instruction[5:0]), .b(6'b010001), .eq(comparator_39_eq));  // open: gt, lt
  Comparator #(.width(6)) comparator_40 (.a(Instruction[5:0]), .b(6'b010011), .eq(comparator_40_eq));  // open: gt, lt
  buf sw (MEM_ctl_1_store__2_load[0], comparator_1_eq);
  buf lw (MEM_ctl_1_store__2_load[1], comparator_2_eq);
  buf lui (lui_out, comparator_3_eq);
  buf xori (xori_out, comparator_4_eq);
  buf ori (ori_out, comparator_5_eq);
  buf andi (andi_out, comparator_6_eq);
  buf sltiu (sltiu_out, comparator_7_eq);
  buf slti (slti_out, comparator_8_eq);
  buf addiu (addiu_out, comparator_9_eq);
  buf buffer_1 (buffer_1_out, comparator_10_eq);
  buf bgtz (bgtz_out, comparator_11_eq);
  buf blez (blez_out, comparator_12_eq);
  buf bne (bne_out, comparator_13_eq);
  buf beq (beq_out, comparator_14_eq);
  buf j (j_out, comparator_15_eq);
  and bltz (bltz_out, comparator_16_eq, ~bit_extender_1_out);  // AND_Gate
  and bgez (bgez_out, comparator_16_eq, bit_extender_1_out);
  and add (add_out, comparator_17_eq, comparator_18_eq);
  and sub (sub_out, comparator_17_eq, comparator_19_eq);
  and mpy (mpy_out, comparator_17_eq, comparator_20_eq);
  and div (div_out, comparator_17_eq, comparator_21_eq);
  and addu (addu_out, comparator_17_eq, comparator_22_eq);
  and subu (subu_out, comparator_17_eq, comparator_23_eq);
  and \and  (and_out, comparator_17_eq, comparator_24_eq);
  and \or  (or_out, comparator_17_eq, comparator_25_eq);
  and \xor  (xor_out, comparator_17_eq, comparator_26_eq);
  and \nor  (nor_out, comparator_17_eq, comparator_27_eq);
  and slt (slt_out, comparator_17_eq, comparator_28_eq);
  and sltu (sltu_out, comparator_17_eq, comparator_29_eq);
  and sll (sll_out, comparator_17_eq, comparator_30_eq);
  and srl (srl_out, comparator_17_eq, comparator_31_eq);
  and sra (sra_out, comparator_17_eq, comparator_32_eq);
  and sllv (sllv_out, comparator_17_eq, comparator_33_eq);
  and srlv (srlv_out, comparator_17_eq, comparator_34_eq);
  and srav (srav_out, comparator_17_eq, comparator_35_eq);
  and jr (jr_out, comparator_17_eq, comparator_36_eq);
  and mfhi (mfhi_out, comparator_17_eq, comparator_37_eq);
  and mflo (mflo_out, comparator_17_eq, comparator_38_eq);
  and mthi (mthi_out, comparator_17_eq, comparator_39_eq);
  and mtlo (mtlo_out, comparator_17_eq, comparator_40_eq);
  nor unimp (unimp_out, mtlo_out, mthi_out, mflo_out, mfhi_out, jr_out, srav_out, srlv_out, sllv_out, sra_out, srl_out, sll_out, sltu_out, slt_out, nor_out, xor_out);
  nor unimp_2 (unimp_2_out, or_out, and_out, subu_out, addu_out, div_out, mpy_out, sub_out, add_out, bgez_out, bltz_out, j_out, beq_out, bne_out, blez_out, bgtz_out, buffer_1_out, addiu_out, slti_out, sltiu_out, andi_out, ori_out, xori_out, lui_out, MEM_ctl_1_store__2_load[1], MEM_ctl_1_store__2_load[0]);
  and and_2 (and_2_out, unimp_2_out, unimp_out);
  or or_2 (or_2_out, bgtz_out, blez_out, bne_out, beq_out, bltz_out, bgez_out);
  or or_3 (or_3_out, lui_out, xori_out, ori_out, andi_out);
  or or_4 (or_4_out, slti_out, buffer_1_out, MEM_ctl_1_store__2_load[1], MEM_ctl_1_store__2_load[0]);
  or add_2 (add_2_out, MEM_ctl_1_store__2_load[0], MEM_ctl_1_store__2_load[1], buffer_1_out);
  or or_5 (or_5_out, MEM_ctl_1_store__2_load[1], lui_out, xori_out, ori_out, andi_out, sltiu_out, slti_out, addiu_out, buffer_1_out);
  or or_6 (or_6_out, bgtz_out, blez_out, bltz_out, bgez_out);
  assign ALUop = slti_out ? 6'b101010 : 6'bz;  // Controlled_Buffer controlled_buffer_1
  assign ALUop = sltiu_out ? 6'b101011 : 6'bz;  // Controlled_Buffer controlled_buffer_2
  assign ALUop = add_2_out ? 6'b100000 : 6'bz;  // Controlled_Buffer controlled_buffer_3
  assign ALUop = addiu_out ? 6'b100001 : 6'bz;  // Controlled_Buffer controlled_buffer_4
  assign ALUop = bltz_out ? 6'b110000 : 6'bz;  // Controlled_Buffer controlled_buffer_5
  assign ALUop = bgez_out ? 6'b110001 : 6'bz;  // Controlled_Buffer controlled_buffer_6
  assign ALUop = beq_out ? 6'b110010 : 6'bz;  // Controlled_Buffer controlled_buffer_7
  assign ALUop = bne_out ? 6'b110011 : 6'bz;  // Controlled_Buffer controlled_buffer_8
  assign ALUop = blez_out ? 6'b110100 : 6'bz;  // Controlled_Buffer controlled_buffer_9
  assign ALUop = bgtz_out ? 6'b110101 : 6'bz;  // Controlled_Buffer controlled_buffer_10
  assign ALUop = andi_out ? 6'b100100 : 6'bz;  // Controlled_Buffer controlled_buffer_11
  assign ALUop = ori_out ? 6'b100101 : 6'bz;  // Controlled_Buffer controlled_buffer_12
  assign ALUop = xori_out ? 6'b100110 : 6'bz;  // Controlled_Buffer controlled_buffer_13
  assign ALUop = lui_out ? {6{1'b0}} : 6'bz;  // Controlled_Buffer controlled_buffer_14
  or or_7 (or_7_out, or_2_out, comparator_17_eq);
  nor nor_2 (nor_2_out, or_7_out, or_4_out, or_3_out);
  nor nor_3 (nor_3_out, or_2_out, jr_out, j_out);
  nor nor_4 (nor_4_out, MEM_ctl_1_store__2_load[0], bgtz_out, blez_out, bne_out, beq_out, j_out, bltz_out, bgez_out, mpy_out, div_out, jr_out, mthi_out, mtlo_out);
  and and_3 (WB_enable, nor_4_out, ~and_2_out);  // AND_Gate
  or or_8 (HILO_write, div_out, mthi_out, mtlo_out, mpy_out);
  Priority_Encoder #(.select(1), .disabled(0)) priority_encoder_1 (
    .in0(mflo_out), .in1(mfhi_out), .out(HILO_readmux), .gs(WB_mux));  // open: en_out, en_in
  or or_9 (or_9_out, mtlo_out, mthi_out);
  Priority_Encoder #(.select(2), .disabled(0)) priority_encoder_2 (
    .in0(or_9_out), .in1(mtlo_out), .in2(mthi_out), .in3(or_10_out), .out(HILO_writemux));  // open: gs, en_out, en_in
  or or_10 (or_10_out, mpy_out, div_out);
  Priority_Encoder #(.select(2)) priority_encoder_3 (
    .in0(or_7_out), .in1(or_4_out), .in2(or_3_out), .in3(nor_2_out),
    .out(Op_B_mux__0__t__1_signedimm__2_unsignedimm__3_0));  // open: gs, en_out, en_in
  Priority_Encoder #(.select(2)) priority_encoder_4 (
    .in0(nor_3_out), .in1(or_2_out), .in2(jr_out), .in3(j_out),
    .out(PC_Mux__0_pc_1__1_pc_imm__2__s__3_jmpAddr));  // open: gs, en_out, en_in
  Pull_Resistor pull_resistor_1 (.node(HILO_writemux));
  Pull_Resistor pull_resistor_2 (.node(HILO_readmux));
  Multiplexer #(.width(32), .disabled(0), .enable("false")) multiplexer_1 (
    .in0(Instruction), .in1({32{1'b0}}), .out({multiplexer_1_out, JumpAddr[25:16], imm16}), .sel(and_2_out));
  or or_11 (or_11_out, comparator_17_eq, and_2_out);
  Multiplexer #(.width(5), .disabled(0), .enable("false")) multiplexer_2 (
    .in0(JumpAddr[20:16]), .in1({5{1'b0}}), .out(rt), .sel(or_6_out));
  assign ALUop = or_11_out ? imm16[5:0] : 6'bz;  // Controlled_Buffer controlled_buffer_15
  not not_1 (not_1_out, lui_out);
  assign shamt = lui_out ? 5'b10000 : 5'bz;  // Controlled_Buffer controlled_buffer_16
  assign shamt = not_1_out ? imm16[10:6] : 5'bz;  // Controlled_Buffer controlled_buffer_17
  Multiplexer #(.width(5), .disabled(0), .enable("false")) multiplexer_3 (
    .in0(imm16[15:11]), .in1(rt), .out(rd), .sel(or_5_out));

  assign JumpAddr[15:0] = imm16;
  assign rs = JumpAddr[25:21];

  // Notes on the sheet:
  //   addi
endmodule

module Register_File (
  input  Clock,
  input  Clear,
  input  [31:0] d,
  input  [4:0] rs,
  input  rd_enable,
  input  [4:0] rd,
  input  [4:0] rt,
  output [31:0] s,
  output [31:0] t
);

  wire decoder_1_out1, decoder_1_out2, decoder_1_out3, decoder_1_out4, decoder_1_out5, decoder_1_out6,
       decoder_1_out7, decoder_1_out8, decoder_1_out9, decoder_1_out10, decoder_1_out11, decoder_1_out12,
       decoder_1_out13, decoder_1_out14, decoder_1_out15, decoder_1_out16, decoder_1_out17, decoder_1_out18,
       decoder_1_out19, decoder_1_out20, decoder_1_out21, decoder_1_out22, decoder_1_out23, decoder_1_out24,
       decoder_1_out25, decoder_1_out26, decoder_1_out27, decoder_1_out28, decoder_1_out29, decoder_1_out30,
       decoder_1_out31;
  wire [31:0] _1_q, _1a_q, _1b_q, _1c_q, _1d_q, _1e_q, _1f_q, _2_q, _3_q, _4_q, _5_q, _6_q, _7_q, _8_q, _9_q,
       _10_q, _11_q, _12_q, _13_q, _14_q, _15_q, _16_q, _17_q, _18_q, _19_q, a_q, b_q, c_q, d_q, e_q, f_q;

  Decoder #(.select(5), .disabled(0)) decoder_1 (
    .out1(decoder_1_out1), .out2(decoder_1_out2), .out3(decoder_1_out3), .out4(decoder_1_out4),
    .out5(decoder_1_out5), .out6(decoder_1_out6), .out7(decoder_1_out7), .out8(decoder_1_out8),
    .out9(decoder_1_out9), .out10(decoder_1_out10), .out11(decoder_1_out11), .out12(decoder_1_out12),
    .out13(decoder_1_out13), .out14(decoder_1_out14), .out15(decoder_1_out15), .out16(decoder_1_out16),
    .out17(decoder_1_out17), .out18(decoder_1_out18), .out19(decoder_1_out19), .out20(decoder_1_out20),
    .out21(decoder_1_out21), .out22(decoder_1_out22), .out23(decoder_1_out23), .out24(decoder_1_out24),
    .out25(decoder_1_out25), .out26(decoder_1_out26), .out27(decoder_1_out27), .out28(decoder_1_out28),
    .out29(decoder_1_out29), .out30(decoder_1_out30), .out31(decoder_1_out31), .sel(rd), .en(rd_enable));  // open: out0
  Register #(.width(32), .trigger("falling")) _1 (.D(d), .en(decoder_1_out1), .Q(_1_q), .clk(Clock), .clr(Clear));
  Register #(.width(32), .trigger("falling")) _2 (.D(d), .en(decoder_1_out2), .Q(_2_q), .clk(Clock), .clr(Clear));
  Register #(.width(32), .trigger("falling")) _3 (.D(d), .en(decoder_1_out3), .Q(_3_q), .clk(Clock), .clr(Clear));
  Register #(.width(32), .trigger("falling")) _4 (.D(d), .en(decoder_1_out4), .Q(_4_q), .clk(Clock), .clr(Clear));
  Register #(.width(32), .trigger("falling")) _5 (.D(d), .en(decoder_1_out5), .Q(_5_q), .clk(Clock), .clr(Clear));
  Register #(.width(32), .trigger("falling")) _6 (.D(d), .en(decoder_1_out6), .Q(_6_q), .clk(Clock), .clr(Clear));
  Register #(.width(32), .trigger("falling")) _7 (.D(d), .en(decoder_1_out7), .Q(_7_q), .clk(Clock), .clr(Clear));
  Register #(.width(32), .trigger("falling")) _8 (.D(d), .en(decoder_1_out8), .Q(_8_q), .clk(Clock), .clr(Clear));
  Register #(.width(32), .trigger("falling")) _9 (.D(d), .en(decoder_1_out9), .Q(_9_q), .clk(Clock), .clr(Clear));
  Register #(.width(32), .trigger("falling")) a (.D(d), .en(decoder_1_out10), .Q(a_q), .clk(Clock), .clr(Clear));
  Register #(.width(32), .trigger("falling")) b (.D(d), .en(decoder_1_out11), .Q(b_q), .clk(Clock), .clr(Clear));
  Register #(.width(32), .trigger("falling")) c (.D(d), .en(decoder_1_out12), .Q(c_q), .clk(Clock), .clr(Clear));
  Register #(.width(32), .trigger("falling")) u_d (.D(d), .en(decoder_1_out13), .Q(d_q), .clk(Clock), .clr(Clear));
  Register #(.width(32), .trigger("falling")) e (.D(d), .en(decoder_1_out14), .Q(e_q), .clk(Clock), .clr(Clear));
  Register #(.width(32), .trigger("falling")) f (.D(d), .en(decoder_1_out15), .Q(f_q), .clk(Clock), .clr(Clear));
  Register #(.width(32), .trigger("falling")) _10 (.D(d), .en(decoder_1_out16), .Q(_10_q), .clk(Clock), .clr(Clear));
  Register #(.width(32), .trigger("falling")) _11 (.D(d), .en(decoder_1_out17), .Q(_11_q), .clk(Clock), .clr(Clear));
  Register #(.width(32), .trigger("falling")) _12 (.D(d), .en(decoder_1_out18), .Q(_12_q), .clk(Clock), .clr(Clear));
  Register #(.width(32), .trigger("falling")) _13 (.D(d), .en(decoder_1_out19), .Q(_13_q), .clk(Clock), .clr(Clear));
  Register #(.width(32), .trigger("falling")) _14 (.D(d), .en(decoder_1_out20), .Q(_14_q), .clk(Clock), .clr(Clear));
  Register #(.width(32), .trigger("falling")) _15 (.D(d), .en(decoder_1_out21), .Q(_15_q), .clk(Clock), .clr(Clear));
  Register #(.width(32), .trigger("falling")) _16 (.D(d), .en(decoder_1_out22), .Q(_16_q), .clk(Clock), .clr(Clear));
  Register #(.width(32), .trigger("falling")) _17 (.D(d), .en(decoder_1_out23), .Q(_17_q), .clk(Clock), .clr(Clear));
  Register #(.width(32), .trigger("falling")) _18 (.D(d), .en(decoder_1_out24), .Q(_18_q), .clk(Clock), .clr(Clear));
  Register #(.width(32), .trigger("falling")) _19 (.D(d), .en(decoder_1_out25), .Q(_19_q), .clk(Clock), .clr(Clear));
  Register #(.width(32), .trigger("falling")) _1a (.D(d), .en(decoder_1_out26), .Q(_1a_q), .clk(Clock), .clr(Clear));
  Register #(.width(32), .trigger("falling")) _1b (.D(d), .en(decoder_1_out27), .Q(_1b_q), .clk(Clock), .clr(Clear));
  Register #(.width(32), .trigger("falling")) _1c (.D(d), .en(decoder_1_out28), .Q(_1c_q), .clk(Clock), .clr(Clear));
  Register #(.width(32), .trigger("falling")) _1d (.D(d), .en(decoder_1_out29), .Q(_1d_q), .clk(Clock), .clr(Clear));
  Register #(.width(32), .trigger("falling")) _1e (.D(d), .en(decoder_1_out30), .Q(_1e_q), .clk(Clock), .clr(Clear));
  Register #(.width(32), .trigger("falling")) _1f (.D(d), .en(decoder_1_out31), .Q(_1f_q), .clk(Clock), .clr(Clear));
  Multiplexer #(.select(5), .width(32), .enable("false")) multiplexer_1 (
    .in0({32{1'b0}}), .in1(_1_q), .in2(_2_q), .in3(_3_q), .in4(_4_q), .in5(_5_q), .in6(_6_q), .in7(_7_q),
    .in8(_8_q), .in9(_9_q), .in10(a_q), .in11(b_q), .in12(c_q), .in13(d_q), .in14(e_q), .in15(f_q),
    .in16(_10_q), .in17(_11_q), .in18(_12_q), .in19(_13_q), .in20(_14_q), .in21(_15_q), .in22(_16_q),
    .in23(_17_q), .in24(_18_q), .in25(_19_q), .in26(_1a_q), .in27(_1b_q), .in28(_1c_q), .in29(_1d_q),
    .in30(_1e_q), .in31(_1f_q), .out(s), .sel(rs));
  Multiplexer #(.select(5), .width(32), .enable("false")) multiplexer_2 (
    .in0({32{1'b0}}), .in1(_1_q), .in2(_2_q), .in3(_3_q), .in4(_4_q), .in5(_5_q), .in6(_6_q), .in7(_7_q),
    .in8(_8_q), .in9(_9_q), .in10(a_q), .in11(b_q), .in12(c_q), .in13(d_q), .in14(e_q), .in15(f_q),
    .in16(_10_q), .in17(_11_q), .in18(_12_q), .in19(_13_q), .in20(_14_q), .in21(_15_q), .in22(_16_q),
    .in23(_17_q), .in24(_18_q), .in25(_19_q), .in26(_1a_q), .in27(_1b_q), .in28(_1c_q), .in29(_1d_q),
    .in30(_1e_q), .in31(_1f_q), .out(t), .sel(rt));
endmodule

module reg_template (
  input  in_1,
  input  in_2,
  input  Clock,
  input  Clear,
  output out_5,
  output out_6
);

  Register #(.width(1)) register_1 (.D(in_1), .en(Clock), .Q(out_5), .clk(Clock), .clr(Clear));
  Register #(.width(1)) register_2 (.D(in_2), .en(Clock), .Q(out_6), .clk(Clock), .clr(Clear));
endmodule

module branch_predictor (
  input  [31:0] PCNext,
  input  [31:0] PC___1,
  input  [1:0] PCmux,
  input  [15:0] imm16,
  input  [31:0] s,
  input  [25:0] jAddr,
  output [31:0] PCNext_2,
  output branch_taken
);

  wire and_1_out, decoder_1_out1;
  wire [31:0] adder_1_out, bit_extender_1_out, bit_extender_2_out, multiplexer_1_out;

  assign bit_extender_1_out = {{16{imm16[15]}}, imm16};  // Bit_Extender bit_extender_1
  Multiplexer #(.width(32), .disabled(0), .enable("false")) multiplexer_1 (
    .in0(PCNext), .in1(adder_1_out), .out(multiplexer_1_out), .sel(and_1_out));
  Adder #(.width(32)) adder_1 (.a(PC___1), .b(bit_extender_1_out), .out(adder_1_out));  // open: cin, cout
  and and_1 (and_1_out, decoder_1_out1, imm16[15]);
  Decoder #(.select(2), .disabled(0), .enable("false")) decoder_1 (
    .out1(decoder_1_out1), .sel(PCmux));  // open: out0, out2, out3
  Multiplexer #(.select(2), .width(32), .disabled(0), .enable("false")) multiplexer_2 (
    .in0(PCNext), .in1(multiplexer_1_out), .in2(s), .in3(bit_extender_2_out), .out(PCNext_2), .sel(PCmux));
  assign bit_extender_2_out = {{6{1'b0}}, jAddr};  // Bit_Extender bit_extender_2

  assign branch_taken = imm16[15];
endmodule

module branch_unit (
  input  [31:0] PCNext__in,
  input  [31:0] PC___1,
  input  prediction,
  input  [15:0] imm16,
  input  [1:0] PCmux,
  input  [31:0] s,
  input  [31:0] s_new,
  input  test_result,
  output [31:0] PCNext__out,
  output branch_correction_needed
);

  wire and_1_out, and_2_out, comparator_1_eq, decoder_1_out1, decoder_1_out2, demultiplexer_1_out0,
       demultiplexer_1_out1, multiplexer_2_out, xor_1_out;
  wire [1:0] priority_encoder_1_out;
  wire [31:0] adder_1_out, adder_2_out, bit_extender_1_out;

  assign bit_extender_1_out = {{16{imm16[15]}}, imm16};  // Bit_Extender bit_extender_1
  Adder #(.width(32)) adder_1 (.a(32'h1), .b(PC___1), .out(adder_1_out));  // open: cin, cout
  Adder #(.width(32)) adder_2 (.a(PC___1), .b(bit_extender_1_out), .out(adder_2_out));  // open: cin, cout
  Decoder #(.select(2), .disabled(0), .enable("false")) decoder_1 (
    .out1(decoder_1_out1), .out2(decoder_1_out2), .sel(PCmux));  // open: out0, out3
  Multiplexer #(.select(2), .width(32), .disabled(0), .enable("false")) multiplexer_1 (
    .in0(PCNext__in), .in1(adder_1_out), .in2(adder_2_out), .in3(s_new), .out(PCNext__out),
    .sel(priority_encoder_1_out));
  Comparator #(.width(32)) comparator_1 (.a(s_new), .b(s), .eq(comparator_1_eq));  // open: gt, lt
  and and_1 (and_1_out, ~comparator_1_eq, decoder_1_out2);  // AND_Gate
  and and_2 (and_2_out, decoder_1_out1, test_result);
  xor xor_1 (xor_1_out, and_2_out, prediction);
  Demultiplexer #(.disabled(0), .enable("false")) demultiplexer_1 (
    .out0(demultiplexer_1_out0), .out1(demultiplexer_1_out1), .in(multiplexer_2_out), .sel(test_result));
  Multiplexer #(.disabled(0), .enable("false")) multiplexer_2 (
    .in0(1'b0), .in1(xor_1_out), .out(multiplexer_2_out), .sel(decoder_1_out1));
  Priority_Encoder #(.select(2)) priority_encoder_1 (
    .in0(1'b1), .in1(demultiplexer_1_out0), .in2(demultiplexer_1_out1), .in3(and_1_out),
    .out(priority_encoder_1_out));  // open: gs, en_out, en_in
  or or_1 (branch_correction_needed, demultiplexer_1_out0, and_1_out, demultiplexer_1_out1);

  // Notes on the sheet:
  //   Problem Cases:
  //   predicted branch, did not branch
  //   predicted no branch, branched
  //   jr old $s data
  //   Solution
  //   clear if/id, change PCmux to new PC
  //   (PC + 1)++, set new PC
  //   new $s, set new PC
  //   (PC + 1) + branch, set new PC
  //   predicted no branch, branched
  //   predicted branched, didn't branch
endmodule

module forward (
  input  [31:0] d__mem,
  input  [4:0] rd__mem,
  input  clk,
  input  [31:0] d__ex,
  input  [4:0] rs,
  input  [4:0] rt,
  input  [4:0] rd__ex,
  input  wb_en__ex,
  input  [31:0] s,
  input  [31:0] t,
  input  [4:0] WB_addr__wb,
  input  wb_en__wb,
  input  mem_load,
  output [31:0] A,
  output [31:0] B
);

  wire and_1_out, and_2_out, and_3_out, and_4_out, and_5_out, and_6_out, and_7_out, and_8_out, and_9_out,
       and_10_out, and_11_out, and_12_out, and_13_out, and_14_out, and_15_out, and_16_out, and_17_out,
       and_18_out, and_19_out, and_20_out, and_21_out, and_22_out, and_23_out, and_24_out, and_not_0_1_out_3,
       and_not_0_2_out_3, and_not_0_3_out_3, and_not_0_4_out_3, and_not_0_5_out_3, and_not_0_6_out_3,
       comparator_1_eq, comparator_2_eq, comparator_3_eq, comparator_4_eq, comparator_5_eq, comparator_6_eq,
       comparator_7_eq, comparator_8_eq, comparator_9_eq, comparator_10_eq, comparator_11_eq,
       comparator_12_eq, comparator_13_eq, comparator_14_eq, comparator_15_eq, comparator_16_eq,
       comparator_17_eq, comparator_18_eq, comparator_19_eq, comparator_20_eq, comparator_21_eq,
       comparator_22_eq, comparator_23_eq, comparator_24_eq, comparator_25_eq, comparator_26_eq,
       comparator_27_eq, comparator_28_eq, decoder_1_out0, decoder_1_out1, decoder_1_out2, decoder_1_out3,
       decoder_2_out0, decoder_2_out1, decoder_2_out2, decoder_2_out3, decoder_3_out0, decoder_3_out1,
       decoder_3_out2, decoder_3_out3, decoder_4_out0, decoder_4_out1, decoder_4_out2, decoder_4_out3,
       falling_edge_1_out_2, n4x1_comparator_1_out_6, n4x1_comparator_1_out_7, n4x1_comparator_1_out_8,
       n4x1_comparator_1_out_9, n4x1_comparator_2_out_6, n4x1_comparator_2_out_7, n4x1_comparator_2_out_8,
       n4x1_comparator_2_out_9, n4x1_comparator_3_out_6, n4x1_comparator_3_out_7, n4x1_comparator_3_out_8,
       n4x1_comparator_3_out_9, n4x1_comparator_4_out_6, n4x1_comparator_4_out_7, n4x1_comparator_4_out_8,
       n4x1_comparator_4_out_9, nor_1_out, nor_2_out, or_1_out, or_2_out, or_3_out, or_4_out, or_5_out,
       or_6_out, or_7_out, or_8_out, priority_encoder_1_gs, priority_encoder_2_en_out, priority_encoder_3_gs,
       priority_encoder_4_gs, priority_encoder_5_gs, priority_encoder_6_en_out, priority_encoder_7_gs,
       priority_encoder_8_gs, s_r_ff_1_qn, s_r_ff_2_qn, s_r_ff_3_qn, s_r_ff_4_qn, s_r_ff_5_qn, s_r_ff_6_qn,
       s_r_ff_7_qn, s_r_ff_8_qn;
  wire [1:0] multiplexer_5_out, multiplexer_6_out, priority_encoder_1_out, priority_encoder_2_out,
       priority_encoder_3_out, priority_encoder_4_out, priority_encoder_5_out, priority_encoder_6_out,
       priority_encoder_7_out, priority_encoder_8_out, priority_encoder_9_out, priority_encoder_10_out;
  wire [4:0] register_1_q, register_3_q, register_5_q, register_7_q, register_9_q, register_11_q,
       register_13_q, register_15_q;
  wire [31:0] multiplexer_1_out, multiplexer_2_out, multiplexer_3_out, multiplexer_4_out, multiplexer_7_out,
       multiplexer_8_out, register_2_q, register_4_q, register_6_q, register_8_q, register_10_q,
       register_12_q, register_14_q, register_16_q;

  falling_edge falling_edge_1 (.in_1(clk), .out_2(falling_edge_1_out_2));
  Comparator #(.width(5)) comparator_1 (.a(rd__ex), .b({5{1'b0}}), .eq(comparator_1_eq));  // open: gt, lt
  Comparator #(.width(5)) comparator_2 (.a(rd__ex), .b(register_1_q), .eq(comparator_2_eq));  // open: gt, lt
  Register #(.width(5)) register_1 (.D(rd__ex), .en(or_4_out), .Q(register_1_q), .clk(clk), .clr(and_1_out));
  Register #(.width(32)) register_2 (.D(d__ex), .en(or_4_out), .Q(register_2_q), .clk(clk), .clr(and_1_out));
  S_R_Flip_Flop s_r_ff_1 (
    .S(or_4_out), .clk(clk), .R(1'b0), .Qn(s_r_ff_1_qn), .reset(and_1_out), .en(clk));  // open: Q, preset
  and and_1 (and_1_out, comparator_3_eq, falling_edge_1_out_2, wb_en__wb);
  Comparator #(.width(5)) comparator_3 (.a(register_1_q), .b(WB_addr__wb), .eq(comparator_3_eq));  // open: gt, lt
  Comparator #(.width(5)) comparator_4 (.a(rd__mem), .b({5{1'b0}}), .eq(comparator_4_eq));  // open: gt, lt
  Comparator #(.width(5)) comparator_5 (.a(rd__mem), .b(register_3_q), .eq(comparator_5_eq));  // open: gt, lt
  Register #(.width(5)) register_3 (.D(rd__mem), .en(or_8_out), .Q(register_3_q), .clk(clk), .clr(and_2_out));
  Register #(.width(32)) register_4 (.D(d__mem), .en(or_8_out), .Q(register_4_q), .clk(clk), .clr(and_2_out));
  S_R_Flip_Flop s_r_ff_2 (
    .S(or_8_out), .clk(clk), .R(1'b0), .Qn(s_r_ff_2_qn), .reset(and_2_out), .en(clk));  // open: Q, preset
  and and_2 (and_2_out, comparator_6_eq, falling_edge_1_out_2, wb_en__wb);
  Comparator #(.width(5)) comparator_6 (.a(register_3_q), .b(WB_addr__wb), .eq(comparator_6_eq));  // open: gt, lt
  and and_3 (and_3_out, comparator_2_eq, ~comparator_1_eq);  // AND_Gate
  and and_4 (and_4_out, comparator_5_eq, ~comparator_4_eq);  // AND_Gate
  Comparator #(.width(5)) comparator_7 (.a(rd__ex), .b({5{1'b0}}), .eq(comparator_7_eq));  // open: gt, lt
  Comparator #(.width(5)) comparator_8 (.a(rd__ex), .b(register_5_q), .eq(comparator_8_eq));  // open: gt, lt
  and and_5 (and_5_out, comparator_8_eq, ~comparator_7_eq);  // AND_Gate
  Register #(.width(5)) register_5 (.D(rd__ex), .en(or_3_out), .Q(register_5_q), .clk(clk), .clr(and_6_out));
  Register #(.width(32)) register_6 (.D(d__ex), .en(or_3_out), .Q(register_6_q), .clk(clk), .clr(and_6_out));
  S_R_Flip_Flop s_r_ff_3 (
    .S(or_3_out), .clk(clk), .R(1'b0), .Qn(s_r_ff_3_qn), .reset(and_6_out), .en(clk));  // open: Q, preset
  and and_6 (and_6_out, comparator_9_eq, falling_edge_1_out_2, wb_en__wb);
  Comparator #(.width(5)) comparator_9 (.a(register_5_q), .b(WB_addr__wb), .eq(comparator_9_eq));  // open: gt, lt
  Comparator #(.width(5)) comparator_10 (.a(rd__mem), .b({5{1'b0}}), .eq(comparator_10_eq));  // open: gt, lt
  Comparator #(.width(5)) comparator_11 (.a(rd__mem), .b(register_7_q), .eq(comparator_11_eq));  // open: gt, lt
  and and_7 (and_7_out, comparator_11_eq, ~comparator_10_eq);  // AND_Gate
  Register #(.width(5)) register_7 (.D(rd__mem), .en(or_7_out), .Q(register_7_q), .clk(clk), .clr(and_8_out));
  Register #(.width(32)) register_8 (.D(d__mem), .en(or_7_out), .Q(register_8_q), .clk(clk), .clr(and_8_out));
  S_R_Flip_Flop s_r_ff_4 (
    .S(or_7_out), .clk(clk), .R(1'b0), .Qn(s_r_ff_4_qn), .reset(and_8_out), .en(clk));  // open: Q, preset
  and and_8 (and_8_out, comparator_12_eq, falling_edge_1_out_2, wb_en__wb);
  Comparator #(.width(5)) comparator_12 (.a(register_7_q), .b(WB_addr__wb), .eq(comparator_12_eq));  // open: gt, lt
  Comparator #(.width(5)) comparator_13 (.a(register_9_q), .b(WB_addr__wb), .eq(comparator_13_eq));  // open: gt, lt
  Comparator #(.width(5)) comparator_14 (.a(register_11_q), .b(WB_addr__wb), .eq(comparator_14_eq));  // open: gt, lt
  Comparator #(.width(5)) comparator_15 (.a(rd__ex), .b({5{1'b0}}), .eq(comparator_15_eq));  // open: gt, lt
  Comparator #(.width(5)) comparator_16 (.a(rd__ex), .b(register_9_q), .eq(comparator_16_eq));  // open: gt, lt
  and and_9 (and_9_out, comparator_16_eq, ~comparator_15_eq);  // AND_Gate
  Register #(.width(5)) register_9 (.D(rd__ex), .en(or_2_out), .Q(register_9_q), .clk(clk), .clr(and_10_out));
  Register #(.width(32)) register_10 (.D(d__ex), .en(or_2_out), .Q(register_10_q), .clk(clk), .clr(and_10_out));
  S_R_Flip_Flop s_r_ff_5 (
    .S(or_2_out), .clk(clk), .R(1'b0), .Qn(s_r_ff_5_qn), .reset(and_10_out), .en(clk));  // open: Q, preset
  and and_10 (and_10_out, comparator_13_eq, falling_edge_1_out_2, wb_en__wb);
  Comparator #(.width(5)) comparator_17 (.a(rd__mem), .b({5{1'b0}}), .eq(comparator_17_eq));  // open: gt, lt
  Comparator #(.width(5)) comparator_18 (.a(rd__mem), .b(register_11_q), .eq(comparator_18_eq));  // open: gt, lt
  and and_11 (and_11_out, comparator_18_eq, ~comparator_17_eq);  // AND_Gate
  Register #(.width(5)) register_11 (.D(rd__mem), .en(or_6_out), .Q(register_11_q), .clk(clk), .clr(and_12_out));
  Register #(.width(32)) register_12 (.D(d__mem), .en(or_6_out), .Q(register_12_q), .clk(clk), .clr(and_12_out));
  S_R_Flip_Flop s_r_ff_6 (
    .S(or_6_out), .clk(clk), .R(1'b0), .Qn(s_r_ff_6_qn), .reset(and_12_out), .en(clk));  // open: Q, preset
  and and_12 (and_12_out, comparator_14_eq, falling_edge_1_out_2, wb_en__wb);
  Register #(.width(5)) register_13 (.D(rd__ex), .en(or_1_out), .Q(register_13_q), .clk(clk), .clr(and_13_out));
  Register #(.width(32)) register_14 (.D(d__ex), .en(or_1_out), .Q(register_14_q), .clk(clk), .clr(and_13_out));
  S_R_Flip_Flop s_r_ff_7 (
    .S(or_1_out), .clk(clk), .R(1'b0), .Qn(s_r_ff_7_qn), .reset(and_13_out), .en(clk));  // open: Q, preset
  and and_13 (and_13_out, comparator_19_eq, falling_edge_1_out_2, wb_en__wb);
  Comparator #(.width(5)) comparator_19 (.a(register_13_q), .b(WB_addr__wb), .eq(comparator_19_eq));  // open: gt, lt
  Register #(.width(5)) register_15 (.D(rd__mem), .en(or_5_out), .Q(register_15_q), .clk(clk), .clr(and_14_out));
  Register #(.width(32)) register_16 (.D(d__mem), .en(or_5_out), .Q(register_16_q), .clk(clk), .clr(and_14_out));
  S_R_Flip_Flop s_r_ff_8 (
    .S(or_5_out), .clk(clk), .R(1'b0), .Qn(s_r_ff_8_qn), .reset(and_14_out), .en(clk));  // open: Q, preset
  and and_14 (and_14_out, comparator_20_eq, falling_edge_1_out_2, wb_en__wb);
  Comparator #(.width(5)) comparator_20 (.a(register_15_q), .b(WB_addr__wb), .eq(comparator_20_eq));  // open: gt, lt
  Comparator #(.width(5)) comparator_21 (.a(rd__ex), .b({5{1'b0}}), .eq(comparator_21_eq));  // open: gt, lt
  Comparator #(.width(5)) comparator_22 (.a(rd__ex), .b(register_13_q), .eq(comparator_22_eq));  // open: gt, lt
  and and_15 (and_15_out, comparator_22_eq, ~comparator_21_eq);  // AND_Gate
  or or_1 (or_1_out, decoder_1_out0, decoder_2_out0);
  or or_2 (or_2_out, decoder_1_out1, decoder_2_out1);
  or or_3 (or_3_out, decoder_1_out2, decoder_2_out2);
  or or_4 (or_4_out, decoder_1_out3, decoder_2_out3);
  Comparator #(.width(5)) comparator_23 (.a(rd__mem), .b({5{1'b0}}), .eq(comparator_23_eq));  // open: gt, lt
  Comparator #(.width(5)) comparator_24 (.a(rd__mem), .b(register_15_q), .eq(comparator_24_eq));  // open: gt, lt
  and and_16 (and_16_out, comparator_24_eq, ~comparator_23_eq);  // AND_Gate
  or or_5 (or_5_out, decoder_3_out0, decoder_4_out0);
  or or_6 (or_6_out, decoder_3_out1, decoder_4_out1);
  or or_7 (or_7_out, decoder_3_out2, decoder_4_out2);
  or or_8 (or_8_out, decoder_3_out3, decoder_4_out3);
  Comparator #(.width(5)) comparator_25 (.a(rd__ex), .b({5{1'b0}}), .eq(comparator_25_eq));  // open: gt, lt
  Priority_Encoder #(.select(2)) priority_encoder_1 (
    .in0(and_15_out), .in1(and_9_out), .in2(and_5_out), .in3(and_3_out), .out(priority_encoder_1_out),
    .gs(priority_encoder_1_gs));  // open: en_out, en_in
  Priority_Encoder #(.select(2)) priority_encoder_2 (
    .in0(s_r_ff_7_qn), .in1(s_r_ff_5_qn), .in2(s_r_ff_3_qn), .in3(s_r_ff_1_qn), .out(priority_encoder_2_out),
    .en_out(priority_encoder_2_en_out));  // open: gs, en_in
  _4x1_comparator u_4x1_comparator_1 (
    .in_2(register_13_q), .in_3(register_9_q), .in_4(register_5_q), .in_5(register_1_q), .in_1(rs),
    .out_6(n4x1_comparator_1_out_6), .out_7(n4x1_comparator_1_out_7), .out_8(n4x1_comparator_1_out_8),
    .out_9(n4x1_comparator_1_out_9));
  Priority_Encoder #(.select(2)) priority_encoder_3 (
    .in0(n4x1_comparator_1_out_6), .in1(n4x1_comparator_1_out_7), .in2(n4x1_comparator_1_out_8),
    .in3(n4x1_comparator_1_out_9), .out(priority_encoder_3_out), .gs(priority_encoder_3_gs));  // open: en_out, en_in
  _4x1_comparator u_4x1_comparator_2 (
    .in_2(register_13_q), .in_3(register_9_q), .in_4(register_5_q), .in_5(register_1_q), .in_1(rt),
    .out_6(n4x1_comparator_2_out_6), .out_7(n4x1_comparator_2_out_7), .out_8(n4x1_comparator_2_out_8),
    .out_9(n4x1_comparator_2_out_9));
  Priority_Encoder #(.select(2)) priority_encoder_4 (
    .in0(n4x1_comparator_2_out_6), .in1(n4x1_comparator_2_out_7), .in2(n4x1_comparator_2_out_8),
    .in3(n4x1_comparator_2_out_9), .out(priority_encoder_4_out), .gs(priority_encoder_4_gs));  // open: en_out, en_in
  Multiplexer #(.select(2), .width(32), .disabled(0), .enable("false")) multiplexer_1 (
    .in0(register_14_q), .in1(register_10_q), .in2(register_6_q), .in3(register_2_q),
    .out(multiplexer_1_out), .sel(priority_encoder_3_out));
  Multiplexer #(.select(2), .width(32), .disabled(0), .enable("false")) multiplexer_2 (
    .in0(register_14_q), .in1(register_10_q), .in2(register_6_q), .in3(register_2_q),
    .out(multiplexer_2_out), .sel(priority_encoder_4_out));
  Priority_Encoder #(.select(2)) priority_encoder_5 (
    .in0(and_16_out), .in1(and_11_out), .in2(and_7_out), .in3(and_4_out), .out(priority_encoder_5_out),
    .gs(priority_encoder_5_gs));  // open: en_out, en_in
  Priority_Encoder #(.select(2)) priority_encoder_6 (
    .in0(s_r_ff_8_qn), .in1(s_r_ff_6_qn), .in2(s_r_ff_4_qn), .in3(s_r_ff_2_qn), .out(priority_encoder_6_out),
    .en_out(priority_encoder_6_en_out));  // open: gs, en_in
  _4x1_comparator u_4x1_comparator_3 (
    .in_2(register_15_q), .in_3(register_11_q), .in_4(register_7_q), .in_5(register_3_q), .in_1(rs),
    .out_6(n4x1_comparator_3_out_6), .out_7(n4x1_comparator_3_out_7), .out_8(n4x1_comparator_3_out_8),
    .out_9(n4x1_comparator_3_out_9));
  Priority_Encoder #(.select(2)) priority_encoder_7 (
    .in0(n4x1_comparator_3_out_6), .in1(n4x1_comparator_3_out_7), .in2(n4x1_comparator_3_out_8),
    .in3(n4x1_comparator_3_out_9), .out(priority_encoder_7_out), .gs(priority_encoder_7_gs));  // open: en_out, en_in
  _4x1_comparator u_4x1_comparator_4 (
    .in_2(register_15_q), .in_3(register_11_q), .in_4(register_7_q), .in_5(register_3_q), .in_1(rt),
    .out_6(n4x1_comparator_4_out_6), .out_7(n4x1_comparator_4_out_7), .out_8(n4x1_comparator_4_out_8),
    .out_9(n4x1_comparator_4_out_9));
  Priority_Encoder #(.select(2)) priority_encoder_8 (
    .in0(n4x1_comparator_4_out_6), .in1(n4x1_comparator_4_out_7), .in2(n4x1_comparator_4_out_8),
    .in3(n4x1_comparator_4_out_9), .out(priority_encoder_8_out), .gs(priority_encoder_8_gs));  // open: en_out, en_in
  Multiplexer #(.select(2), .width(32), .disabled(0), .enable("false")) multiplexer_3 (
    .in0(register_16_q), .in1(register_12_q), .in2(register_8_q), .in3(register_4_q),
    .out(multiplexer_3_out), .sel(priority_encoder_7_out));
  Multiplexer #(.select(2), .width(32), .disabled(0), .enable("false")) multiplexer_4 (
    .in0(register_16_q), .in1(register_12_q), .in2(register_8_q), .in3(register_4_q),
    .out(multiplexer_4_out), .sel(priority_encoder_8_out));
  Multiplexer #(.width(2), .disabled(0), .enable("false")) multiplexer_5 (
    .in0(priority_encoder_2_out), .in1(2'b11), .out(multiplexer_5_out), .sel(priority_encoder_2_en_out));
  and and_17 (and_17_out, wb_en__ex, ~priority_encoder_1_gs, ~comparator_25_eq);  // AND_Gate
  Decoder #(.select(2), .disabled(0)) decoder_1 (
    .out0(decoder_1_out0), .out1(decoder_1_out1), .out2(decoder_1_out2), .out3(decoder_1_out3),
    .sel(multiplexer_5_out), .en(and_17_out));
  and and_18 (and_18_out, wb_en__ex, priority_encoder_1_gs, ~comparator_25_eq);  // AND_Gate
  Decoder #(.select(2), .disabled(0)) decoder_2 (
    .out0(decoder_2_out0), .out1(decoder_2_out1), .out2(decoder_2_out2), .out3(decoder_2_out3),
    .sel(priority_encoder_1_out), .en(and_18_out));
  and_not_0 and_not_0_1 (.in_2(priority_encoder_3_gs), .out_3(and_not_0_1_out_3), .in_1(rs));
  Comparator #(.width(5)) comparator_26 (.a(rd__mem), .b(rs), .eq(comparator_26_eq));  // open: gt, lt
  and_not_0 and_not_0_2 (.in_2(priority_encoder_4_gs), .out_3(and_not_0_2_out_3), .in_1(rt));
  Comparator #(.width(5)) comparator_27 (.a({5{1'b0}}), .b(rd__mem), .eq(comparator_27_eq));  // open: gt, lt
  Multiplexer #(.width(2), .disabled(0), .enable("false")) multiplexer_6 (
    .in0(priority_encoder_6_out), .in1(2'b11), .out(multiplexer_6_out), .sel(priority_encoder_6_en_out));
  and and_19 (and_19_out, mem_load, ~priority_encoder_5_gs, ~comparator_27_eq);  // AND_Gate
  Decoder #(.select(2), .disabled(0)) decoder_3 (
    .out0(decoder_3_out0), .out1(decoder_3_out1), .out2(decoder_3_out2), .out3(decoder_3_out3),
    .sel(multiplexer_6_out), .en(and_19_out));
  Decoder #(.select(2), .disabled(0)) decoder_4 (
    .out0(decoder_4_out0), .out1(decoder_4_out1), .out2(decoder_4_out2), .out3(decoder_4_out3),
    .sel(priority_encoder_5_out), .en(and_20_out));
  and and_20 (and_20_out, mem_load, priority_encoder_5_gs, ~comparator_27_eq);  // AND_Gate
  and_not_0 and_not_0_3 (.in_2(priority_encoder_7_gs), .out_3(and_not_0_3_out_3), .in_1(rs));
  and_not_0 and_not_0_4 (.in_2(priority_encoder_8_gs), .out_3(and_not_0_4_out_3), .in_1(rt));
  and_not_0 and_not_0_5 (.in_2(comparator_26_eq), .out_3(and_not_0_5_out_3), .in_1(rs));
  and_not_0 and_not_0_6 (.in_2(comparator_28_eq), .out_3(and_not_0_6_out_3), .in_1(rt));
  Comparator #(.width(5)) comparator_28 (.a(rd__mem), .b(rt), .eq(comparator_28_eq));  // open: gt, lt
  and and_21 (and_21_out, ~and_not_0_1_out_3, and_not_0_3_out_3);  // AND_Gate
  and and_22 (and_22_out, and_not_0_5_out_3, mem_load);
  and and_23 (and_23_out, ~and_not_0_2_out_3, and_not_0_4_out_3);  // AND_Gate
  nor nor_1 (nor_1_out, and_not_0_1_out_3, and_21_out, and_22_out);
  nor nor_2 (nor_2_out, and_not_0_2_out_3, and_23_out, and_24_out);
  and and_24 (and_24_out, and_not_0_6_out_3, mem_load);
  Priority_Encoder #(.select(2)) priority_encoder_9 (
    .in0(nor_1_out), .in1(and_not_0_1_out_3), .in2(and_21_out), .in3(and_22_out), .out(priority_encoder_9_out));  // open: gs, en_out, en_in
  Priority_Encoder #(.select(2)) priority_encoder_10 (
    .in0(nor_2_out), .in1(and_not_0_2_out_3), .in2(and_23_out), .in3(and_24_out),
    .out(priority_encoder_10_out));  // open: gs, en_out, en_in
  Register #(.width(32), .trigger("high")) buff (.D(multiplexer_7_out), .Q(A), .clk(clk));  // open: en, clr
  Multiplexer #(.select(2), .width(32), .disabled(0), .enable("false")) multiplexer_7 (
    .in0(s), .in1(multiplexer_1_out), .in2(multiplexer_3_out), .in3(d__mem), .out(multiplexer_7_out),
    .sel(priority_encoder_9_out));
  Multiplexer #(.select(2), .width(32), .disabled(0), .enable("false")) multiplexer_8 (
    .in0(t), .in1(multiplexer_2_out), .in2(multiplexer_4_out), .in3(d__mem), .out(multiplexer_8_out),
    .sel(priority_encoder_10_out));
  Register #(.width(32), .trigger("high")) buff_2 (.D(multiplexer_8_out), .Q(B), .clk(clk));  // open: en, clr

  // Notes on the sheet:
  //   EX
  //   MEM
endmodule

module HILO_register (
  input  [31:0] res,
  input  write_en,
  input  read_mux,
  input  [1:0] write_mux,
  input  [31:0] HI,
  input  [31:0] LO,
  input  clk,
  output [31:0] HI_LO
);

  wire decoder_1_out0, decoder_1_out1, decoder_1_out2, decoder_1_out3, not_1_out, or_1_out, or_2_out;
  wire [31:0] HI_q, LO_q, multiplexer_1_out, multiplexer_2_out;

  Decoder #(.select(2), .disabled(0)) decoder_1 (
    .out0(decoder_1_out0), .out1(decoder_1_out1), .out2(decoder_1_out2), .out3(decoder_1_out3),
    .sel(write_mux), .en(write_en));
  or or_1 (or_1_out, decoder_1_out1, decoder_1_out3);
  or or_2 (or_2_out, decoder_1_out3, decoder_1_out2);
  Multiplexer #(.width(32), .disabled(0), .enable("false")) multiplexer_1 (
    .in0(HI), .in1(res), .out(multiplexer_1_out), .sel(decoder_1_out0));
  Multiplexer #(.width(32), .disabled(0), .enable("false")) multiplexer_2 (
    .in0(LO), .in1(res), .out(multiplexer_2_out), .sel(decoder_1_out0));
  Register #(.width(32), .trigger("falling")) u_HI (
    .D(multiplexer_1_out), .en(or_2_out), .Q(HI_q), .clk(clk));  // open: clr
  Register #(.width(32), .trigger("falling")) u_LO (
    .D(multiplexer_2_out), .en(or_1_out), .Q(LO_q), .clk(clk));  // open: clr
  not not_1 (not_1_out, read_mux);
  Multiplexer #(.width(32), .disabled(0), .enable("false")) multiplexer_3 (
    .in0(HI_q), .in1(LO_q), .out(HI_LO), .sel(not_1_out));
endmodule

module opB_selector (
  input  [31:0] B_in,
  input  [15:0] imm_in,
  input  [1:0] opBmux,
  output [31:0] B_out
);

  wire [31:0] bit_extender_1_out, bit_extender_2_out;

  assign bit_extender_1_out = {{16{imm_in[15]}}, imm_in};  // Bit_Extender bit_extender_1
  assign bit_extender_2_out = {{16{1'b0}}, imm_in};  // Bit_Extender bit_extender_2
  Multiplexer #(.select(2), .width(32), .enable("false")) multiplexer_1 (
    .in0(B_in), .in1(bit_extender_1_out), .in2(bit_extender_2_out), .out(B_out), .sel(opBmux));  // open: in3
endmodule

module delay_x10 (
  input  in_1,
  output out_2
);

  wire buffer_1_out, buffer_2_out, buffer_3_out, buffer_4_out, buffer_5_out, buffer_6_out, buffer_7_out;

  buf buffer_1 (buffer_1_out, buffer_2_out);
  buf buffer_2 (buffer_2_out, in_1);
  buf buffer_3 (buffer_3_out, buffer_6_out);
  buf buffer_4 (buffer_4_out, buffer_5_out);
  buf buffer_5 (buffer_5_out, buffer_1_out);
  buf buffer_6 (buffer_6_out, buffer_4_out);
  buf buffer_7 (buffer_7_out, buffer_3_out);
  buf buffer_8 (out_2, buffer_7_out);
endmodule

module falling_edge (
  input  in_1,
  output out_2
);

  wire not_1_out, not_2_out;

  not not_1 (not_1_out, in_1);
  and and_1 (out_2, not_1_out, not_2_out);
  not not_2 (not_2_out, not_1_out);
endmodule

module forwarding_cell (
);

  wire and_1_out, and_2_out, comparator_1_eq, comparator_2_eq, comparator_3_eq, s_r_ff_1_qn, undriven_4,
       undriven_5, undriven_6, undriven_7;
  wire [4:0] register_1_q, undriven, undriven_3;
  wire [31:0] register_2_q, undriven_2;

  Comparator #(.width(5)) comparator_1 (.a(undriven), .b({5{1'b0}}), .eq(comparator_1_eq));  // open: gt, lt
  Comparator #(.width(5)) comparator_2 (.a(undriven), .b(register_1_q), .eq(comparator_2_eq));  // open: gt, lt
  Register #(.width(5)) register_1 (.D(undriven), .en(undriven_6), .Q(register_1_q), .clk(undriven_7), .clr(and_1_out));
  Register #(.width(32)) register_2 (
    .D(undriven_2), .en(undriven_6), .Q(register_2_q), .clk(undriven_7), .clr(and_1_out));
  S_R_Flip_Flop s_r_ff_1 (
    .S(undriven_6), .clk(undriven_7), .R(1'b0), .Qn(s_r_ff_1_qn), .reset(and_1_out), .en(undriven_7));  // open: Q, preset
  and and_1 (and_1_out, comparator_3_eq, undriven_5, undriven_4);
  Comparator #(.width(5)) comparator_3 (.a(register_1_q), .b(undriven_3), .eq(comparator_3_eq));  // open: gt, lt
  and and_2 (and_2_out, comparator_2_eq, ~comparator_1_eq);  // AND_Gate

  // Notes on the sheet:
  //   rd
  //   $d
  //   clk
  //   wb addr
  //   wb en
  //   $d stored
  //   new value
  //   is empty
  //   set new val
  //   rd stored
  //   clk (falling edge)
endmodule

module _4x1_comparator (
  input  [4:0] in_1,
  input  [4:0] in_2,
  input  [4:0] in_3,
  input  [4:0] in_4,
  input  [4:0] in_5,
  output out_6,
  output out_7,
  output out_8,
  output out_9
);

  Comparator #(.width(5)) comparator_1 (.a(in_2), .b(in_1), .eq(out_6));  // open: gt, lt
  Comparator #(.width(5)) comparator_2 (.a(in_3), .b(in_1), .eq(out_7));  // open: gt, lt
  Comparator #(.width(5)) comparator_3 (.a(in_4), .b(in_1), .eq(out_8));  // open: gt, lt
  Comparator #(.width(5)) comparator_4 (.a(in_5), .b(in_1), .eq(out_9));  // open: gt, lt
endmodule

module and_not_0 (
  input  [4:0] in_1,
  input  in_2,
  output out_3
);

  wire comparator_1_eq;

  Comparator #(.width(5)) comparator_1 (.a(in_1), .b({5{1'b0}}), .eq(comparator_1_eq));  // open: gt, lt
  and and_1 (out_3, ~comparator_1_eq, in_2);  // AND_Gate
endmodule

module forwarding (
  input  [31:0] result__from_mem,
  input  [4:0] rd__from_mem,
  input  clk,
  input  [4:0] rd,
  input  [4:0] rs,
  input  [4:0] rt,
  input  [31:0] s,
  input  [31:0] t,
  input  [31:0] result,
  input  [4:0] wbAddr,
  input  wbEn,
  output [31:0] s_2,
  output [31:0] t_2
);

  wire and_1_out, and_2_out, and_3_out, and_4_out, and_5_out, and_6_out, and_7_out, and_8_out, and_9_out,
       buffer_1_out, buffer_2_out, buffer_3_out, buffer_4_out, buffer_5_out, buffer_6_out, comparator_1_eq,
       comparator_2_eq, comparator_3_eq, comparator_4_eq, comparator_5_eq, comparator_6_eq, comparator_7_eq,
       comparator_8_eq, comparator_9_eq, comparator_10_eq, comparator_11_eq, decoder_1_out0, decoder_1_out1,
       decoder_1_out2, decoder_1_out3, decoder_1_out4, decoder_1_out5, decoder_1_out6, decoder_1_out7,
       delay_x10_1_out_2, n8x1_comparator_1_out_10, n8x1_comparator_1_out_11, n8x1_comparator_1_out_12,
       n8x1_comparator_1_out_13, n8x1_comparator_1_out_14, n8x1_comparator_1_out_15,
       n8x1_comparator_1_out_16, n8x1_comparator_1_out_17, n8x1_comparator_2_out_10,
       n8x1_comparator_2_out_11, n8x1_comparator_2_out_12, n8x1_comparator_2_out_13,
       n8x1_comparator_2_out_14, n8x1_comparator_2_out_15, n8x1_comparator_2_out_16,
       n8x1_comparator_2_out_17, not_1_out, not_2_out, not_3_out, or_1_out, priority_encoder_1_en_out,
       priority_encoder_2_en_out, priority_encoder_3_en_out, s_r_ff_1_qn, s_r_ff_2_qn, s_r_ff_3_qn,
       s_r_ff_4_qn, s_r_ff_5_qn, s_r_ff_6_qn, s_r_ff_7_qn, s_r_ff_8_qn;
  wire [2:0] multiplexer_3_out, priority_encoder_1_out, priority_encoder_2_out, priority_encoder_3_out;
  wire [4:0] multiplexer_1_out, register_1_q, register_3_q, register_5_q, register_7_q, register_9_q,
       register_11_q, register_13_q, register_15_q;
  wire [31:0] multiplexer_2_out, multiplexer_4_out, multiplexer_5_out, multiplexer_6_out, multiplexer_8_out,
       register_2_q, register_4_q, register_6_q, register_8_q, register_10_q, register_12_q, register_14_q,
       register_16_q;

  not not_1 (not_1_out, buffer_5_out);
  delay_x10 delay_x10_1 (.in_1(clk), .out_2(delay_x10_1_out_2));
  buf buffer_1 (buffer_1_out, delay_x10_1_out_2);
  not not_2 (not_2_out, not_1_out);
  buf buffer_2 (buffer_2_out, not_2_out);
  buf buffer_3 (buffer_3_out, buffer_2_out);
  Multiplexer #(.width(5), .disabled(0), .enable("false")) multiplexer_1 (
    .in0(rd), .in1(rd__from_mem), .out(multiplexer_1_out), .sel(clk));
  Multiplexer #(.width(32), .disabled(0), .enable("false")) multiplexer_2 (
    .in0(result), .in1(result__from_mem), .out(multiplexer_2_out), .sel(clk));
  buf buffer_4 (buffer_4_out, buffer_1_out);
  buf buffer_5 (buffer_5_out, buffer_4_out);
  buf buffer_6 (buffer_6_out, buffer_3_out);
  and and_1 (and_1_out, buffer_6_out, not_1_out);
  S_R_Flip_Flop s_r_ff_1 (
    .S(decoder_1_out7), .clk(or_1_out), .R(1'b0), .Qn(s_r_ff_1_qn), .reset(and_2_out), .en(or_1_out));  // open: Q, preset
  or or_1 (or_1_out, buffer_5_out, and_1_out);
  S_R_Flip_Flop s_r_ff_2 (
    .S(decoder_1_out6), .clk(or_1_out), .R(1'b0), .Qn(s_r_ff_2_qn), .reset(and_3_out));  // open: Q, preset, en
  Register #(.width(5)) register_1 (
    .D(multiplexer_1_out), .en(decoder_1_out7), .Q(register_1_q), .clk(or_1_out), .clr(and_2_out));
  Register #(.width(32)) register_2 (
    .D(multiplexer_2_out), .en(decoder_1_out7), .Q(register_2_q), .clk(or_1_out), .clr(and_2_out));
  and and_2 (and_2_out, comparator_1_eq, wbEn);
  Comparator #(.width(5)) comparator_1 (.a(register_1_q), .b(wbAddr), .eq(comparator_1_eq));  // open: gt, lt
  S_R_Flip_Flop s_r_ff_3 (
    .S(decoder_1_out5), .clk(or_1_out), .R(1'b0), .Qn(s_r_ff_3_qn), .reset(and_4_out));  // open: Q, preset, en
  Register #(.width(5)) register_3 (
    .D(multiplexer_1_out), .en(decoder_1_out6), .Q(register_3_q), .clk(or_1_out), .clr(and_3_out));
  Register #(.width(32)) register_4 (
    .D(multiplexer_2_out), .en(decoder_1_out6), .Q(register_4_q), .clk(or_1_out), .clr(and_3_out));
  and and_3 (and_3_out, comparator_2_eq, wbEn);
  Comparator #(.width(5)) comparator_2 (.a(register_3_q), .b(wbAddr), .eq(comparator_2_eq));  // open: gt, lt
  Comparator #(.width(5)) comparator_3 (.a({5{1'b0}}), .b(multiplexer_1_out), .eq(comparator_3_eq));  // open: gt, lt
  Register #(.width(5)) register_5 (
    .D(multiplexer_1_out), .en(decoder_1_out5), .Q(register_5_q), .clk(or_1_out), .clr(and_4_out));
  Register #(.width(32)) register_6 (
    .D(multiplexer_2_out), .en(decoder_1_out5), .Q(register_6_q), .clk(or_1_out), .clr(and_4_out));
  and and_4 (and_4_out, comparator_4_eq, wbEn);
  Comparator #(.width(5)) comparator_4 (.a(register_5_q), .b(wbAddr), .eq(comparator_4_eq));  // open: gt, lt
  not not_3 (not_3_out, comparator_3_eq);
  S_R_Flip_Flop s_r_ff_4 (
    .S(decoder_1_out4), .clk(or_1_out), .R(1'b0), .Qn(s_r_ff_4_qn), .reset(and_5_out));  // open: Q, preset, en
  Register #(.width(5)) register_7 (
    .D(multiplexer_1_out), .en(decoder_1_out4), .Q(register_7_q), .clk(or_1_out), .clr(and_5_out));
  Register #(.width(32)) register_8 (
    .D(multiplexer_2_out), .en(decoder_1_out4), .Q(register_8_q), .clk(or_1_out), .clr(and_5_out));
  and and_5 (and_5_out, comparator_5_eq, wbEn);
  Comparator #(.width(5)) comparator_5 (.a(register_7_q), .b(wbAddr), .eq(comparator_5_eq));  // open: gt, lt
  S_R_Flip_Flop s_r_ff_5 (
    .S(decoder_1_out3), .clk(or_1_out), .R(1'b0), .Qn(s_r_ff_5_qn), .reset(and_6_out));  // open: Q, preset, en
  Register #(.width(5)) register_9 (
    .D(multiplexer_1_out), .en(decoder_1_out3), .Q(register_9_q), .clk(or_1_out), .clr(and_6_out));
  Register #(.width(32)) register_10 (
    .D(multiplexer_2_out), .en(decoder_1_out3), .Q(register_10_q), .clk(or_1_out), .clr(and_6_out));
  and and_6 (and_6_out, comparator_6_eq, wbEn);
  Comparator #(.width(5)) comparator_6 (.a(register_9_q), .b(wbAddr), .eq(comparator_6_eq));  // open: gt, lt
  S_R_Flip_Flop s_r_ff_6 (
    .S(decoder_1_out2), .clk(or_1_out), .R(1'b0), .Qn(s_r_ff_6_qn), .reset(and_7_out));  // open: Q, preset, en
  Register #(.width(5)) register_11 (
    .D(multiplexer_1_out), .en(decoder_1_out2), .Q(register_11_q), .clk(or_1_out), .clr(and_7_out));
  Register #(.width(32)) register_12 (
    .D(multiplexer_2_out), .en(decoder_1_out2), .Q(register_12_q), .clk(or_1_out), .clr(and_7_out));
  Comparator #(.width(5)) comparator_7 (.a(register_11_q), .b(wbAddr), .eq(comparator_7_eq));  // open: gt, lt
  S_R_Flip_Flop s_r_ff_7 (
    .S(decoder_1_out1), .clk(or_1_out), .R(1'b0), .Qn(s_r_ff_7_qn), .reset(and_8_out));  // open: Q, preset, en
  Register #(.width(5)) register_13 (
    .D(multiplexer_1_out), .en(decoder_1_out1), .Q(register_13_q), .clk(or_1_out), .clr(and_8_out));
  Register #(.width(32)) register_14 (
    .D(multiplexer_2_out), .en(decoder_1_out1), .Q(register_14_q), .clk(or_1_out), .clr(and_8_out));
  and and_7 (and_7_out, comparator_7_eq, wbEn);
  S_R_Flip_Flop s_r_ff_8 (
    .S(decoder_1_out0), .clk(or_1_out), .R(1'b0), .Qn(s_r_ff_8_qn), .reset(and_9_out));  // open: Q, preset, en
  Register #(.width(5)) register_15 (
    .D(multiplexer_1_out), .en(decoder_1_out0), .Q(register_15_q), .clk(or_1_out), .clr(and_9_out));
  Register #(.width(32)) register_16 (
    .D(multiplexer_2_out), .en(decoder_1_out0), .Q(register_16_q), .clk(or_1_out), .clr(and_9_out));
  and and_8 (and_8_out, comparator_8_eq, wbEn);
  Comparator #(.width(5)) comparator_8 (.a(register_13_q), .b(wbAddr), .eq(comparator_8_eq));  // open: gt, lt
  and and_9 (and_9_out, comparator_9_eq, wbEn);
  Comparator #(.width(5)) comparator_9 (.a(register_15_q), .b(wbAddr), .eq(comparator_9_eq));  // open: gt, lt
  Priority_Encoder priority_encoder_1 (
    .in0(s_r_ff_8_qn), .in1(s_r_ff_7_qn), .in2(s_r_ff_6_qn), .in3(s_r_ff_5_qn), .in4(s_r_ff_4_qn),
    .in5(s_r_ff_3_qn), .in6(s_r_ff_2_qn), .in7(s_r_ff_1_qn), .out(priority_encoder_1_out),
    .en_out(priority_encoder_1_en_out));  // open: en_in, gs
  Multiplexer #(.width(3), .disabled(0), .enable("false")) multiplexer_3 (
    .in0(priority_encoder_1_out), .in1(3'b111), .out(multiplexer_3_out), .sel(priority_encoder_1_en_out));
  Decoder #(.select(3), .disabled(0)) decoder_1 (
    .out0(decoder_1_out0), .out1(decoder_1_out1), .out2(decoder_1_out2), .out3(decoder_1_out3),
    .out4(decoder_1_out4), .out5(decoder_1_out5), .out6(decoder_1_out6), .out7(decoder_1_out7),
    .sel(multiplexer_3_out), .en(not_3_out));
  Comparator #(.width(5)) comparator_10 (.a(rs), .b(rd__from_mem), .eq(comparator_10_eq));  // open: gt, lt
  Comparator #(.width(5)) comparator_11 (.a(rd__from_mem), .b(rt), .eq(comparator_11_eq));  // open: gt, lt
  Multiplexer #(.select(3), .width(32), .disabled(0), .enable("false")) multiplexer_4 (
    .in0(register_2_q), .in1(register_4_q), .in2(register_6_q), .in3(register_8_q), .in4(register_10_q),
    .in5(register_12_q), .in6(register_14_q), .in7(register_16_q), .out(multiplexer_4_out),
    .sel(priority_encoder_2_out));
  Multiplexer #(.width(32), .disabled(0), .enable("false")) multiplexer_5 (
    .in0(multiplexer_4_out), .in1(s), .out(multiplexer_5_out), .sel(priority_encoder_2_en_out));
  Multiplexer #(.select(3), .width(32), .disabled(0), .enable("false")) multiplexer_6 (
    .in0(register_2_q), .in1(register_4_q), .in2(register_6_q), .in3(register_8_q), .in4(register_10_q),
    .in5(register_12_q), .in6(register_14_q), .in7(register_16_q), .out(multiplexer_6_out),
    .sel(priority_encoder_3_out));
  _8x1_comparator u_8x1_comparator_1 (
    .in_2(register_1_q), .in_3(register_3_q), .in_4(register_5_q), .in_5(register_7_q), .in_6(register_9_q),
    .in_7(register_11_q), .in_8(register_13_q), .in_9(register_15_q), .out_10(n8x1_comparator_1_out_10),
    .out_11(n8x1_comparator_1_out_11), .out_12(n8x1_comparator_1_out_12), .out_13(n8x1_comparator_1_out_13),
    .out_14(n8x1_comparator_1_out_14), .out_15(n8x1_comparator_1_out_15), .out_16(n8x1_comparator_1_out_16),
    .out_17(n8x1_comparator_1_out_17));  // open: in_1
  Priority_Encoder priority_encoder_2 (
    .in0(n8x1_comparator_1_out_10), .in1(n8x1_comparator_1_out_11), .in2(n8x1_comparator_1_out_12),
    .in3(n8x1_comparator_1_out_13), .in4(n8x1_comparator_1_out_14), .in5(n8x1_comparator_1_out_15),
    .in6(n8x1_comparator_1_out_16), .in7(n8x1_comparator_1_out_17), .out(priority_encoder_2_out),
    .en_out(priority_encoder_2_en_out));  // open: en_in, gs
  _8x1_comparator u_8x1_comparator_2 (
    .in_2(register_1_q), .in_3(register_3_q), .in_4(register_5_q), .in_5(register_7_q), .in_6(register_9_q),
    .in_7(register_11_q), .in_8(register_13_q), .in_9(register_15_q), .out_10(n8x1_comparator_2_out_10),
    .out_11(n8x1_comparator_2_out_11), .out_12(n8x1_comparator_2_out_12), .out_13(n8x1_comparator_2_out_13),
    .out_14(n8x1_comparator_2_out_14), .out_15(n8x1_comparator_2_out_15), .out_16(n8x1_comparator_2_out_16),
    .out_17(n8x1_comparator_2_out_17));  // open: in_1
  Priority_Encoder priority_encoder_3 (
    .in0(n8x1_comparator_2_out_10), .in1(n8x1_comparator_2_out_11), .in2(n8x1_comparator_2_out_12),
    .in3(n8x1_comparator_2_out_13), .in4(n8x1_comparator_2_out_14), .in5(n8x1_comparator_2_out_15),
    .in6(n8x1_comparator_2_out_16), .in7(n8x1_comparator_2_out_17), .out(priority_encoder_3_out),
    .en_out(priority_encoder_3_en_out));  // open: en_in, gs
  Multiplexer #(.width(32), .disabled(0), .enable("false")) multiplexer_7 (
    .in0(multiplexer_5_out), .in1(result__from_mem), .out(s_2), .sel(comparator_10_eq));
  Multiplexer #(.width(32), .disabled(0), .enable("false")) multiplexer_8 (
    .in0(multiplexer_6_out), .in1(t), .out(multiplexer_8_out), .sel(priority_encoder_3_en_out));
  Multiplexer #(.width(32), .disabled(0), .enable("false")) multiplexer_9 (
    .in0(multiplexer_8_out), .in1(result__from_mem), .out(t_2), .sel(comparator_11_eq));

  // Notes on the sheet:
  //   OLD CIRCUIT
endmodule
module forwarding_v2 (
  input  mem_enable,
  input  [31:0] d__from_mem,
  input  [4:0] rd__from_mem,
  input  [31:0] d,
  input  clk,
  input  [4:0] WB_addr__wb,
  input  WB_en__wb,
  input  WB_en__ex,
  input  [4:0] rs,
  input  [4:0] rt,
  input  [4:0] rd,
  input  [31:0] s,
  input  [31:0] t,
  output [31:0] s_2,
  output [31:0] t_2
);

  wire and_1_out, and_2_out, and_3_out, and_4_out, and_5_out, and_6_out, and_7_out, and_8_out, and_9_out,
       and_10_out, and_11_out, and_12_out, and_13_out, and_14_out, and_15_out, and_16_out, and_17_out,
       and_18_out, and_19_out, and_20_out, and_21_out, buffer_1_out, buffer_2_out, buffer_3_out,
       comparator_1_eq, comparator_2_eq, comparator_3_eq, comparator_4_eq, comparator_5_eq, comparator_6_eq,
       comparator_7_eq, comparator_8_eq, comparator_9_eq, comparator_10_eq, comparator_11_eq,
       comparator_12_eq, comparator_13_eq, comparator_14_eq, comparator_15_eq, comparator_16_eq,
       comparator_17_eq, comparator_18_eq, comparator_19_eq, comparator_20_eq, comparator_21_eq,
       comparator_22_eq, comparator_23_eq, comparator_24_eq, comparator_25_eq, comparator_26_eq,
       comparator_27_eq, decoder_1_out0, decoder_1_out1, decoder_1_out2, decoder_1_out3, decoder_1_out4,
       decoder_1_out5, decoder_1_out6, decoder_1_out7, decoder_2_out0, decoder_2_out1, decoder_2_out2,
       decoder_2_out3, decoder_2_out4, decoder_2_out5, decoder_2_out6, decoder_2_out7, falling_edge_1_out_2,
       n8x1_comparator_1_out_10, n8x1_comparator_1_out_11, n8x1_comparator_1_out_12,
       n8x1_comparator_1_out_13, n8x1_comparator_1_out_14, n8x1_comparator_1_out_15,
       n8x1_comparator_1_out_16, n8x1_comparator_1_out_17, n8x1_comparator_2_out_10,
       n8x1_comparator_2_out_11, n8x1_comparator_2_out_12, n8x1_comparator_2_out_13,
       n8x1_comparator_2_out_14, n8x1_comparator_2_out_15, n8x1_comparator_2_out_16,
       n8x1_comparator_2_out_17, not_1_out, not_2_out, or_1_out, or_2_out, or_3_out, or_4_out, or_5_out,
       or_6_out, or_7_out, or_8_out, or_9_out, priority_encoder_1_gs, priority_encoder_2_en_out,
       priority_encoder_3_en_out, priority_encoder_4_en_out, s_r_ff_1_qn, s_r_ff_2_qn, s_r_ff_3_qn,
       s_r_ff_4_qn, s_r_ff_5_qn, s_r_ff_6_qn, s_r_ff_7_qn, s_r_ff_8_qn;
  wire [2:0] multiplexer_5_out, priority_encoder_1_out, priority_encoder_2_out, priority_encoder_3_out,
       priority_encoder_4_out;
  wire [4:0] multiplexer_2_out, multiplexer_11_out, register_1_q, register_3_q, register_5_q, register_7_q,
       register_9_q, register_11_q, register_13_q, register_15_q;
  wire [31:0] multiplexer_1_out, multiplexer_3_out, multiplexer_4_out, multiplexer_6_out, multiplexer_7_out,
       multiplexer_8_out, multiplexer_9_out, multiplexer_10_out, register_2_q, register_4_q, register_6_q,
       register_8_q, register_10_q, register_12_q, register_14_q, register_16_q;

  not not_1 (not_1_out, clk);
  buf buffer_1 (buffer_1_out, buffer_2_out);
  buf buffer_2 (buffer_2_out, not_1_out);
  falling_edge falling_edge_1 (.in_1(clk), .out_2(falling_edge_1_out_2));
  buf buffer_3 (buffer_3_out, buffer_1_out);
  not not_2 (not_2_out, buffer_3_out);
  and and_1 (and_1_out, not_2_out, not_1_out);
  Multiplexer #(.width(32), .disabled(0), .enable("false")) multiplexer_1 (
    .in0(d), .in1(multiplexer_10_out), .out(multiplexer_1_out), .sel(clk));
  Multiplexer #(.width(5), .disabled(0), .enable("false")) multiplexer_2 (
    .in0(rd), .in1(multiplexer_11_out), .out(multiplexer_2_out), .sel(clk));
  or or_1 (or_1_out, clk, and_1_out);
  Comparator #(.width(5)) comparator_1 (.a(register_1_q), .b(WB_addr__wb), .eq(comparator_1_eq));  // open: gt, lt
  Comparator #(.width(5)) comparator_2 (.a(multiplexer_2_out), .b({5{1'b0}}), .eq(comparator_2_eq));  // open: gt, lt
  Comparator #(.width(5)) comparator_3 (.a(multiplexer_2_out), .b(register_1_q), .eq(comparator_3_eq));  // open: gt, lt
  and and_2 (and_2_out, comparator_3_eq, ~comparator_2_eq);  // AND_Gate
  Register #(.width(5)) register_1 (
    .D(multiplexer_2_out), .en(or_9_out), .Q(register_1_q), .clk(or_1_out), .clr(and_3_out));
  Register #(.width(32)) register_2 (
    .D(multiplexer_1_out), .en(or_9_out), .Q(register_2_q), .clk(or_1_out), .clr(and_3_out));
  S_R_Flip_Flop s_r_ff_1 (
    .S(or_9_out), .clk(or_1_out), .R(1'b0), .Qn(s_r_ff_1_qn), .reset(and_3_out), .en(or_1_out));  // open: Q, preset
  and and_3 (and_3_out, comparator_1_eq, falling_edge_1_out_2, WB_en__wb);
  Register #(.width(5)) register_3 (
    .D(multiplexer_2_out), .en(or_8_out), .Q(register_3_q), .clk(or_1_out), .clr(and_4_out));
  Register #(.width(32)) register_4 (
    .D(multiplexer_1_out), .en(or_8_out), .Q(register_4_q), .clk(or_1_out), .clr(and_4_out));
  S_R_Flip_Flop s_r_ff_2 (
    .S(or_8_out), .clk(or_1_out), .R(1'b0), .Qn(s_r_ff_2_qn), .reset(and_4_out), .en(or_1_out));  // open: Q, preset
  and and_4 (and_4_out, comparator_4_eq, falling_edge_1_out_2, WB_en__wb);
  Comparator #(.width(5)) comparator_4 (.a(register_3_q), .b(WB_addr__wb), .eq(comparator_4_eq));  // open: gt, lt
  Comparator #(.width(5)) comparator_5 (.a(multiplexer_2_out), .b({5{1'b0}}), .eq(comparator_5_eq));  // open: gt, lt
  Comparator #(.width(5)) comparator_6 (.a(multiplexer_2_out), .b(register_3_q), .eq(comparator_6_eq));  // open: gt, lt
  and and_5 (and_5_out, comparator_6_eq, ~comparator_5_eq);  // AND_Gate
  Comparator #(.width(5)) comparator_7 (.a(multiplexer_2_out), .b({5{1'b0}}), .eq(comparator_7_eq));  // open: gt, lt
  Comparator #(.width(5)) comparator_8 (.a(multiplexer_2_out), .b(register_5_q), .eq(comparator_8_eq));  // open: gt, lt
  Register #(.width(5)) register_5 (
    .D(multiplexer_2_out), .en(or_7_out), .Q(register_5_q), .clk(or_1_out), .clr(and_6_out));
  Register #(.width(32)) register_6 (
    .D(multiplexer_1_out), .en(or_7_out), .Q(register_6_q), .clk(or_1_out), .clr(and_6_out));
  S_R_Flip_Flop s_r_ff_3 (
    .S(or_7_out), .clk(or_1_out), .R(1'b0), .Qn(s_r_ff_3_qn), .reset(and_6_out), .en(or_1_out));  // open: Q, preset
  and and_6 (and_6_out, comparator_9_eq, falling_edge_1_out_2, WB_en__wb);
  Comparator #(.width(5)) comparator_9 (.a(register_5_q), .b(WB_addr__wb), .eq(comparator_9_eq));  // open: gt, lt
  and and_7 (and_7_out, comparator_8_eq, ~comparator_7_eq);  // AND_Gate
  Comparator #(.width(5)) comparator_10 (.a(multiplexer_2_out), .b({5{1'b0}}), .eq(comparator_10_eq));  // open: gt, lt
  Comparator #(.width(5)) comparator_11 (
    .a(multiplexer_2_out), .b(register_7_q), .eq(comparator_11_eq));  // open: gt, lt
  and and_8 (and_8_out, comparator_11_eq, ~comparator_10_eq);  // AND_Gate
  Register #(.width(5)) register_7 (
    .D(multiplexer_2_out), .en(or_6_out), .Q(register_7_q), .clk(or_1_out), .clr(and_9_out));
  Register #(.width(32)) register_8 (
    .D(multiplexer_1_out), .en(or_6_out), .Q(register_8_q), .clk(or_1_out), .clr(and_9_out));
  S_R_Flip_Flop s_r_ff_4 (
    .S(or_6_out), .clk(or_1_out), .R(1'b0), .Qn(s_r_ff_4_qn), .reset(and_9_out), .en(or_1_out));  // open: Q, preset
  and and_9 (and_9_out, comparator_12_eq, falling_edge_1_out_2, WB_en__wb);
  Comparator #(.width(5)) comparator_12 (.a(register_7_q), .b(WB_addr__wb), .eq(comparator_12_eq));  // open: gt, lt
  Comparator #(.width(5)) comparator_13 (.a(register_9_q), .b(WB_addr__wb), .eq(comparator_13_eq));  // open: gt, lt
  Comparator #(.width(5)) comparator_14 (.a(multiplexer_2_out), .b({5{1'b0}}), .eq(comparator_14_eq));  // open: gt, lt
  Comparator #(.width(5)) comparator_15 (
    .a(multiplexer_2_out), .b(register_9_q), .eq(comparator_15_eq));  // open: gt, lt
  and and_10 (and_10_out, comparator_15_eq, ~comparator_14_eq);  // AND_Gate
  Register #(.width(5)) register_9 (
    .D(multiplexer_2_out), .en(or_5_out), .Q(register_9_q), .clk(or_1_out), .clr(and_11_out));
  Register #(.width(32)) register_10 (
    .D(multiplexer_1_out), .en(or_5_out), .Q(register_10_q), .clk(or_1_out), .clr(and_11_out));
  S_R_Flip_Flop s_r_ff_5 (
    .S(or_5_out), .clk(or_1_out), .R(1'b0), .Qn(s_r_ff_5_qn), .reset(and_11_out), .en(or_1_out));  // open: Q, preset
  and and_11 (and_11_out, comparator_13_eq, falling_edge_1_out_2, WB_en__wb);
  Register #(.width(5)) register_11 (
    .D(multiplexer_2_out), .en(or_4_out), .Q(register_11_q), .clk(or_1_out), .clr(and_12_out));
  Register #(.width(32)) register_12 (
    .D(multiplexer_1_out), .en(or_4_out), .Q(register_12_q), .clk(or_1_out), .clr(and_12_out));
  S_R_Flip_Flop s_r_ff_6 (
    .S(or_4_out), .clk(or_1_out), .R(1'b0), .Qn(s_r_ff_6_qn), .reset(and_12_out), .en(or_1_out));  // open: Q, preset
  and and_12 (and_12_out, comparator_16_eq, falling_edge_1_out_2, WB_en__wb);
  Comparator #(.width(5)) comparator_16 (.a(register_11_q), .b(WB_addr__wb), .eq(comparator_16_eq));  // open: gt, lt
  Comparator #(.width(5)) comparator_17 (.a(multiplexer_2_out), .b({5{1'b0}}), .eq(comparator_17_eq));  // open: gt, lt
  Comparator #(.width(5)) comparator_18 (
    .a(multiplexer_2_out), .b(register_11_q), .eq(comparator_18_eq));  // open: gt, lt
  and and_13 (and_13_out, comparator_18_eq, ~comparator_17_eq);  // AND_Gate
  Comparator #(.width(5)) comparator_19 (.a(multiplexer_2_out), .b({5{1'b0}}), .eq(comparator_19_eq));  // open: gt, lt
  Comparator #(.width(5)) comparator_20 (
    .a(multiplexer_2_out), .b(register_13_q), .eq(comparator_20_eq));  // open: gt, lt
  Register #(.width(5)) register_13 (
    .D(multiplexer_2_out), .en(or_3_out), .Q(register_13_q), .clk(or_1_out), .clr(and_14_out));
  Register #(.width(32)) register_14 (
    .D(multiplexer_1_out), .en(or_3_out), .Q(register_14_q), .clk(or_1_out), .clr(and_14_out));
  S_R_Flip_Flop s_r_ff_7 (
    .S(or_3_out), .clk(or_1_out), .R(1'b0), .Qn(s_r_ff_7_qn), .reset(and_14_out), .en(or_1_out));  // open: Q, preset
  and and_14 (and_14_out, comparator_21_eq, falling_edge_1_out_2, WB_en__wb);
  Comparator #(.width(5)) comparator_21 (.a(register_13_q), .b(WB_addr__wb), .eq(comparator_21_eq));  // open: gt, lt
  and and_15 (and_15_out, comparator_20_eq, ~comparator_19_eq);  // AND_Gate
  Comparator #(.width(5)) comparator_22 (.a(multiplexer_2_out), .b({5{1'b0}}), .eq(comparator_22_eq));  // open: gt, lt
  Comparator #(.width(5)) comparator_23 (
    .a(multiplexer_2_out), .b(register_15_q), .eq(comparator_23_eq));  // open: gt, lt
  and and_16 (and_16_out, comparator_23_eq, ~comparator_22_eq);  // AND_Gate
  Register #(.width(5)) register_15 (
    .D(multiplexer_2_out), .en(or_2_out), .Q(register_15_q), .clk(or_1_out), .clr(and_17_out));
  Register #(.width(32)) register_16 (
    .D(multiplexer_1_out), .en(or_2_out), .Q(register_16_q), .clk(or_1_out), .clr(and_17_out));
  S_R_Flip_Flop s_r_ff_8 (
    .S(or_2_out), .clk(or_1_out), .R(1'b0), .Qn(s_r_ff_8_qn), .reset(and_17_out), .en(or_1_out));  // open: Q, preset
  and and_17 (and_17_out, comparator_24_eq, falling_edge_1_out_2, WB_en__wb);
  Comparator #(.width(5)) comparator_24 (.a(register_15_q), .b(WB_addr__wb), .eq(comparator_24_eq));  // open: gt, lt
  Priority_Encoder priority_encoder_1 (
    .in0(and_16_out), .in1(and_15_out), .in2(and_13_out), .in3(and_10_out), .in4(and_8_out), .in5(and_7_out),
    .in6(and_5_out), .in7(and_2_out), .out(priority_encoder_1_out), .gs(priority_encoder_1_gs));  // open: en_in, en_out
  Priority_Encoder priority_encoder_2 (
    .in0(s_r_ff_8_qn), .in1(s_r_ff_7_qn), .in2(s_r_ff_6_qn), .in3(s_r_ff_5_qn), .in4(s_r_ff_4_qn),
    .in5(s_r_ff_3_qn), .in6(s_r_ff_2_qn), .in7(s_r_ff_1_qn), .out(priority_encoder_2_out),
    .en_out(priority_encoder_2_en_out));  // open: en_in, gs
  or or_2 (or_2_out, decoder_1_out0, decoder_2_out0);
  or or_3 (or_3_out, decoder_1_out1, decoder_2_out1);
  or or_4 (or_4_out, decoder_1_out2, decoder_2_out2);
  or or_5 (or_5_out, decoder_1_out3, decoder_2_out3);
  or or_6 (or_6_out, decoder_1_out4, decoder_2_out4);
  or or_7 (or_7_out, decoder_1_out5, decoder_2_out5);
  or or_8 (or_8_out, decoder_1_out6, decoder_2_out6);
  or or_9 (or_9_out, decoder_1_out7, decoder_2_out7);
  _8x1_comparator u_8x1_comparator_1 (
    .in_2(register_15_q), .in_3(register_13_q), .in_4(register_11_q), .in_5(register_9_q),
    .in_6(register_7_q), .in_7(register_5_q), .in_8(register_3_q), .in_9(register_1_q), .in_1(rs),
    .out_10(n8x1_comparator_1_out_10), .out_11(n8x1_comparator_1_out_11), .out_12(n8x1_comparator_1_out_12),
    .out_13(n8x1_comparator_1_out_13), .out_14(n8x1_comparator_1_out_14), .out_15(n8x1_comparator_1_out_15),
    .out_16(n8x1_comparator_1_out_16), .out_17(n8x1_comparator_1_out_17));
  _8x1_comparator u_8x1_comparator_2 (
    .in_2(register_15_q), .in_3(register_13_q), .in_4(register_11_q), .in_5(register_9_q),
    .in_6(register_7_q), .in_7(register_5_q), .in_8(register_3_q), .in_9(register_1_q), .in_1(rt),
    .out_10(n8x1_comparator_2_out_10), .out_11(n8x1_comparator_2_out_11), .out_12(n8x1_comparator_2_out_12),
    .out_13(n8x1_comparator_2_out_13), .out_14(n8x1_comparator_2_out_14), .out_15(n8x1_comparator_2_out_15),
    .out_16(n8x1_comparator_2_out_16), .out_17(n8x1_comparator_2_out_17));
  Multiplexer #(.select(3), .width(32), .disabled(0), .enable("false")) multiplexer_3 (
    .in0(register_16_q), .in1(register_14_q), .in2(register_12_q), .in3(register_10_q), .in4(register_8_q),
    .in5(register_6_q), .in6(register_4_q), .in7(register_2_q), .out(multiplexer_3_out),
    .sel(priority_encoder_3_out));
  Multiplexer #(.select(3), .width(32), .disabled(0), .enable("false")) multiplexer_4 (
    .in0(register_16_q), .in1(register_14_q), .in2(register_12_q), .in3(register_10_q), .in4(register_8_q),
    .in5(register_6_q), .in6(register_4_q), .in7(register_2_q), .out(multiplexer_4_out),
    .sel(priority_encoder_4_out));
  Comparator #(.width(5)) comparator_25 (.a(multiplexer_2_out), .b({5{1'b0}}), .eq(comparator_25_eq));  // open: gt, lt
  Priority_Encoder priority_encoder_3 (
    .in0(n8x1_comparator_1_out_10), .in1(n8x1_comparator_1_out_11), .in2(n8x1_comparator_1_out_12),
    .in3(n8x1_comparator_1_out_13), .in4(n8x1_comparator_1_out_14), .in5(n8x1_comparator_1_out_15),
    .in6(n8x1_comparator_1_out_16), .in7(n8x1_comparator_1_out_17), .out(priority_encoder_3_out),
    .en_out(priority_encoder_3_en_out));  // open: en_in, gs
  Priority_Encoder priority_encoder_4 (
    .in0(n8x1_comparator_2_out_10), .in1(n8x1_comparator_2_out_11), .in2(n8x1_comparator_2_out_12),
    .in3(n8x1_comparator_2_out_13), .in4(n8x1_comparator_2_out_14), .in5(n8x1_comparator_2_out_15),
    .in6(n8x1_comparator_2_out_16), .in7(n8x1_comparator_2_out_17), .out(priority_encoder_4_out),
    .en_out(priority_encoder_4_en_out));  // open: en_in, gs
  Multiplexer #(.width(3), .enable("false")) multiplexer_5 (
    .in0(priority_encoder_2_out), .in1(3'b111), .out(multiplexer_5_out), .sel(priority_encoder_2_en_out));
  Decoder #(.select(3), .disabled(0)) decoder_1 (
    .out0(decoder_1_out0), .out1(decoder_1_out1), .out2(decoder_1_out2), .out3(decoder_1_out3),
    .out4(decoder_1_out4), .out5(decoder_1_out5), .out6(decoder_1_out6), .out7(decoder_1_out7),
    .sel(multiplexer_5_out), .en(and_18_out));
  Decoder #(.select(3), .disabled(0)) decoder_2 (
    .out0(decoder_2_out0), .out1(decoder_2_out1), .out2(decoder_2_out2), .out3(decoder_2_out3),
    .out4(decoder_2_out4), .out5(decoder_2_out5), .out6(decoder_2_out6), .out7(decoder_2_out7),
    .sel(priority_encoder_1_out), .en(and_19_out));
  Multiplexer #(.width(32), .disabled(0), .enable("false")) multiplexer_6 (
    .in0(multiplexer_3_out), .in1(s), .out(multiplexer_6_out), .sel(priority_encoder_3_en_out));
  Multiplexer #(.width(32), .disabled(0), .enable("false")) multiplexer_7 (
    .in0(multiplexer_6_out), .in1(multiplexer_10_out), .out(multiplexer_7_out), .sel(and_21_out));
  Multiplexer #(.width(32), .disabled(0), .enable("false")) multiplexer_8 (
    .in0(multiplexer_4_out), .in1(t), .out(multiplexer_8_out), .sel(priority_encoder_4_en_out));
  Multiplexer #(.width(32), .disabled(0), .enable("false")) multiplexer_9 (
    .in0(multiplexer_8_out), .in1(multiplexer_10_out), .out(multiplexer_9_out), .sel(and_20_out));
  and and_18 (and_18_out, WB_en__ex, ~priority_encoder_1_gs, ~comparator_25_eq);  // AND_Gate
  and and_19 (and_19_out, priority_encoder_1_gs, WB_en__ex, ~comparator_25_eq);  // AND_Gate
  Comparator #(.width(5)) comparator_26 (.a(rs), .b(multiplexer_11_out), .eq(comparator_26_eq));  // open: gt, lt
  and and_20 (and_20_out, comparator_26_eq, mem_enable);
  Comparator #(.width(5)) comparator_27 (.a(rt), .b(multiplexer_11_out), .eq(comparator_27_eq));  // open: gt, lt
  and and_21 (and_21_out, comparator_27_eq, mem_enable);
  Register #(.width(32), .trigger("high")) register_17 (
    .D(multiplexer_7_out), .en(clk), .Q(s_2), .clk(clk));  // open: clr
  Register #(.width(32), .trigger("high")) register_18 (
    .D(multiplexer_9_out), .en(clk), .Q(t_2), .clk(clk));  // open: clr
  // Probe on multiplexer_9_out
  // Probe on multiplexer_7_out
  Multiplexer #(.width(32), .disabled(0), .enable("false")) multiplexer_10 (
    .in0({32{1'b0}}), .in1(d__from_mem), .out(multiplexer_10_out), .sel(mem_enable));
  Multiplexer #(.width(5), .disabled(0), .enable("false")) multiplexer_11 (
    .in0({5{1'b0}}), .in1(rd__from_mem), .out(multiplexer_11_out), .sel(mem_enable));

  // Notes on the sheet:
  //   OLD CIRCUIT
endmodule

module _8x1_comparator (
  input  [4:0] in_1,
  input  [4:0] in_2,
  input  [4:0] in_3,
  input  [4:0] in_4,
  input  [4:0] in_5,
  input  [4:0] in_6,
  input  [4:0] in_7,
  input  [4:0] in_8,
  input  [4:0] in_9,
  output out_10,
  output out_11,
  output out_12,
  output out_13,
  output out_14,
  output out_15,
  output out_16,
  output out_17
);

  Comparator #(.width(5)) comparator_1 (.a(in_2), .b(in_1), .eq(out_10));  // open: gt, lt
  Comparator #(.width(5)) comparator_2 (.a(in_3), .b(in_1), .eq(out_11));  // open: gt, lt
  Comparator #(.width(5)) comparator_3 (.a(in_4), .b(in_1), .eq(out_12));  // open: gt, lt
  Comparator #(.width(5)) comparator_4 (.a(in_5), .b(in_1), .eq(out_13));  // open: gt, lt
  Comparator #(.width(5)) comparator_5 (.a(in_6), .b(in_1), .eq(out_14));  // open: gt, lt
  Comparator #(.width(5)) comparator_6 (.a(in_7), .b(in_1), .eq(out_15));  // open: gt, lt
  Comparator #(.width(5)) comparator_7 (.a(in_8), .b(in_1), .eq(out_16));  // open: gt, lt
  Comparator #(.width(5)) comparator_8 (.a(in_9), .b(in_1), .eq(out_17));  // open: gt, lt

  // Notes on the sheet:
  //   used in old forwarding units
endmodule
