// Logisim project muCPU[rev1].circ as structural Verilog: 3 circuits, main circuit main
module main (
);

  wire and_1_out, and_2_out, and_4_out, and_5_out, and_6_out, bit_extender_3_out, clock_1_out,
       comparator_1_eq, ctl_3_q, decoder_1_out0, decoder_1_out1, decoder_1_out2, decoder_1_out3,
       decoder_2_out1, decoder_2_out2, decoder_2_out3, mem_en, not_1_out, not_2_out, or_1_out, or_2_out,
       or_3_out, register_4_q, write_to_mem;
  wire [1:0] controlled_buffer_2_out, counter_1_q, multiplexer_3_out, rd_q, register_2_q, register_3_q,
       res_3_q;
  wire [1:1] ctl_2_q;
  wire [2:0] bit_extender_1_out, ctl_q, or_4_out;
  wire [7:0] adder_1_out, adder_2_out, adder_3_out, adder_4_out, bit_extender_2_out, data_from_mem,
       data_to_mem, imm_2_q, imm_q, mem_address, multiplexer_1_out, multiplexer_2_out, multiplexer_4_out,
       multiplexer_5_out, multiplexer_6_out, multiplexer_7_out, multiplexer_8_out, multiplexer_9_out,
       nand_1_out, PCnext_2_q, PCnext_3_q, PCnext_q, r1_q, r2_q, r3_q, register_1_q, res_2_q, s_q,
       shift_register_1_q0, shift_register_1_q1, shifter_1_out, t_q;
  wire [15:0] IR_q;

  Multiplexer #(.width(8), .disabled(0), .enable("false")) multiplexer_1 (
    .in0(adder_1_out), .in1(multiplexer_8_out), .out(multiplexer_1_out), .sel(decoder_1_out2));
  or or_1 (or_1_out, decoder_1_out2, or_2_out);
  Adder adder_1 (.a(8'h1), .b(register_1_q), .out(adder_1_out));  // open: cin, cout
  Register register_1 (.D(multiplexer_1_out), .en(or_1_out), .Q(register_1_q), .clk(clock_1_out));  // open: clr
  Multiplexer #(.width(8), .disabled(0), .enable("false")) multiplexer_2 (
    .in0(register_1_q), .in1(mem_address), .out(multiplexer_2_out), .sel(mem_en));
  not not_1 (not_1_out, write_to_mem);
  Clock clock_1 (.out(clock_1_out));
  assign data_from_mem = write_to_mem ? data_to_mem : 8'bz;  // Controlled_Buffer controlled_buffer_1
  RAM ram_1 (
    .addr(multiplexer_2_out), .data(data_from_mem), .sel(1'b1), .clk(clock_1_out), .ld(not_1_out));  // open: clr
  or or_2 (or_2_out, decoder_1_out0, decoder_1_out1);
  Decoder #(.select(2), .disabled(0), .enable("false")) decoder_1 (
    .out0(decoder_1_out0), .out1(decoder_1_out1), .out2(decoder_1_out2), .out3(decoder_1_out3),
    .sel(counter_1_q));
  Counter #(.width(2), .max('h3)) counter_1 (
    .count(1'b1), .Q(counter_1_q), .clk(clock_1_out));  // open: load, D, carry, clr
  Shift_Register #(.width(8), .length(2)) shift_register_1 (
    .shift(or_2_out), .in(data_from_mem), .clk(clock_1_out), .q0(shift_register_1_q0),
    .q1(shift_register_1_q1));  // open: out, load, clr, d0, d1
  // Probe on {shift_register_1_q1, shift_register_1_q0}
  Decoder #(.select(2), .disabled(0)) decoder_2 (
    .out1(decoder_2_out1), .out2(decoder_2_out2), .out3(decoder_2_out3), .sel(res_3_q), .en(and_6_out));  // open: out0
  Register #(.width(16)) IR (
    .D({shift_register_1_q1, shift_register_1_q0}), .en(decoder_1_out3), .Q(IR_q), .clk(clock_1_out),
    .clr(decoder_1_out1));
  Register PCnext (.D(register_1_q), .en(decoder_1_out3), .Q(PCnext_q), .clk(clock_1_out), .clr(decoder_1_out1));
  Register r1 (.D(res_2_q), .en(decoder_2_out1), .Q(r1_q), .clk(clock_1_out));  // open: clr
  and and_1 (and_1_out, IR_q[12], IR_q[13], ~IR_q[14]);  // AND_Gate
  and and_2 (and_2_out, ~IR_q[12], ~IR_q[13], IR_q[14]);  // AND_Gate
  and and_3 (or_4_out[2], IR_q[12], ~IR_q[13], IR_q[14]);  // AND_Gate
  Register r2 (.D(res_2_q), .en(decoder_2_out2), .Q(r2_q), .clk(clock_1_out));  // open: clr
  Register r3 (.D(res_2_q), .en(decoder_2_out3), .Q(r3_q), .clk(clock_1_out));  // open: clr
  or or_3 (or_3_out, and_1_out, and_2_out, or_4_out[2]);
  Multiplexer #(.width(2), .disabled(0), .enable("false")) multiplexer_3 (
    .in0(IR_q[7:6]), .in1(IR_q[11:10]), .out(multiplexer_3_out), .sel(or_3_out));
  nor nor_1 (or_4_out[1], and_1_out, or_4_out[2]);
  or or_4 (or_4_out[0], and_2_out, or_4_out[2]);
  Multiplexer #(.select(2), .width(8), .disabled(0), .enable("false")) multiplexer_4 (
    .in0({8{1'b0}}), .in1(r1_q), .in2(r2_q), .in3(r3_q), .out(multiplexer_4_out), .sel(IR_q[9:8]));
  Multiplexer #(.select(2), .width(8), .disabled(0), .enable("false")) multiplexer_5 (
    .in0({8{1'b0}}), .in1(r1_q), .in2(r2_q), .in3(r3_q), .out(multiplexer_5_out), .sel(multiplexer_3_out));
  assign controlled_buffer_2_out = or_4_out[0] ? 2'b01 : 2'bz;  // Controlled_Buffer controlled_buffer_2
  assign controlled_buffer_2_out = not_2_out ? IR_q[13:12] : 2'bz;  // Controlled_Buffer controlled_buffer_3
  not not_2 (not_2_out, or_4_out[0]);
  Register s (.D(multiplexer_4_out), .en(decoder_1_out0), .Q(s_q), .clk(clock_1_out), .clr(decoder_1_out2));
  Register t (.D(multiplexer_5_out), .en(decoder_1_out0), .Q(t_q), .clk(clock_1_out), .clr(decoder_1_out2));
  Register imm (.D(IR_q[7:0]), .en(decoder_1_out0), .Q(imm_q), .clk(clock_1_out), .clr(decoder_1_out2));
  Register #(.width(2)) register_2 (
    .D(IR_q[11:10]), .en(decoder_1_out0), .Q(register_2_q), .clk(clock_1_out), .clr(decoder_1_out2));
  Register #(.width(2)) register_3 (
    .D(controlled_buffer_2_out), .en(decoder_1_out0), .Q(register_3_q), .clk(clock_1_out),
    .clr(decoder_1_out2));
  Register #(.width(3)) ctl (.D(or_4_out), .en(decoder_1_out0), .Q(ctl_q), .clk(clock_1_out), .clr(decoder_1_out2));
  Register PCnext_2 (.D(PCnext_q), .en(decoder_1_out0), .Q(PCnext_2_q), .clk(clock_1_out), .clr(decoder_1_out2));
  Bit_Extender #(.out_width(3)) bit_extender_1 (.in(multiplexer_6_out), .out(bit_extender_1_out));
  Multiplexer #(.width(8), .disabled(0), .enable("false")) multiplexer_6 (
    .in0(t_q), .in1(imm_q), .out(multiplexer_6_out), .sel(ctl_q[0]));
  Shifter shifter_1 (.in(s_q), .\dist (bit_extender_1_out), .out(shifter_1_out));
  Adder adder_2 (.a(s_q), .b(multiplexer_6_out), .out(adder_2_out));  // open: cin, cout
  assign nand_1_out = ~(s_q & multiplexer_6_out);  // NAND_Gate nand_1, 8 bits wide
  Comparator comparator_1 (.a(s_q), .b(multiplexer_6_out), .eq(comparator_1_eq));  // open: gt, lt
  assign bit_extender_2_out = {{7{1'b0}}, comparator_1_eq};  // Bit_Extender bit_extender_2
  Multiplexer #(.select(2), .width(8), .disabled(0), .enable("false")) multiplexer_7 (
    .in0(shifter_1_out), .in1(adder_2_out), .in2(nand_1_out), .in3(bit_extender_2_out),
    .out(multiplexer_7_out), .sel(register_3_q));
  Bit_Extender #(.out_width(1)) bit_extender_3 (.in(multiplexer_7_out), .out(bit_extender_3_out));
  and and_4 (and_4_out, register_3_q[0], register_3_q[1], bit_extender_3_out);
  Register res (.D(multiplexer_7_out), .en(decoder_1_out1), .Q(mem_address), .clk(clock_1_out), .clr(decoder_1_out3));
  Register t_2 (.D(t_q), .en(decoder_1_out1), .Q(data_to_mem), .clk(clock_1_out), .clr(decoder_1_out3));
  Register #(.width(2)) rd (.D(register_2_q), .en(decoder_1_out1), .Q(rd_q), .clk(clock_1_out), .clr(decoder_1_out3));
  Register #(.width(1)) register_4 (
    .D(and_4_out), .en(decoder_1_out1), .Q(register_4_q), .clk(clock_1_out), .clr(decoder_1_out3));
  Register #(.width(3)) ctl_2 (
    .D(ctl_q), .en(decoder_1_out1), .Q({write_to_mem, ctl_2_q[1], mem_en}), .clk(clock_1_out),
    .clr(decoder_1_out3));
  Register PCnext_3 (.D(PCnext_2_q), .en(decoder_1_out1), .Q(PCnext_3_q), .clk(clock_1_out), .clr(decoder_1_out3));
  Register imm_2 (.D(imm_q), .en(decoder_1_out1), .Q(imm_2_q), .clk(clock_1_out), .clr(decoder_1_out3));
  and and_5 (and_5_out, ~write_to_mem, mem_en);  // AND_Gate
  Adder adder_3 (.a(8'h2), .b(PCnext_3_q), .out(adder_3_out));  // open: cin, cout
  Multiplexer #(.width(8), .disabled(0), .enable("false")) multiplexer_8 (
    .in0(adder_3_out), .in1(adder_4_out), .out(multiplexer_8_out), .sel(register_4_q));
  Adder adder_4 (.a(PCnext_3_q), .b(imm_2_q), .out(adder_4_out));  // open: cin, cout
  Multiplexer #(.width(8), .disabled(0), .enable("false")) multiplexer_9 (
    .in0(mem_address), .in1(data_from_mem), .out(multiplexer_9_out), .sel(and_5_out));
  Register res_2 (.D(multiplexer_9_out), .en(decoder_1_out2), .Q(res_2_q), .clk(clock_1_out), .clr(decoder_1_out0));
  Register #(.width(2)) res_3 (.D(rd_q), .en(decoder_1_out2), .Q(res_3_q), .clk(clock_1_out), .clr(decoder_1_out0));
  Register #(.width(1)) ctl_3 (
    .D(ctl_2_q[1]), .en(decoder_1_out2), .Q(ctl_3_q), .clk(clock_1_out), .clr(decoder_1_out0));
  and and_6 (and_6_out, ctl_3_q, decoder_1_out3);

  // Notes on the sheet:
  //   Instruction Access [t0-t1] RAM Access [t2-t3]
  //   REGISTER FILE
  //   rt
  //   wb enable
  //   rs
  //   opcode
endmodule

module ALU (
  input  [3:0] s,
  input  [3:0] t,
  input  [1:0] opcode,
  output [3:0] result
);

  wire comparator_1_eq;
  wire [1:0] bit_extender_1_out;
  wire [3:0] adder_1_out, bit_extender_2_out, nand_1_out, shifter_1_out;

  Bit_Extender #(.in_width(4), .out_width(2)) bit_extender_1 (.in(t), .out(bit_extender_1_out));
  Shifter #(.width(4)) shifter_1 (.in(s), .\dist (bit_extender_1_out), .out(shifter_1_out));
  Adder #(.width(4)) adder_1 (.a(s), .b(t), .out(adder_1_out));  // open: cin, cout
  assign nand_1_out = ~(s & t);  // NAND_Gate nand_1, 4 bits wide
  Comparator #(.width(4)) comparator_1 (.a(s), .b(t), .eq(comparator_1_eq));  // open: gt, lt
  assign bit_extender_2_out = {{3{1'b0}}, comparator_1_eq};  // Bit_Extender bit_extender_2
  Multiplexer #(.select(2), .width(4), .disabled(0), .enable("false")) multiplexer_1 (
    .in0(shifter_1_out), .in1(adder_1_out), .in2(nand_1_out), .in3(bit_extender_2_out), .out(result),
    .sel(opcode));
endmodule

module hex_decoder (
  input  [3:0] in_1,
  input  [1:0] in_2,
  input  [1:0] in_3,
  input  [1:0] in_4,
  input  [5:0] in_5,
  input  [7:0] in_6,
  output [15:0] out_7
);

  wire and_1_out, and_2_out, and_3_out, not_1_out, or_1_out;

  Multiplexer #(.width(16), .disabled(0), .enable("false")) multiplexer_1 (
    .in0({in_1, in_2, in_3, in_6}), .in1({in_1, in_2, in_3, in_4, in_5}), .out(out_7), .sel(not_1_out));
  not not_1 (not_1_out, or_1_out);
  and and_1 (and_1_out, in_1[0], in_1[1], ~in_1[2]);  // AND_Gate
  or or_1 (or_1_out, and_1_out, and_2_out, and_3_out);
  and and_2 (and_2_out, ~in_1[0], ~in_1[1], in_1[2]);  // AND_Gate
  and and_3 (and_3_out, in_1[0], ~in_1[1], in_1[2]);  // AND_Gate
endmodule
