// Logisim project 000.circ as structural Verilog
module WaveNet (
  input  [15:0] In
);

  wire undriven, undriven_2, undriven_3, undriven_4, undriven_5;

  Shift_Register #(.width(16)) shift_register_1 (
    .clk(undriven), .clr(undriven_5));  // open: shift, in, out, load, d0, q0, d1, q1, d2, q2, d3, q3, d4, q4, d5, q5, d6, q6, d7, q7
  Shift_Register #(.width(16), .length(4)) shift_register_2 (
    .clk(undriven_2), .clr(undriven_5));  // open: shift, in, out, load, d0, q0, d1, q1, d2, q2, d3, q3
  Shift_Register #(.width(16), .length(2)) shift_register_3 (
    .clk(undriven_3), .clr(undriven_5));  // open: shift, in, out, load, d0, q0, d1, q1
  Shift_Register #(.width(16), .length(1)) shift_register_4 (
    .in(In), .clk(undriven_4), .clr(undriven_5));  // open: shift, out, load, d0, q0
endmodule

module Gate (
  input  [15:0] In
);

  wire undriven;

  ROM #(.addrWidth(16), .dataWidth(16)) rom_1 (.addr(In), .sel(undriven));  // open: data
  ROM #(.addrWidth(16), .dataWidth(16)) rom_2 (.addr(In), .sel(undriven));  // open: data
endmodule
