// Logisim project 2333.circ as structural Verilog: 4 circuits, main circuit 0
module main (
  input  [3:0] in_1,
  input  [3:0] in_2,
  input  [3:0] in_3,
  input  [3:0] in_4,
  input  [3:0] in_5,
  input  [3:0] in_6,
  input  [3:0] in_7,
  input  [3:0] in_8,
  input  [3:0] in_9,
  input  [2:0] in_10,
  input  in_11,
  input  in_12,
  output [3:0] out_13,
  output [3:0] out_14,
  output [3:0] out_15,
  output [3:0] out_16,
  output [3:0] out_17,
  output [3:0] out_18,
  output [3:0] out_19,
  output [3:0] out_20,
  output [3:0] out_21
);

  wire demultiplexer_2_out0, demultiplexer_2_out1, demultiplexer_2_out2, demultiplexer_2_out3,
       demultiplexer_2_out4, demultiplexer_2_out5, demultiplexer_2_out6, demultiplexer_2_out7, \突触_1_p7 ;
  wire [3:0] demultiplexer_1_out0, demultiplexer_1_out1, demultiplexer_1_out2, demultiplexer_1_out3,
       demultiplexer_1_out4, demultiplexer_1_out5, demultiplexer_1_out6, demultiplexer_1_out7;
  wire [7:0] \突触_1_p10 , \突触_2_p14 , \突触_3_p13 , \突触_4_p13 , \突触_5_p13 , \突触_6_p13 , \突触_7_p13 , \突触_8_p12 ;

  Demultiplexer #(.select(3), .width(4), .disabled(0), .enable("false")) demultiplexer_1 (
    .out0(demultiplexer_1_out0), .out1(demultiplexer_1_out1), .out2(demultiplexer_1_out2),
    .out3(demultiplexer_1_out3), .out4(demultiplexer_1_out4), .out5(demultiplexer_1_out5),
    .out6(demultiplexer_1_out6), .out7(demultiplexer_1_out7), .in(in_9), .sel(in_10));
  Demultiplexer #(.select(3), .disabled(0), .enable("false")) demultiplexer_2 (
    .out0(demultiplexer_2_out0), .out1(demultiplexer_2_out1), .out2(demultiplexer_2_out2),
    .out3(demultiplexer_2_out3), .out4(demultiplexer_2_out4), .out5(demultiplexer_2_out5),
    .out6(demultiplexer_2_out6), .out7(demultiplexer_2_out7), .in(in_11), .sel(in_10));
  // 突触 突触_1: pin names not known; wires that end beside it: in_1, in_1[3], in_2, demultiplexer_1_out0, demultiplexer_2_out0, in_12, \突触_1_p7 , out_13, \突触_1_p7 , \突触_1_p10 
  // 突触 突触_2: pin names not known; wires that end beside it: in_1[3], in_2, in_2[3], in_3, demultiplexer_1_out0, demultiplexer_1_out1, demultiplexer_2_out0, demultiplexer_2_out1, in_12, out_13, \突触_1_p7 , out_14, \突触_1_p7 , \突触_2_p14 
  // 突触 突触_3: pin names not known; wires that end beside it: in_2[3], in_3, in_3[3], in_4, demultiplexer_1_out1, demultiplexer_1_out2, demultiplexer_2_out1, demultiplexer_2_out2, out_14, \突触_1_p7 , out_16, \突触_1_p7 , \突触_3_p13 
  // 突触 突触_4: pin names not known; wires that end beside it: in_3[3], in_4, in_4[3], in_5, demultiplexer_1_out2, demultiplexer_1_out3, demultiplexer_2_out2, demultiplexer_2_out3, out_16, \突触_1_p7 , out_17, \突触_1_p7 , \突触_4_p13 
  // 突触 突触_5: pin names not known; wires that end beside it: in_4[3], in_5, in_5[3], in_6, demultiplexer_1_out3, demultiplexer_1_out4, demultiplexer_2_out3, demultiplexer_2_out4, out_17, \突触_1_p7 , out_18, \突触_1_p7 , \突触_5_p13 
  // 突触 突触_6: pin names not known; wires that end beside it: in_5[3], in_6, in_6[3], in_7, demultiplexer_1_out4, demultiplexer_1_out5, demultiplexer_2_out4, demultiplexer_2_out5, out_18, \突触_1_p7 , out_19, \突触_1_p7 , \突触_6_p13 
  // 突触 突触_7: pin names not known; wires that end beside it: in_6[3], in_7, in_7[3], in_8, demultiplexer_1_out5, demultiplexer_1_out6, demultiplexer_2_out6, demultiplexer_2_out5, out_19, \突触_1_p7 , out_20, \突触_1_p7 , \突触_7_p13 
  // 突触 突触_8: pin names not known; wires that end beside it: in_7[3], in_8, in_8[3], demultiplexer_1_out6, demultiplexer_1_out7, demultiplexer_2_out6, demultiplexer_2_out7, demultiplexer_2_out5, out_20, \突触_1_p7 , out_21, \突触_8_p12 
  \神经元  \u_神经元_1  (
    .In1(\突触_1_p10 ), .In2(\突触_2_p14 ), .In3(\突触_3_p13 ), .In4(\突触_4_p13 ), .In5(\突触_5_p13 ),
    .In6(\突触_6_p13 ), .In7(\突触_7_p13 ), .In8(\突触_8_p12 ));  // open: bais, out_10
endmodule

module \突触  (
  input  [7:0] in_1,
  input  [7:0] in_2,
  input  in_3,
  output [7:0] out_4
);

  wire [7:0] adder_1_out, multiplier_1_cout, register_1_q;

  Multiplier multiplier_1 (.a(in_1), .b(in_2), .cout(multiplier_1_cout));  // open: out, cin
  Register register_1 (.D(adder_1_out), .Q(register_1_q), .clk(in_3));  // open: en, clr
  Multiplier multiplier_2 (.a(in_1), .b(register_1_q), .cout(out_4));  // open: out, cin
  Adder adder_1 (.a(register_1_q), .b(multiplier_1_cout), .out(adder_1_out));  // open: cin, cout
endmodule

module \神经元  (
  input  [7:0] In1,
  input  [7:0] In2,
  input  [7:0] In3,
  input  [7:0] In4,
  input  [7:0] In5,
  input  [7:0] In6,
  input  [7:0] In7,
  input  [7:0] In8,
  input  [7:0] bais,
  output [7:0] out_10
);

  wire adder_9_cout, comparator_1_gt;
  wire [3:0] bitadder_1_out;
  wire [7:0] adder_1_out, adder_2_out, adder_3_out, adder_4_out, adder_5_out, adder_6_out, adder_7_out,
       adder_8_cout, adder_8_out, adder_9_out, bit_extender_1_out, multiplexer_1_out, pull_resistor_9_node,
       pull_resistor_10_node;

  Pull_Resistor pull_resistor_1 (.node(In1));
  Pull_Resistor pull_resistor_2 (.node(In2));
  Pull_Resistor pull_resistor_3 (.node(In3));
  Pull_Resistor pull_resistor_4 (.node(In4));
  Pull_Resistor pull_resistor_5 (.node(In5));
  Pull_Resistor pull_resistor_6 (.node(In6));
  Pull_Resistor pull_resistor_7 (.node(In7));
  Pull_Resistor pull_resistor_8 (.node(In8));
  Adder adder_1 (.a(In1), .b(In2), .out(adder_1_out), .cout(adder_8_cout[2]));  // open: cin
  Adder adder_2 (.a(In3), .b(In4), .out(adder_2_out), .cout(adder_8_cout[3]));  // open: cin
  Adder adder_3 (.a(In5), .b(In6), .out(adder_3_out), .cout(adder_8_cout[4]));  // open: cin
  Adder adder_4 (.a(In7), .b(In8), .out(adder_4_out), .cout(adder_8_cout[5]));  // open: cin
  Adder adder_5 (.a(adder_1_out), .b(adder_2_out), .out(adder_5_out), .cout(adder_8_cout[1]));  // open: cin
  Adder adder_6 (.a(adder_3_out), .b(adder_4_out), .out(adder_6_out), .cout(adder_8_cout[6]));  // open: cin
  Adder adder_7 (.a(adder_8_out), .b(bais), .out(adder_7_out), .cout(adder_8_cout[7]));  // open: cin
  Adder adder_8 (.a(adder_5_out), .b(adder_6_out), .out(adder_8_out), .cout(adder_8_cout[0]));  // open: cin
  BitAdder bitadder_1 (.in0(adder_8_cout), .out(bitadder_1_out));
  assign bit_extender_1_out = {{4{1'b0}}, bitadder_1_out};  // Bit_Extender bit_extender_1
  Pull_Resistor pull_resistor_9 (.node(pull_resistor_9_node));
  Adder adder_9 (.a(adder_7_out), .b(bit_extender_1_out), .out(adder_9_out), .cout(adder_9_cout));  // open: cin
  Pull_Resistor pull_resistor_10 (.node(pull_resistor_10_node));
  Comparator comparator_1 (.a(adder_9_out), .b(pull_resistor_10_node), .gt(comparator_1_gt));  // open: eq, lt
  Multiplexer #(.width(8), .enable("false")) multiplexer_1 (
    .in0(pull_resistor_9_node), .in1(adder_9_out), .out(multiplexer_1_out), .sel(comparator_1_gt));
  Multiplexer #(.width(8), .enable("false")) multiplexer_2 (
    .in0(multiplexer_1_out), .in1(8'h7f), .out(out_10), .sel(adder_9_cout));
endmodule

module _0 (
);

  wire clock_1_out, clock_2_out, clock_3_out, clock_4_out;
  wire [3:0] counter_1_q, counter_1_q_2, register_1_q, register_1_q_2, register_2_q, register_2_q_2,
       register_4_q, register_4_q_2, register_5_q, register_5_q_2, register_6_q, register_6_q_2,
       register_7_q, register_7_q_2, register_8_q, register_8_q_2, register_9_q, register_9_q_2,
       register_11_q, register_11_q_2, register_12_q, register_12_q_2, \神经元_25_out_10 , \神经元_25_out_10_2 ,
       \神经元_26_out_10 , \神经元_26_out_10_2 , \神经元_27_out_10 , \神经元_27_out_10_2 , \神经元_28_out_10 ,
       \神经元_28_out_10_2 , \神经元_29_out_10 , \神经元_29_out_10_2 , \神经元_30_out_10 , \神经元_30_out_10_2 ,
       \神经元_31_out_10 , \神经元_31_out_10_2 , \神经元_32_out_10 , \神经元_32_out_10_2 ;
  wire [7:0] register_3_q, register_10_q, undriven, \神经元_1_out_10 , \神经元_2_out_10 , \神经元_3_out_10 ,
       \神经元_4_out_10 , \神经元_5_out_10 , \神经元_6_out_10 , \神经元_7_out_10 , \神经元_8_out_10 , \神经元_9_out_10 ,
       \神经元_10_out_10 , \神经元_11_out_10 , \神经元_12_out_10 , \神经元_13_out_10 , \神经元_14_out_10 , \神经元_16_out_10 ,
       \神经元_17_out_10 , \神经元_18_out_10 , \神经元_19_out_10 , \神经元_20_out_10 , \神经元_21_out_10 , \神经元_22_out_10 ,
       \神经元_23_out_10 , \神经元_24_out_10 , \突触_1_out_4 , \突触_2_out_4 , \突触_3_out_4 , \突触_4_out_4 ,
       \突触_5_out_4 , \突触_6_out_4 , \突触_7_out_4 , \突触_8_out_4 , \突触_9_out_4 , \突触_10_out_4 , \突触_11_out_4 ,
       \突触_12_out_4 , \突触_13_out_4 , \突触_14_out_4 , \突触_15_out_4 , \突触_16_out_4 , \突触_17_out_4 ,
       \突触_18_out_4 , \突触_19_out_4 , \突触_20_out_4 , \突触_21_out_4 , \突触_22_out_4 , \突触_23_out_4 ,
       \突触_24_out_4 , \突触_25_out_4 , \突触_26_out_4 , \突触_27_out_4 , \突触_28_out_4 , \突触_29_out_4 ,
       \突触_30_out_4 , \突触_31_out_4 , \突触_32_out_4 , \突触_33_out_4 , \突触_34_out_4 , \突触_35_out_4 ,
       \突触_36_out_4 , \突触_37_out_4 , \突触_38_out_4 , \突触_39_out_4 , \突触_40_out_4 , \突触_41_out_4 ,
       \突触_42_out_4 , \突触_43_out_4 , \突触_44_out_4 , \突触_45_out_4 , \突触_46_out_4 , \突触_47_out_4 ,
       \突触_48_out_4 , \突触_49_out_4 , \突触_50_out_4 , \突触_51_out_4 , \突触_52_out_4 , \突触_53_out_4 ,
       \突触_54_out_4 , \突触_55_out_4 , \突触_56_out_4 , \突触_57_out_4 , \突触_58_out_4 , \突触_59_out_4 ,
       \突触_60_out_4 , \突触_61_out_4 , \突触_62_out_4 , \突触_63_out_4 , \突触_64_out_4 , \突触_65_out_4 ,
       \突触_66_out_4 , \突触_67_out_4 , \突触_68_out_4 , \突触_69_out_4 , \突触_70_out_4 , \突触_71_out_4 ,
       \突触_72_out_4 , \突触_73_out_4 , \突触_74_out_4 , \突触_75_out_4 , \突触_76_out_4 , \突触_77_out_4 ,
       \突触_78_out_4 , \突触_79_out_4 , \突触_80_out_4 , \突触_81_out_4 , \突触_82_out_4 , \突触_83_out_4 ,
       \突触_84_out_4 , \突触_85_out_4 , \突触_86_out_4 , \突触_87_out_4 , \突触_88_out_4 , \突触_89_out_4 ,
       \突触_90_out_4 , \突触_91_out_4 , \突触_92_out_4 , \突触_93_out_4 , \突触_94_out_4 , \突触_95_out_4 ,
       \突触_96_out_4 , \突触_97_out_4 , \突触_98_out_4 , \突触_99_out_4 , \突触_100_out_4 , \突触_101_out_4 ,
       \突触_102_out_4 , \突触_103_out_4 , \突触_104_out_4 , \突触_105_out_4 , \突触_106_out_4 , \突触_107_out_4 ,
       \突触_108_out_4 , \突触_109_out_4 , \突触_110_out_4 , \突触_111_out_4 , \突触_112_out_4 , \突触_113_out_4 ,
       \突触_114_out_4 , \突触_115_out_4 , \突触_116_out_4 , \突触_117_out_4 , \突触_118_out_4 , \突触_119_out_4 ,
       \突触_120_out_4 , \突触_121_out_4 , \突触_122_out_4 , \突触_123_out_4 , \突触_124_out_4 , \突触_125_out_4 ,
       \突触_126_out_4 , \突触_127_out_4 , \突触_128_out_4 , \突触_129_out_4 , \突触_130_out_4 , \突触_131_out_4 ,
       \突触_132_out_4 , \突触_133_out_4 , \突触_134_out_4 , \突触_135_out_4 , \突触_136_out_4 , \突触_137_out_4 ,
       \突触_138_out_4 , \突触_139_out_4 , \突触_140_out_4 , \突触_141_out_4 , \突触_142_out_4 , \突触_143_out_4 ,
       \突触_144_out_4 , \突触_145_out_4 , \突触_146_out_4 , \突触_147_out_4 , \突触_148_out_4 , \突触_149_out_4 ,
       \突触_150_out_4 , \突触_151_out_4 , \突触_152_out_4 , \突触_153_out_4 , \突触_154_out_4 , \突触_155_out_4 ,
       \突触_156_out_4 , \突触_157_out_4 , \突触_158_out_4 , \突触_159_out_4 , \突触_160_out_4 , \突触_161_out_4 ,
       \突触_162_out_4 , \突触_163_out_4 , \突触_164_out_4 , \突触_165_out_4 , \突触_166_out_4 , \突触_167_out_4 ,
       \突触_168_out_4 , \突触_169_out_4 , \突触_170_out_4 , \突触_171_out_4 , \突触_172_out_4 , \突触_173_out_4 ,
       \突触_174_out_4 , \突触_175_out_4 , \突触_176_out_4 , \突触_177_out_4 , \突触_178_out_4 , \突触_179_out_4 ,
       \突触_180_out_4 , \突触_181_out_4 , \突触_182_out_4 , \突触_183_out_4 , \突触_184_out_4 , \突触_185_out_4 ,
       \突触_186_out_4 , \突触_187_out_4 , \突触_188_out_4 , \突触_189_out_4 , \突触_190_out_4 , \突触_191_out_4 ,
       \突触_192_out_4 , \突触_193_out_4 , \突触_194_out_4 , \突触_195_out_4 , \突触_196_out_4 , \突触_197_out_4 ,
       \突触_198_out_4 , \突触_199_out_4 , \突触_200_out_4 , \突触_201_out_4 , \突触_202_out_4 , \突触_203_out_4 ,
       \突触_204_out_4 , \突触_205_out_4 , \突触_206_out_4 , \突触_207_out_4 , \突触_208_out_4 , \突触_209_out_4 ,
       \突触_210_out_4 , \突触_211_out_4 , \突触_212_out_4 , \突触_213_out_4 , \突触_214_out_4 , \突触_215_out_4 ,
       \突触_216_out_4 , \突触_217_out_4 , \突触_218_out_4 , \突触_219_out_4 , \突触_220_out_4 , \突触_221_out_4 ,
       \突触_222_out_4 , \突触_223_out_4 , \突触_224_out_4 , \突触_225_out_4 , \突触_226_out_4 , \突触_227_out_4 ,
       \突触_228_out_4 , \突触_229_out_4 , \突触_230_out_4 , \突触_231_out_4 , \突触_232_out_4 , \突触_233_out_4 ,
       \突触_234_out_4 , \突触_235_out_4 , \突触_236_out_4 , \突触_237_out_4 , \突触_238_out_4 , \突触_239_out_4 ,
       \突触_240_out_4 , \突触_241_out_4 , \突触_242_out_4 , \突触_243_out_4 , \突触_244_out_4 , \突触_245_out_4 ,
       \突触_246_out_4 , \突触_247_out_4 , \突触_248_out_4 , \突触_249_out_4 , \突触_250_out_4 , \突触_251_out_4 ,
       \突触_252_out_4 , \突触_253_out_4 , \突触_254_out_4 , \突触_255_out_4 , \突触_256_out_4 ;

  Register register_1 (.Q({register_1_q_2, register_1_q}));  // open: D, en, clk, clr
  Register register_2 (.Q({register_2_q_2, register_2_q}));  // open: D, en, clk, clr
  Register register_3 (.Q(register_3_q));  // open: D, en, clk, clr
  Register register_4 (.Q({register_4_q_2, register_4_q}));  // open: D, en, clk, clr
  Register register_5 (.Q({register_5_q_2, register_5_q}));  // open: D, en, clk, clr
  Register register_6 (.Q({register_6_q_2, register_6_q}));  // open: D, en, clk, clr
  Register register_7 (.Q({register_7_q_2, register_7_q}));  // open: D, en, clk, clr
  Register register_8 (.Q({register_8_q_2, register_8_q}));  // open: D, en, clk, clr
  Hex_Digit_Display hex_digit_display_1 (.value(register_5_q_2));  // open: dp
  Hex_Digit_Display hex_digit_display_2 (.value(register_5_q));  // open: dp
  Register register_9 (.Q({register_9_q_2, register_9_q}));  // open: D, en, clk, clr
  Register register_10 (.Q(register_10_q));  // open: D, en, clk, clr
  Register register_11 (.Q({register_11_q_2, register_11_q}));  // open: D, en, clk, clr
  Register register_12 (.Q({register_12_q_2, register_12_q}));  // open: D, en, clk, clr
  Hex_Digit_Display hex_digit_display_3 (.value(register_1_q_2));  // open: dp
  Hex_Digit_Display hex_digit_display_4 (.value(register_1_q));  // open: dp
  Hex_Digit_Display hex_digit_display_5 (.value(register_6_q_2));  // open: dp
  Hex_Digit_Display hex_digit_display_6 (.value(register_2_q));  // open: dp
  Hex_Digit_Display hex_digit_display_7 (.value(register_2_q_2));  // open: dp
  Hex_Digit_Display hex_digit_display_8 (.value(register_7_q_2));  // open: dp
  Hex_Digit_Display hex_digit_display_9 (.value(register_6_q));  // open: dp
  Hex_Digit_Display hex_digit_display_10 (.value(register_3_q[7:4]));  // open: dp
  Hex_Digit_Display hex_digit_display_11 (.value(register_3_q[3:0]));  // open: dp
  Hex_Digit_Display hex_digit_display_12 (.value(register_8_q_2));  // open: dp
  Hex_Digit_Display hex_digit_display_13 (.value(register_7_q));  // open: dp
  Hex_Digit_Display hex_digit_display_14 (.value(register_4_q));  // open: dp
  Hex_Digit_Display hex_digit_display_15 (.value(register_4_q_2));  // open: dp
  Hex_Digit_Display hex_digit_display_16 (.value(register_8_q));  // open: dp
  Hex_Digit_Display hex_digit_display_17 (.value(register_9_q_2));  // open: dp
  Hex_Digit_Display hex_digit_display_18 (.value(register_9_q));  // open: dp
  Hex_Digit_Display hex_digit_display_19 (.value(register_10_q[7:4]));  // open: dp
  Hex_Digit_Display hex_digit_display_20 (.value(register_10_q[3:0]));  // open: dp
  Hex_Digit_Display hex_digit_display_21 (.value(counter_1_q_2));  // open: dp
  Hex_Digit_Display hex_digit_display_22 (.value(register_11_q));  // open: dp
  Hex_Digit_Display hex_digit_display_23 (.value(register_11_q_2));  // open: dp
  Clock clock_1 (.out(clock_1_out));
  Hex_Digit_Display hex_digit_display_24 (.value(counter_1_q));  // open: dp
  Hex_Digit_Display hex_digit_display_25 (.value(register_12_q_2));  // open: dp
  Hex_Digit_Display hex_digit_display_26 (.value(register_12_q));  // open: dp
  \突触  \u_突触_1  (
    .in_1({register_1_q_2, register_1_q}), .in_2(\神经元_1_out_10 ), .in_3(clock_1_out), .out_4(\突触_1_out_4 ));
  \突触  \u_突触_2  (
    .in_1({register_2_q_2, register_2_q}), .in_2(\神经元_1_out_10 ), .in_3(clock_1_out), .out_4(\突触_2_out_4 ));
  \突触  \u_突触_3  (.in_1(register_3_q), .in_2(\神经元_1_out_10 ), .in_3(clock_1_out), .out_4(\突触_3_out_4 ));
  \突触  \u_突触_4  (
    .in_1({register_4_q_2, register_4_q}), .in_2(\神经元_1_out_10 ), .in_3(clock_1_out), .out_4(\突触_4_out_4 ));
  \突触  \u_突触_5  (
    .in_1({register_5_q_2, register_5_q}), .in_2(\神经元_1_out_10 ), .in_3(clock_1_out), .out_4(\突触_5_out_4 ));
  \突触  \u_突触_6  (
    .in_1({register_6_q_2, register_6_q}), .in_2(\神经元_1_out_10 ), .in_3(clock_1_out), .out_4(\突触_6_out_4 ));
  \突触  \u_突触_7  (
    .in_1({register_7_q_2, register_7_q}), .in_2(\神经元_1_out_10 ), .in_3(clock_1_out), .out_4(\突触_7_out_4 ));
  \突触  \u_突触_8  (
    .in_1({register_8_q_2, register_8_q}), .in_2(\神经元_1_out_10 ), .in_3(clock_1_out), .out_4(\突触_8_out_4 ));
  \突触  \u_突触_9  (
    .in_1({register_1_q_2, register_1_q}), .in_2(\神经元_2_out_10 ), .in_3(clock_1_out), .out_4(\突触_9_out_4 ));
  \突触  \u_突触_10  (
    .in_1({register_2_q_2, register_2_q}), .in_2(\神经元_2_out_10 ), .in_3(clock_1_out), .out_4(\突触_10_out_4 ));
  \突触  \u_突触_11  (.in_1(register_3_q), .in_2(\神经元_2_out_10 ), .in_3(clock_1_out), .out_4(\突触_11_out_4 ));
  \突触  \u_突触_12  (
    .in_1({register_4_q_2, register_4_q}), .in_2(\神经元_2_out_10 ), .in_3(clock_1_out), .out_4(\突触_12_out_4 ));
  \突触  \u_突触_13  (
    .in_1({register_5_q_2, register_5_q}), .in_2(\神经元_2_out_10 ), .in_3(clock_1_out), .out_4(\突触_13_out_4 ));
  \突触  \u_突触_14  (
    .in_1({register_6_q_2, register_6_q}), .in_2(\神经元_2_out_10 ), .in_3(clock_1_out), .out_4(\突触_14_out_4 ));
  \突触  \u_突触_15  (
    .in_1({register_7_q_2, register_7_q}), .in_2(\神经元_2_out_10 ), .in_3(clock_1_out), .out_4(\突触_15_out_4 ));
  \突触  \u_突触_16  (
    .in_1({register_8_q_2, register_8_q}), .in_2(\神经元_2_out_10 ), .in_3(clock_1_out), .out_4(\突触_16_out_4 ));
  \突触  \u_突触_17  (
    .in_1({register_1_q_2, register_1_q}), .in_2(\神经元_3_out_10 ), .in_3(clock_1_out), .out_4(\突触_17_out_4 ));
  \突触  \u_突触_18  (
    .in_1({register_2_q_2, register_2_q}), .in_2(\神经元_3_out_10 ), .in_3(clock_1_out), .out_4(\突触_18_out_4 ));
  \突触  \u_突触_19  (.in_1(register_3_q), .in_2(\神经元_3_out_10 ), .in_3(clock_1_out), .out_4(\突触_19_out_4 ));
  \突触  \u_突触_20  (
    .in_1({register_4_q_2, register_4_q}), .in_2(\神经元_3_out_10 ), .in_3(clock_1_out), .out_4(\突触_20_out_4 ));
  \突触  \u_突触_21  (
    .in_1({register_5_q_2, register_5_q}), .in_2(\神经元_3_out_10 ), .in_3(clock_1_out), .out_4(\突触_21_out_4 ));
  \突触  \u_突触_22  (
    .in_1({register_6_q_2, register_6_q}), .in_2(\神经元_3_out_10 ), .in_3(clock_1_out), .out_4(\突触_22_out_4 ));
  \突触  \u_突触_23  (
    .in_1({register_7_q_2, register_7_q}), .in_2(\神经元_3_out_10 ), .in_3(clock_1_out), .out_4(\突触_23_out_4 ));
  \突触  \u_突触_24  (
    .in_1({register_8_q_2, register_8_q}), .in_2(\神经元_3_out_10 ), .in_3(clock_1_out), .out_4(\突触_24_out_4 ));
  \突触  \u_突触_25  (
    .in_1({register_1_q_2, register_1_q}), .in_2(\神经元_4_out_10 ), .in_3(clock_1_out), .out_4(\突触_25_out_4 ));
  \突触  \u_突触_26  (
    .in_1({register_2_q_2, register_2_q}), .in_2(\神经元_4_out_10 ), .in_3(clock_1_out), .out_4(\突触_26_out_4 ));
  \突触  \u_突触_27  (.in_1(register_3_q), .in_2(\神经元_4_out_10 ), .in_3(clock_1_out), .out_4(\突触_27_out_4 ));
  \突触  \u_突触_28  (
    .in_1({register_4_q_2, register_4_q}), .in_2(\神经元_4_out_10 ), .in_3(clock_1_out), .out_4(\突触_28_out_4 ));
  \突触  \u_突触_29  (
    .in_1({register_5_q_2, register_5_q}), .in_2(\神经元_4_out_10 ), .in_3(clock_1_out), .out_4(\突触_29_out_4 ));
  \突触  \u_突触_30  (
    .in_1({register_6_q_2, register_6_q}), .in_2(\神经元_4_out_10 ), .in_3(clock_1_out), .out_4(\突触_30_out_4 ));
  \突触  \u_突触_31  (
    .in_1({register_7_q_2, register_7_q}), .in_2(\神经元_4_out_10 ), .in_3(clock_1_out), .out_4(\突触_31_out_4 ));
  \突触  \u_突触_32  (
    .in_1({register_8_q_2, register_8_q}), .in_2(\神经元_4_out_10 ), .in_3(clock_1_out), .out_4(\突触_32_out_4 ));
  \突触  \u_突触_33  (
    .in_1({register_1_q_2, register_1_q}), .in_2(\神经元_5_out_10 ), .in_3(clock_1_out), .out_4(\突触_33_out_4 ));
  \突触  \u_突触_34  (
    .in_1({register_2_q_2, register_2_q}), .in_2(\神经元_5_out_10 ), .in_3(clock_1_out), .out_4(\突触_34_out_4 ));
  \突触  \u_突触_35  (.in_1(register_3_q), .in_2(\神经元_5_out_10 ), .in_3(clock_1_out), .out_4(\突触_35_out_4 ));
  \突触  \u_突触_36  (
    .in_1({register_4_q_2, register_4_q}), .in_2(\神经元_5_out_10 ), .in_3(clock_1_out), .out_4(\突触_36_out_4 ));
  \突触  \u_突触_37  (
    .in_1({register_5_q_2, register_5_q}), .in_2(\神经元_5_out_10 ), .in_3(clock_1_out), .out_4(\突触_37_out_4 ));
  \突触  \u_突触_38  (
    .in_1({register_6_q_2, register_6_q}), .in_2(\神经元_5_out_10 ), .in_3(clock_1_out), .out_4(\突触_38_out_4 ));
  \突触  \u_突触_39  (
    .in_1({register_7_q_2, register_7_q}), .in_2(\神经元_5_out_10 ), .in_3(clock_1_out), .out_4(\突触_39_out_4 ));
  \突触  \u_突触_40  (
    .in_1({register_8_q_2, register_8_q}), .in_2(\神经元_5_out_10 ), .in_3(clock_1_out), .out_4(\突触_40_out_4 ));
  \突触  \u_突触_41  (
    .in_1({register_1_q_2, register_1_q}), .in_2(\神经元_6_out_10 ), .in_3(clock_1_out), .out_4(\突触_41_out_4 ));
  \突触  \u_突触_42  (
    .in_1({register_2_q_2, register_2_q}), .in_2(\神经元_6_out_10 ), .in_3(clock_1_out), .out_4(\突触_42_out_4 ));
  \突触  \u_突触_43  (.in_1(register_3_q), .in_2(\神经元_6_out_10 ), .in_3(clock_1_out), .out_4(\突触_43_out_4 ));
  \突触  \u_突触_44  (
    .in_1({register_4_q_2, register_4_q}), .in_2(\神经元_6_out_10 ), .in_3(clock_1_out), .out_4(\突触_44_out_4 ));
  \突触  \u_突触_45  (
    .in_1({register_5_q_2, register_5_q}), .in_2(\神经元_6_out_10 ), .in_3(clock_1_out), .out_4(\突触_45_out_4 ));
  \突触  \u_突触_46  (
    .in_1({register_6_q_2, register_6_q}), .in_2(\神经元_6_out_10 ), .in_3(clock_1_out), .out_4(\突触_46_out_4 ));
  \突触  \u_突触_47  (
    .in_1({register_7_q_2, register_7_q}), .in_2(\神经元_6_out_10 ), .in_3(clock_1_out), .out_4(\突触_47_out_4 ));
  \突触  \u_突触_48  (
    .in_1({register_8_q_2, register_8_q}), .in_2(\神经元_6_out_10 ), .in_3(clock_1_out), .out_4(\突触_48_out_4 ));
  \突触  \u_突触_49  (
    .in_1({register_1_q_2, register_1_q}), .in_2(\神经元_7_out_10 ), .in_3(clock_1_out), .out_4(\突触_49_out_4 ));
  \突触  \u_突触_50  (
    .in_1({register_2_q_2, register_2_q}), .in_2(\神经元_7_out_10 ), .in_3(clock_1_out), .out_4(\突触_50_out_4 ));
  \突触  \u_突触_51  (.in_1(register_3_q), .in_2(\神经元_7_out_10 ), .in_3(clock_1_out), .out_4(\突触_51_out_4 ));
  \突触  \u_突触_52  (
    .in_1({register_4_q_2, register_4_q}), .in_2(\神经元_7_out_10 ), .in_3(clock_1_out), .out_4(\突触_52_out_4 ));
  \突触  \u_突触_53  (
    .in_1({register_5_q_2, register_5_q}), .in_2(\神经元_7_out_10 ), .in_3(clock_1_out), .out_4(\突触_53_out_4 ));
  \突触  \u_突触_54  (
    .in_1({register_6_q_2, register_6_q}), .in_2(\神经元_7_out_10 ), .in_3(clock_1_out), .out_4(\突触_54_out_4 ));
  \突触  \u_突触_55  (
    .in_1({register_7_q_2, register_7_q}), .in_2(\神经元_7_out_10 ), .in_3(clock_1_out), .out_4(\突触_55_out_4 ));
  \突触  \u_突触_56  (
    .in_1({register_8_q_2, register_8_q}), .in_2(\神经元_7_out_10 ), .in_3(clock_1_out), .out_4(\突触_56_out_4 ));
  \突触  \u_突触_57  (
    .in_1({register_1_q_2, register_1_q}), .in_2(\神经元_8_out_10 ), .in_3(clock_1_out), .out_4(\突触_57_out_4 ));
  \突触  \u_突触_58  (
    .in_1({register_2_q_2, register_2_q}), .in_2(\神经元_8_out_10 ), .in_3(clock_1_out), .out_4(\突触_58_out_4 ));
  \突触  \u_突触_59  (.in_1(register_3_q), .in_2(\神经元_8_out_10 ), .in_3(clock_1_out), .out_4(\突触_59_out_4 ));
  \突触  \u_突触_60  (
    .in_1({register_4_q_2, register_4_q}), .in_2(\神经元_8_out_10 ), .in_3(clock_1_out), .out_4(\突触_60_out_4 ));
  \突触  \u_突触_61  (
    .in_1({register_5_q_2, register_5_q}), .in_2(\神经元_8_out_10 ), .in_3(clock_1_out), .out_4(\突触_61_out_4 ));
  \突触  \u_突触_62  (
    .in_1({register_6_q_2, register_6_q}), .in_2(\神经元_8_out_10 ), .in_3(clock_1_out), .out_4(\突触_62_out_4 ));
  \突触  \u_突触_63  (
    .in_1({register_7_q_2, register_7_q}), .in_2(\神经元_8_out_10 ), .in_3(clock_1_out), .out_4(\突触_63_out_4 ));
  \突触  \u_突触_64  (
    .in_1({register_8_q_2, register_8_q}), .in_2(\神经元_8_out_10 ), .in_3(clock_1_out), .out_4(\突触_64_out_4 ));
  Counter counter_1 (.Q({counter_1_q_2, counter_1_q}), .clk(clock_1_out));  // open: load, D, count, carry, clr
  \神经元  \u_神经元_1  (
    .In1(\突触_1_out_4 ), .In2(\突触_2_out_4 ), .In3(\突触_3_out_4 ), .In4(\突触_4_out_4 ), .In5(\突触_5_out_4 ),
    .In6(\突触_6_out_4 ), .In7(\突触_7_out_4 ), .In8(\突触_8_out_4 ), .bais({register_9_q_2, register_9_q}),
    .out_10(\神经元_1_out_10 ));
  \神经元  \u_神经元_2  (
    .In1(\突触_9_out_4 ), .In2(\突触_10_out_4 ), .In3(\突触_11_out_4 ), .In4(\突触_12_out_4 ), .In5(\突触_13_out_4 ),
    .In6(\突触_14_out_4 ), .In7(\突触_15_out_4 ), .In8(\突触_16_out_4 ), .bais({register_9_q_2, register_9_q}),
    .out_10(\神经元_2_out_10 ));
  \神经元  \u_神经元_3  (
    .In1(\突触_17_out_4 ), .In2(\突触_18_out_4 ), .In3(\突触_19_out_4 ), .In4(\突触_20_out_4 ), .In5(\突触_21_out_4 ),
    .In6(\突触_22_out_4 ), .In7(\突触_23_out_4 ), .In8(\突触_24_out_4 ), .bais({register_9_q_2, register_9_q}),
    .out_10(\神经元_3_out_10 ));
  \神经元  \u_神经元_4  (
    .In1(\突触_25_out_4 ), .In2(\突触_26_out_4 ), .In3(\突触_27_out_4 ), .In4(\突触_28_out_4 ), .In5(\突触_29_out_4 ),
    .In6(\突触_30_out_4 ), .In7(\突触_31_out_4 ), .In8(\突触_32_out_4 ), .bais({register_9_q_2, register_9_q}),
    .out_10(\神经元_4_out_10 ));
  \神经元  \u_神经元_5  (
    .In1(\突触_33_out_4 ), .In2(\突触_34_out_4 ), .In3(\突触_35_out_4 ), .In4(\突触_36_out_4 ), .In5(\突触_37_out_4 ),
    .In6(\突触_38_out_4 ), .In7(\突触_39_out_4 ), .In8(\突触_40_out_4 ), .bais({register_9_q_2, register_9_q}),
    .out_10(\神经元_5_out_10 ));
  \神经元  \u_神经元_6  (
    .In1(\突触_41_out_4 ), .In2(\突触_42_out_4 ), .In3(\突触_43_out_4 ), .In4(\突触_44_out_4 ), .In5(\突触_45_out_4 ),
    .In6(\突触_46_out_4 ), .In7(\突触_47_out_4 ), .In8(\突触_48_out_4 ), .bais({register_9_q_2, register_9_q}),
    .out_10(\神经元_6_out_10 ));
  \神经元  \u_神经元_7  (
    .In1(\突触_49_out_4 ), .In2(\突触_50_out_4 ), .In3(\突触_51_out_4 ), .In4(\突触_52_out_4 ), .In5(\突触_53_out_4 ),
    .In6(\突触_54_out_4 ), .In7(\突触_55_out_4 ), .In8(\突触_56_out_4 ), .bais({register_9_q_2, register_9_q}),
    .out_10(\神经元_7_out_10 ));
  \神经元  \u_神经元_8  (
    .In1(\突触_57_out_4 ), .In2(\突触_58_out_4 ), .In3(\突触_59_out_4 ), .In4(\突触_60_out_4 ), .In5(\突触_61_out_4 ),
    .In6(\突触_62_out_4 ), .In7(\突触_63_out_4 ), .In8(\突触_64_out_4 ), .bais({register_9_q_2, register_9_q}),
    .out_10(\神经元_8_out_10 ));
  Hex_Digit_Display hex_digit_display_27 (.value(\神经元_25_out_10_2 ));  // open: dp
  Hex_Digit_Display hex_digit_display_28 (.value(\神经元_25_out_10 ));  // open: dp
  Hex_Digit_Display hex_digit_display_29 (.value(\神经元_26_out_10 ));  // open: dp
  Hex_Digit_Display hex_digit_display_30 (.value(\神经元_26_out_10_2 ));  // open: dp
  Hex_Digit_Display hex_digit_display_31 (.value(\神经元_27_out_10_2 ));  // open: dp
  Hex_Digit_Display hex_digit_display_32 (.value(\神经元_27_out_10 ));  // open: dp
  Hex_Digit_Display hex_digit_display_33 (.value(\神经元_28_out_10 ));  // open: dp
  Hex_Digit_Display hex_digit_display_34 (.value(\神经元_28_out_10_2 ));  // open: dp
  Clock clock_2 (.out(clock_2_out));
  Hex_Digit_Display hex_digit_display_35 (.value(\神经元_29_out_10_2 ));  // open: dp
  Hex_Digit_Display hex_digit_display_36 (.value(\神经元_29_out_10 ));  // open: dp
  \突触  \u_突触_65  (.in_1(\神经元_1_out_10 ), .in_2(\神经元_9_out_10 ), .in_3(clock_2_out), .out_4(\突触_65_out_4 ));
  \突触  \u_突触_66  (.in_1(\神经元_2_out_10 ), .in_2(\神经元_9_out_10 ), .in_3(clock_2_out), .out_4(\突触_66_out_4 ));
  \突触  \u_突触_67  (.in_1(\神经元_3_out_10 ), .in_2(\神经元_9_out_10 ), .in_3(clock_2_out), .out_4(\突触_67_out_4 ));
  \突触  \u_突触_68  (.in_1(\神经元_4_out_10 ), .in_2(\神经元_9_out_10 ), .in_3(clock_2_out), .out_4(\突触_68_out_4 ));
  \突触  \u_突触_69  (.in_1(\神经元_5_out_10 ), .in_2(\神经元_9_out_10 ), .in_3(clock_2_out), .out_4(\突触_69_out_4 ));
  \突触  \u_突触_70  (.in_1(\神经元_6_out_10 ), .in_2(\神经元_9_out_10 ), .in_3(clock_2_out), .out_4(\突触_70_out_4 ));
  \突触  \u_突触_71  (.in_1(\神经元_7_out_10 ), .in_2(\神经元_9_out_10 ), .in_3(clock_2_out), .out_4(\突触_71_out_4 ));
  \突触  \u_突触_72  (.in_1(\神经元_8_out_10 ), .in_2(\神经元_9_out_10 ), .in_3(clock_2_out), .out_4(\突触_72_out_4 ));
  \突触  \u_突触_73  (.in_1(\神经元_1_out_10 ), .in_2(\神经元_10_out_10 ), .in_3(clock_2_out), .out_4(\突触_73_out_4 ));
  \突触  \u_突触_74  (.in_1(\神经元_2_out_10 ), .in_2(\神经元_10_out_10 ), .in_3(clock_2_out), .out_4(\突触_74_out_4 ));
  \突触  \u_突触_75  (.in_1(\神经元_3_out_10 ), .in_2(\神经元_10_out_10 ), .in_3(clock_2_out), .out_4(\突触_75_out_4 ));
  \突触  \u_突触_76  (.in_1(\神经元_4_out_10 ), .in_2(\神经元_10_out_10 ), .in_3(clock_2_out), .out_4(\突触_76_out_4 ));
  \突触  \u_突触_77  (.in_1(\神经元_5_out_10 ), .in_2(\神经元_10_out_10 ), .in_3(clock_2_out), .out_4(\突触_77_out_4 ));
  \突触  \u_突触_78  (.in_1(\神经元_6_out_10 ), .in_2(\神经元_10_out_10 ), .in_3(clock_2_out), .out_4(\突触_78_out_4 ));
  \突触  \u_突触_79  (.in_1(\神经元_7_out_10 ), .in_2(\神经元_10_out_10 ), .in_3(clock_2_out), .out_4(\突触_79_out_4 ));
  \突触  \u_突触_80  (.in_1(\神经元_8_out_10 ), .in_2(\神经元_10_out_10 ), .in_3(clock_2_out), .out_4(\突触_80_out_4 ));
  \突触  \u_突触_81  (.in_1(\神经元_1_out_10 ), .in_2(\神经元_11_out_10 ), .in_3(clock_2_out), .out_4(\突触_81_out_4 ));
  \突触  \u_突触_82  (.in_1(\神经元_2_out_10 ), .in_2(\神经元_11_out_10 ), .in_3(clock_2_out), .out_4(\突触_82_out_4 ));
  \突触  \u_突触_83  (.in_1(\神经元_3_out_10 ), .in_2(\神经元_11_out_10 ), .in_3(clock_2_out), .out_4(\突触_83_out_4 ));
  \突触  \u_突触_84  (.in_1(\神经元_4_out_10 ), .in_2(\神经元_11_out_10 ), .in_3(clock_2_out), .out_4(\突触_84_out_4 ));
  \突触  \u_突触_85  (.in_1(\神经元_5_out_10 ), .in_2(\神经元_11_out_10 ), .in_3(clock_2_out), .out_4(\突触_85_out_4 ));
  \突触  \u_突触_86  (.in_1(\神经元_6_out_10 ), .in_2(\神经元_11_out_10 ), .in_3(clock_2_out), .out_4(\突触_86_out_4 ));
  \突触  \u_突触_87  (.in_1(\神经元_7_out_10 ), .in_2(\神经元_11_out_10 ), .in_3(clock_2_out), .out_4(\突触_87_out_4 ));
  \突触  \u_突触_88  (.in_1(\神经元_8_out_10 ), .in_2(\神经元_11_out_10 ), .in_3(clock_2_out), .out_4(\突触_88_out_4 ));
  \突触  \u_突触_89  (.in_1(\神经元_1_out_10 ), .in_2(\神经元_12_out_10 ), .in_3(clock_2_out), .out_4(\突触_89_out_4 ));
  \突触  \u_突触_90  (.in_1(\神经元_2_out_10 ), .in_2(\神经元_12_out_10 ), .in_3(clock_2_out), .out_4(\突触_90_out_4 ));
  \突触  \u_突触_91  (.in_1(\神经元_3_out_10 ), .in_2(\神经元_12_out_10 ), .in_3(clock_2_out), .out_4(\突触_91_out_4 ));
  \突触  \u_突触_92  (.in_1(\神经元_4_out_10 ), .in_2(\神经元_12_out_10 ), .in_3(clock_2_out), .out_4(\突触_92_out_4 ));
  \突触  \u_突触_93  (.in_1(\神经元_5_out_10 ), .in_2(\神经元_12_out_10 ), .in_3(clock_2_out), .out_4(\突触_93_out_4 ));
  \突触  \u_突触_94  (.in_1(\神经元_6_out_10 ), .in_2(\神经元_12_out_10 ), .in_3(clock_2_out), .out_4(\突触_94_out_4 ));
  \突触  \u_突触_95  (.in_1(\神经元_7_out_10 ), .in_2(\神经元_12_out_10 ), .in_3(clock_2_out), .out_4(\突触_95_out_4 ));
  \突触  \u_突触_96  (.in_1(\神经元_8_out_10 ), .in_2(\神经元_12_out_10 ), .in_3(clock_2_out), .out_4(\突触_96_out_4 ));
  \突触  \u_突触_97  (.in_1(\神经元_1_out_10 ), .in_2(\神经元_13_out_10 ), .in_3(clock_2_out), .out_4(\突触_97_out_4 ));
  \突触  \u_突触_98  (.in_1(\神经元_2_out_10 ), .in_2(\神经元_13_out_10 ), .in_3(clock_2_out), .out_4(\突触_98_out_4 ));
  \突触  \u_突触_99  (.in_1(\神经元_3_out_10 ), .in_2(\神经元_13_out_10 ), .in_3(clock_2_out), .out_4(\突触_99_out_4 ));
  \突触  \u_突触_100  (.in_1(\神经元_4_out_10 ), .in_2(\神经元_13_out_10 ), .in_3(clock_2_out), .out_4(\突触_100_out_4 ));
  \突触  \u_突触_101  (.in_1(\神经元_5_out_10 ), .in_2(\神经元_13_out_10 ), .in_3(clock_2_out), .out_4(\突触_101_out_4 ));
  \突触  \u_突触_102  (.in_1(\神经元_6_out_10 ), .in_2(\神经元_13_out_10 ), .in_3(clock_2_out), .out_4(\突触_102_out_4 ));
  \突触  \u_突触_103  (.in_1(\神经元_7_out_10 ), .in_2(\神经元_13_out_10 ), .in_3(clock_2_out), .out_4(\突触_103_out_4 ));
  \突触  \u_突触_104  (.in_1(\神经元_8_out_10 ), .in_2(\神经元_13_out_10 ), .in_3(clock_2_out), .out_4(\突触_104_out_4 ));
  \突触  \u_突触_105  (.in_1(\神经元_1_out_10 ), .in_2(\神经元_14_out_10 ), .in_3(clock_2_out), .out_4(\突触_105_out_4 ));
  \突触  \u_突触_106  (.in_1(\神经元_2_out_10 ), .in_2(\神经元_14_out_10 ), .in_3(clock_2_out), .out_4(\突触_106_out_4 ));
  \突触  \u_突触_107  (.in_1(\神经元_3_out_10 ), .in_2(\神经元_14_out_10 ), .in_3(clock_2_out), .out_4(\突触_107_out_4 ));
  \突触  \u_突触_108  (.in_1(\神经元_4_out_10 ), .in_2(\神经元_14_out_10 ), .in_3(clock_2_out), .out_4(\突触_108_out_4 ));
  \突触  \u_突触_109  (.in_1(\神经元_5_out_10 ), .in_2(\神经元_14_out_10 ), .in_3(clock_2_out), .out_4(\突触_109_out_4 ));
  \突触  \u_突触_110  (.in_1(\神经元_6_out_10 ), .in_2(\神经元_14_out_10 ), .in_3(clock_2_out), .out_4(\突触_110_out_4 ));
  \突触  \u_突触_111  (.in_1(\神经元_7_out_10 ), .in_2(\神经元_14_out_10 ), .in_3(clock_2_out), .out_4(\突触_111_out_4 ));
  \突触  \u_突触_112  (.in_1(\神经元_8_out_10 ), .in_2(\神经元_14_out_10 ), .in_3(clock_2_out), .out_4(\突触_112_out_4 ));
  \突触  \u_突触_113  (.in_1(\神经元_1_out_10 ), .in_2(\神经元_14_out_10 ), .in_3(clock_2_out), .out_4(\突触_113_out_4 ));
  \突触  \u_突触_114  (.in_1(\神经元_2_out_10 ), .in_2(\神经元_14_out_10 ), .in_3(clock_2_out), .out_4(\突触_114_out_4 ));
  \突触  \u_突触_115  (.in_1(\神经元_3_out_10 ), .in_2(\神经元_14_out_10 ), .in_3(clock_2_out), .out_4(\突触_115_out_4 ));
  \突触  \u_突触_116  (.in_1(\神经元_4_out_10 ), .in_2(\神经元_14_out_10 ), .in_3(clock_2_out), .out_4(\突触_116_out_4 ));
  \突触  \u_突触_117  (.in_1(\神经元_5_out_10 ), .in_2(\神经元_14_out_10 ), .in_3(clock_2_out), .out_4(\突触_117_out_4 ));
  \突触  \u_突触_118  (.in_1(\神经元_6_out_10 ), .in_2(\神经元_14_out_10 ), .in_3(clock_2_out), .out_4(\突触_118_out_4 ));
  \突触  \u_突触_119  (.in_1(\神经元_7_out_10 ), .in_2(\神经元_14_out_10 ), .in_3(clock_2_out), .out_4(\突触_119_out_4 ));
  \突触  \u_突触_120  (.in_1(\神经元_8_out_10 ), .in_2(\神经元_14_out_10 ), .in_3(clock_2_out), .out_4(\突触_120_out_4 ));
  \突触  \u_突触_121  (.in_1(\神经元_1_out_10 ), .in_2(\神经元_16_out_10 ), .in_3(clock_2_out), .out_4(\突触_121_out_4 ));
  \突触  \u_突触_122  (.in_1(\神经元_2_out_10 ), .in_2(\神经元_16_out_10 ), .in_3(clock_2_out), .out_4(\突触_122_out_4 ));
  \突触  \u_突触_123  (.in_1(\神经元_3_out_10 ), .in_2(\神经元_16_out_10 ), .in_3(clock_2_out), .out_4(\突触_123_out_4 ));
  \突触  \u_突触_124  (.in_1(\神经元_4_out_10 ), .in_2(\神经元_16_out_10 ), .in_3(clock_2_out), .out_4(\突触_124_out_4 ));
  \突触  \u_突触_125  (.in_1(\神经元_5_out_10 ), .in_2(\神经元_16_out_10 ), .in_3(clock_2_out), .out_4(\突触_125_out_4 ));
  \突触  \u_突触_126  (.in_1(\神经元_6_out_10 ), .in_2(\神经元_16_out_10 ), .in_3(clock_2_out), .out_4(\突触_126_out_4 ));
  \突触  \u_突触_127  (.in_1(\神经元_7_out_10 ), .in_2(\神经元_16_out_10 ), .in_3(clock_2_out), .out_4(\突触_127_out_4 ));
  \突触  \u_突触_128  (.in_1(\神经元_8_out_10 ), .in_2(\神经元_16_out_10 ), .in_3(clock_2_out), .out_4(\突触_128_out_4 ));
  Hex_Digit_Display hex_digit_display_37 (.value(\神经元_30_out_10 ));  // open: dp
  Hex_Digit_Display hex_digit_display_38 (.value(\神经元_30_out_10_2 ));  // open: dp
  \神经元  \u_神经元_9  (
    .In1(\突触_65_out_4 ), .In2(\突触_66_out_4 ), .In3(\突触_67_out_4 ), .In4(\突触_68_out_4 ), .In5(\突触_69_out_4 ),
    .In6(\突触_70_out_4 ), .In7(\突触_71_out_4 ), .In8(\突触_72_out_4 ), .bais(register_10_q),
    .out_10(\神经元_9_out_10 ));
  \神经元  \u_神经元_10  (
    .In1(\突触_73_out_4 ), .In2(\突触_74_out_4 ), .In3(\突触_75_out_4 ), .In4(\突触_76_out_4 ), .In5(\突触_77_out_4 ),
    .In6(\突触_78_out_4 ), .In7(\突触_79_out_4 ), .In8(\突触_80_out_4 ), .bais(register_10_q),
    .out_10(\神经元_10_out_10 ));
  \神经元  \u_神经元_11  (
    .In1(\突触_81_out_4 ), .In2(\突触_82_out_4 ), .In3(\突触_83_out_4 ), .In4(\突触_84_out_4 ), .In5(\突触_85_out_4 ),
    .In6(\突触_86_out_4 ), .In7(\突触_87_out_4 ), .In8(\突触_88_out_4 ), .bais(register_10_q),
    .out_10(\神经元_11_out_10 ));
  \神经元  \u_神经元_12  (
    .In1(\突触_89_out_4 ), .In2(\突触_90_out_4 ), .In3(\突触_91_out_4 ), .In4(\突触_92_out_4 ), .In5(\突触_93_out_4 ),
    .In6(\突触_94_out_4 ), .In7(\突触_95_out_4 ), .In8(\突触_96_out_4 ), .bais(register_10_q),
    .out_10(\神经元_12_out_10 ));
  \神经元  \u_神经元_13  (
    .In1(\突触_97_out_4 ), .In2(\突触_98_out_4 ), .In3(\突触_99_out_4 ), .In4(\突触_100_out_4 ),
    .In5(\突触_101_out_4 ), .In6(\突触_102_out_4 ), .In7(\突触_103_out_4 ), .In8(\突触_104_out_4 ),
    .bais(register_10_q), .out_10(\神经元_13_out_10 ));
  \神经元  \u_神经元_14  (
    .In1(\突触_105_out_4 ), .In2(\突触_106_out_4 ), .In3(\突触_107_out_4 ), .In4(\突触_108_out_4 ),
    .In5(\突触_109_out_4 ), .In6(\突触_110_out_4 ), .In7(\突触_111_out_4 ), .In8(\突触_112_out_4 ),
    .bais(register_10_q), .out_10(\神经元_14_out_10 ));
  \神经元  \u_神经元_15  (
    .In1(\突触_113_out_4 ), .In2(\突触_114_out_4 ), .In3(\突触_115_out_4 ), .In4(\突触_116_out_4 ),
    .In5(\突触_117_out_4 ), .In6(\突触_118_out_4 ), .In7(\突触_119_out_4 ), .In8(\突触_120_out_4 ),
    .bais(register_10_q), .out_10(\神经元_14_out_10 ));
  \神经元  \u_神经元_16  (
    .In1(\突触_121_out_4 ), .In2(\突触_122_out_4 ), .In3(\突触_123_out_4 ), .In4(\突触_124_out_4 ),
    .In5(\突触_125_out_4 ), .In6(\突触_126_out_4 ), .In7(\突触_127_out_4 ), .In8(\突触_128_out_4 ),
    .bais(register_10_q), .out_10(\神经元_16_out_10 ));
  Hex_Digit_Display hex_digit_display_39 (.value(\神经元_31_out_10 ));  // open: dp
  Hex_Digit_Display hex_digit_display_40 (.value(\神经元_31_out_10_2 ));  // open: dp
  Hex_Digit_Display hex_digit_display_41 (.value(\神经元_32_out_10 ));  // open: dp
  Hex_Digit_Display hex_digit_display_42 (.value(\神经元_32_out_10_2 ));  // open: dp
  Clock clock_3 (.out(clock_3_out));
  \突触  \u_突触_129  (.in_1(\神经元_9_out_10 ), .in_2(\神经元_17_out_10 ), .in_3(clock_3_out), .out_4(\突触_129_out_4 ));
  \突触  \u_突触_130  (.in_1(\神经元_10_out_10 ), .in_2(\神经元_17_out_10 ), .in_3(clock_3_out), .out_4(\突触_130_out_4 ));
  \突触  \u_突触_131  (.in_1(undriven), .in_2(\神经元_17_out_10 ), .in_3(clock_3_out), .out_4(\突触_131_out_4 ));
  \突触  \u_突触_132  (.in_1(\神经元_11_out_10 ), .in_2(\神经元_17_out_10 ), .in_3(clock_3_out), .out_4(\突触_132_out_4 ));
  \突触  \u_突触_133  (.in_1(\神经元_12_out_10 ), .in_2(\神经元_17_out_10 ), .in_3(clock_3_out), .out_4(\突触_133_out_4 ));
  \突触  \u_突触_134  (.in_1(\神经元_13_out_10 ), .in_2(\神经元_17_out_10 ), .in_3(clock_3_out), .out_4(\突触_134_out_4 ));
  \突触  \u_突触_135  (.in_1(\神经元_14_out_10 ), .in_2(\神经元_17_out_10 ), .in_3(clock_3_out), .out_4(\突触_135_out_4 ));
  \突触  \u_突触_136  (.in_1(\神经元_16_out_10 ), .in_2(\神经元_17_out_10 ), .in_3(clock_3_out), .out_4(\突触_136_out_4 ));
  \突触  \u_突触_137  (.in_1(\神经元_9_out_10 ), .in_2(\神经元_18_out_10 ), .in_3(clock_3_out), .out_4(\突触_137_out_4 ));
  \突触  \u_突触_138  (.in_1(\神经元_10_out_10 ), .in_2(\神经元_18_out_10 ), .in_3(clock_3_out), .out_4(\突触_138_out_4 ));
  \突触  \u_突触_139  (.in_1(undriven), .in_2(\神经元_18_out_10 ), .in_3(clock_3_out), .out_4(\突触_139_out_4 ));
  \突触  \u_突触_140  (.in_1(\神经元_11_out_10 ), .in_2(\神经元_18_out_10 ), .in_3(clock_3_out), .out_4(\突触_140_out_4 ));
  \突触  \u_突触_141  (.in_1(\神经元_12_out_10 ), .in_2(\神经元_18_out_10 ), .in_3(clock_3_out), .out_4(\突触_141_out_4 ));
  \突触  \u_突触_142  (.in_1(\神经元_13_out_10 ), .in_2(\神经元_18_out_10 ), .in_3(clock_3_out), .out_4(\突触_142_out_4 ));
  \突触  \u_突触_143  (.in_1(\神经元_14_out_10 ), .in_2(\神经元_18_out_10 ), .in_3(clock_3_out), .out_4(\突触_143_out_4 ));
  \突触  \u_突触_144  (.in_1(\神经元_16_out_10 ), .in_2(\神经元_18_out_10 ), .in_3(clock_3_out), .out_4(\突触_144_out_4 ));
  \突触  \u_突触_145  (.in_1(\神经元_9_out_10 ), .in_2(\神经元_19_out_10 ), .in_3(clock_3_out), .out_4(\突触_145_out_4 ));
  \突触  \u_突触_146  (.in_1(\神经元_10_out_10 ), .in_2(\神经元_19_out_10 ), .in_3(clock_3_out), .out_4(\突触_146_out_4 ));
  \突触  \u_突触_147  (.in_1(undriven), .in_2(\神经元_19_out_10 ), .in_3(clock_3_out), .out_4(\突触_147_out_4 ));
  \突触  \u_突触_148  (.in_1(\神经元_11_out_10 ), .in_2(\神经元_19_out_10 ), .in_3(clock_3_out), .out_4(\突触_148_out_4 ));
  \突触  \u_突触_149  (.in_1(\神经元_12_out_10 ), .in_2(\神经元_19_out_10 ), .in_3(clock_3_out), .out_4(\突触_149_out_4 ));
  \突触  \u_突触_150  (.in_1(\神经元_13_out_10 ), .in_2(\神经元_19_out_10 ), .in_3(clock_3_out), .out_4(\突触_150_out_4 ));
  \突触  \u_突触_151  (.in_1(\神经元_14_out_10 ), .in_2(\神经元_19_out_10 ), .in_3(clock_3_out), .out_4(\突触_151_out_4 ));
  \突触  \u_突触_152  (.in_1(\神经元_16_out_10 ), .in_2(\神经元_19_out_10 ), .in_3(clock_3_out), .out_4(\突触_152_out_4 ));
  \突触  \u_突触_153  (.in_1(\神经元_9_out_10 ), .in_2(\神经元_20_out_10 ), .in_3(clock_3_out), .out_4(\突触_153_out_4 ));
  \突触  \u_突触_154  (.in_1(\神经元_10_out_10 ), .in_2(\神经元_20_out_10 ), .in_3(clock_3_out), .out_4(\突触_154_out_4 ));
  \突触  \u_突触_155  (.in_1(undriven), .in_2(\神经元_20_out_10 ), .in_3(clock_3_out), .out_4(\突触_155_out_4 ));
  \突触  \u_突触_156  (.in_1(\神经元_11_out_10 ), .in_2(\神经元_20_out_10 ), .in_3(clock_3_out), .out_4(\突触_156_out_4 ));
  \突触  \u_突触_157  (.in_1(\神经元_12_out_10 ), .in_2(\神经元_20_out_10 ), .in_3(clock_3_out), .out_4(\突触_157_out_4 ));
  \突触  \u_突触_158  (.in_1(\神经元_13_out_10 ), .in_2(\神经元_20_out_10 ), .in_3(clock_3_out), .out_4(\突触_158_out_4 ));
  \突触  \u_突触_159  (.in_1(\神经元_14_out_10 ), .in_2(\神经元_20_out_10 ), .in_3(clock_3_out), .out_4(\突触_159_out_4 ));
  \突触  \u_突触_160  (.in_1(\神经元_16_out_10 ), .in_2(\神经元_20_out_10 ), .in_3(clock_3_out), .out_4(\突触_160_out_4 ));
  \突触  \u_突触_161  (.in_1(\神经元_9_out_10 ), .in_2(\神经元_21_out_10 ), .in_3(clock_3_out), .out_4(\突触_161_out_4 ));
  \突触  \u_突触_162  (.in_1(\神经元_10_out_10 ), .in_2(\神经元_21_out_10 ), .in_3(clock_3_out), .out_4(\突触_162_out_4 ));
  \突触  \u_突触_163  (.in_1(undriven), .in_2(\神经元_21_out_10 ), .in_3(clock_3_out), .out_4(\突触_163_out_4 ));
  \突触  \u_突触_164  (.in_1(\神经元_11_out_10 ), .in_2(\神经元_21_out_10 ), .in_3(clock_3_out), .out_4(\突触_164_out_4 ));
  \突触  \u_突触_165  (.in_1(\神经元_12_out_10 ), .in_2(\神经元_21_out_10 ), .in_3(clock_3_out), .out_4(\突触_165_out_4 ));
  \突触  \u_突触_166  (.in_1(\神经元_13_out_10 ), .in_2(\神经元_21_out_10 ), .in_3(clock_3_out), .out_4(\突触_166_out_4 ));
  \突触  \u_突触_167  (.in_1(\神经元_14_out_10 ), .in_2(\神经元_21_out_10 ), .in_3(clock_3_out), .out_4(\突触_167_out_4 ));
  \突触  \u_突触_168  (.in_1(\神经元_16_out_10 ), .in_2(\神经元_21_out_10 ), .in_3(clock_3_out), .out_4(\突触_168_out_4 ));
  \突触  \u_突触_169  (.in_1(\神经元_9_out_10 ), .in_2(\神经元_22_out_10 ), .in_3(clock_3_out), .out_4(\突触_169_out_4 ));
  \突触  \u_突触_170  (.in_1(\神经元_10_out_10 ), .in_2(\神经元_22_out_10 ), .in_3(clock_3_out), .out_4(\突触_170_out_4 ));
  \突触  \u_突触_171  (.in_1(undriven), .in_2(\神经元_22_out_10 ), .in_3(clock_3_out), .out_4(\突触_171_out_4 ));
  \突触  \u_突触_172  (.in_1(\神经元_11_out_10 ), .in_2(\神经元_22_out_10 ), .in_3(clock_3_out), .out_4(\突触_172_out_4 ));
  \突触  \u_突触_173  (.in_1(\神经元_12_out_10 ), .in_2(\神经元_22_out_10 ), .in_3(clock_3_out), .out_4(\突触_173_out_4 ));
  \突触  \u_突触_174  (.in_1(\神经元_13_out_10 ), .in_2(\神经元_22_out_10 ), .in_3(clock_3_out), .out_4(\突触_174_out_4 ));
  \突触  \u_突触_175  (.in_1(\神经元_14_out_10 ), .in_2(\神经元_22_out_10 ), .in_3(clock_3_out), .out_4(\突触_175_out_4 ));
  \突触  \u_突触_176  (.in_1(\神经元_16_out_10 ), .in_2(\神经元_22_out_10 ), .in_3(clock_3_out), .out_4(\突触_176_out_4 ));
  \突触  \u_突触_177  (.in_1(\神经元_9_out_10 ), .in_2(\神经元_23_out_10 ), .in_3(clock_3_out), .out_4(\突触_177_out_4 ));
  \突触  \u_突触_178  (.in_1(\神经元_10_out_10 ), .in_2(\神经元_23_out_10 ), .in_3(clock_3_out), .out_4(\突触_178_out_4 ));
  \突触  \u_突触_179  (.in_1(undriven), .in_2(\神经元_23_out_10 ), .in_3(clock_3_out), .out_4(\突触_179_out_4 ));
  \突触  \u_突触_180  (.in_1(\神经元_11_out_10 ), .in_2(\神经元_23_out_10 ), .in_3(clock_3_out), .out_4(\突触_180_out_4 ));
  \突触  \u_突触_181  (.in_1(\神经元_12_out_10 ), .in_2(\神经元_23_out_10 ), .in_3(clock_3_out), .out_4(\突触_181_out_4 ));
  \突触  \u_突触_182  (.in_1(\神经元_13_out_10 ), .in_2(\神经元_23_out_10 ), .in_3(clock_3_out), .out_4(\突触_182_out_4 ));
  \突触  \u_突触_183  (.in_1(\神经元_14_out_10 ), .in_2(\神经元_23_out_10 ), .in_3(clock_3_out), .out_4(\突触_183_out_4 ));
  \突触  \u_突触_184  (.in_1(\神经元_16_out_10 ), .in_2(\神经元_23_out_10 ), .in_3(clock_3_out), .out_4(\突触_184_out_4 ));
  \突触  \u_突触_185  (.in_1(\神经元_9_out_10 ), .in_2(\神经元_24_out_10 ), .in_3(clock_3_out), .out_4(\突触_185_out_4 ));
  \突触  \u_突触_186  (.in_1(\神经元_10_out_10 ), .in_2(\神经元_24_out_10 ), .in_3(clock_3_out), .out_4(\突触_186_out_4 ));
  \突触  \u_突触_187  (.in_1(undriven), .in_2(\神经元_24_out_10 ), .in_3(clock_3_out), .out_4(\突触_187_out_4 ));
  \突触  \u_突触_188  (.in_1(\神经元_11_out_10 ), .in_2(\神经元_24_out_10 ), .in_3(clock_3_out), .out_4(\突触_188_out_4 ));
  \突触  \u_突触_189  (.in_1(\神经元_12_out_10 ), .in_2(\神经元_24_out_10 ), .in_3(clock_3_out), .out_4(\突触_189_out_4 ));
  \突触  \u_突触_190  (.in_1(\神经元_13_out_10 ), .in_2(\神经元_24_out_10 ), .in_3(clock_3_out), .out_4(\突触_190_out_4 ));
  \突触  \u_突触_191  (.in_1(\神经元_14_out_10 ), .in_2(\神经元_24_out_10 ), .in_3(clock_3_out), .out_4(\突触_191_out_4 ));
  \突触  \u_突触_192  (.in_1(\神经元_16_out_10 ), .in_2(\神经元_24_out_10 ), .in_3(clock_3_out), .out_4(\突触_192_out_4 ));
  \神经元  \u_神经元_17  (
    .In1(\突触_129_out_4 ), .In2(\突触_130_out_4 ), .In3(\突触_131_out_4 ), .In4(\突触_132_out_4 ),
    .In5(\突触_133_out_4 ), .In6(\突触_134_out_4 ), .In7(\突触_135_out_4 ), .In8(\突触_136_out_4 ),
    .bais({register_11_q_2, register_11_q}), .out_10(\神经元_17_out_10 ));
  \神经元  \u_神经元_18  (
    .In1(\突触_137_out_4 ), .In2(\突触_138_out_4 ), .In3(\突触_139_out_4 ), .In4(\突触_140_out_4 ),
    .In5(\突触_141_out_4 ), .In6(\突触_142_out_4 ), .In7(\突触_143_out_4 ), .In8(\突触_144_out_4 ),
    .bais({register_11_q_2, register_11_q}), .out_10(\神经元_18_out_10 ));
  \神经元  \u_神经元_19  (
    .In1(\突触_145_out_4 ), .In2(\突触_146_out_4 ), .In3(\突触_147_out_4 ), .In4(\突触_148_out_4 ),
    .In5(\突触_149_out_4 ), .In6(\突触_150_out_4 ), .In7(\突触_151_out_4 ), .In8(\突触_152_out_4 ),
    .bais({register_11_q_2, register_11_q}), .out_10(\神经元_19_out_10 ));
  \神经元  \u_神经元_20  (
    .In1(\突触_153_out_4 ), .In2(\突触_154_out_4 ), .In3(\突触_155_out_4 ), .In4(\突触_156_out_4 ),
    .In5(\突触_157_out_4 ), .In6(\突触_158_out_4 ), .In7(\突触_159_out_4 ), .In8(\突触_160_out_4 ),
    .bais({register_11_q_2, register_11_q}), .out_10(\神经元_20_out_10 ));
  \神经元  \u_神经元_21  (
    .In1(\突触_161_out_4 ), .In2(\突触_162_out_4 ), .In3(\突触_163_out_4 ), .In4(\突触_164_out_4 ),
    .In5(\突触_165_out_4 ), .In6(\突触_166_out_4 ), .In7(\突触_167_out_4 ), .In8(\突触_168_out_4 ),
    .bais({register_11_q_2, register_11_q}), .out_10(\神经元_21_out_10 ));
  \神经元  \u_神经元_22  (
    .In1(\突触_169_out_4 ), .In2(\突触_170_out_4 ), .In3(\突触_171_out_4 ), .In4(\突触_172_out_4 ),
    .In5(\突触_173_out_4 ), .In6(\突触_174_out_4 ), .In7(\突触_175_out_4 ), .In8(\突触_176_out_4 ),
    .bais({register_11_q_2, register_11_q}), .out_10(\神经元_22_out_10 ));
  \神经元  \u_神经元_23  (
    .In1(\突触_177_out_4 ), .In2(\突触_178_out_4 ), .In3(\突触_179_out_4 ), .In4(\突触_180_out_4 ),
    .In5(\突触_181_out_4 ), .In6(\突触_182_out_4 ), .In7(\突触_183_out_4 ), .In8(\突触_184_out_4 ),
    .bais({register_11_q_2, register_11_q}), .out_10(\神经元_23_out_10 ));
  \神经元  \u_神经元_24  (
    .In1(\突触_185_out_4 ), .In2(\突触_186_out_4 ), .In3(\突触_187_out_4 ), .In4(\突触_188_out_4 ),
    .In5(\突触_189_out_4 ), .In6(\突触_190_out_4 ), .In7(\突触_191_out_4 ), .In8(\突触_192_out_4 ),
    .bais({register_11_q_2, register_11_q}), .out_10(\神经元_24_out_10 ));
  Clock clock_4 (.out(clock_4_out));
  \突触  \u_突触_193  (
    .in_1(\神经元_17_out_10 ), .in_2({\神经元_25_out_10_2 , \神经元_25_out_10 }), .in_3(clock_4_out),
    .out_4(\突触_193_out_4 ));
  \突触  \u_突触_194  (
    .in_1(\神经元_18_out_10 ), .in_2({\神经元_25_out_10_2 , \神经元_25_out_10 }), .in_3(clock_4_out),
    .out_4(\突触_194_out_4 ));
  \突触  \u_突触_195  (
    .in_1(\神经元_19_out_10 ), .in_2({\神经元_25_out_10_2 , \神经元_25_out_10 }), .in_3(clock_4_out),
    .out_4(\突触_195_out_4 ));
  \突触  \u_突触_196  (
    .in_1(\神经元_20_out_10 ), .in_2({\神经元_25_out_10_2 , \神经元_25_out_10 }), .in_3(clock_4_out),
    .out_4(\突触_196_out_4 ));
  \突触  \u_突触_197  (
    .in_1(\神经元_21_out_10 ), .in_2({\神经元_25_out_10_2 , \神经元_25_out_10 }), .in_3(clock_4_out),
    .out_4(\突触_197_out_4 ));
  \突触  \u_突触_198  (
    .in_1(\神经元_22_out_10 ), .in_2({\神经元_25_out_10_2 , \神经元_25_out_10 }), .in_3(clock_4_out),
    .out_4(\突触_198_out_4 ));
  \突触  \u_突触_199  (
    .in_1(\神经元_23_out_10 ), .in_2({\神经元_25_out_10_2 , \神经元_25_out_10 }), .in_3(clock_4_out),
    .out_4(\突触_199_out_4 ));
  \突触  \u_突触_200  (
    .in_1(\神经元_24_out_10 ), .in_2({\神经元_25_out_10_2 , \神经元_25_out_10 }), .in_3(clock_4_out),
    .out_4(\突触_200_out_4 ));
  \突触  \u_突触_201  (
    .in_1(\神经元_17_out_10 ), .in_2({\神经元_26_out_10_2 , \神经元_26_out_10 }), .in_3(clock_4_out),
    .out_4(\突触_201_out_4 ));
  \突触  \u_突触_202  (
    .in_1(\神经元_18_out_10 ), .in_2({\神经元_26_out_10_2 , \神经元_26_out_10 }), .in_3(clock_4_out),
    .out_4(\突触_202_out_4 ));
  \突触  \u_突触_203  (
    .in_1(\神经元_19_out_10 ), .in_2({\神经元_26_out_10_2 , \神经元_26_out_10 }), .in_3(clock_4_out),
    .out_4(\突触_203_out_4 ));
  \突触  \u_突触_204  (
    .in_1(\神经元_20_out_10 ), .in_2({\神经元_26_out_10_2 , \神经元_26_out_10 }), .in_3(clock_4_out),
    .out_4(\突触_204_out_4 ));
  \突触  \u_突触_205  (
    .in_1(\神经元_21_out_10 ), .in_2({\神经元_26_out_10_2 , \神经元_26_out_10 }), .in_3(clock_4_out),
    .out_4(\突触_205_out_4 ));
  \突触  \u_突触_206  (
    .in_1(\神经元_22_out_10 ), .in_2({\神经元_26_out_10_2 , \神经元_26_out_10 }), .in_3(clock_4_out),
    .out_4(\突触_206_out_4 ));
  \突触  \u_突触_207  (
    .in_1(\神经元_23_out_10 ), .in_2({\神经元_26_out_10_2 , \神经元_26_out_10 }), .in_3(clock_4_out),
    .out_4(\突触_207_out_4 ));
  \突触  \u_突触_208  (
    .in_1(\神经元_24_out_10 ), .in_2({\神经元_26_out_10_2 , \神经元_26_out_10 }), .in_3(clock_4_out),
    .out_4(\突触_208_out_4 ));
  \突触  \u_突触_209  (
    .in_1(\神经元_17_out_10 ), .in_2({\神经元_27_out_10_2 , \神经元_27_out_10 }), .in_3(clock_4_out),
    .out_4(\突触_209_out_4 ));
  \突触  \u_突触_210  (
    .in_1(\神经元_18_out_10 ), .in_2({\神经元_27_out_10_2 , \神经元_27_out_10 }), .in_3(clock_4_out),
    .out_4(\突触_210_out_4 ));
  \突触  \u_突触_211  (
    .in_1(\神经元_19_out_10 ), .in_2({\神经元_27_out_10_2 , \神经元_27_out_10 }), .in_3(clock_4_out),
    .out_4(\突触_211_out_4 ));
  \突触  \u_突触_212  (
    .in_1(\神经元_20_out_10 ), .in_2({\神经元_27_out_10_2 , \神经元_27_out_10 }), .in_3(clock_4_out),
    .out_4(\突触_212_out_4 ));
  \突触  \u_突触_213  (
    .in_1(\神经元_21_out_10 ), .in_2({\神经元_27_out_10_2 , \神经元_27_out_10 }), .in_3(clock_4_out),
    .out_4(\突触_213_out_4 ));
  \突触  \u_突触_214  (
    .in_1(\神经元_22_out_10 ), .in_2({\神经元_27_out_10_2 , \神经元_27_out_10 }), .in_3(clock_4_out),
    .out_4(\突触_214_out_4 ));
  \突触  \u_突触_215  (
    .in_1(\神经元_23_out_10 ), .in_2({\神经元_27_out_10_2 , \神经元_27_out_10 }), .in_3(clock_4_out),
    .out_4(\突触_215_out_4 ));
  \突触  \u_突触_216  (
    .in_1(\神经元_24_out_10 ), .in_2({\神经元_27_out_10_2 , \神经元_27_out_10 }), .in_3(clock_4_out),
    .out_4(\突触_216_out_4 ));
  \突触  \u_突触_217  (
    .in_1(\神经元_17_out_10 ), .in_2({\神经元_28_out_10_2 , \神经元_28_out_10 }), .in_3(clock_4_out),
    .out_4(\突触_217_out_4 ));
  \突触  \u_突触_218  (
    .in_1(\神经元_18_out_10 ), .in_2({\神经元_28_out_10_2 , \神经元_28_out_10 }), .in_3(clock_4_out),
    .out_4(\突触_218_out_4 ));
  \突触  \u_突触_219  (
    .in_1(\神经元_19_out_10 ), .in_2({\神经元_28_out_10_2 , \神经元_28_out_10 }), .in_3(clock_4_out),
    .out_4(\突触_219_out_4 ));
  \突触  \u_突触_220  (
    .in_1(\神经元_20_out_10 ), .in_2({\神经元_28_out_10_2 , \神经元_28_out_10 }), .in_3(clock_4_out),
    .out_4(\突触_220_out_4 ));
  \突触  \u_突触_221  (
    .in_1(\神经元_21_out_10 ), .in_2({\神经元_28_out_10_2 , \神经元_28_out_10 }), .in_3(clock_4_out),
    .out_4(\突触_221_out_4 ));
  \突触  \u_突触_222  (
    .in_1(\神经元_22_out_10 ), .in_2({\神经元_28_out_10_2 , \神经元_28_out_10 }), .in_3(clock_4_out),
    .out_4(\突触_222_out_4 ));
  \突触  \u_突触_223  (
    .in_1(\神经元_23_out_10 ), .in_2({\神经元_28_out_10_2 , \神经元_28_out_10 }), .in_3(clock_4_out),
    .out_4(\突触_223_out_4 ));
  \突触  \u_突触_224  (
    .in_1(\神经元_24_out_10 ), .in_2({\神经元_28_out_10_2 , \神经元_28_out_10 }), .in_3(clock_4_out),
    .out_4(\突触_224_out_4 ));
  \突触  \u_突触_225  (
    .in_1(\神经元_17_out_10 ), .in_2({\神经元_29_out_10_2 , \神经元_29_out_10 }), .in_3(clock_4_out),
    .out_4(\突触_225_out_4 ));
  \突触  \u_突触_226  (
    .in_1(\神经元_18_out_10 ), .in_2({\神经元_29_out_10_2 , \神经元_29_out_10 }), .in_3(clock_4_out),
    .out_4(\突触_226_out_4 ));
  \突触  \u_突触_227  (
    .in_1(\神经元_19_out_10 ), .in_2({\神经元_29_out_10_2 , \神经元_29_out_10 }), .in_3(clock_4_out),
    .out_4(\突触_227_out_4 ));
  \突触  \u_突触_228  (
    .in_1(\神经元_20_out_10 ), .in_2({\神经元_29_out_10_2 , \神经元_29_out_10 }), .in_3(clock_4_out),
    .out_4(\突触_228_out_4 ));
  \突触  \u_突触_229  (
    .in_1(\神经元_21_out_10 ), .in_2({\神经元_29_out_10_2 , \神经元_29_out_10 }), .in_3(clock_4_out),
    .out_4(\突触_229_out_4 ));
  \突触  \u_突触_230  (
    .in_1(\神经元_22_out_10 ), .in_2({\神经元_29_out_10_2 , \神经元_29_out_10 }), .in_3(clock_4_out),
    .out_4(\突触_230_out_4 ));
  \突触  \u_突触_231  (
    .in_1(\神经元_23_out_10 ), .in_2({\神经元_29_out_10_2 , \神经元_29_out_10 }), .in_3(clock_4_out),
    .out_4(\突触_231_out_4 ));
  \突触  \u_突触_232  (
    .in_1(\神经元_24_out_10 ), .in_2({\神经元_29_out_10_2 , \神经元_29_out_10 }), .in_3(clock_4_out),
    .out_4(\突触_232_out_4 ));
  \突触  \u_突触_233  (
    .in_1(\神经元_17_out_10 ), .in_2({\神经元_30_out_10_2 , \神经元_30_out_10 }), .in_3(clock_4_out),
    .out_4(\突触_233_out_4 ));
  \突触  \u_突触_234  (
    .in_1(\神经元_18_out_10 ), .in_2({\神经元_30_out_10_2 , \神经元_30_out_10 }), .in_3(clock_4_out),
    .out_4(\突触_234_out_4 ));
  \突触  \u_突触_235  (
    .in_1(\神经元_19_out_10 ), .in_2({\神经元_30_out_10_2 , \神经元_30_out_10 }), .in_3(clock_4_out),
    .out_4(\突触_235_out_4 ));
  \突触  \u_突触_236  (
    .in_1(\神经元_20_out_10 ), .in_2({\神经元_30_out_10_2 , \神经元_30_out_10 }), .in_3(clock_4_out),
    .out_4(\突触_236_out_4 ));
  \突触  \u_突触_237  (
    .in_1(\神经元_21_out_10 ), .in_2({\神经元_30_out_10_2 , \神经元_30_out_10 }), .in_3(clock_4_out),
    .out_4(\突触_237_out_4 ));
  \突触  \u_突触_238  (
    .in_1(\神经元_22_out_10 ), .in_2({\神经元_30_out_10_2 , \神经元_30_out_10 }), .in_3(clock_4_out),
    .out_4(\突触_238_out_4 ));
  \突触  \u_突触_239  (
    .in_1(\神经元_23_out_10 ), .in_2({\神经元_30_out_10_2 , \神经元_30_out_10 }), .in_3(clock_4_out),
    .out_4(\突触_239_out_4 ));
  \突触  \u_突触_240  (
    .in_1(\神经元_24_out_10 ), .in_2({\神经元_30_out_10_2 , \神经元_30_out_10 }), .in_3(clock_4_out),
    .out_4(\突触_240_out_4 ));
  \突触  \u_突触_241  (
    .in_1(\神经元_17_out_10 ), .in_2({\神经元_31_out_10_2 , \神经元_31_out_10 }), .in_3(clock_4_out),
    .out_4(\突触_241_out_4 ));
  \突触  \u_突触_242  (
    .in_1(\神经元_18_out_10 ), .in_2({\神经元_31_out_10_2 , \神经元_31_out_10 }), .in_3(clock_4_out),
    .out_4(\突触_242_out_4 ));
  \突触  \u_突触_243  (
    .in_1(\神经元_19_out_10 ), .in_2({\神经元_31_out_10_2 , \神经元_31_out_10 }), .in_3(clock_4_out),
    .out_4(\突触_243_out_4 ));
  \突触  \u_突触_244  (
    .in_1(\神经元_20_out_10 ), .in_2({\神经元_31_out_10_2 , \神经元_31_out_10 }), .in_3(clock_4_out),
    .out_4(\突触_244_out_4 ));
  \突触  \u_突触_245  (
    .in_1(\神经元_21_out_10 ), .in_2({\神经元_31_out_10_2 , \神经元_31_out_10 }), .in_3(clock_4_out),
    .out_4(\突触_245_out_4 ));
  \突触  \u_突触_246  (
    .in_1(\神经元_22_out_10 ), .in_2({\神经元_31_out_10_2 , \神经元_31_out_10 }), .in_3(clock_4_out),
    .out_4(\突触_246_out_4 ));
  \突触  \u_突触_247  (
    .in_1(\神经元_23_out_10 ), .in_2({\神经元_31_out_10_2 , \神经元_31_out_10 }), .in_3(clock_4_out),
    .out_4(\突触_247_out_4 ));
  \突触  \u_突触_248  (
    .in_1(\神经元_24_out_10 ), .in_2({\神经元_31_out_10_2 , \神经元_31_out_10 }), .in_3(clock_4_out),
    .out_4(\突触_248_out_4 ));
  \突触  \u_突触_249  (
    .in_1(\神经元_17_out_10 ), .in_2({\神经元_32_out_10_2 , \神经元_32_out_10 }), .in_3(clock_4_out),
    .out_4(\突触_249_out_4 ));
  \突触  \u_突触_250  (
    .in_1(\神经元_18_out_10 ), .in_2({\神经元_32_out_10_2 , \神经元_32_out_10 }), .in_3(clock_4_out),
    .out_4(\突触_250_out_4 ));
  \突触  \u_突触_251  (
    .in_1(\神经元_19_out_10 ), .in_2({\神经元_32_out_10_2 , \神经元_32_out_10 }), .in_3(clock_4_out),
    .out_4(\突触_251_out_4 ));
  \突触  \u_突触_252  (
    .in_1(\神经元_20_out_10 ), .in_2({\神经元_32_out_10_2 , \神经元_32_out_10 }), .in_3(clock_4_out),
    .out_4(\突触_252_out_4 ));
  \突触  \u_突触_253  (
    .in_1(\神经元_21_out_10 ), .in_2({\神经元_32_out_10_2 , \神经元_32_out_10 }), .in_3(clock_4_out),
    .out_4(\突触_253_out_4 ));
  \突触  \u_突触_254  (
    .in_1(\神经元_22_out_10 ), .in_2({\神经元_32_out_10_2 , \神经元_32_out_10 }), .in_3(clock_4_out),
    .out_4(\突触_254_out_4 ));
  \突触  \u_突触_255  (
    .in_1(\神经元_23_out_10 ), .in_2({\神经元_32_out_10_2 , \神经元_32_out_10 }), .in_3(clock_4_out),
    .out_4(\突触_255_out_4 ));
  \突触  \u_突触_256  (
    .in_1(\神经元_24_out_10 ), .in_2({\神经元_32_out_10_2 , \神经元_32_out_10 }), .in_3(clock_4_out),
    .out_4(\突触_256_out_4 ));
  \神经元  \u_神经元_25  (
    .In1(\突触_193_out_4 ), .In2(\突触_194_out_4 ), .In3(\突触_195_out_4 ), .In4(\突触_196_out_4 ),
    .In5(\突触_197_out_4 ), .In6(\突触_198_out_4 ), .In7(\突触_199_out_4 ), .In8(\突触_200_out_4 ),
    .bais({register_12_q_2, register_12_q}), .out_10({\神经元_25_out_10_2 , \神经元_25_out_10 }));
  \神经元  \u_神经元_26  (
    .In1(\突触_201_out_4 ), .In2(\突触_202_out_4 ), .In3(\突触_203_out_4 ), .In4(\突触_204_out_4 ),
    .In5(\突触_205_out_4 ), .In6(\突触_206_out_4 ), .In7(\突触_207_out_4 ), .In8(\突触_208_out_4 ),
    .bais({register_12_q_2, register_12_q}), .out_10({\神经元_26_out_10_2 , \神经元_26_out_10 }));
  \神经元  \u_神经元_27  (
    .In1(\突触_209_out_4 ), .In2(\突触_210_out_4 ), .In3(\突触_211_out_4 ), .In4(\突触_212_out_4 ),
    .In5(\突触_213_out_4 ), .In6(\突触_214_out_4 ), .In7(\突触_215_out_4 ), .In8(\突触_216_out_4 ),
    .bais({register_12_q_2, register_12_q}), .out_10({\神经元_27_out_10_2 , \神经元_27_out_10 }));
  \神经元  \u_神经元_28  (
    .In1(\突触_217_out_4 ), .In2(\突触_218_out_4 ), .In3(\突触_219_out_4 ), .In4(\突触_220_out_4 ),
    .In5(\突触_221_out_4 ), .In6(\突触_222_out_4 ), .In7(\突触_223_out_4 ), .In8(\突触_224_out_4 ),
    .bais({register_12_q_2, register_12_q}), .out_10({\神经元_28_out_10_2 , \神经元_28_out_10 }));
  \神经元  \u_神经元_29  (
    .In1(\突触_225_out_4 ), .In2(\突触_226_out_4 ), .In3(\突触_227_out_4 ), .In4(\突触_228_out_4 ),
    .In5(\突触_229_out_4 ), .In6(\突触_230_out_4 ), .In7(\突触_231_out_4 ), .In8(\突触_232_out_4 ),
    .bais({register_12_q_2, register_12_q}), .out_10({\神经元_29_out_10_2 , \神经元_29_out_10 }));
  \神经元  \u_神经元_30  (
    .In1(\突触_233_out_4 ), .In2(\突触_234_out_4 ), .In3(\突触_235_out_4 ), .In4(\突触_236_out_4 ),
    .In5(\突触_237_out_4 ), .In6(\突触_238_out_4 ), .In7(\突触_239_out_4 ), .In8(\突触_240_out_4 ),
    .bais({register_12_q_2, register_12_q}), .out_10({\神经元_30_out_10_2 , \神经元_30_out_10 }));
  \神经元  \u_神经元_31  (
    .In1(\突触_241_out_4 ), .In2(\突触_242_out_4 ), .In3(\突触_243_out_4 ), .In4(\突触_244_out_4 ),
    .In5(\突触_245_out_4 ), .In6(\突触_246_out_4 ), .In7(\突触_247_out_4 ), .In8(\突触_248_out_4 ),
    .bais({register_12_q_2, register_12_q}), .out_10({\神经元_31_out_10_2 , \神经元_31_out_10 }));
  \神经元  \u_神经元_32  (
    .In1(\突触_249_out_4 ), .In2(\突触_250_out_4 ), .In3(\突触_251_out_4 ), .In4(\突触_252_out_4 ),
    .In5(\突触_253_out_4 ), .In6(\突触_254_out_4 ), .In7(\突触_255_out_4 ), .In8(\突触_256_out_4 ),
    .bais({register_12_q_2, register_12_q}), .out_10({\神经元_32_out_10_2 , \神经元_32_out_10 }));
endmodule
