// Logisim project snns.circ as structural Verilog: 3 circuits, main circuit SNNs
module SNNs (
  input  in_1,
  input  in_2,
  input  in_3
);

  wire _1, _2, _3, _4, clock_1_out, neuroph_2_out_6, neuroph_3_out_6, neuroph_4_out_6, neuroph_5_out_6,
       neuroph_6_out_6, neuroph_8_out_6, neuroph_9_out_6, neuroph_10_out_6, neuroph_11_out_6,
       neuroph_12_out_6, neuroph_13_out_6, neuroph_14_out_6, neuroph_15_out_6, neuroph_16_out_6,
       neuroph_17_out_6, neuroph_19_out_6, neuroph_20_out_6, neuroph_21_out_6, neuroph_22_out_6,
       neuroph_23_out_6, not_1_out;
  wire [31:0] shift_register_1_q31, shift_register_2_q31, shift_register_3_q31, shift_register_4_q31;

  not not_1 (not_1_out, in_1);
  Clock #(.highDuration(2), .lowDuration(2)) clock_1 (.out(clock_1_out));
  Shift_Register #(.length(32)) shift_register_1 (
    .shift(not_1_out), .in(_4), .clk(clock_1_out), .clr(in_2), .q0(shift_register_1_q31[31]),
    .q1(shift_register_1_q31[30]), .q2(shift_register_1_q31[29]), .q3(shift_register_1_q31[28]),
    .q4(shift_register_1_q31[27]), .q5(shift_register_1_q31[26]), .q6(shift_register_1_q31[25]),
    .q7(shift_register_1_q31[24]), .q8(shift_register_1_q31[23]), .q9(shift_register_1_q31[22]),
    .q10(shift_register_1_q31[21]), .q11(shift_register_1_q31[20]), .q12(shift_register_1_q31[19]),
    .q13(shift_register_1_q31[18]), .q14(shift_register_1_q31[17]), .q15(shift_register_1_q31[16]),
    .q16(shift_register_1_q31[15]), .q17(shift_register_1_q31[14]), .q18(shift_register_1_q31[13]),
    .q19(shift_register_1_q31[12]), .q20(shift_register_1_q31[11]), .q21(shift_register_1_q31[10]),
    .q22(shift_register_1_q31[9]), .q23(shift_register_1_q31[8]), .q24(shift_register_1_q31[7]),
    .q25(shift_register_1_q31[6]), .q26(shift_register_1_q31[5]), .q27(shift_register_1_q31[4]),
    .q28(shift_register_1_q31[3]), .q29(shift_register_1_q31[2]), .q30(shift_register_1_q31[1]),
    .q31(shift_register_1_q31[0]));  // open: out, load, d0, d1, d2, d3, d4, d5, d6, d7, d8, d9, d10, d11, d12, d13, d14, d15, d16, d17, d18, d19, d20, d21, d22, d23, d24, d25, d26, d27, d28, d29, d30, d31
  Shift_Register #(.length(32)) shift_register_2 (
    .shift(not_1_out), .in(_3), .clk(clock_1_out), .clr(in_2), .q0(shift_register_2_q31[31]),
    .q1(shift_register_2_q31[30]), .q2(shift_register_2_q31[29]), .q3(shift_register_2_q31[28]),
    .q4(shift_register_2_q31[27]), .q5(shift_register_2_q31[26]), .q6(shift_register_2_q31[25]),
    .q7(shift_register_2_q31[24]), .q8(shift_register_2_q31[23]), .q9(shift_register_2_q31[22]),
    .q10(shift_register_2_q31[21]), .q11(shift_register_2_q31[20]), .q12(shift_register_2_q31[19]),
    .q13(shift_register_2_q31[18]), .q14(shift_register_2_q31[17]), .q15(shift_register_2_q31[16]),
    .q16(shift_register_2_q31[15]), .q17(shift_register_2_q31[14]), .q18(shift_register_2_q31[13]),
    .q19(shift_register_2_q31[12]), .q20(shift_register_2_q31[11]), .q21(shift_register_2_q31[10]),
    .q22(shift_register_2_q31[9]), .q23(shift_register_2_q31[8]), .q24(shift_register_2_q31[7]),
    .q25(shift_register_2_q31[6]), .q26(shift_register_2_q31[5]), .q27(shift_register_2_q31[4]),
    .q28(shift_register_2_q31[3]), .q29(shift_register_2_q31[2]), .q30(shift_register_2_q31[1]),
    .q31(shift_register_2_q31[0]));  // open: out, load, d0, d1, d2, d3, d4, d5, d6, d7, d8, d9, d10, d11, d12, d13, d14, d15, d16, d17, d18, d19, d20, d21, d22, d23, d24, d25, d26, d27, d28, d29, d30, d31
  Shift_Register #(.length(32)) shift_register_3 (
    .shift(not_1_out), .in(_2), .clk(clock_1_out), .clr(in_2), .q0(shift_register_3_q31[31]),
    .q1(shift_register_3_q31[30]), .q2(shift_register_3_q31[29]), .q3(shift_register_3_q31[28]),
    .q4(shift_register_3_q31[27]), .q5(shift_register_3_q31[26]), .q6(shift_register_3_q31[25]),
    .q7(shift_register_3_q31[24]), .q8(shift_register_3_q31[23]), .q9(shift_register_3_q31[22]),
    .q10(shift_register_3_q31[21]), .q11(shift_register_3_q31[20]), .q12(shift_register_3_q31[19]),
    .q13(shift_register_3_q31[18]), .q14(shift_register_3_q31[17]), .q15(shift_register_3_q31[16]),
    .q16(shift_register_3_q31[15]), .q17(shift_register_3_q31[14]), .q18(shift_register_3_q31[13]),
    .q19(shift_register_3_q31[12]), .q20(shift_register_3_q31[11]), .q21(shift_register_3_q31[10]),
    .q22(shift_register_3_q31[9]), .q23(shift_register_3_q31[8]), .q24(shift_register_3_q31[7]),
    .q25(shift_register_3_q31[6]), .q26(shift_register_3_q31[5]), .q27(shift_register_3_q31[4]),
    .q28(shift_register_3_q31[3]), .q29(shift_register_3_q31[2]), .q30(shift_register_3_q31[1]),
    .q31(shift_register_3_q31[0]));  // open: out, load, d0, d1, d2, d3, d4, d5, d6, d7, d8, d9, d10, d11, d12, d13, d14, d15, d16, d17, d18, d19, d20, d21, d22, d23, d24, d25, d26, d27, d28, d29, d30, d31
  Shift_Register #(.length(32)) shift_register_4 (
    .shift(not_1_out), .in(_1), .clk(clock_1_out), .clr(in_2), .q0(shift_register_4_q31[31]),
    .q1(shift_register_4_q31[30]), .q2(shift_register_4_q31[29]), .q3(shift_register_4_q31[28]),
    .q4(shift_register_4_q31[27]), .q5(shift_register_4_q31[26]), .q6(shift_register_4_q31[25]),
    .q7(shift_register_4_q31[24]), .q8(shift_register_4_q31[23]), .q9(shift_register_4_q31[22]),
    .q10(shift_register_4_q31[21]), .q11(shift_register_4_q31[20]), .q12(shift_register_4_q31[19]),
    .q13(shift_register_4_q31[18]), .q14(shift_register_4_q31[17]), .q15(shift_register_4_q31[16]),
    .q16(shift_register_4_q31[15]), .q17(shift_register_4_q31[14]), .q18(shift_register_4_q31[13]),
    .q19(shift_register_4_q31[12]), .q20(shift_register_4_q31[11]), .q21(shift_register_4_q31[10]),
    .q22(shift_register_4_q31[9]), .q23(shift_register_4_q31[8]), .q24(shift_register_4_q31[7]),
    .q25(shift_register_4_q31[6]), .q26(shift_register_4_q31[5]), .q27(shift_register_4_q31[4]),
    .q28(shift_register_4_q31[3]), .q29(shift_register_4_q31[2]), .q30(shift_register_4_q31[1]),
    .q31(shift_register_4_q31[0]));  // open: out, load, d0, d1, d2, d3, d4, d5, d6, d7, d8, d9, d10, d11, d12, d13, d14, d15, d16, d17, d18, d19, d20, d21, d22, d23, d24, d25, d26, d27, d28, d29, d30, d31
  neuroph neuroph_1 (.in_1(neuroph_8_out_6), .in_5(in_2), .out_6(_4));  // open: in_2, in_3, in_4
  LED led_1 (.in(_4));
  neuroph neuroph_2 (.in_1(_4), .in_5(in_2), .out_6(neuroph_2_out_6));  // open: in_2, in_3, in_4
  LED led_2 (.in(neuroph_2_out_6));
  LED led_3 (.in(neuroph_3_out_6));
  neuroph neuroph_3 (.in_1(neuroph_2_out_6), .in_5(in_2), .out_6(neuroph_3_out_6));  // open: in_2, in_3, in_4
  neuroph neuroph_4 (.in_1(neuroph_3_out_6), .in_5(in_2), .out_6(neuroph_4_out_6));  // open: in_2, in_3, in_4
  LED led_4 (.in(neuroph_4_out_6));
  neuroph neuroph_5 (.in_1(neuroph_4_out_6), .in_5(in_2), .out_6(neuroph_5_out_6));  // open: in_2, in_3, in_4
  LED led_5 (.in(neuroph_5_out_6));
  LED led_6 (.in(neuroph_6_out_6));
  neuroph neuroph_6 (.in_1(neuroph_5_out_6), .in_5(in_2), .out_6(neuroph_6_out_6));  // open: in_2, in_3, in_4
  neuroph neuroph_7 (.in_1(neuroph_6_out_6), .in_5(in_2), .out_6(_1));  // open: in_2, in_3, in_4
  LED led_7 (.in(_1));
  neuroph neuroph_8 (.in_1(neuroph_10_out_6), .in_5(in_2), .out_6(neuroph_8_out_6));  // open: in_2, in_3, in_4
  LED led_8 (.in(neuroph_8_out_6));
  LED led_9 (.in(neuroph_9_out_6));
  neuroph neuroph_9 (.in_1(_1), .in_2(in_3), .in_5(in_2), .out_6(neuroph_9_out_6));  // open: in_3, in_4
  LED led_10 (.in(neuroph_10_out_6));
  neuroph neuroph_10 (.in_1(neuroph_13_out_6), .in_5(in_2), .out_6(neuroph_10_out_6));  // open: in_2, in_3, in_4
  neuroph neuroph_11 (.in_1(neuroph_12_out_6), .in_5(in_2), .out_6(neuroph_11_out_6));  // open: in_2, in_3, in_4
  neuroph neuroph_12 (.in_1(neuroph_9_out_6), .in_5(in_2), .out_6(neuroph_12_out_6));  // open: in_2, in_3, in_4
  LED led_11 (.in(neuroph_11_out_6));
  LED led_12 (.in(neuroph_12_out_6));
  LED led_13 (.in(neuroph_13_out_6));
  neuroph neuroph_13 (.in_1(neuroph_15_out_6), .in_5(in_2), .out_6(neuroph_13_out_6));  // open: in_2, in_3, in_4
  neuroph neuroph_14 (.in_1(neuroph_11_out_6), .in_5(in_2), .out_6(neuroph_14_out_6));  // open: in_2, in_3, in_4
  LED led_14 (.in(neuroph_14_out_6));
  neuroph neuroph_15 (.in_1(neuroph_17_out_6), .in_5(in_2), .out_6(neuroph_15_out_6));  // open: in_2, in_3, in_4
  LED led_15 (.in(neuroph_15_out_6));
  neuroph neuroph_16 (.in_1(neuroph_14_out_6), .in_5(in_2), .out_6(neuroph_16_out_6));  // open: in_2, in_3, in_4
  LED led_16 (.in(neuroph_16_out_6));
  DotMatrix #(.inputtype("row"), .matrixcols(32), .matrixrows(4)) dotmatrix_1 (
    .row0(shift_register_1_q31), .row1(shift_register_2_q31), .row2(shift_register_3_q31),
    .row3(shift_register_4_q31));
  LED led_17 (.in(neuroph_17_out_6));
  neuroph neuroph_17 (.in_1(_3), .in_5(in_2), .out_6(neuroph_17_out_6));  // open: in_2, in_3, in_4
  LED led_18 (.in(_3));
  neuroph neuroph_18 (.in_1(neuroph_19_out_6), .in_5(in_2), .out_6(_3));  // open: in_2, in_3, in_4
  neuroph neuroph_19 (.in_1(neuroph_20_out_6), .in_5(in_2), .out_6(neuroph_19_out_6));  // open: in_2, in_3, in_4
  LED led_19 (.in(neuroph_19_out_6));
  neuroph neuroph_20 (.in_1(neuroph_21_out_6), .in_5(in_2), .out_6(neuroph_20_out_6));  // open: in_2, in_3, in_4
  LED led_20 (.in(neuroph_20_out_6));
  LED led_21 (.in(neuroph_21_out_6));
  neuroph neuroph_21 (.in_1(neuroph_22_out_6), .in_5(in_2), .out_6(neuroph_21_out_6));  // open: in_2, in_3, in_4
  neuroph neuroph_22 (.in_1(neuroph_23_out_6), .in_5(in_2), .out_6(neuroph_22_out_6));  // open: in_2, in_3, in_4
  LED led_22 (.in(neuroph_22_out_6));
  neuroph neuroph_23 (.in_1(_2), .in_5(in_2), .out_6(neuroph_23_out_6));  // open: in_2, in_3, in_4
  LED led_23 (.in(neuroph_23_out_6));
  LED led_24 (.in(_2));
  neuroph neuroph_24 (.in_1(neuroph_16_out_6), .in_5(in_2), .out_6(_2));  // open: in_2, in_3, in_4
endmodule

module neuroph (
  input  in_1,
  input  in_2,
  input  in_3,
  input  in_4,
  input  in_5,
  output out_6
);

  wire adder_1_cout, adder_2_cout, adder_3_cout, and_1_out, clock_1_out, clock_2_out, comparator_1_gt,
       comparator_2_eq, comparator_3_eq, counter_1_carry, counter_2_q, d_ff_1_q, d_ff_1_qn, not_1_out,
       or_1_out, or_2_out, or_3_out;
  wire [1:0] bitadder_1_out;
  wire [7:0] counter_1_q;
  wire [8:0] adder_1_out, adder_2_out, adder_3_out, n00_1_out_4, n00_2_out_4, n00_3_out_4, n00_4_out_4;
  wire [10:0] divider_1_out, divider_1_rem;

  Pull_Resistor pull_resistor_1 (.node(in_1));
  Pull_Resistor pull_resistor_2 (.node(in_2));
  Pull_Resistor pull_resistor_3 (.node(in_3));
  Pull_Resistor pull_resistor_4 (.node(in_4));
  Clock clock_1 (.out(clock_1_out));
  _00 u_00_1 (.clock(clock_1_out), .reset(or_1_out), .spiking(in_1), .out_4(n00_1_out_4));
  _00 u_00_2 (.clock(clock_1_out), .reset(or_1_out), .spiking(in_2), .out_4(n00_2_out_4));
  _00 u_00_3 (.clock(clock_1_out), .reset(or_1_out), .spiking(in_3), .out_4(n00_3_out_4));
  _00 u_00_4 (.clock(clock_1_out), .reset(or_1_out), .spiking(in_4), .out_4(n00_4_out_4));
  or or_1 (or_1_out, in_5, not_1_out);
  Adder #(.width(9)) adder_1 (.a(n00_1_out_4), .b(n00_2_out_4), .out(adder_1_out), .cout(adder_1_cout));  // open: cin
  Adder #(.width(9)) adder_2 (.a(n00_3_out_4), .b(n00_4_out_4), .out(adder_2_out), .cout(adder_2_cout));  // open: cin
  Adder #(.width(9)) adder_3 (.a(adder_1_out), .b(adder_2_out), .out(adder_3_out), .cout(adder_3_cout));  // open: cin
  BitAdder #(.width(1)) bitadder_1 (.in0(adder_3_cout), .in1(adder_1_cout), .in2(adder_2_cout), .out(bitadder_1_out));
  Divider #(.width(11)) divider_1 (
    .a(11'h1f4), .b({bitadder_1_out, adder_3_out}), .out(divider_1_out), .rem(divider_1_rem));  // open: upper
  Comparator #(.width(11), .mode("unsigned")) comparator_1 (
    .a({bitadder_1_out, adder_3_out}), .b(11'h10), .gt(comparator_1_gt));  // open: eq, lt
  or or_2 (or_2_out, not_1_out, in_5);
  or or_3 (or_3_out, counter_1_carry, and_1_out);
  Counter #(.trigger("falling")) counter_1 (
    .load(1'b1), .D({divider_1_rem[10:7], divider_1_out[3:0]}), .count(comparator_2_eq), .Q(counter_1_q),
    .carry(counter_1_carry), .clk(clock_2_out), .clr(or_2_out));
  Clock #(.highDuration(2), .lowDuration(2)) clock_2 (.out(clock_2_out));
  Counter #(.width(1), .max('h1), .ongoal("stay")) counter_2 (
    .Q(counter_2_q), .clk(clock_2_out));  // open: load, D, count, carry, clr
  not not_1 (not_1_out, counter_2_q);
  D_Flip_Flop d_ff_1 (.clk(or_3_out), .D(d_ff_1_qn), .Q(d_ff_1_q), .Qn(d_ff_1_qn));  // open: preset, en, reset
  and and_1 (and_1_out, comparator_2_eq, ~comparator_3_eq);  // AND_Gate
  Comparator comparator_2 (
    .a(counter_1_q), .b({divider_1_rem[10:7], divider_1_out[3:0]}), .eq(comparator_2_eq));  // open: gt, lt
  Comparator comparator_3 (
    .a({divider_1_rem[10:7], divider_1_out[3:0]}), .b(8'h4), .eq(comparator_3_eq));  // open: gt, lt
  and and_2 (out_6, comparator_1_gt, d_ff_1_q);
endmodule

module _00 (
  input  clock,
  input  reset,
  input  spiking,
  output [8:0] out_4
);

  wire shift_register_1_q0, shift_register_1_q1, shift_register_1_q2, shift_register_1_q3,
       shift_register_1_q4, shift_register_1_q5, shift_register_1_q6, shift_register_1_q7,
       shift_register_1_q8, shift_register_1_q9, shift_register_1_q10, shift_register_1_q11,
       shift_register_1_q12, shift_register_1_q13, shift_register_1_q14, shift_register_1_q15;
  wire [15:0] multiplexer_1_out, multiplexer_2_out, multiplexer_3_out, multiplexer_4_out, multiplexer_5_out,
       multiplexer_6_out, multiplexer_7_out, multiplexer_8_out, multiplexer_9_out, multiplexer_10_out,
       multiplexer_11_out, multiplexer_12_out, multiplexer_13_out, multiplexer_14_out, multiplexer_15_out,
       multiplexer_16_out;

  Shift_Register #(.length(16)) shift_register_1 (
    .in(spiking), .clk(clock), .clr(reset), .q0(shift_register_1_q0), .q1(shift_register_1_q1),
    .q2(shift_register_1_q2), .q3(shift_register_1_q3), .q4(shift_register_1_q4), .q5(shift_register_1_q5),
    .q6(shift_register_1_q6), .q7(shift_register_1_q7), .q8(shift_register_1_q8), .q9(shift_register_1_q9),
    .q10(shift_register_1_q10), .q11(shift_register_1_q11), .q12(shift_register_1_q12),
    .q13(shift_register_1_q13), .q14(shift_register_1_q14), .q15(shift_register_1_q15));  // open: shift, out, load, d0, d1, d2, d3, d4, d5, d6, d7, d8, d9, d10, d11, d12, d13, d14, d15
  Multiplexer #(.width(16), .enable("false")) multiplexer_1 (
    .in0({16{1'b0}}), .in1(16'hf), .out(multiplexer_1_out), .sel(shift_register_1_q0));
  Multiplexer #(.width(16), .enable("false")) multiplexer_2 (
    .in0({16{1'b0}}), .in1(16'h7f), .out(multiplexer_2_out), .sel(shift_register_1_q1));
  Multiplexer #(.width(16), .enable("false")) multiplexer_3 (
    .in0({16{1'b0}}), .in1(16'h7ff), .out(multiplexer_3_out), .sel(shift_register_1_q2));
  Multiplexer #(.width(16), .enable("false")) multiplexer_4 (
    .in0({16{1'b0}}), .in1(16'h3fff), .out(multiplexer_4_out), .sel(shift_register_1_q3));
  Multiplexer #(.width(16), .enable("false")) multiplexer_5 (
    .in0({16{1'b0}}), .in1({16{1'b1}}), .out(multiplexer_5_out), .sel(shift_register_1_q4));
  Multiplexer #(.width(16), .enable("false")) multiplexer_6 (
    .in0({16{1'b0}}), .in1({16{1'b1}}), .out(multiplexer_6_out), .sel(shift_register_1_q5));
  Multiplexer #(.width(16), .enable("false")) multiplexer_7 (
    .in0({16{1'b0}}), .in1(16'h3fff), .out(multiplexer_7_out), .sel(shift_register_1_q6));
  Multiplexer #(.width(16), .enable("false")) multiplexer_8 (
    .in0({16{1'b0}}), .in1(16'h7ff), .out(multiplexer_8_out), .sel(shift_register_1_q7));
  Multiplexer #(.width(16), .enable("false")) multiplexer_9 (
    .in0({16{1'b0}}), .in1(16'hff), .out(multiplexer_9_out), .sel(shift_register_1_q8));
  Multiplexer #(.width(16), .enable("false")) multiplexer_10 (
    .in0({16{1'b0}}), .in1(16'h7f), .out(multiplexer_10_out), .sel(shift_register_1_q9));
  Multiplexer #(.width(16), .enable("false")) multiplexer_11 (
    .in0({16{1'b0}}), .in1(16'h3f), .out(multiplexer_11_out), .sel(shift_register_1_q10));
  Multiplexer #(.width(16), .enable("false")) multiplexer_12 (
    .in0({16{1'b0}}), .in1(16'h1f), .out(multiplexer_12_out), .sel(shift_register_1_q11));
  Multiplexer #(.width(16), .enable("false")) multiplexer_13 (
    .in0({16{1'b0}}), .in1(16'hf), .out(multiplexer_13_out), .sel(shift_register_1_q12));
  Multiplexer #(.width(16), .enable("false")) multiplexer_14 (
    .in0({16{1'b0}}), .in1(16'h7), .out(multiplexer_14_out), .sel(shift_register_1_q13));
  Multiplexer #(.width(16), .enable("false")) multiplexer_15 (
    .in0({16{1'b0}}), .in1(16'h3), .out(multiplexer_15_out), .sel(shift_register_1_q14));
  Multiplexer #(.width(16), .enable("false")) multiplexer_16 (
    .in0({16{1'b0}}), .in1(16'h1), .out(multiplexer_16_out), .sel(shift_register_1_q15));
  BitAdder #(.width(16)) bitadder_1 (
    .in0(multiplexer_1_out), .in1(multiplexer_2_out), .in2(multiplexer_3_out), .in3(multiplexer_4_out),
    .in4(multiplexer_5_out), .in5(multiplexer_6_out), .in6(multiplexer_7_out), .in7(multiplexer_8_out),
    .in8(multiplexer_9_out), .in9(multiplexer_10_out), .in10(multiplexer_11_out), .in11(multiplexer_12_out),
    .in12(multiplexer_13_out), .in13(multiplexer_14_out), .in14(multiplexer_15_out),
    .in15(multiplexer_16_out), .out(out_4));

  // Other names for the same wires on the sheet: clk = clock; rst = reset
endmodule
