// Logisim project 歌词显示器.circ as structural Verilog: 1 circuit, main circuit main
module main (
  input  in_1,
  input  in_2,
  input  in_3,
  input  in_4,
  input  in_5
);

  wire and_1_out, comparator_1_eq, inst_HLT, keyboard_1_avail, not_1_out;
  wire [7:0] counter_1_q, keyboard_1_data, ram_1_data;

  Keyboard keyboard_1 (.clk(in_2), .clr(in_5), .avail(keyboard_1_avail), .data(keyboard_1_data[6:0]));  // open: re
  Counter counter_1 (.Q(counter_1_q), .clk(and_1_out));  // open: load, D, count, carry, clr
  and and_1 (and_1_out, in_1, ~inst_HLT);  // AND_Gate
  Pull_Resistor pull_resistor_1 (.node(keyboard_1_data[7]));
  RAM #(.bus("separate")) ram_1 (
    .addr(counter_1_q), .din(keyboard_1_data), .data(ram_1_data), .str(keyboard_1_avail), .clk(in_3));  // open: sel, ld, clr
  and and_2 (inst_HLT, ram_1_data[7], comparator_1_eq);
  Comparator #(.width(7)) comparator_1 (.a(ram_1_data[6:0]), .b({7{1'b1}}), .eq(comparator_1_eq));  // open: gt, lt
  TTY #(.rows(4)) tty_1 (.data(ram_1_data[6:0]), .clk(in_4), .we(not_1_out));  // open: clr
  not not_1 (not_1_out, ram_1_data[7]);

  // Notes on the sheet:
  //   INST
  //   ff HLT
endmodule
